// Logisim project basicgates.circ as structural Verilog: 22 circuits, main circuit main
module main (
);

  wire [63:0] multiplier_1_cout, multiplier_1_out;

  // Probe on multiplier_1_out
  Multiplier #(.width(64)) multiplier_1 (
    .a(64'hfffffffff), .b(64'hffffffffffffffee), .out(multiplier_1_out), .cin(64'h1234),
    .cout(multiplier_1_cout));
  // Probe on multiplier_1_cout
  // Probe on nothing
  // Probe on nothing
endmodule

module adder64bit (
  input  inflow,
  input  [63:0] input1,
  input  [63:0] input2,
  output overflow,
  output [63:0] output1
);

  wire and_1_out, and_2_out, and_3_out, and_4_out, and_5_out, and_6_out, and_7_out, and_8_out, and_9_out,
       and_10_out, and_11_out, and_12_out, and_13_out, and_14_out, and_15_out, and_16_out, and_17_out,
       and_18_out, and_19_out, and_20_out, and_21_out, and_22_out, and_23_out, and_24_out, and_25_out,
       and_26_out, and_27_out, and_28_out, and_29_out, and_30_out, and_31_out, and_32_out, and_33_out,
       and_34_out, and_35_out, and_36_out, and_37_out, and_38_out, and_39_out, and_40_out, and_41_out,
       and_42_out, and_43_out, and_44_out, and_45_out, and_46_out, and_47_out, and_48_out, and_49_out,
       and_50_out, and_51_out, and_52_out, and_53_out, and_54_out, and_55_out, and_56_out, and_57_out,
       and_58_out, and_59_out, and_60_out, and_61_out, and_62_out, and_63_out, and_64_out, and_65_out,
       and_66_out, and_67_out, and_68_out, and_69_out, and_70_out, and_71_out, and_72_out, and_73_out,
       and_74_out, and_75_out, and_76_out, and_77_out, and_78_out, and_79_out, and_80_out, and_81_out,
       and_82_out, and_83_out, and_84_out, and_85_out, and_86_out, and_87_out, and_88_out, and_89_out,
       and_90_out, and_91_out, and_92_out, and_93_out, and_94_out, and_95_out, and_96_out, and_97_out,
       and_98_out, and_99_out, and_100_out, and_101_out, and_102_out, and_103_out, and_104_out, and_105_out,
       and_106_out, and_107_out, and_108_out, and_109_out, and_110_out, and_111_out, and_112_out,
       and_113_out, and_114_out, and_115_out, and_116_out, and_117_out, and_118_out, and_119_out,
       and_120_out, and_121_out, and_122_out, and_123_out, and_124_out, and_125_out, and_126_out,
       and_127_out, and_128_out, or_1_out, or_2_out, or_3_out, or_4_out, or_5_out, or_6_out, or_7_out,
       or_8_out, or_9_out, or_10_out, or_11_out, or_12_out, or_13_out, or_14_out, or_15_out, or_16_out,
       or_17_out, or_18_out, or_19_out, or_20_out, or_21_out, or_22_out, or_23_out, or_24_out, or_25_out,
       or_26_out, or_27_out, or_28_out, or_29_out, or_30_out, or_31_out, or_32_out, or_33_out, or_34_out,
       or_35_out, or_36_out, or_37_out, or_38_out, or_39_out, or_40_out, or_41_out, or_42_out, or_43_out,
       or_44_out, or_45_out, or_46_out, or_47_out, or_48_out, or_49_out, or_50_out, or_51_out, or_52_out,
       or_53_out, or_54_out, or_55_out, or_56_out, or_57_out, or_58_out, or_59_out, or_60_out, or_61_out,
       or_62_out, or_63_out, xor_1_out, xor_2_out, xor_3_out, xor_4_out, xor_5_out, xor_6_out, xor_7_out,
       xor_8_out, xor_17_out, xor_18_out, xor_19_out, xor_20_out, xor_21_out, xor_22_out, xor_23_out,
       xor_24_out, xor_33_out, xor_34_out, xor_35_out, xor_36_out, xor_37_out, xor_38_out, xor_39_out,
       xor_40_out, xor_49_out, xor_50_out, xor_51_out, xor_52_out, xor_53_out, xor_54_out, xor_55_out,
       xor_56_out, xor_65_out, xor_66_out, xor_67_out, xor_68_out, xor_69_out, xor_70_out, xor_71_out,
       xor_72_out, xor_81_out, xor_82_out, xor_83_out, xor_84_out, xor_85_out, xor_86_out, xor_87_out,
       xor_88_out, xor_97_out, xor_99_out, xor_101_out, xor_103_out, xor_105_out, xor_107_out, xor_109_out,
       xor_111_out, xor_113_out, xor_114_out, xor_115_out, xor_116_out, xor_117_out, xor_118_out,
       xor_119_out, xor_120_out;

  and and_1 (and_1_out, input1[0], input2[0]);
  xor xor_1 (xor_1_out, input1[0], input2[0]);
  and and_2 (and_2_out, input1[8], input2[8]);
  xor xor_2 (xor_2_out, input1[8], input2[8]);
  and and_3 (and_3_out, input1[16], input2[16]);
  xor xor_3 (xor_3_out, input1[16], input2[16]);
  and and_4 (and_4_out, input1[24], input2[24]);
  xor xor_4 (xor_4_out, input1[24], input2[24]);
  and and_5 (and_5_out, input1[32], input2[32]);
  xor xor_5 (xor_5_out, input1[32], input2[32]);
  and and_6 (and_6_out, input1[40], input2[40]);
  xor xor_6 (xor_6_out, input1[40], input2[40]);
  and and_7 (and_7_out, input1[48], input2[48]);
  xor xor_7 (xor_7_out, input1[48], input2[48]);
  and and_8 (and_8_out, input1[56], input2[56]);
  xor xor_8 (xor_8_out, input1[56], input2[56]);
  and and_9 (and_9_out, inflow, xor_1_out);
  xor xor_9 (output1[0], inflow, xor_1_out);
  and and_10 (and_10_out, or_57_out, xor_2_out);
  xor xor_10 (output1[8], or_57_out, xor_2_out);
  and and_11 (and_11_out, or_58_out, xor_3_out);
  xor xor_11 (output1[16], or_58_out, xor_3_out);
  and and_12 (and_12_out, or_59_out, xor_4_out);
  xor xor_12 (output1[24], or_59_out, xor_4_out);
  and and_13 (and_13_out, or_60_out, xor_5_out);
  xor xor_13 (output1[32], or_60_out, xor_5_out);
  and and_14 (and_14_out, or_61_out, xor_6_out);
  xor xor_14 (output1[40], or_61_out, xor_6_out);
  and and_15 (and_15_out, or_62_out, xor_7_out);
  xor xor_15 (output1[48], or_62_out, xor_7_out);
  and and_16 (and_16_out, or_63_out, xor_8_out);
  xor xor_16 (output1[56], or_63_out, xor_8_out);
  or or_1 (or_1_out, and_1_out, and_9_out);
  and and_17 (and_17_out, input1[1], input2[1]);
  or or_2 (or_2_out, and_2_out, and_10_out);
  and and_18 (and_18_out, input1[9], input2[9]);
  or or_3 (or_3_out, and_3_out, and_11_out);
  and and_19 (and_19_out, input1[17], input2[17]);
  or or_4 (or_4_out, and_4_out, and_12_out);
  and and_20 (and_20_out, input1[25], input2[25]);
  or or_5 (or_5_out, and_5_out, and_13_out);
  and and_21 (and_21_out, input1[33], input2[33]);
  or or_6 (or_6_out, and_6_out, and_14_out);
  and and_22 (and_22_out, input1[41], input2[41]);
  or or_7 (or_7_out, and_7_out, and_15_out);
  and and_23 (and_23_out, input1[49], input2[49]);
  or or_8 (or_8_out, and_8_out, and_16_out);
  and and_24 (and_24_out, input1[57], input2[57]);
  and and_25 (and_25_out, or_1_out, xor_17_out);
  xor xor_17 (xor_17_out, input1[1], input2[1]);
  and and_26 (and_26_out, or_2_out, xor_18_out);
  xor xor_18 (xor_18_out, input1[9], input2[9]);
  and and_27 (and_27_out, or_3_out, xor_19_out);
  xor xor_19 (xor_19_out, input1[17], input2[17]);
  and and_28 (and_28_out, or_4_out, xor_20_out);
  xor xor_20 (xor_20_out, input1[25], input2[25]);
  and and_29 (and_29_out, or_5_out, xor_21_out);
  xor xor_21 (xor_21_out, input1[33], input2[33]);
  and and_30 (and_30_out, or_6_out, xor_22_out);
  xor xor_22 (xor_22_out, input1[41], input2[41]);
  and and_31 (and_31_out, or_7_out, xor_23_out);
  xor xor_23 (xor_23_out, input1[49], input2[49]);
  and and_32 (and_32_out, or_8_out, xor_24_out);
  xor xor_24 (xor_24_out, input1[57], input2[57]);
  or or_9 (or_9_out, and_17_out, and_25_out);
  xor xor_25 (output1[1], or_1_out, xor_17_out);
  or or_10 (or_10_out, and_18_out, and_26_out);
  xor xor_26 (output1[9], or_2_out, xor_18_out);
  or or_11 (or_11_out, and_19_out, and_27_out);
  xor xor_27 (output1[17], or_3_out, xor_19_out);
  or or_12 (or_12_out, and_20_out, and_28_out);
  xor xor_28 (output1[25], or_4_out, xor_20_out);
  or or_13 (or_13_out, and_21_out, and_29_out);
  xor xor_29 (output1[33], or_5_out, xor_21_out);
  or or_14 (or_14_out, and_22_out, and_30_out);
  xor xor_30 (output1[41], or_6_out, xor_22_out);
  or or_15 (or_15_out, and_23_out, and_31_out);
  xor xor_31 (output1[49], or_7_out, xor_23_out);
  or or_16 (or_16_out, and_24_out, and_32_out);
  xor xor_32 (output1[57], or_8_out, xor_24_out);
  and and_33 (and_33_out, input1[2], input2[2]);
  xor xor_33 (xor_33_out, input1[2], input2[2]);
  and and_34 (and_34_out, input1[10], input2[10]);
  xor xor_34 (xor_34_out, input1[10], input2[10]);
  and and_35 (and_35_out, input1[18], input2[18]);
  xor xor_35 (xor_35_out, input1[18], input2[18]);
  and and_36 (and_36_out, input1[26], input2[26]);
  xor xor_36 (xor_36_out, input1[26], input2[26]);
  and and_37 (and_37_out, input1[34], input2[34]);
  xor xor_37 (xor_37_out, input1[34], input2[34]);
  and and_38 (and_38_out, input1[42], input2[42]);
  xor xor_38 (xor_38_out, input1[42], input2[42]);
  and and_39 (and_39_out, input1[50], input2[50]);
  xor xor_39 (xor_39_out, input1[50], input2[50]);
  and and_40 (and_40_out, input1[58], input2[58]);
  xor xor_40 (xor_40_out, input1[58], input2[58]);
  or or_17 (or_17_out, and_33_out, and_41_out);
  and and_41 (and_41_out, or_9_out, xor_33_out);
  xor xor_41 (output1[2], or_9_out, xor_33_out);
  or or_18 (or_18_out, and_34_out, and_42_out);
  and and_42 (and_42_out, or_10_out, xor_34_out);
  xor xor_42 (output1[10], or_10_out, xor_34_out);
  or or_19 (or_19_out, and_35_out, and_43_out);
  and and_43 (and_43_out, or_11_out, xor_35_out);
  xor xor_43 (output1[18], or_11_out, xor_35_out);
  or or_20 (or_20_out, and_36_out, and_44_out);
  and and_44 (and_44_out, or_12_out, xor_36_out);
  xor xor_44 (output1[26], or_12_out, xor_36_out);
  or or_21 (or_21_out, and_37_out, and_45_out);
  and and_45 (and_45_out, or_13_out, xor_37_out);
  xor xor_45 (output1[34], or_13_out, xor_37_out);
  or or_22 (or_22_out, and_38_out, and_46_out);
  and and_46 (and_46_out, or_14_out, xor_38_out);
  xor xor_46 (output1[42], or_14_out, xor_38_out);
  or or_23 (or_23_out, and_39_out, and_47_out);
  and and_47 (and_47_out, or_15_out, xor_39_out);
  xor xor_47 (output1[50], or_15_out, xor_39_out);
  or or_24 (or_24_out, and_40_out, and_48_out);
  and and_48 (and_48_out, or_16_out, xor_40_out);
  xor xor_48 (output1[58], or_16_out, xor_40_out);
  and and_49 (and_49_out, input1[3], input2[3]);
  xor xor_49 (xor_49_out, input1[3], input2[3]);
  and and_50 (and_50_out, input1[11], input2[11]);
  xor xor_50 (xor_50_out, input1[11], input2[11]);
  and and_51 (and_51_out, input1[19], input2[19]);
  xor xor_51 (xor_51_out, input1[19], input2[19]);
  and and_52 (and_52_out, input1[27], input2[27]);
  xor xor_52 (xor_52_out, input1[27], input2[27]);
  and and_53 (and_53_out, input1[35], input2[35]);
  xor xor_53 (xor_53_out, input1[35], input2[35]);
  and and_54 (and_54_out, input1[43], input2[43]);
  xor xor_54 (xor_54_out, input1[43], input2[43]);
  and and_55 (and_55_out, input1[51], input2[51]);
  xor xor_55 (xor_55_out, input1[51], input2[51]);
  and and_56 (and_56_out, input1[59], input2[59]);
  xor xor_56 (xor_56_out, input1[59], input2[59]);
  and and_57 (and_57_out, or_17_out, xor_49_out);
  xor xor_57 (output1[3], or_17_out, xor_49_out);
  and and_58 (and_58_out, or_18_out, xor_50_out);
  xor xor_58 (output1[11], or_18_out, xor_50_out);
  and and_59 (and_59_out, or_19_out, xor_51_out);
  xor xor_59 (output1[19], or_19_out, xor_51_out);
  and and_60 (and_60_out, or_20_out, xor_52_out);
  xor xor_60 (output1[27], or_20_out, xor_52_out);
  and and_61 (and_61_out, or_21_out, xor_53_out);
  xor xor_61 (output1[35], or_21_out, xor_53_out);
  and and_62 (and_62_out, or_22_out, xor_54_out);
  xor xor_62 (output1[43], or_22_out, xor_54_out);
  and and_63 (and_63_out, or_23_out, xor_55_out);
  xor xor_63 (output1[51], or_23_out, xor_55_out);
  and and_64 (and_64_out, or_24_out, xor_56_out);
  xor xor_64 (output1[59], or_24_out, xor_56_out);
  or or_25 (or_25_out, and_49_out, and_57_out);
  or or_26 (or_26_out, and_50_out, and_58_out);
  or or_27 (or_27_out, and_51_out, and_59_out);
  or or_28 (or_28_out, and_52_out, and_60_out);
  or or_29 (or_29_out, and_53_out, and_61_out);
  or or_30 (or_30_out, and_54_out, and_62_out);
  or or_31 (or_31_out, and_55_out, and_63_out);
  or or_32 (or_32_out, and_56_out, and_64_out);
  and and_65 (and_65_out, input1[4], input2[4]);
  xor xor_65 (xor_65_out, input1[4], input2[4]);
  and and_66 (and_66_out, input1[12], input2[12]);
  xor xor_66 (xor_66_out, input1[12], input2[12]);
  and and_67 (and_67_out, input1[20], input2[20]);
  xor xor_67 (xor_67_out, input1[20], input2[20]);
  and and_68 (and_68_out, input1[28], input2[28]);
  xor xor_68 (xor_68_out, input1[28], input2[28]);
  and and_69 (and_69_out, input1[36], input2[36]);
  xor xor_69 (xor_69_out, input1[36], input2[36]);
  and and_70 (and_70_out, input1[44], input2[44]);
  xor xor_70 (xor_70_out, input1[44], input2[44]);
  and and_71 (and_71_out, input1[52], input2[52]);
  xor xor_71 (xor_71_out, input1[52], input2[52]);
  and and_72 (and_72_out, input1[60], input2[60]);
  xor xor_72 (xor_72_out, input1[60], input2[60]);
  or or_33 (or_33_out, and_65_out, and_73_out);
  and and_73 (and_73_out, or_25_out, xor_65_out);
  xor xor_73 (output1[4], or_25_out, xor_65_out);
  or or_34 (or_34_out, and_66_out, and_74_out);
  and and_74 (and_74_out, or_26_out, xor_66_out);
  xor xor_74 (output1[12], or_26_out, xor_66_out);
  or or_35 (or_35_out, and_67_out, and_75_out);
  and and_75 (and_75_out, or_27_out, xor_67_out);
  xor xor_75 (output1[20], or_27_out, xor_67_out);
  or or_36 (or_36_out, and_68_out, and_76_out);
  and and_76 (and_76_out, or_28_out, xor_68_out);
  xor xor_76 (output1[28], or_28_out, xor_68_out);
  or or_37 (or_37_out, and_69_out, and_77_out);
  and and_77 (and_77_out, or_29_out, xor_69_out);
  xor xor_77 (output1[36], or_29_out, xor_69_out);
  or or_38 (or_38_out, and_70_out, and_78_out);
  and and_78 (and_78_out, or_30_out, xor_70_out);
  xor xor_78 (output1[44], or_30_out, xor_70_out);
  or or_39 (or_39_out, and_71_out, and_79_out);
  and and_79 (and_79_out, or_31_out, xor_71_out);
  xor xor_79 (output1[52], or_31_out, xor_71_out);
  or or_40 (or_40_out, and_72_out, and_80_out);
  and and_80 (and_80_out, or_32_out, xor_72_out);
  xor xor_80 (output1[60], or_32_out, xor_72_out);
  and and_81 (and_81_out, input1[5], input2[5]);
  xor xor_81 (xor_81_out, input1[5], input2[5]);
  and and_82 (and_82_out, input1[13], input2[13]);
  xor xor_82 (xor_82_out, input1[13], input2[13]);
  and and_83 (and_83_out, input1[21], input2[21]);
  xor xor_83 (xor_83_out, input1[21], input2[21]);
  and and_84 (and_84_out, input1[29], input2[29]);
  xor xor_84 (xor_84_out, input1[29], input2[29]);
  and and_85 (and_85_out, input1[37], input2[37]);
  xor xor_85 (xor_85_out, input1[37], input2[37]);
  and and_86 (and_86_out, input1[45], input2[45]);
  xor xor_86 (xor_86_out, input1[45], input2[45]);
  and and_87 (and_87_out, input1[53], input2[53]);
  xor xor_87 (xor_87_out, input1[53], input2[53]);
  and and_88 (and_88_out, input1[61], input2[61]);
  xor xor_88 (xor_88_out, input1[61], input2[61]);
  or or_41 (or_41_out, and_81_out, and_89_out);
  and and_89 (and_89_out, or_33_out, xor_81_out);
  xor xor_89 (output1[5], or_33_out, xor_81_out);
  or or_42 (or_42_out, and_82_out, and_90_out);
  and and_90 (and_90_out, or_34_out, xor_82_out);
  xor xor_90 (output1[13], or_34_out, xor_82_out);
  or or_43 (or_43_out, and_83_out, and_91_out);
  and and_91 (and_91_out, or_35_out, xor_83_out);
  xor xor_91 (output1[21], or_35_out, xor_83_out);
  or or_44 (or_44_out, and_84_out, and_92_out);
  and and_92 (and_92_out, or_36_out, xor_84_out);
  xor xor_92 (output1[29], or_36_out, xor_84_out);
  or or_45 (or_45_out, and_85_out, and_93_out);
  and and_93 (and_93_out, or_37_out, xor_85_out);
  xor xor_93 (output1[37], or_37_out, xor_85_out);
  or or_46 (or_46_out, and_86_out, and_94_out);
  and and_94 (and_94_out, or_38_out, xor_86_out);
  xor xor_94 (output1[45], or_38_out, xor_86_out);
  or or_47 (or_47_out, and_87_out, and_95_out);
  and and_95 (and_95_out, or_39_out, xor_87_out);
  xor xor_95 (output1[53], or_39_out, xor_87_out);
  or or_48 (or_48_out, and_88_out, and_96_out);
  and and_96 (and_96_out, or_40_out, xor_88_out);
  xor xor_96 (output1[61], or_40_out, xor_88_out);
  and and_97 (and_97_out, input1[6], input2[6]);
  and and_98 (and_98_out, input1[14], input2[14]);
  and and_99 (and_99_out, input1[22], input2[22]);
  and and_100 (and_100_out, input1[30], input2[30]);
  and and_101 (and_101_out, input1[38], input2[38]);
  and and_102 (and_102_out, input1[46], input2[46]);
  and and_103 (and_103_out, input1[54], input2[54]);
  and and_104 (and_104_out, input1[62], input2[62]);
  and and_105 (and_105_out, or_41_out, xor_97_out);
  xor xor_97 (xor_97_out, input1[6], input2[6]);
  xor xor_98 (output1[6], or_41_out, xor_97_out);
  and and_106 (and_106_out, or_42_out, xor_99_out);
  xor xor_99 (xor_99_out, input1[14], input2[14]);
  xor xor_100 (output1[14], or_42_out, xor_99_out);
  and and_107 (and_107_out, or_43_out, xor_101_out);
  xor xor_101 (xor_101_out, input1[22], input2[22]);
  xor xor_102 (output1[22], or_43_out, xor_101_out);
  and and_108 (and_108_out, or_44_out, xor_103_out);
  xor xor_103 (xor_103_out, input1[30], input2[30]);
  xor xor_104 (output1[30], or_44_out, xor_103_out);
  and and_109 (and_109_out, or_45_out, xor_105_out);
  xor xor_105 (xor_105_out, input1[38], input2[38]);
  xor xor_106 (output1[38], or_45_out, xor_105_out);
  and and_110 (and_110_out, or_46_out, xor_107_out);
  xor xor_107 (xor_107_out, input1[46], input2[46]);
  xor xor_108 (output1[46], or_46_out, xor_107_out);
  and and_111 (and_111_out, or_47_out, xor_109_out);
  xor xor_109 (xor_109_out, input1[54], input2[54]);
  xor xor_110 (output1[54], or_47_out, xor_109_out);
  and and_112 (and_112_out, or_48_out, xor_111_out);
  xor xor_111 (xor_111_out, input1[62], input2[62]);
  xor xor_112 (output1[62], or_48_out, xor_111_out);
  or or_49 (or_49_out, and_97_out, and_105_out);
  or or_50 (or_50_out, and_98_out, and_106_out);
  or or_51 (or_51_out, and_99_out, and_107_out);
  or or_52 (or_52_out, and_100_out, and_108_out);
  or or_53 (or_53_out, and_101_out, and_109_out);
  or or_54 (or_54_out, and_102_out, and_110_out);
  or or_55 (or_55_out, and_103_out, and_111_out);
  or or_56 (or_56_out, and_104_out, and_112_out);
  and and_113 (and_113_out, input1[7], input2[7]);
  xor xor_113 (xor_113_out, input1[7], input2[7]);
  and and_114 (and_114_out, input1[15], input2[15]);
  xor xor_114 (xor_114_out, input1[15], input2[15]);
  and and_115 (and_115_out, input1[23], input2[23]);
  xor xor_115 (xor_115_out, input1[23], input2[23]);
  and and_116 (and_116_out, input1[31], input2[31]);
  xor xor_116 (xor_116_out, input1[31], input2[31]);
  and and_117 (and_117_out, input1[39], input2[39]);
  xor xor_117 (xor_117_out, input1[39], input2[39]);
  and and_118 (and_118_out, input1[47], input2[47]);
  xor xor_118 (xor_118_out, input1[47], input2[47]);
  and and_119 (and_119_out, input1[55], input2[55]);
  xor xor_119 (xor_119_out, input1[55], input2[55]);
  and and_120 (and_120_out, input1[63], input2[63]);
  xor xor_120 (xor_120_out, input1[63], input2[63]);
  or or_57 (or_57_out, and_113_out, and_121_out);
  and and_121 (and_121_out, or_49_out, xor_113_out);
  xor xor_121 (output1[7], or_49_out, xor_113_out);
  or or_58 (or_58_out, and_114_out, and_122_out);
  and and_122 (and_122_out, or_50_out, xor_114_out);
  xor xor_122 (output1[15], or_50_out, xor_114_out);
  or or_59 (or_59_out, and_115_out, and_123_out);
  and and_123 (and_123_out, or_51_out, xor_115_out);
  xor xor_123 (output1[23], or_51_out, xor_115_out);
  or or_60 (or_60_out, and_116_out, and_124_out);
  and and_124 (and_124_out, or_52_out, xor_116_out);
  xor xor_124 (output1[31], or_52_out, xor_116_out);
  or or_61 (or_61_out, and_117_out, and_125_out);
  and and_125 (and_125_out, or_53_out, xor_117_out);
  xor xor_125 (output1[39], or_53_out, xor_117_out);
  or or_62 (or_62_out, and_118_out, and_126_out);
  and and_126 (and_126_out, or_54_out, xor_118_out);
  xor xor_126 (output1[47], or_54_out, xor_118_out);
  or or_63 (or_63_out, and_119_out, and_127_out);
  and and_127 (and_127_out, or_55_out, xor_119_out);
  xor xor_127 (output1[55], or_55_out, xor_119_out);
  or or_64 (overflow, and_120_out, and_128_out);
  and and_128 (and_128_out, or_56_out, xor_120_out);
  xor xor_128 (output1[63], or_56_out, xor_120_out);

  // Notes on the sheet:
  //   input1: initial=0xffffffffffffff
  //   input2: initial=0x1313131313131313
endmodule

module negate64bit (
  input  [63:0] input1,
  output [63:0] output1
);

  wire [63:0] not_1_out;

  assign not_1_out = ~input1;  // NOT_Gate not_1, 64 bits wide
  adder64bit adder64bit_1 (.input1(64'h1), .input2(not_1_out), .output1(output1));  // open: inflow, overflow
endmodule

module subtractor64bit (
  input  inborrow,
  input  [63:0] input1,
  input  [63:0] input2,
  output borrow,
  output [63:0] output1
);

  wire and_1_out, and_2_out, and_3_out, and_4_out, and_5_out, and_6_out, and_7_out, and_8_out, and_9_out,
       and_10_out, and_11_out, and_12_out, and_13_out, and_14_out, and_15_out, and_16_out, and_17_out,
       and_18_out, and_19_out, and_20_out, and_21_out, and_22_out, and_23_out, and_24_out, and_25_out,
       and_26_out, and_27_out, and_28_out, and_29_out, and_30_out, and_31_out, and_32_out, and_33_out,
       and_34_out, and_35_out, and_36_out, and_37_out, and_38_out, and_39_out, and_40_out, and_41_out,
       and_42_out, and_43_out, and_44_out, and_45_out, and_46_out, and_47_out, and_48_out, and_49_out,
       and_50_out, and_51_out, and_52_out, and_53_out, and_54_out, and_55_out, and_56_out, and_57_out,
       and_58_out, and_59_out, and_60_out, and_61_out, and_62_out, and_63_out, and_64_out, and_65_out,
       and_66_out, and_67_out, and_68_out, and_69_out, and_70_out, and_71_out, and_72_out, and_73_out,
       and_74_out, and_75_out, and_76_out, and_77_out, and_78_out, and_79_out, and_80_out, and_81_out,
       and_82_out, and_83_out, and_84_out, and_85_out, and_86_out, and_87_out, and_88_out, and_89_out,
       and_90_out, and_91_out, and_92_out, and_93_out, and_94_out, and_95_out, and_96_out, and_97_out,
       and_98_out, and_99_out, and_100_out, and_101_out, and_102_out, and_103_out, and_104_out, and_105_out,
       and_106_out, and_107_out, and_108_out, and_109_out, and_110_out, and_111_out, and_112_out,
       and_113_out, and_114_out, and_115_out, and_116_out, and_117_out, and_118_out, and_119_out,
       and_120_out, and_121_out, and_122_out, and_123_out, and_124_out, and_125_out, and_126_out,
       and_127_out, and_128_out, not_1_out, not_2_out, not_3_out, not_4_out, not_5_out, not_6_out, not_7_out,
       not_8_out, not_9_out, not_10_out, not_11_out, not_12_out, not_13_out, not_14_out, not_15_out,
       not_16_out, not_17_out, not_18_out, not_19_out, not_20_out, not_21_out, not_22_out, not_23_out,
       not_24_out, not_25_out, not_26_out, not_27_out, not_28_out, not_29_out, not_30_out, not_31_out,
       not_32_out, not_33_out, not_34_out, not_35_out, not_36_out, not_37_out, not_38_out, not_39_out,
       not_40_out, not_41_out, not_42_out, not_43_out, not_44_out, not_45_out, not_46_out, not_47_out,
       not_48_out, not_49_out, not_50_out, not_51_out, not_52_out, not_53_out, not_54_out, not_55_out,
       not_56_out, not_57_out, not_58_out, not_59_out, not_60_out, not_61_out, not_62_out, not_63_out,
       not_64_out, not_65_out, not_66_out, not_67_out, not_68_out, not_69_out, not_70_out, not_71_out,
       not_72_out, not_73_out, not_74_out, not_75_out, not_76_out, not_77_out, not_78_out, not_79_out,
       not_80_out, not_81_out, not_82_out, not_83_out, not_84_out, not_85_out, not_86_out, not_87_out,
       not_88_out, not_89_out, not_90_out, not_91_out, not_92_out, not_93_out, not_94_out, not_95_out,
       not_96_out, not_97_out, not_98_out, not_99_out, not_100_out, not_101_out, not_102_out, not_103_out,
       not_104_out, not_105_out, not_106_out, not_107_out, not_108_out, not_109_out, not_110_out,
       not_111_out, not_112_out, not_113_out, not_114_out, not_115_out, not_116_out, not_117_out,
       not_118_out, not_119_out, not_120_out, not_121_out, not_122_out, not_123_out, not_124_out,
       not_125_out, not_126_out, not_127_out, not_128_out, or_1_out, or_2_out, or_3_out, or_4_out, or_5_out,
       or_6_out, or_7_out, or_8_out, or_9_out, or_10_out, or_11_out, or_12_out, or_13_out, or_14_out,
       or_15_out, or_16_out, or_17_out, or_18_out, or_19_out, or_20_out, or_21_out, or_22_out, or_23_out,
       or_24_out, or_25_out, or_26_out, or_27_out, or_28_out, or_29_out, or_30_out, or_31_out, or_32_out,
       or_33_out, or_34_out, or_35_out, or_36_out, or_37_out, or_38_out, or_39_out, or_40_out, or_41_out,
       or_42_out, or_43_out, or_44_out, or_45_out, or_46_out, or_47_out, or_48_out, or_49_out, or_50_out,
       or_51_out, or_52_out, or_53_out, or_54_out, or_55_out, or_56_out, or_57_out, or_58_out, or_59_out,
       or_60_out, or_61_out, or_62_out, or_63_out, xor_1_out, xor_2_out, xor_3_out, xor_4_out, xor_5_out,
       xor_6_out, xor_7_out, xor_8_out, xor_17_out, xor_18_out, xor_19_out, xor_20_out, xor_21_out,
       xor_22_out, xor_23_out, xor_24_out, xor_33_out, xor_34_out, xor_35_out, xor_36_out, xor_37_out,
       xor_38_out, xor_39_out, xor_40_out, xor_49_out, xor_50_out, xor_51_out, xor_52_out, xor_53_out,
       xor_54_out, xor_55_out, xor_56_out, xor_65_out, xor_66_out, xor_67_out, xor_68_out, xor_69_out,
       xor_70_out, xor_71_out, xor_72_out, xor_81_out, xor_82_out, xor_83_out, xor_84_out, xor_85_out,
       xor_86_out, xor_87_out, xor_88_out, xor_97_out, xor_99_out, xor_101_out, xor_103_out, xor_105_out,
       xor_107_out, xor_109_out, xor_111_out, xor_113_out, xor_114_out, xor_115_out, xor_116_out,
       xor_117_out, xor_118_out, xor_119_out, xor_120_out;

  not not_1 (not_1_out, input1[0]);
  and and_1 (and_1_out, not_1_out, input2[0]);
  xor xor_1 (xor_1_out, input1[0], input2[0]);
  not not_2 (not_2_out, input1[8]);
  and and_2 (and_2_out, not_2_out, input2[8]);
  xor xor_2 (xor_2_out, input1[8], input2[8]);
  not not_3 (not_3_out, input1[16]);
  and and_3 (and_3_out, not_3_out, input2[16]);
  xor xor_3 (xor_3_out, input1[16], input2[16]);
  not not_4 (not_4_out, input1[24]);
  and and_4 (and_4_out, not_4_out, input2[24]);
  xor xor_4 (xor_4_out, input1[24], input2[24]);
  not not_5 (not_5_out, input1[32]);
  and and_5 (and_5_out, not_5_out, input2[32]);
  xor xor_5 (xor_5_out, input1[32], input2[32]);
  not not_6 (not_6_out, input1[40]);
  and and_6 (and_6_out, not_6_out, input2[40]);
  xor xor_6 (xor_6_out, input1[40], input2[40]);
  not not_7 (not_7_out, input1[48]);
  and and_7 (and_7_out, not_7_out, input2[48]);
  xor xor_7 (xor_7_out, input1[48], input2[48]);
  not not_8 (not_8_out, input1[56]);
  and and_8 (and_8_out, not_8_out, input2[56]);
  xor xor_8 (xor_8_out, input1[56], input2[56]);
  and and_9 (and_9_out, inborrow, not_9_out);
  not not_9 (not_9_out, xor_1_out);
  xor xor_9 (output1[0], inborrow, xor_1_out);
  and and_10 (and_10_out, or_57_out, not_10_out);
  not not_10 (not_10_out, xor_2_out);
  xor xor_10 (output1[8], or_57_out, xor_2_out);
  and and_11 (and_11_out, or_58_out, not_11_out);
  not not_11 (not_11_out, xor_3_out);
  xor xor_11 (output1[16], or_58_out, xor_3_out);
  and and_12 (and_12_out, or_59_out, not_12_out);
  not not_12 (not_12_out, xor_4_out);
  xor xor_12 (output1[24], or_59_out, xor_4_out);
  and and_13 (and_13_out, or_60_out, not_13_out);
  not not_13 (not_13_out, xor_5_out);
  xor xor_13 (output1[32], or_60_out, xor_5_out);
  and and_14 (and_14_out, or_61_out, not_14_out);
  not not_14 (not_14_out, xor_6_out);
  xor xor_14 (output1[40], or_61_out, xor_6_out);
  and and_15 (and_15_out, or_62_out, not_15_out);
  not not_15 (not_15_out, xor_7_out);
  xor xor_15 (output1[48], or_62_out, xor_7_out);
  and and_16 (and_16_out, or_63_out, not_16_out);
  not not_16 (not_16_out, xor_8_out);
  xor xor_16 (output1[56], or_63_out, xor_8_out);
  not not_17 (not_17_out, input1[1]);
  or or_1 (or_1_out, and_1_out, and_9_out);
  and and_17 (and_17_out, not_17_out, input2[1]);
  not not_18 (not_18_out, input1[9]);
  or or_2 (or_2_out, and_2_out, and_10_out);
  and and_18 (and_18_out, not_18_out, input2[9]);
  not not_19 (not_19_out, input1[17]);
  or or_3 (or_3_out, and_3_out, and_11_out);
  and and_19 (and_19_out, not_19_out, input2[17]);
  not not_20 (not_20_out, input1[25]);
  or or_4 (or_4_out, and_4_out, and_12_out);
  and and_20 (and_20_out, not_20_out, input2[25]);
  not not_21 (not_21_out, input1[33]);
  or or_5 (or_5_out, and_5_out, and_13_out);
  and and_21 (and_21_out, not_21_out, input2[33]);
  not not_22 (not_22_out, input1[41]);
  or or_6 (or_6_out, and_6_out, and_14_out);
  and and_22 (and_22_out, not_22_out, input2[41]);
  not not_23 (not_23_out, input1[49]);
  or or_7 (or_7_out, and_7_out, and_15_out);
  and and_23 (and_23_out, not_23_out, input2[49]);
  not not_24 (not_24_out, input1[57]);
  or or_8 (or_8_out, and_8_out, and_16_out);
  and and_24 (and_24_out, not_24_out, input2[57]);
  not not_25 (not_25_out, xor_17_out);
  xor xor_17 (xor_17_out, input1[1], input2[1]);
  not not_26 (not_26_out, xor_18_out);
  xor xor_18 (xor_18_out, input1[9], input2[9]);
  not not_27 (not_27_out, xor_19_out);
  xor xor_19 (xor_19_out, input1[17], input2[17]);
  not not_28 (not_28_out, xor_20_out);
  xor xor_20 (xor_20_out, input1[25], input2[25]);
  not not_29 (not_29_out, xor_21_out);
  xor xor_21 (xor_21_out, input1[33], input2[33]);
  not not_30 (not_30_out, xor_22_out);
  xor xor_22 (xor_22_out, input1[41], input2[41]);
  not not_31 (not_31_out, xor_23_out);
  xor xor_23 (xor_23_out, input1[49], input2[49]);
  not not_32 (not_32_out, xor_24_out);
  xor xor_24 (xor_24_out, input1[57], input2[57]);
  not not_33 (not_33_out, input1[2]);
  or or_9 (or_9_out, and_17_out, and_25_out);
  and and_25 (and_25_out, or_1_out, not_25_out);
  xor xor_25 (output1[1], or_1_out, xor_17_out);
  not not_34 (not_34_out, input1[10]);
  or or_10 (or_10_out, and_18_out, and_26_out);
  and and_26 (and_26_out, or_2_out, not_26_out);
  xor xor_26 (output1[9], or_2_out, xor_18_out);
  not not_35 (not_35_out, input1[18]);
  or or_11 (or_11_out, and_19_out, and_27_out);
  and and_27 (and_27_out, or_3_out, not_27_out);
  xor xor_27 (output1[17], or_3_out, xor_19_out);
  not not_36 (not_36_out, input1[26]);
  or or_12 (or_12_out, and_20_out, and_28_out);
  and and_28 (and_28_out, or_4_out, not_28_out);
  xor xor_28 (output1[25], or_4_out, xor_20_out);
  not not_37 (not_37_out, input1[34]);
  or or_13 (or_13_out, and_21_out, and_29_out);
  and and_29 (and_29_out, or_5_out, not_29_out);
  xor xor_29 (output1[33], or_5_out, xor_21_out);
  not not_38 (not_38_out, input1[42]);
  or or_14 (or_14_out, and_22_out, and_30_out);
  and and_30 (and_30_out, or_6_out, not_30_out);
  xor xor_30 (output1[41], or_6_out, xor_22_out);
  not not_39 (not_39_out, input1[50]);
  or or_15 (or_15_out, and_23_out, and_31_out);
  and and_31 (and_31_out, or_7_out, not_31_out);
  xor xor_31 (output1[49], or_7_out, xor_23_out);
  not not_40 (not_40_out, input1[58]);
  or or_16 (or_16_out, and_24_out, and_32_out);
  and and_32 (and_32_out, or_8_out, not_32_out);
  xor xor_32 (output1[57], or_8_out, xor_24_out);
  and and_33 (and_33_out, not_33_out, input2[2]);
  xor xor_33 (xor_33_out, input1[2], input2[2]);
  and and_34 (and_34_out, not_34_out, input2[10]);
  xor xor_34 (xor_34_out, input1[10], input2[10]);
  and and_35 (and_35_out, not_35_out, input2[18]);
  xor xor_35 (xor_35_out, input1[18], input2[18]);
  and and_36 (and_36_out, not_36_out, input2[26]);
  xor xor_36 (xor_36_out, input1[26], input2[26]);
  and and_37 (and_37_out, not_37_out, input2[34]);
  xor xor_37 (xor_37_out, input1[34], input2[34]);
  and and_38 (and_38_out, not_38_out, input2[42]);
  xor xor_38 (xor_38_out, input1[42], input2[42]);
  and and_39 (and_39_out, not_39_out, input2[50]);
  xor xor_39 (xor_39_out, input1[50], input2[50]);
  and and_40 (and_40_out, not_40_out, input2[58]);
  xor xor_40 (xor_40_out, input1[58], input2[58]);
  or or_17 (or_17_out, and_33_out, and_41_out);
  and and_41 (and_41_out, or_9_out, not_41_out);
  not not_41 (not_41_out, xor_33_out);
  xor xor_41 (output1[2], or_9_out, xor_33_out);
  or or_18 (or_18_out, and_34_out, and_42_out);
  and and_42 (and_42_out, or_10_out, not_42_out);
  not not_42 (not_42_out, xor_34_out);
  xor xor_42 (output1[10], or_10_out, xor_34_out);
  or or_19 (or_19_out, and_35_out, and_43_out);
  and and_43 (and_43_out, or_11_out, not_43_out);
  not not_43 (not_43_out, xor_35_out);
  xor xor_43 (output1[18], or_11_out, xor_35_out);
  or or_20 (or_20_out, and_36_out, and_44_out);
  and and_44 (and_44_out, or_12_out, not_44_out);
  not not_44 (not_44_out, xor_36_out);
  xor xor_44 (output1[26], or_12_out, xor_36_out);
  or or_21 (or_21_out, and_37_out, and_45_out);
  and and_45 (and_45_out, or_13_out, not_45_out);
  not not_45 (not_45_out, xor_37_out);
  xor xor_45 (output1[34], or_13_out, xor_37_out);
  or or_22 (or_22_out, and_38_out, and_46_out);
  and and_46 (and_46_out, or_14_out, not_46_out);
  not not_46 (not_46_out, xor_38_out);
  xor xor_46 (output1[42], or_14_out, xor_38_out);
  or or_23 (or_23_out, and_39_out, and_47_out);
  and and_47 (and_47_out, or_15_out, not_47_out);
  not not_47 (not_47_out, xor_39_out);
  xor xor_47 (output1[50], or_15_out, xor_39_out);
  or or_24 (or_24_out, and_40_out, and_48_out);
  and and_48 (and_48_out, or_16_out, not_48_out);
  not not_48 (not_48_out, xor_40_out);
  xor xor_48 (output1[58], or_16_out, xor_40_out);
  not not_49 (not_49_out, input1[3]);
  and and_49 (and_49_out, not_49_out, input2[3]);
  xor xor_49 (xor_49_out, input1[3], input2[3]);
  not not_50 (not_50_out, input1[11]);
  and and_50 (and_50_out, not_50_out, input2[11]);
  xor xor_50 (xor_50_out, input1[11], input2[11]);
  not not_51 (not_51_out, input1[19]);
  and and_51 (and_51_out, not_51_out, input2[19]);
  xor xor_51 (xor_51_out, input1[19], input2[19]);
  not not_52 (not_52_out, input1[27]);
  and and_52 (and_52_out, not_52_out, input2[27]);
  xor xor_52 (xor_52_out, input1[27], input2[27]);
  not not_53 (not_53_out, input1[35]);
  and and_53 (and_53_out, not_53_out, input2[35]);
  xor xor_53 (xor_53_out, input1[35], input2[35]);
  not not_54 (not_54_out, input1[43]);
  and and_54 (and_54_out, not_54_out, input2[43]);
  xor xor_54 (xor_54_out, input1[43], input2[43]);
  not not_55 (not_55_out, input1[51]);
  and and_55 (and_55_out, not_55_out, input2[51]);
  xor xor_55 (xor_55_out, input1[51], input2[51]);
  not not_56 (not_56_out, input1[59]);
  and and_56 (and_56_out, not_56_out, input2[59]);
  xor xor_56 (xor_56_out, input1[59], input2[59]);
  and and_57 (and_57_out, or_17_out, not_57_out);
  not not_57 (not_57_out, xor_49_out);
  xor xor_57 (output1[3], or_17_out, xor_49_out);
  and and_58 (and_58_out, or_18_out, not_58_out);
  not not_58 (not_58_out, xor_50_out);
  xor xor_58 (output1[11], or_18_out, xor_50_out);
  and and_59 (and_59_out, or_19_out, not_59_out);
  not not_59 (not_59_out, xor_51_out);
  xor xor_59 (output1[19], or_19_out, xor_51_out);
  and and_60 (and_60_out, or_20_out, not_60_out);
  not not_60 (not_60_out, xor_52_out);
  xor xor_60 (output1[27], or_20_out, xor_52_out);
  and and_61 (and_61_out, or_21_out, not_61_out);
  not not_61 (not_61_out, xor_53_out);
  xor xor_61 (output1[35], or_21_out, xor_53_out);
  and and_62 (and_62_out, or_22_out, not_62_out);
  not not_62 (not_62_out, xor_54_out);
  xor xor_62 (output1[43], or_22_out, xor_54_out);
  and and_63 (and_63_out, or_23_out, not_63_out);
  not not_63 (not_63_out, xor_55_out);
  xor xor_63 (output1[51], or_23_out, xor_55_out);
  and and_64 (and_64_out, or_24_out, not_64_out);
  not not_64 (not_64_out, xor_56_out);
  xor xor_64 (output1[59], or_24_out, xor_56_out);
  not not_65 (not_65_out, input1[4]);
  or or_25 (or_25_out, and_49_out, and_57_out);
  not not_66 (not_66_out, input1[12]);
  or or_26 (or_26_out, and_50_out, and_58_out);
  not not_67 (not_67_out, input1[20]);
  or or_27 (or_27_out, and_51_out, and_59_out);
  not not_68 (not_68_out, input1[28]);
  or or_28 (or_28_out, and_52_out, and_60_out);
  not not_69 (not_69_out, input1[36]);
  or or_29 (or_29_out, and_53_out, and_61_out);
  not not_70 (not_70_out, input1[44]);
  or or_30 (or_30_out, and_54_out, and_62_out);
  not not_71 (not_71_out, input1[52]);
  or or_31 (or_31_out, and_55_out, and_63_out);
  not not_72 (not_72_out, input1[60]);
  or or_32 (or_32_out, and_56_out, and_64_out);
  and and_65 (and_65_out, not_65_out, input2[4]);
  not not_73 (not_73_out, xor_65_out);
  xor xor_65 (xor_65_out, input1[4], input2[4]);
  and and_66 (and_66_out, not_66_out, input2[12]);
  not not_74 (not_74_out, xor_66_out);
  xor xor_66 (xor_66_out, input1[12], input2[12]);
  and and_67 (and_67_out, not_67_out, input2[20]);
  not not_75 (not_75_out, xor_67_out);
  xor xor_67 (xor_67_out, input1[20], input2[20]);
  and and_68 (and_68_out, not_68_out, input2[28]);
  not not_76 (not_76_out, xor_68_out);
  xor xor_68 (xor_68_out, input1[28], input2[28]);
  and and_69 (and_69_out, not_69_out, input2[36]);
  not not_77 (not_77_out, xor_69_out);
  xor xor_69 (xor_69_out, input1[36], input2[36]);
  and and_70 (and_70_out, not_70_out, input2[44]);
  not not_78 (not_78_out, xor_70_out);
  xor xor_70 (xor_70_out, input1[44], input2[44]);
  and and_71 (and_71_out, not_71_out, input2[52]);
  not not_79 (not_79_out, xor_71_out);
  xor xor_71 (xor_71_out, input1[52], input2[52]);
  and and_72 (and_72_out, not_72_out, input2[60]);
  not not_80 (not_80_out, xor_72_out);
  xor xor_72 (xor_72_out, input1[60], input2[60]);
  or or_33 (or_33_out, and_65_out, and_73_out);
  and and_73 (and_73_out, or_25_out, not_73_out);
  xor xor_73 (output1[4], or_25_out, xor_65_out);
  or or_34 (or_34_out, and_66_out, and_74_out);
  and and_74 (and_74_out, or_26_out, not_74_out);
  xor xor_74 (output1[12], or_26_out, xor_66_out);
  or or_35 (or_35_out, and_67_out, and_75_out);
  and and_75 (and_75_out, or_27_out, not_75_out);
  xor xor_75 (output1[20], or_27_out, xor_67_out);
  or or_36 (or_36_out, and_68_out, and_76_out);
  and and_76 (and_76_out, or_28_out, not_76_out);
  xor xor_76 (output1[28], or_28_out, xor_68_out);
  or or_37 (or_37_out, and_69_out, and_77_out);
  and and_77 (and_77_out, or_29_out, not_77_out);
  xor xor_77 (output1[36], or_29_out, xor_69_out);
  or or_38 (or_38_out, and_70_out, and_78_out);
  and and_78 (and_78_out, or_30_out, not_78_out);
  xor xor_78 (output1[44], or_30_out, xor_70_out);
  or or_39 (or_39_out, and_71_out, and_79_out);
  and and_79 (and_79_out, or_31_out, not_79_out);
  xor xor_79 (output1[52], or_31_out, xor_71_out);
  or or_40 (or_40_out, and_72_out, and_80_out);
  and and_80 (and_80_out, or_32_out, not_80_out);
  xor xor_80 (output1[60], or_32_out, xor_72_out);
  not not_81 (not_81_out, input1[5]);
  and and_81 (and_81_out, not_81_out, input2[5]);
  xor xor_81 (xor_81_out, input1[5], input2[5]);
  not not_82 (not_82_out, input1[13]);
  and and_82 (and_82_out, not_82_out, input2[13]);
  xor xor_82 (xor_82_out, input1[13], input2[13]);
  not not_83 (not_83_out, input1[21]);
  and and_83 (and_83_out, not_83_out, input2[21]);
  xor xor_83 (xor_83_out, input1[21], input2[21]);
  not not_84 (not_84_out, input1[29]);
  and and_84 (and_84_out, not_84_out, input2[29]);
  xor xor_84 (xor_84_out, input1[29], input2[29]);
  not not_85 (not_85_out, input1[37]);
  and and_85 (and_85_out, not_85_out, input2[37]);
  xor xor_85 (xor_85_out, input1[37], input2[37]);
  not not_86 (not_86_out, input1[45]);
  and and_86 (and_86_out, not_86_out, input2[45]);
  xor xor_86 (xor_86_out, input1[45], input2[45]);
  not not_87 (not_87_out, input1[53]);
  and and_87 (and_87_out, not_87_out, input2[53]);
  xor xor_87 (xor_87_out, input1[53], input2[53]);
  not not_88 (not_88_out, input1[61]);
  and and_88 (and_88_out, not_88_out, input2[61]);
  xor xor_88 (xor_88_out, input1[61], input2[61]);
  and and_89 (and_89_out, or_33_out, not_89_out);
  not not_89 (not_89_out, xor_81_out);
  xor xor_89 (output1[5], or_33_out, xor_81_out);
  and and_90 (and_90_out, or_34_out, not_90_out);
  not not_90 (not_90_out, xor_82_out);
  xor xor_90 (output1[13], or_34_out, xor_82_out);
  and and_91 (and_91_out, or_35_out, not_91_out);
  not not_91 (not_91_out, xor_83_out);
  xor xor_91 (output1[21], or_35_out, xor_83_out);
  and and_92 (and_92_out, or_36_out, not_92_out);
  not not_92 (not_92_out, xor_84_out);
  xor xor_92 (output1[29], or_36_out, xor_84_out);
  and and_93 (and_93_out, or_37_out, not_93_out);
  not not_93 (not_93_out, xor_85_out);
  xor xor_93 (output1[37], or_37_out, xor_85_out);
  and and_94 (and_94_out, or_38_out, not_94_out);
  not not_94 (not_94_out, xor_86_out);
  xor xor_94 (output1[45], or_38_out, xor_86_out);
  and and_95 (and_95_out, or_39_out, not_95_out);
  not not_95 (not_95_out, xor_87_out);
  xor xor_95 (output1[53], or_39_out, xor_87_out);
  and and_96 (and_96_out, or_40_out, not_96_out);
  not not_96 (not_96_out, xor_88_out);
  xor xor_96 (output1[61], or_40_out, xor_88_out);
  not not_97 (not_97_out, input1[6]);
  or or_41 (or_41_out, and_81_out, and_89_out);
  and and_97 (and_97_out, not_97_out, input2[6]);
  not not_98 (not_98_out, input1[14]);
  or or_42 (or_42_out, and_82_out, and_90_out);
  and and_98 (and_98_out, not_98_out, input2[14]);
  not not_99 (not_99_out, input1[22]);
  or or_43 (or_43_out, and_83_out, and_91_out);
  and and_99 (and_99_out, not_99_out, input2[22]);
  not not_100 (not_100_out, input1[30]);
  or or_44 (or_44_out, and_84_out, and_92_out);
  and and_100 (and_100_out, not_100_out, input2[30]);
  not not_101 (not_101_out, input1[38]);
  or or_45 (or_45_out, and_85_out, and_93_out);
  and and_101 (and_101_out, not_101_out, input2[38]);
  not not_102 (not_102_out, input1[46]);
  or or_46 (or_46_out, and_86_out, and_94_out);
  and and_102 (and_102_out, not_102_out, input2[46]);
  not not_103 (not_103_out, input1[54]);
  or or_47 (or_47_out, and_87_out, and_95_out);
  and and_103 (and_103_out, not_103_out, input2[54]);
  not not_104 (not_104_out, input1[62]);
  or or_48 (or_48_out, and_88_out, and_96_out);
  and and_104 (and_104_out, not_104_out, input2[62]);
  and and_105 (and_105_out, or_41_out, not_105_out);
  not not_105 (not_105_out, xor_97_out);
  xor xor_97 (xor_97_out, input1[6], input2[6]);
  xor xor_98 (output1[6], or_41_out, xor_97_out);
  and and_106 (and_106_out, or_42_out, not_106_out);
  not not_106 (not_106_out, xor_99_out);
  xor xor_99 (xor_99_out, input1[14], input2[14]);
  xor xor_100 (output1[14], or_42_out, xor_99_out);
  and and_107 (and_107_out, or_43_out, not_107_out);
  not not_107 (not_107_out, xor_101_out);
  xor xor_101 (xor_101_out, input1[22], input2[22]);
  xor xor_102 (output1[22], or_43_out, xor_101_out);
  and and_108 (and_108_out, or_44_out, not_108_out);
  not not_108 (not_108_out, xor_103_out);
  xor xor_103 (xor_103_out, input1[30], input2[30]);
  xor xor_104 (output1[30], or_44_out, xor_103_out);
  and and_109 (and_109_out, or_45_out, not_109_out);
  not not_109 (not_109_out, xor_105_out);
  xor xor_105 (xor_105_out, input1[38], input2[38]);
  xor xor_106 (output1[38], or_45_out, xor_105_out);
  and and_110 (and_110_out, or_46_out, not_110_out);
  not not_110 (not_110_out, xor_107_out);
  xor xor_107 (xor_107_out, input1[46], input2[46]);
  xor xor_108 (output1[46], or_46_out, xor_107_out);
  and and_111 (and_111_out, or_47_out, not_111_out);
  not not_111 (not_111_out, xor_109_out);
  xor xor_109 (xor_109_out, input1[54], input2[54]);
  xor xor_110 (output1[54], or_47_out, xor_109_out);
  and and_112 (and_112_out, or_48_out, not_112_out);
  not not_112 (not_112_out, xor_111_out);
  xor xor_111 (xor_111_out, input1[62], input2[62]);
  xor xor_112 (output1[62], or_48_out, xor_111_out);
  not not_113 (not_113_out, input1[7]);
  or or_49 (or_49_out, and_97_out, and_105_out);
  not not_114 (not_114_out, input1[15]);
  or or_50 (or_50_out, and_98_out, and_106_out);
  not not_115 (not_115_out, input1[23]);
  or or_51 (or_51_out, and_99_out, and_107_out);
  not not_116 (not_116_out, input1[31]);
  or or_52 (or_52_out, and_100_out, and_108_out);
  not not_117 (not_117_out, input1[39]);
  or or_53 (or_53_out, and_101_out, and_109_out);
  not not_118 (not_118_out, input1[47]);
  or or_54 (or_54_out, and_102_out, and_110_out);
  not not_119 (not_119_out, input1[55]);
  or or_55 (or_55_out, and_103_out, and_111_out);
  not not_120 (not_120_out, input1[63]);
  or or_56 (or_56_out, and_104_out, and_112_out);
  and and_113 (and_113_out, not_113_out, input2[7]);
  not not_121 (not_121_out, xor_113_out);
  xor xor_113 (xor_113_out, input1[7], input2[7]);
  and and_114 (and_114_out, not_114_out, input2[15]);
  not not_122 (not_122_out, xor_114_out);
  xor xor_114 (xor_114_out, input1[15], input2[15]);
  and and_115 (and_115_out, not_115_out, input2[23]);
  not not_123 (not_123_out, xor_115_out);
  xor xor_115 (xor_115_out, input1[23], input2[23]);
  and and_116 (and_116_out, not_116_out, input2[31]);
  not not_124 (not_124_out, xor_116_out);
  xor xor_116 (xor_116_out, input1[31], input2[31]);
  and and_117 (and_117_out, not_117_out, input2[39]);
  not not_125 (not_125_out, xor_117_out);
  xor xor_117 (xor_117_out, input1[39], input2[39]);
  and and_118 (and_118_out, not_118_out, input2[47]);
  not not_126 (not_126_out, xor_118_out);
  xor xor_118 (xor_118_out, input1[47], input2[47]);
  and and_119 (and_119_out, not_119_out, input2[55]);
  not not_127 (not_127_out, xor_119_out);
  xor xor_119 (xor_119_out, input1[55], input2[55]);
  and and_120 (and_120_out, not_120_out, input2[63]);
  not not_128 (not_128_out, xor_120_out);
  xor xor_120 (xor_120_out, input1[63], input2[63]);
  or or_57 (or_57_out, and_113_out, and_121_out);
  and and_121 (and_121_out, or_49_out, not_121_out);
  xor xor_121 (output1[7], or_49_out, xor_113_out);
  or or_58 (or_58_out, and_114_out, and_122_out);
  and and_122 (and_122_out, or_50_out, not_122_out);
  xor xor_122 (output1[15], or_50_out, xor_114_out);
  or or_59 (or_59_out, and_115_out, and_123_out);
  and and_123 (and_123_out, or_51_out, not_123_out);
  xor xor_123 (output1[23], or_51_out, xor_115_out);
  or or_60 (or_60_out, and_116_out, and_124_out);
  and and_124 (and_124_out, or_52_out, not_124_out);
  xor xor_124 (output1[31], or_52_out, xor_116_out);
  or or_61 (or_61_out, and_117_out, and_125_out);
  and and_125 (and_125_out, or_53_out, not_125_out);
  xor xor_125 (output1[39], or_53_out, xor_117_out);
  or or_62 (or_62_out, and_118_out, and_126_out);
  and and_126 (and_126_out, or_54_out, not_126_out);
  xor xor_126 (output1[47], or_54_out, xor_118_out);
  or or_63 (or_63_out, and_119_out, and_127_out);
  and and_127 (and_127_out, or_55_out, not_127_out);
  xor xor_127 (output1[55], or_55_out, xor_119_out);
  or or_64 (borrow, and_120_out, and_128_out);
  and and_128 (and_128_out, or_56_out, not_128_out);
  xor xor_128 (output1[63], or_56_out, xor_120_out);

  // Notes on the sheet:
  //   input1: initial=0x1313131313131313
  //   input2: initial=0xffffffffffffff
endmodule

module adder128bit (
  input  inflow,
  input  [63:0] input1a,
  input  [63:0] input1b,
  input  [63:0] input2a,
  input  [63:0] input2b,
  output overflow,
  output [63:0] output1a,
  output [63:0] output1b
);

  wire adder64bit_1_overflow;

  adder64bit adder64bit_1 (
    .inflow(inflow), .input1(input1a), .input2(input2a), .overflow(adder64bit_1_overflow), .output1(output1a));
  adder64bit adder64bit_2 (
    .inflow(adder64bit_1_overflow), .input1(input1b), .input2(input2b), .overflow(overflow),
    .output1(output1b));
endmodule

module negate128bit (
  input  [63:0] input1a,
  input  [63:0] input1b,
  output [63:0] output1a,
  output [63:0] output1b
);

  wire [63:0] not_1_out, not_2_out;

  assign not_1_out = ~input1a;  // NOT_Gate not_1, 64 bits wide
  assign not_2_out = ~input1b;  // NOT_Gate not_2, 64 bits wide
  adder128bit adder128bit_1 (
    .input1a(64'h1), .input2a(not_1_out), .input2b(not_2_out), .output1a(output1a), .output1b(output1b));  // open: inflow, input1b, overflow
endmodule

module subtractor128bit (
  input  inborrow,
  input  [63:0] input1a,
  input  [63:0] input1b,
  input  [63:0] input2a,
  input  [63:0] input2b,
  output borrow,
  output [63:0] output1a,
  output [63:0] output1b
);

  wire subtractor64bit_1_borrow;

  subtractor64bit subtractor64bit_1 (
    .inborrow(inborrow), .input1(input1a), .input2(input2a), .borrow(subtractor64bit_1_borrow),
    .output1(output1a));
  subtractor64bit subtractor64bit_2 (
    .inborrow(subtractor64bit_1_borrow), .input1(input1b), .input2(input2b), .borrow(borrow),
    .output1(output1b));
endmodule

module cbuffer64bit (
  input  buffer1,
  input  [63:0] input1,
  output [63:0] output1
);

  assign output1 = {64{buffer1}} & input1;  // AND_Gate and_1, 64 bits wide
endmodule

module cbuffer128bit (
  input  buffer1,
  input  [63:0] input1a,
  input  [63:0] input1b,
  output [63:0] output1a,
  output [63:0] output1b
);

  assign output1a = {64{buffer1}} & input1a;  // AND_Gate and_1, 64 bits wide
  assign output1b = {64{buffer1}} & input1b;  // AND_Gate and_2, 64 bits wide
endmodule

module multiplier64bit (
  input  [63:0] inflow,
  input  [63:0] input1,
  input  [63:0] input2,
  output [63:0] overflow,
  output [63:0] output1
);
endmodule

module comparatoru64bit (
  input  [63:0] input1,
  input  [63:0] input2,
  output greater1,
  output equal1,
  output less1
);

  wire and_2_out, and_3_out, undriven, undriven_2, undriven_3, undriven_4, undriven_5, undriven_6;

  and and_1 (equal1, undriven_5, undriven_3);
  or or_1 (greater1, undriven, and_2_out);
  and and_2 (and_2_out, undriven_5, undriven_2);
  or or_2 (less1, undriven_4, and_3_out);
  and and_3 (and_3_out, undriven_5, undriven_6);

  // Notes on the sheet:
  //   input1: initial=0x2
  //   input2: initial=0x3
endmodule

module cbuffer256bit (
  input  buffer1,
  input  [63:0] input1a,
  input  [63:0] input1b,
  input  [63:0] input1c,
  input  [63:0] input1d,
  output [63:0] output1a,
  output [63:0] output1b,
  output [63:0] output1c,
  output [63:0] output1d
);

  assign output1a = {64{buffer1}} & input1a;  // AND_Gate and_1, 64 bits wide
  assign output1b = {64{buffer1}} & input1b;  // AND_Gate and_2, 64 bits wide
  assign output1c = {64{buffer1}} & input1c;  // AND_Gate and_3, 64 bits wide
  assign output1d = {64{buffer1}} & input1d;  // AND_Gate and_4, 64 bits wide
endmodule

module subtractor256bit (
  input  inborrow,
  input  [63:0] input1a,
  input  [63:0] input1b,
  input  [63:0] input1c,
  input  [63:0] input1d,
  input  [63:0] input2a,
  input  [63:0] input2b,
  input  [63:0] input2c,
  input  [63:0] input2d,
  output borrow,
  output [63:0] output1a,
  output [63:0] output1b,
  output [63:0] output1c,
  output [63:0] output1d
);

  wire subtractor128bit_1_borrow;

  subtractor128bit subtractor128bit_1 (
    .inborrow(inborrow), .input1a(input1a), .input1b(input1b), .input2a(input2a), .input2b(input2b),
    .borrow(subtractor128bit_1_borrow), .output1a(output1a), .output1b(output1b));
  subtractor128bit subtractor128bit_2 (
    .inborrow(subtractor128bit_1_borrow), .input1a(input1c), .input1b(input1d), .input2a(input2c),
    .input2b(input2d), .borrow(borrow), .output1a(output1c), .output1b(output1d));
endmodule

module negate256bit (
  input  [63:0] input1a,
  input  [63:0] input1b,
  input  [63:0] input1c,
  input  [63:0] input1d,
  output [63:0] output1a,
  output [63:0] output1b,
  output [63:0] output1c,
  output [63:0] output1d
);

  wire [63:0] not_1_out, not_2_out, not_3_out, not_4_out;

  assign not_1_out = ~input1a;  // NOT_Gate not_1, 64 bits wide
  assign not_2_out = ~input1b;  // NOT_Gate not_2, 64 bits wide
  assign not_3_out = ~input1c;  // NOT_Gate not_3, 64 bits wide
  assign not_4_out = ~input1d;  // NOT_Gate not_4, 64 bits wide
  adder256bit adder256bit_1 (
    .input1a(64'h1), .input2a(not_1_out), .input2b(not_2_out), .input2c(not_3_out), .input2d(not_4_out),
    .output1a(output1a), .output1b(output1b), .output1c(output1c), .output1d(output1d));  // open: inflow, input1b, input1c, input1d, overflow
endmodule

module adder256bit (
  input  inflow,
  input  [63:0] input1a,
  input  [63:0] input1b,
  input  [63:0] input1c,
  input  [63:0] input1d,
  input  [63:0] input2a,
  input  [63:0] input2b,
  input  [63:0] input2c,
  input  [63:0] input2d,
  output overflow,
  output [63:0] output1a,
  output [63:0] output1b,
  output [63:0] output1c,
  output [63:0] output1d
);

  wire adder128bit_1_overflow;

  adder128bit adder128bit_1 (
    .inflow(inflow), .input1a(input1a), .input1b(input1b), .input2a(input2a), .input2b(input2b),
    .overflow(adder128bit_1_overflow), .output1a(output1a), .output1b(output1b));
  adder128bit adder128bit_2 (
    .inflow(adder128bit_1_overflow), .input1a(input1c), .input1b(input1d), .input2a(input2c),
    .input2b(input2d), .overflow(overflow), .output1a(output1c), .output1b(output1d));
endmodule

module shiftleft64bit (
  input  [63:0] input1,
  input  [7:0] shiftleft1,
  output [63:0] output1
);

  wire [63:8] undriven;

  mux6x64bit mux6x64bit_1 (
    .select1({undriven, shiftleft1}), .input0(input1), .input1({input1[62:0], 1'b0}),
    .input2({input1[61:0], 2'b00}), .input3({input1[60:0], 3'b000}), .input4({input1[59:0], 4'b0000}),
    .input5({input1[58:0], {5{1'b0}}}), .input6({input1[57:0], {6{1'b0}}}),
    .input7({input1[56:0], {7{1'b0}}}), .input8({input1[55:0], {8{1'b0}}}),
    .input9({input1[54:0], {9{1'b0}}}), .input10({input1[53:0], {10{1'b0}}}),
    .input11({input1[52:0], {11{1'b0}}}), .input12({input1[51:0], {12{1'b0}}}),
    .input13({input1[50:0], {13{1'b0}}}), .input14({input1[49:0], {14{1'b0}}}),
    .input15({input1[48:0], {15{1'b0}}}), .input16({input1[47:0], {16{1'b0}}}),
    .input17({input1[46:0], {17{1'b0}}}), .input18({input1[45:0], {18{1'b0}}}),
    .input19({input1[44:0], {19{1'b0}}}), .input20({input1[43:0], {20{1'b0}}}),
    .input21({input1[42:0], {21{1'b0}}}), .input22({input1[41:0], {22{1'b0}}}),
    .input23({input1[40:0], {23{1'b0}}}), .input24({input1[39:0], {24{1'b0}}}),
    .input25({input1[38:0], {25{1'b0}}}), .input26({input1[37:0], {26{1'b0}}}),
    .input27({input1[36:0], {27{1'b0}}}), .input28({input1[35:0], {28{1'b0}}}),
    .input29({input1[34:0], {29{1'b0}}}), .input30({input1[33:0], {30{1'b0}}}),
    .input31({input1[32:0], {31{1'b0}}}), .input32({input1[31:0], {32{1'b0}}}),
    .input33({input1[30:0], {33{1'b0}}}), .input34({input1[29:0], {34{1'b0}}}),
    .input35({input1[28:0], {35{1'b0}}}), .input36({input1[27:0], {36{1'b0}}}),
    .input37({input1[26:0], {37{1'b0}}}), .input38({input1[25:0], {38{1'b0}}}),
    .input39({input1[24:0], {39{1'b0}}}), .input40({input1[23:0], {40{1'b0}}}),
    .input41({input1[22:0], {41{1'b0}}}), .input42({input1[21:0], {42{1'b0}}}),
    .input43({input1[20:0], {43{1'b0}}}), .input44({input1[19:0], {44{1'b0}}}),
    .input45({input1[18:0], {45{1'b0}}}), .input46({input1[17:0], {46{1'b0}}}),
    .input47({input1[16:0], {47{1'b0}}}), .input48({input1[15:0], {48{1'b0}}}),
    .input49({input1[14:0], {49{1'b0}}}), .input50({input1[13:0], {50{1'b0}}}),
    .input51({input1[12:0], {51{1'b0}}}), .input52({input1[11:0], {52{1'b0}}}),
    .input53({input1[10:0], {53{1'b0}}}), .input54({input1[9:0], {54{1'b0}}}),
    .input55({input1[8:0], {55{1'b0}}}), .input56({input1[7:0], {56{1'b0}}}),
    .input57({input1[6:0], {57{1'b0}}}), .input58({input1[5:0], {58{1'b0}}}),
    .input59({input1[4:0], {59{1'b0}}}), .input60({input1[3:0], {60{1'b0}}}),
    .input61({input1[2:0], {61{1'b0}}}), .input62({input1[1:0], {62{1'b0}}}),
    .input63({input1[0], {63{1'b0}}}), .output1(output1));
  // Pins of 8 and 64 bits meet at {undriven, shiftleft1}

  // Notes on the sheet:
  //   shiftleft1: initial=0x30
  //   input1: initial=0xcafebabecafebabe
endmodule

module mux6x64bit (
  input  [63:0] select1,
  input  [63:0] input0,
  input  [63:0] input1,
  input  [63:0] input2,
  input  [63:0] input3,
  input  [63:0] input4,
  input  [63:0] input5,
  input  [63:0] input6,
  input  [63:0] input7,
  input  [63:0] input8,
  input  [63:0] input9,
  input  [63:0] input10,
  input  [63:0] input11,
  input  [63:0] input12,
  input  [63:0] input13,
  input  [63:0] input14,
  input  [63:0] input15,
  input  [63:0] input16,
  input  [63:0] input17,
  input  [63:0] input18,
  input  [63:0] input19,
  input  [63:0] input20,
  input  [63:0] input21,
  input  [63:0] input22,
  input  [63:0] input23,
  input  [63:0] input24,
  input  [63:0] input25,
  input  [63:0] input26,
  input  [63:0] input27,
  input  [63:0] input28,
  input  [63:0] input29,
  input  [63:0] input30,
  input  [63:0] input31,
  input  [63:0] input32,
  input  [63:0] input33,
  input  [63:0] input34,
  input  [63:0] input35,
  input  [63:0] input36,
  input  [63:0] input37,
  input  [63:0] input38,
  input  [63:0] input39,
  input  [63:0] input40,
  input  [63:0] input41,
  input  [63:0] input42,
  input  [63:0] input43,
  input  [63:0] input44,
  input  [63:0] input45,
  input  [63:0] input46,
  input  [63:0] input47,
  input  [63:0] input48,
  input  [63:0] input49,
  input  [63:0] input50,
  input  [63:0] input51,
  input  [63:0] input52,
  input  [63:0] input53,
  input  [63:0] input54,
  input  [63:0] input55,
  input  [63:0] input56,
  input  [63:0] input57,
  input  [63:0] input58,
  input  [63:0] input59,
  input  [63:0] input60,
  input  [63:0] input61,
  input  [63:0] input62,
  input  [63:0] input63,
  output [63:0] output1
);

  wire comparatoru64bit_1_equal1, comparatoru64bit_2_equal1, comparatoru64bit_3_equal1,
       comparatoru64bit_4_equal1, comparatoru64bit_5_equal1, comparatoru64bit_6_equal1,
       comparatoru64bit_7_equal1, comparatoru64bit_8_equal1, comparatoru64bit_9_equal1,
       comparatoru64bit_10_equal1, comparatoru64bit_11_equal1, comparatoru64bit_12_equal1,
       comparatoru64bit_13_equal1, comparatoru64bit_14_equal1, comparatoru64bit_15_equal1,
       comparatoru64bit_16_equal1, comparatoru64bit_17_equal1, comparatoru64bit_18_equal1,
       comparatoru64bit_19_equal1, comparatoru64bit_20_equal1, comparatoru64bit_21_equal1,
       comparatoru64bit_22_equal1, comparatoru64bit_23_equal1, comparatoru64bit_24_equal1,
       comparatoru64bit_25_equal1, comparatoru64bit_26_equal1, comparatoru64bit_27_equal1,
       comparatoru64bit_28_equal1, comparatoru64bit_29_equal1, comparatoru64bit_30_equal1,
       comparatoru64bit_31_equal1, comparatoru64bit_32_equal1, comparatoru64bit_33_equal1,
       comparatoru64bit_34_equal1, comparatoru64bit_35_equal1, comparatoru64bit_36_equal1,
       comparatoru64bit_37_equal1, comparatoru64bit_38_equal1, comparatoru64bit_39_equal1,
       comparatoru64bit_40_equal1, comparatoru64bit_41_equal1, comparatoru64bit_42_equal1,
       comparatoru64bit_43_equal1, comparatoru64bit_44_equal1, comparatoru64bit_45_equal1,
       comparatoru64bit_46_equal1, comparatoru64bit_47_equal1, comparatoru64bit_48_equal1,
       comparatoru64bit_49_equal1, comparatoru64bit_50_equal1, comparatoru64bit_51_equal1,
       comparatoru64bit_52_equal1, comparatoru64bit_53_equal1, comparatoru64bit_54_equal1,
       comparatoru64bit_55_equal1, comparatoru64bit_56_equal1, comparatoru64bit_57_equal1,
       comparatoru64bit_58_equal1, comparatoru64bit_59_equal1, comparatoru64bit_60_equal1,
       comparatoru64bit_61_equal1, comparatoru64bit_62_equal1, comparatoru64bit_63_equal1,
       comparatoru64bit_64_equal1;
  wire [63:0] cbuffer64bit_1_output1, cbuffer64bit_2_output1, cbuffer64bit_3_output1, cbuffer64bit_4_output1,
       cbuffer64bit_5_output1, cbuffer64bit_6_output1, cbuffer64bit_7_output1, cbuffer64bit_8_output1,
       cbuffer64bit_9_output1, cbuffer64bit_10_output1, cbuffer64bit_11_output1, cbuffer64bit_12_output1,
       cbuffer64bit_13_output1, cbuffer64bit_14_output1, cbuffer64bit_15_output1, cbuffer64bit_16_output1,
       cbuffer64bit_17_output1, cbuffer64bit_18_output1, cbuffer64bit_19_output1, cbuffer64bit_20_output1,
       cbuffer64bit_21_output1, cbuffer64bit_22_output1, cbuffer64bit_23_output1, cbuffer64bit_24_output1,
       cbuffer64bit_25_output1, cbuffer64bit_26_output1, cbuffer64bit_27_output1, cbuffer64bit_28_output1,
       cbuffer64bit_29_output1, cbuffer64bit_30_output1, cbuffer64bit_31_output1, cbuffer64bit_32_output1,
       cbuffer64bit_33_output1, cbuffer64bit_34_output1, cbuffer64bit_35_output1, cbuffer64bit_36_output1,
       cbuffer64bit_37_output1, cbuffer64bit_38_output1, cbuffer64bit_39_output1, cbuffer64bit_40_output1,
       cbuffer64bit_41_output1, cbuffer64bit_42_output1, cbuffer64bit_43_output1, cbuffer64bit_44_output1,
       cbuffer64bit_45_output1, cbuffer64bit_46_output1, cbuffer64bit_47_output1, cbuffer64bit_48_output1,
       cbuffer64bit_49_output1, cbuffer64bit_50_output1, cbuffer64bit_51_output1, cbuffer64bit_52_output1,
       cbuffer64bit_53_output1, cbuffer64bit_54_output1, cbuffer64bit_55_output1, cbuffer64bit_56_output1,
       cbuffer64bit_57_output1, cbuffer64bit_58_output1, cbuffer64bit_59_output1, cbuffer64bit_60_output1,
       cbuffer64bit_61_output1, cbuffer64bit_62_output1, cbuffer64bit_63_output1, cbuffer64bit_64_output1;

  comparatoru64bit comparatoru64bit_1 (
    .input1(select1), .input2({64{1'b0}}), .equal1(comparatoru64bit_1_equal1));  // open: greater1, less1
  comparatoru64bit comparatoru64bit_2 (
    .input1(select1), .input2(64'h1), .equal1(comparatoru64bit_2_equal1));  // open: greater1, less1
  comparatoru64bit comparatoru64bit_3 (
    .input1(select1), .input2(64'h2), .equal1(comparatoru64bit_3_equal1));  // open: greater1, less1
  comparatoru64bit comparatoru64bit_4 (
    .input1(select1), .input2(64'h3), .equal1(comparatoru64bit_4_equal1));  // open: greater1, less1
  comparatoru64bit comparatoru64bit_5 (
    .input1(select1), .input2(64'h4), .equal1(comparatoru64bit_5_equal1));  // open: greater1, less1
  comparatoru64bit comparatoru64bit_6 (
    .input1(select1), .input2(64'h5), .equal1(comparatoru64bit_6_equal1));  // open: greater1, less1
  comparatoru64bit comparatoru64bit_7 (
    .input1(select1), .input2(64'h6), .equal1(comparatoru64bit_7_equal1));  // open: greater1, less1
  comparatoru64bit comparatoru64bit_8 (
    .input1(select1), .input2(64'h7), .equal1(comparatoru64bit_8_equal1));  // open: greater1, less1
  comparatoru64bit comparatoru64bit_9 (
    .input1(select1), .input2(64'h8), .equal1(comparatoru64bit_9_equal1));  // open: greater1, less1
  comparatoru64bit comparatoru64bit_10 (
    .input1(select1), .input2(64'h9), .equal1(comparatoru64bit_10_equal1));  // open: greater1, less1
  comparatoru64bit comparatoru64bit_11 (
    .input1(select1), .input2(64'ha), .equal1(comparatoru64bit_11_equal1));  // open: greater1, less1
  comparatoru64bit comparatoru64bit_12 (
    .input1(select1), .input2(64'hb), .equal1(comparatoru64bit_12_equal1));  // open: greater1, less1
  comparatoru64bit comparatoru64bit_13 (
    .input1(select1), .input2(64'hc), .equal1(comparatoru64bit_13_equal1));  // open: greater1, less1
  comparatoru64bit comparatoru64bit_14 (
    .input1(select1), .input2(64'hd), .equal1(comparatoru64bit_14_equal1));  // open: greater1, less1
  comparatoru64bit comparatoru64bit_15 (
    .input1(select1), .input2(64'he), .equal1(comparatoru64bit_15_equal1));  // open: greater1, less1
  comparatoru64bit comparatoru64bit_16 (
    .input1(select1), .input2(64'hf), .equal1(comparatoru64bit_16_equal1));  // open: greater1, less1
  comparatoru64bit comparatoru64bit_17 (
    .input1(select1), .input2(64'h10), .equal1(comparatoru64bit_17_equal1));  // open: greater1, less1
  comparatoru64bit comparatoru64bit_18 (
    .input1(select1), .input2(64'h11), .equal1(comparatoru64bit_18_equal1));  // open: greater1, less1
  comparatoru64bit comparatoru64bit_19 (
    .input1(select1), .input2(64'h12), .equal1(comparatoru64bit_19_equal1));  // open: greater1, less1
  comparatoru64bit comparatoru64bit_20 (
    .input1(select1), .input2(64'h13), .equal1(comparatoru64bit_20_equal1));  // open: greater1, less1
  comparatoru64bit comparatoru64bit_21 (
    .input1(select1), .input2(64'h14), .equal1(comparatoru64bit_21_equal1));  // open: greater1, less1
  comparatoru64bit comparatoru64bit_22 (
    .input1(select1), .input2(64'h15), .equal1(comparatoru64bit_22_equal1));  // open: greater1, less1
  comparatoru64bit comparatoru64bit_23 (
    .input1(select1), .input2(64'h16), .equal1(comparatoru64bit_23_equal1));  // open: greater1, less1
  comparatoru64bit comparatoru64bit_24 (
    .input1(select1), .input2(64'h17), .equal1(comparatoru64bit_24_equal1));  // open: greater1, less1
  comparatoru64bit comparatoru64bit_25 (
    .input1(select1), .input2(64'h18), .equal1(comparatoru64bit_25_equal1));  // open: greater1, less1
  comparatoru64bit comparatoru64bit_26 (
    .input1(select1), .input2(64'h19), .equal1(comparatoru64bit_26_equal1));  // open: greater1, less1
  comparatoru64bit comparatoru64bit_27 (
    .input1(select1), .input2(64'h1a), .equal1(comparatoru64bit_27_equal1));  // open: greater1, less1
  comparatoru64bit comparatoru64bit_28 (
    .input1(select1), .input2(64'h1b), .equal1(comparatoru64bit_28_equal1));  // open: greater1, less1
  comparatoru64bit comparatoru64bit_29 (
    .input1(select1), .input2(64'h1c), .equal1(comparatoru64bit_29_equal1));  // open: greater1, less1
  comparatoru64bit comparatoru64bit_30 (
    .input1(select1), .input2(64'h1d), .equal1(comparatoru64bit_30_equal1));  // open: greater1, less1
  comparatoru64bit comparatoru64bit_31 (
    .input1(select1), .input2(64'h1e), .equal1(comparatoru64bit_31_equal1));  // open: greater1, less1
  comparatoru64bit comparatoru64bit_32 (
    .input1(select1), .input2(64'h1f), .equal1(comparatoru64bit_32_equal1));  // open: greater1, less1
  comparatoru64bit comparatoru64bit_33 (
    .input1(select1), .input2(64'h20), .equal1(comparatoru64bit_33_equal1));  // open: greater1, less1
  comparatoru64bit comparatoru64bit_34 (
    .input1(select1), .input2(64'h21), .equal1(comparatoru64bit_34_equal1));  // open: greater1, less1
  comparatoru64bit comparatoru64bit_35 (
    .input1(select1), .input2(64'h22), .equal1(comparatoru64bit_35_equal1));  // open: greater1, less1
  comparatoru64bit comparatoru64bit_36 (
    .input1(select1), .input2(64'h23), .equal1(comparatoru64bit_36_equal1));  // open: greater1, less1
  comparatoru64bit comparatoru64bit_37 (
    .input1(select1), .input2(64'h24), .equal1(comparatoru64bit_37_equal1));  // open: greater1, less1
  comparatoru64bit comparatoru64bit_38 (
    .input1(select1), .input2(64'h25), .equal1(comparatoru64bit_38_equal1));  // open: greater1, less1
  comparatoru64bit comparatoru64bit_39 (
    .input1(select1), .input2(64'h26), .equal1(comparatoru64bit_39_equal1));  // open: greater1, less1
  comparatoru64bit comparatoru64bit_40 (
    .input1(select1), .input2(64'h27), .equal1(comparatoru64bit_40_equal1));  // open: greater1, less1
  comparatoru64bit comparatoru64bit_41 (
    .input1(select1), .input2(64'h28), .equal1(comparatoru64bit_41_equal1));  // open: greater1, less1
  comparatoru64bit comparatoru64bit_42 (
    .input1(select1), .input2(64'h29), .equal1(comparatoru64bit_42_equal1));  // open: greater1, less1
  comparatoru64bit comparatoru64bit_43 (
    .input1(select1), .input2(64'h2a), .equal1(comparatoru64bit_43_equal1));  // open: greater1, less1
  comparatoru64bit comparatoru64bit_44 (
    .input1(select1), .input2(64'h2b), .equal1(comparatoru64bit_44_equal1));  // open: greater1, less1
  comparatoru64bit comparatoru64bit_45 (
    .input1(select1), .input2(64'h2c), .equal1(comparatoru64bit_45_equal1));  // open: greater1, less1
  comparatoru64bit comparatoru64bit_46 (
    .input1(select1), .input2(64'h2d), .equal1(comparatoru64bit_46_equal1));  // open: greater1, less1
  comparatoru64bit comparatoru64bit_47 (
    .input1(select1), .input2(64'h2e), .equal1(comparatoru64bit_47_equal1));  // open: greater1, less1
  comparatoru64bit comparatoru64bit_48 (
    .input1(select1), .input2(64'h2f), .equal1(comparatoru64bit_48_equal1));  // open: greater1, less1
  comparatoru64bit comparatoru64bit_49 (
    .input1(select1), .input2(64'h30), .equal1(comparatoru64bit_49_equal1));  // open: greater1, less1
  comparatoru64bit comparatoru64bit_50 (
    .input1(select1), .input2(64'h31), .equal1(comparatoru64bit_50_equal1));  // open: greater1, less1
  comparatoru64bit comparatoru64bit_51 (
    .input1(select1), .input2(64'h32), .equal1(comparatoru64bit_51_equal1));  // open: greater1, less1
  comparatoru64bit comparatoru64bit_52 (
    .input1(select1), .input2(64'h33), .equal1(comparatoru64bit_52_equal1));  // open: greater1, less1
  comparatoru64bit comparatoru64bit_53 (
    .input1(select1), .input2(64'h34), .equal1(comparatoru64bit_53_equal1));  // open: greater1, less1
  comparatoru64bit comparatoru64bit_54 (
    .input1(select1), .input2(64'h35), .equal1(comparatoru64bit_54_equal1));  // open: greater1, less1
  comparatoru64bit comparatoru64bit_55 (
    .input1(select1), .input2(64'h36), .equal1(comparatoru64bit_55_equal1));  // open: greater1, less1
  comparatoru64bit comparatoru64bit_56 (
    .input1(select1), .input2(64'h37), .equal1(comparatoru64bit_56_equal1));  // open: greater1, less1
  comparatoru64bit comparatoru64bit_57 (
    .input1(select1), .input2(64'h38), .equal1(comparatoru64bit_57_equal1));  // open: greater1, less1
  comparatoru64bit comparatoru64bit_58 (
    .input1(select1), .input2(64'h39), .equal1(comparatoru64bit_58_equal1));  // open: greater1, less1
  comparatoru64bit comparatoru64bit_59 (
    .input1(select1), .input2(64'h3a), .equal1(comparatoru64bit_59_equal1));  // open: greater1, less1
  comparatoru64bit comparatoru64bit_60 (
    .input1(select1), .input2(64'h3b), .equal1(comparatoru64bit_60_equal1));  // open: greater1, less1
  comparatoru64bit comparatoru64bit_61 (
    .input1(select1), .input2(64'h3c), .equal1(comparatoru64bit_61_equal1));  // open: greater1, less1
  comparatoru64bit comparatoru64bit_62 (
    .input1(select1), .input2(64'h3d), .equal1(comparatoru64bit_62_equal1));  // open: greater1, less1
  comparatoru64bit comparatoru64bit_63 (
    .input1(select1), .input2(64'h3e), .equal1(comparatoru64bit_63_equal1));  // open: greater1, less1
  comparatoru64bit comparatoru64bit_64 (
    .input1(select1), .input2(64'h3f), .equal1(comparatoru64bit_64_equal1));  // open: greater1, less1
  cbuffer64bit cbuffer64bit_1 (.buffer1(comparatoru64bit_1_equal1), .input1(input0), .output1(cbuffer64bit_1_output1));
  cbuffer64bit cbuffer64bit_2 (.buffer1(comparatoru64bit_2_equal1), .input1(input1), .output1(cbuffer64bit_2_output1));
  cbuffer64bit cbuffer64bit_3 (.buffer1(comparatoru64bit_3_equal1), .input1(input2), .output1(cbuffer64bit_3_output1));
  cbuffer64bit cbuffer64bit_4 (.buffer1(comparatoru64bit_4_equal1), .input1(input3), .output1(cbuffer64bit_4_output1));
  cbuffer64bit cbuffer64bit_5 (.buffer1(comparatoru64bit_5_equal1), .input1(input4), .output1(cbuffer64bit_5_output1));
  cbuffer64bit cbuffer64bit_6 (.buffer1(comparatoru64bit_6_equal1), .input1(input5), .output1(cbuffer64bit_6_output1));
  cbuffer64bit cbuffer64bit_7 (.buffer1(comparatoru64bit_7_equal1), .input1(input6), .output1(cbuffer64bit_7_output1));
  cbuffer64bit cbuffer64bit_8 (.buffer1(comparatoru64bit_8_equal1), .input1(input7), .output1(cbuffer64bit_8_output1));
  cbuffer64bit cbuffer64bit_9 (.buffer1(comparatoru64bit_9_equal1), .input1(input8), .output1(cbuffer64bit_9_output1));
  cbuffer64bit cbuffer64bit_10 (
    .buffer1(comparatoru64bit_10_equal1), .input1(input9), .output1(cbuffer64bit_10_output1));
  cbuffer64bit cbuffer64bit_11 (
    .buffer1(comparatoru64bit_11_equal1), .input1(input10), .output1(cbuffer64bit_11_output1));
  cbuffer64bit cbuffer64bit_12 (
    .buffer1(comparatoru64bit_12_equal1), .input1(input11), .output1(cbuffer64bit_12_output1));
  cbuffer64bit cbuffer64bit_13 (
    .buffer1(comparatoru64bit_13_equal1), .input1(input12), .output1(cbuffer64bit_13_output1));
  cbuffer64bit cbuffer64bit_14 (
    .buffer1(comparatoru64bit_14_equal1), .input1(input13), .output1(cbuffer64bit_14_output1));
  cbuffer64bit cbuffer64bit_15 (
    .buffer1(comparatoru64bit_15_equal1), .input1(input14), .output1(cbuffer64bit_15_output1));
  cbuffer64bit cbuffer64bit_16 (
    .buffer1(comparatoru64bit_16_equal1), .input1(input15), .output1(cbuffer64bit_16_output1));
  cbuffer64bit cbuffer64bit_17 (
    .buffer1(comparatoru64bit_17_equal1), .input1(input16), .output1(cbuffer64bit_17_output1));
  cbuffer64bit cbuffer64bit_18 (
    .buffer1(comparatoru64bit_18_equal1), .input1(input17), .output1(cbuffer64bit_18_output1));
  cbuffer64bit cbuffer64bit_19 (
    .buffer1(comparatoru64bit_19_equal1), .input1(input18), .output1(cbuffer64bit_19_output1));
  cbuffer64bit cbuffer64bit_20 (
    .buffer1(comparatoru64bit_20_equal1), .input1(input19), .output1(cbuffer64bit_20_output1));
  cbuffer64bit cbuffer64bit_21 (
    .buffer1(comparatoru64bit_21_equal1), .input1(input20), .output1(cbuffer64bit_21_output1));
  cbuffer64bit cbuffer64bit_22 (
    .buffer1(comparatoru64bit_22_equal1), .input1(input21), .output1(cbuffer64bit_22_output1));
  cbuffer64bit cbuffer64bit_23 (
    .buffer1(comparatoru64bit_23_equal1), .input1(input22), .output1(cbuffer64bit_23_output1));
  cbuffer64bit cbuffer64bit_24 (
    .buffer1(comparatoru64bit_24_equal1), .input1(input23), .output1(cbuffer64bit_24_output1));
  cbuffer64bit cbuffer64bit_25 (
    .buffer1(comparatoru64bit_25_equal1), .input1(input24), .output1(cbuffer64bit_25_output1));
  cbuffer64bit cbuffer64bit_26 (
    .buffer1(comparatoru64bit_26_equal1), .input1(input25), .output1(cbuffer64bit_26_output1));
  cbuffer64bit cbuffer64bit_27 (
    .buffer1(comparatoru64bit_27_equal1), .input1(input26), .output1(cbuffer64bit_27_output1));
  cbuffer64bit cbuffer64bit_28 (
    .buffer1(comparatoru64bit_28_equal1), .input1(input27), .output1(cbuffer64bit_28_output1));
  cbuffer64bit cbuffer64bit_29 (
    .buffer1(comparatoru64bit_29_equal1), .input1(input28), .output1(cbuffer64bit_29_output1));
  cbuffer64bit cbuffer64bit_30 (
    .buffer1(comparatoru64bit_30_equal1), .input1(input29), .output1(cbuffer64bit_30_output1));
  cbuffer64bit cbuffer64bit_31 (
    .buffer1(comparatoru64bit_31_equal1), .input1(input30), .output1(cbuffer64bit_31_output1));
  cbuffer64bit cbuffer64bit_32 (
    .buffer1(comparatoru64bit_32_equal1), .input1(input31), .output1(cbuffer64bit_32_output1));
  cbuffer64bit cbuffer64bit_33 (
    .buffer1(comparatoru64bit_33_equal1), .input1(input32), .output1(cbuffer64bit_33_output1));
  cbuffer64bit cbuffer64bit_34 (
    .buffer1(comparatoru64bit_34_equal1), .input1(input33), .output1(cbuffer64bit_34_output1));
  cbuffer64bit cbuffer64bit_35 (
    .buffer1(comparatoru64bit_35_equal1), .input1(input34), .output1(cbuffer64bit_35_output1));
  cbuffer64bit cbuffer64bit_36 (
    .buffer1(comparatoru64bit_36_equal1), .input1(input35), .output1(cbuffer64bit_36_output1));
  cbuffer64bit cbuffer64bit_37 (
    .buffer1(comparatoru64bit_37_equal1), .input1(input36), .output1(cbuffer64bit_37_output1));
  cbuffer64bit cbuffer64bit_38 (
    .buffer1(comparatoru64bit_38_equal1), .input1(input37), .output1(cbuffer64bit_38_output1));
  cbuffer64bit cbuffer64bit_39 (
    .buffer1(comparatoru64bit_39_equal1), .input1(input38), .output1(cbuffer64bit_39_output1));
  cbuffer64bit cbuffer64bit_40 (
    .buffer1(comparatoru64bit_40_equal1), .input1(input39), .output1(cbuffer64bit_40_output1));
  cbuffer64bit cbuffer64bit_41 (
    .buffer1(comparatoru64bit_41_equal1), .input1(input40), .output1(cbuffer64bit_41_output1));
  cbuffer64bit cbuffer64bit_42 (
    .buffer1(comparatoru64bit_42_equal1), .input1(input41), .output1(cbuffer64bit_42_output1));
  cbuffer64bit cbuffer64bit_43 (
    .buffer1(comparatoru64bit_43_equal1), .input1(input42), .output1(cbuffer64bit_43_output1));
  cbuffer64bit cbuffer64bit_44 (
    .buffer1(comparatoru64bit_44_equal1), .input1(input43), .output1(cbuffer64bit_44_output1));
  cbuffer64bit cbuffer64bit_45 (
    .buffer1(comparatoru64bit_45_equal1), .input1(input44), .output1(cbuffer64bit_45_output1));
  cbuffer64bit cbuffer64bit_46 (
    .buffer1(comparatoru64bit_46_equal1), .input1(input45), .output1(cbuffer64bit_46_output1));
  cbuffer64bit cbuffer64bit_47 (
    .buffer1(comparatoru64bit_47_equal1), .input1(input46), .output1(cbuffer64bit_47_output1));
  cbuffer64bit cbuffer64bit_48 (
    .buffer1(comparatoru64bit_48_equal1), .input1(input47), .output1(cbuffer64bit_48_output1));
  cbuffer64bit cbuffer64bit_49 (
    .buffer1(comparatoru64bit_49_equal1), .input1(input48), .output1(cbuffer64bit_49_output1));
  cbuffer64bit cbuffer64bit_50 (
    .buffer1(comparatoru64bit_50_equal1), .input1(input49), .output1(cbuffer64bit_50_output1));
  cbuffer64bit cbuffer64bit_51 (
    .buffer1(comparatoru64bit_51_equal1), .input1(input50), .output1(cbuffer64bit_51_output1));
  cbuffer64bit cbuffer64bit_52 (
    .buffer1(comparatoru64bit_52_equal1), .input1(input51), .output1(cbuffer64bit_52_output1));
  cbuffer64bit cbuffer64bit_53 (
    .buffer1(comparatoru64bit_53_equal1), .input1(input52), .output1(cbuffer64bit_53_output1));
  cbuffer64bit cbuffer64bit_54 (
    .buffer1(comparatoru64bit_54_equal1), .input1(input53), .output1(cbuffer64bit_54_output1));
  cbuffer64bit cbuffer64bit_55 (
    .buffer1(comparatoru64bit_55_equal1), .input1(input54), .output1(cbuffer64bit_55_output1));
  cbuffer64bit cbuffer64bit_56 (
    .buffer1(comparatoru64bit_56_equal1), .input1(input55), .output1(cbuffer64bit_56_output1));
  cbuffer64bit cbuffer64bit_57 (
    .buffer1(comparatoru64bit_57_equal1), .input1(input56), .output1(cbuffer64bit_57_output1));
  cbuffer64bit cbuffer64bit_58 (
    .buffer1(comparatoru64bit_58_equal1), .input1(input57), .output1(cbuffer64bit_58_output1));
  cbuffer64bit cbuffer64bit_59 (
    .buffer1(comparatoru64bit_59_equal1), .input1(input58), .output1(cbuffer64bit_59_output1));
  cbuffer64bit cbuffer64bit_60 (
    .buffer1(comparatoru64bit_60_equal1), .input1(input59), .output1(cbuffer64bit_60_output1));
  cbuffer64bit cbuffer64bit_61 (
    .buffer1(comparatoru64bit_61_equal1), .input1(input60), .output1(cbuffer64bit_61_output1));
  cbuffer64bit cbuffer64bit_62 (
    .buffer1(comparatoru64bit_62_equal1), .input1(input61), .output1(cbuffer64bit_62_output1));
  cbuffer64bit cbuffer64bit_63 (
    .buffer1(comparatoru64bit_63_equal1), .input1(input62), .output1(cbuffer64bit_63_output1));
  cbuffer64bit cbuffer64bit_64 (
    .buffer1(comparatoru64bit_64_equal1), .input1(input63), .output1(cbuffer64bit_64_output1));
  assign output1 = cbuffer64bit_1_output1 | cbuffer64bit_2_output1 | cbuffer64bit_3_output1 | cbuffer64bit_4_output1 | cbuffer64bit_5_output1 | cbuffer64bit_6_output1 | cbuffer64bit_7_output1 | cbuffer64bit_8_output1 | cbuffer64bit_9_output1 | cbuffer64bit_10_output1 | cbuffer64bit_11_output1 | cbuffer64bit_12_output1 | cbuffer64bit_13_output1 | cbuffer64bit_14_output1 | cbuffer64bit_15_output1 | cbuffer64bit_16_output1 | cbuffer64bit_17_output1 | cbuffer64bit_18_output1 | cbuffer64bit_19_output1 | cbuffer64bit_20_output1 | cbuffer64bit_21_output1 | cbuffer64bit_22_output1 | cbuffer64bit_23_output1 | cbuffer64bit_24_output1 | cbuffer64bit_25_output1 | cbuffer64bit_26_output1 | cbuffer64bit_27_output1 | cbuffer64bit_28_output1 | cbuffer64bit_29_output1 | cbuffer64bit_30_output1 | cbuffer64bit_31_output1 | cbuffer64bit_32_output1 | cbuffer64bit_33_output1 | cbuffer64bit_34_output1 | cbuffer64bit_35_output1 | cbuffer64bit_36_output1 | cbuffer64bit_37_output1 | cbuffer64bit_38_output1 | cbuffer64bit_39_output1 | cbuffer64bit_40_output1 | cbuffer64bit_41_output1 | cbuffer64bit_42_output1 | cbuffer64bit_43_output1 | cbuffer64bit_44_output1 | cbuffer64bit_45_output1 | cbuffer64bit_46_output1 | cbuffer64bit_47_output1 | cbuffer64bit_48_output1 | cbuffer64bit_49_output1 | cbuffer64bit_50_output1 | cbuffer64bit_51_output1 | cbuffer64bit_52_output1 | cbuffer64bit_53_output1 | cbuffer64bit_54_output1 | cbuffer64bit_55_output1 | cbuffer64bit_56_output1 | cbuffer64bit_57_output1 | cbuffer64bit_58_output1 | cbuffer64bit_59_output1 | cbuffer64bit_60_output1 | cbuffer64bit_61_output1 | cbuffer64bit_62_output1 | cbuffer64bit_63_output1 | cbuffer64bit_64_output1;  // OR_Gate or_1, 64 bits wide
endmodule

module shiftright64bit (
  input  [63:0] input1,
  input  [7:0] shiftright1,
  output [63:0] output1
);

  wire [63:8] undriven;

  mux6x64bit mux6x64bit_1 (
    .select1({undriven, shiftright1}), .input0(input1), .input1({1'b0, input1[63:1]}),
    .input2({2'b00, input1[63:2]}), .input3({3'b000, input1[63:3]}), .input4({4'b0000, input1[63:4]}),
    .input5({{5{1'b0}}, input1[63:5]}), .input6({{6{1'b0}}, input1[63:6]}),
    .input7({{7{1'b0}}, input1[63:7]}), .input8({{8{1'b0}}, input1[63:8]}),
    .input9({{9{1'b0}}, input1[63:9]}), .input10({{10{1'b0}}, input1[63:10]}),
    .input11({{11{1'b0}}, input1[63:11]}), .input12({{12{1'b0}}, input1[63:12]}),
    .input13({{13{1'b0}}, input1[63:13]}), .input14({{14{1'b0}}, input1[63:14]}),
    .input15({{15{1'b0}}, input1[63:15]}), .input16({{16{1'b0}}, input1[63:16]}),
    .input17({{17{1'b0}}, input1[63:17]}), .input18({{18{1'b0}}, input1[63:18]}),
    .input19({{19{1'b0}}, input1[63:19]}), .input20({{20{1'b0}}, input1[63:20]}),
    .input21({{21{1'b0}}, input1[63:21]}), .input22({{22{1'b0}}, input1[63:22]}),
    .input23({{23{1'b0}}, input1[63:23]}), .input24({{24{1'b0}}, input1[63:24]}),
    .input25({{25{1'b0}}, input1[63:25]}), .input26({{26{1'b0}}, input1[63:26]}),
    .input27({{27{1'b0}}, input1[63:27]}), .input28({{28{1'b0}}, input1[63:28]}),
    .input29({{29{1'b0}}, input1[63:29]}), .input30({{30{1'b0}}, input1[63:30]}),
    .input31({{31{1'b0}}, input1[63:31]}), .input32({{32{1'b0}}, input1[63:32]}),
    .input33({{33{1'b0}}, input1[63:33]}), .input34({{34{1'b0}}, input1[63:34]}),
    .input35({{35{1'b0}}, input1[63:35]}), .input36({{36{1'b0}}, input1[63:36]}),
    .input37({{37{1'b0}}, input1[63:37]}), .input38({{38{1'b0}}, input1[63:38]}),
    .input39({{39{1'b0}}, input1[63:39]}), .input40({{40{1'b0}}, input1[63:40]}),
    .input41({{41{1'b0}}, input1[63:41]}), .input42({{42{1'b0}}, input1[63:42]}),
    .input43({{43{1'b0}}, input1[63:43]}), .input44({{44{1'b0}}, input1[63:44]}),
    .input45({{45{1'b0}}, input1[63:45]}), .input46({{46{1'b0}}, input1[63:46]}),
    .input47({{47{1'b0}}, input1[63:47]}), .input48({{48{1'b0}}, input1[63:48]}),
    .input49({{49{1'b0}}, input1[63:49]}), .input50({{50{1'b0}}, input1[63:50]}),
    .input51({{51{1'b0}}, input1[63:51]}), .input52({{52{1'b0}}, input1[63:52]}),
    .input53({{53{1'b0}}, input1[63:53]}), .input54({{54{1'b0}}, input1[63:54]}),
    .input55({{55{1'b0}}, input1[63:55]}), .input56({{56{1'b0}}, input1[63:56]}),
    .input57({{57{1'b0}}, input1[63:57]}), .input58({{58{1'b0}}, input1[63:58]}),
    .input59({{59{1'b0}}, input1[63:59]}), .input60({{60{1'b0}}, input1[63:60]}),
    .input61({{61{1'b0}}, input1[63:61]}), .input62({{62{1'b0}}, input1[63:62]}),
    .input63({{63{1'b0}}, input1[63]}), .output1(output1));
  // Pins of 8 and 64 bits meet at {undriven, shiftright1}

  // Notes on the sheet:
  //   shiftright1: initial=0x30
  //   input1: initial=0xcafebabecafebabe
endmodule

module ashiftright64bit (
  input  [63:0] input1,
  input  [7:0] ashiftright1,
  output [63:0] output1
);

  wire [63:8] undriven;

  mux6x64bit mux6x64bit_1 (
    .select1({undriven, ashiftright1}), .input0(input1), .input1({1'b1, input1[63:1]}),
    .input2({2'b11, input1[63:2]}), .input3({3'b111, input1[63:3]}), .input4({4'b1111, input1[63:4]}),
    .input5({{5{1'b1}}, input1[63:5]}), .input6({{6{1'b1}}, input1[63:6]}),
    .input7({{7{1'b1}}, input1[63:7]}), .input8({{8{1'b1}}, input1[63:8]}),
    .input9({{9{1'b1}}, input1[63:9]}), .input10({{10{1'b1}}, input1[63:10]}),
    .input11({{11{1'b1}}, input1[63:11]}), .input12({{12{1'b1}}, input1[63:12]}),
    .input13({{13{1'b1}}, input1[63:13]}), .input14({{14{1'b1}}, input1[63:14]}),
    .input15({{15{1'b1}}, input1[63:15]}), .input16({{16{1'b1}}, input1[63:16]}),
    .input17({{17{1'b1}}, input1[63:17]}), .input18({{18{1'b1}}, input1[63:18]}),
    .input19({{19{1'b1}}, input1[63:19]}), .input20({{20{1'b1}}, input1[63:20]}),
    .input21({{21{1'b1}}, input1[63:21]}), .input22({{22{1'b1}}, input1[63:22]}),
    .input23({{23{1'b1}}, input1[63:23]}), .input24({{24{1'b1}}, input1[63:24]}),
    .input25({{25{1'b1}}, input1[63:25]}), .input26({{26{1'b1}}, input1[63:26]}),
    .input27({{27{1'b1}}, input1[63:27]}), .input28({{28{1'b1}}, input1[63:28]}),
    .input29({{29{1'b1}}, input1[63:29]}), .input30({{30{1'b1}}, input1[63:30]}),
    .input31({{31{1'b1}}, input1[63:31]}), .input32({{32{1'b1}}, input1[63:32]}),
    .input33({{33{1'b1}}, input1[63:33]}), .input34({{34{1'b1}}, input1[63:34]}),
    .input35({{35{1'b1}}, input1[63:35]}), .input36({{36{1'b1}}, input1[63:36]}),
    .input37({{37{1'b1}}, input1[63:37]}), .input38({{38{1'b1}}, input1[63:38]}),
    .input39({{39{1'b1}}, input1[63:39]}), .input40({{40{1'b1}}, input1[63:40]}),
    .input41({{41{1'b1}}, input1[63:41]}), .input42({{42{1'b1}}, input1[63:42]}),
    .input43({{43{1'b1}}, input1[63:43]}), .input44({{44{1'b1}}, input1[63:44]}),
    .input45({{45{1'b1}}, input1[63:45]}), .input46({{46{1'b1}}, input1[63:46]}),
    .input47({{47{1'b1}}, input1[63:47]}), .input48({{48{1'b1}}, input1[63:48]}),
    .input49({{49{1'b1}}, input1[63:49]}), .input50({{50{1'b1}}, input1[63:50]}),
    .input51({{51{1'b1}}, input1[63:51]}), .input52({{52{1'b1}}, input1[63:52]}),
    .input53({{53{1'b1}}, input1[63:53]}), .input54({{54{1'b1}}, input1[63:54]}),
    .input55({{55{1'b1}}, input1[63:55]}), .input56({{56{1'b1}}, input1[63:56]}),
    .input57({{57{1'b1}}, input1[63:57]}), .input58({{58{1'b1}}, input1[63:58]}),
    .input59({{59{1'b1}}, input1[63:59]}), .input60({{60{1'b1}}, input1[63:60]}),
    .input61({{61{1'b1}}, input1[63:61]}), .input62({{62{1'b1}}, input1[63:62]}),
    .input63({{63{1'b1}}, input1[63]}), .output1(output1));
  // Pins of 8 and 64 bits meet at {undriven, ashiftright1}

  // Notes on the sheet:
  //   ashiftright1: initial=0x30
  //   input1: initial=0xcafebabecafebabe
endmodule

module rotateleft64bit (
  input  [63:0] input1,
  input  [7:0] rotateleft1,
  output [63:0] output1
);

  wire [63:8] undriven;

  mux6x64bit mux6x64bit_1 (
    .select1({undriven, rotateleft1}), .input0(input1), .input1({input1[62:0], input1[63]}),
    .input2({input1[61:0], input1[63:62]}), .input3({input1[60:0], input1[63:61]}),
    .input4({input1[59:0], input1[63:60]}), .input5({input1[58:0], input1[63:59]}),
    .input6({input1[57:0], input1[63:58]}), .input7({input1[56:0], input1[63:57]}),
    .input8({input1[55:0], input1[63:56]}), .input9({input1[54:0], input1[63:55]}),
    .input10({input1[53:0], input1[63:54]}), .input11({input1[52:0], input1[63:53]}),
    .input12({input1[51:0], input1[63:52]}), .input13({input1[50:0], input1[63:51]}),
    .input14({input1[49:0], input1[63:50]}), .input15({input1[48:0], input1[63:49]}),
    .input16({input1[47:0], input1[63:48]}), .input17({input1[46:0], input1[63:47]}),
    .input18({input1[45:0], input1[63:46]}), .input19({input1[44:0], input1[63:45]}),
    .input20({input1[43:0], input1[63:44]}), .input21({input1[42:0], input1[63:43]}),
    .input22({input1[41:0], input1[63:42]}), .input23({input1[40:0], input1[63:41]}),
    .input24({input1[39:0], input1[63:40]}), .input25({input1[38:0], input1[63:39]}),
    .input26({input1[37:0], input1[63:38]}), .input27({input1[36:0], input1[63:37]}),
    .input28({input1[35:0], input1[63:36]}), .input29({input1[34:0], input1[63:35]}),
    .input30({input1[33:0], input1[63:34]}), .input31({input1[32:0], input1[63:33]}),
    .input32({input1[31:0], input1[63:32]}), .input33({input1[30:0], input1[63:31]}),
    .input34({input1[29:0], input1[63:30]}), .input35({input1[28:0], input1[63:29]}),
    .input36({input1[27:0], input1[63:28]}), .input37({input1[26:0], input1[63:27]}),
    .input38({input1[25:0], input1[63:26]}), .input39({input1[24:0], input1[63:25]}),
    .input40({input1[23:0], input1[63:24]}), .input41({input1[22:0], input1[63:23]}),
    .input42({input1[21:0], input1[63:22]}), .input43({input1[20:0], input1[63:21]}),
    .input44({input1[19:0], input1[63:20]}), .input45({input1[18:0], input1[63:19]}),
    .input46({input1[17:0], input1[63:18]}), .input47({input1[16:0], input1[63:17]}),
    .input48({input1[15:0], input1[63:16]}), .input49({input1[14:0], input1[63:15]}),
    .input50({input1[13:0], input1[63:14]}), .input51({input1[12:0], input1[63:13]}),
    .input52({input1[11:0], input1[63:12]}), .input53({input1[10:0], input1[63:11]}),
    .input54({input1[9:0], input1[63:10]}), .input55({input1[8:0], input1[63:9]}),
    .input56({input1[7:0], input1[63:8]}), .input57({input1[6:0], input1[63:7]}),
    .input58({input1[5:0], input1[63:6]}), .input59({input1[4:0], input1[63:5]}),
    .input60({input1[3:0], input1[63:4]}), .input61({input1[2:0], input1[63:3]}),
    .input62({input1[1:0], input1[63:2]}), .input63({input1[0], input1[63:1]}), .output1(output1));
  // Pins of 8 and 64 bits meet at {undriven, rotateleft1}

  // Notes on the sheet:
  //   rotateleft1: initial=0x30
  //   input1: initial=0xcafebabecafebabe
endmodule

module rotateright64bit (
  input  [63:0] input1,
  input  [7:0] rotateright1,
  output [63:0] output1
);

  wire [63:8] undriven;

  mux6x64bit mux6x64bit_1 (
    .select1({undriven, rotateright1}), .input0(input1), .input1({input1[0], input1[63:1]}),
    .input2({input1[1:0], input1[63:2]}), .input3({input1[2:0], input1[63:3]}),
    .input4({input1[3:0], input1[63:4]}), .input5({input1[4:0], input1[63:5]}),
    .input6({input1[5:0], input1[63:6]}), .input7({input1[6:0], input1[63:7]}),
    .input8({input1[7:0], input1[63:8]}), .input9({input1[8:0], input1[63:9]}),
    .input10({input1[9:0], input1[63:10]}), .input11({input1[10:0], input1[63:11]}),
    .input12({input1[11:0], input1[63:12]}), .input13({input1[12:0], input1[63:13]}),
    .input14({input1[13:0], input1[63:14]}), .input15({input1[14:0], input1[63:15]}),
    .input16({input1[15:0], input1[63:16]}), .input17({input1[16:0], input1[63:17]}),
    .input18({input1[17:0], input1[63:18]}), .input19({input1[18:0], input1[63:19]}),
    .input20({input1[19:0], input1[63:20]}), .input21({input1[20:0], input1[63:21]}),
    .input22({input1[21:0], input1[63:22]}), .input23({input1[22:0], input1[63:23]}),
    .input24({input1[23:0], input1[63:24]}), .input25({input1[24:0], input1[63:25]}),
    .input26({input1[25:0], input1[63:26]}), .input27({input1[26:0], input1[63:27]}),
    .input28({input1[27:0], input1[63:28]}), .input29({input1[28:0], input1[63:29]}),
    .input30({input1[29:0], input1[63:30]}), .input31({input1[30:0], input1[63:31]}),
    .input32({input1[31:0], input1[63:32]}), .input33({input1[32:0], input1[63:33]}),
    .input34({input1[33:0], input1[63:34]}), .input35({input1[34:0], input1[63:35]}),
    .input36({input1[35:0], input1[63:36]}), .input37({input1[36:0], input1[63:37]}),
    .input38({input1[37:0], input1[63:38]}), .input39({input1[38:0], input1[63:39]}),
    .input40({input1[39:0], input1[63:40]}), .input41({input1[40:0], input1[63:41]}),
    .input42({input1[41:0], input1[63:42]}), .input43({input1[42:0], input1[63:43]}),
    .input44({input1[43:0], input1[63:44]}), .input45({input1[44:0], input1[63:45]}),
    .input46({input1[45:0], input1[63:46]}), .input47({input1[46:0], input1[63:47]}),
    .input48({input1[47:0], input1[63:48]}), .input49({input1[48:0], input1[63:49]}),
    .input50({input1[49:0], input1[63:50]}), .input51({input1[50:0], input1[63:51]}),
    .input52({input1[51:0], input1[63:52]}), .input53({input1[52:0], input1[63:53]}),
    .input54({input1[53:0], input1[63:54]}), .input55({input1[54:0], input1[63:55]}),
    .input56({input1[55:0], input1[63:56]}), .input57({input1[56:0], input1[63:57]}),
    .input58({input1[57:0], input1[63:58]}), .input59({input1[58:0], input1[63:59]}),
    .input60({input1[59:0], input1[63:60]}), .input61({input1[60:0], input1[63:61]}),
    .input62({input1[61:0], input1[63:62]}), .input63({input1[62:0], input1[63]}), .output1(output1));
  // Pins of 8 and 64 bits meet at {undriven, rotateright1}

  // Notes on the sheet:
  //   rotateright1: initial=0x30
  //   input1: initial=0xcafebabecafebabe
endmodule

module divideru64bit (
  input  [63:0] inupper,
  input  [63:0] input1,
  input  [63:0] input2,
  output [63:0] remainder,
  output [63:0] output1
);
endmodule
