// Logisim project microfpgamux.circ as structural Verilog: 3 circuits, main circuit muxalu
module muxalu (
  input  [63:0] input1,
  input  [63:0] input2,
  input  [5:0] operation1,
  input  [63:0] rom1,
  output [63:0] output1
);

  wire clock_1_out, comparator_1_gt, comparator_2_gt, comparator_3_eq, comparator_4_lt, fpcomparator_1_p3,
       fpcomparator_2_p3, fpcomparator_3_p3;
  wire [5:0] bitselector_1_out, bitselector_2_out, bitselector_3_out, bitselector_4_out, bitselector_5_out;
  wire [63:0] adder_1_out, and_1_out, demultiplexer_1_out0, demultiplexer_1_out1, demultiplexer_1_out2,
       demultiplexer_1_out3, demultiplexer_1_out4, demultiplexer_1_out5, demultiplexer_1_out6,
       demultiplexer_1_out7, demultiplexer_1_out8, demultiplexer_1_out9, demultiplexer_1_out10,
       demultiplexer_1_out11, demultiplexer_1_out12, demultiplexer_1_out13, demultiplexer_1_out14,
       demultiplexer_1_out15, demultiplexer_1_out16, demultiplexer_1_out17, demultiplexer_1_out18,
       demultiplexer_1_out19, demultiplexer_1_out20, demultiplexer_1_out21, demultiplexer_1_out22,
       demultiplexer_1_out23, demultiplexer_1_out24, demultiplexer_1_out25, demultiplexer_1_out26,
       demultiplexer_1_out27, demultiplexer_1_out28, demultiplexer_1_out29, demultiplexer_1_out30,
       demultiplexer_1_out31, demultiplexer_1_out32, demultiplexer_2_out0, demultiplexer_2_out1,
       demultiplexer_2_out2, demultiplexer_2_out3, demultiplexer_2_out4, demultiplexer_2_out5,
       demultiplexer_2_out6, demultiplexer_2_out7, demultiplexer_2_out8, demultiplexer_2_out9,
       demultiplexer_2_out10, demultiplexer_2_out11, demultiplexer_2_out12, demultiplexer_2_out13,
       demultiplexer_2_out14, demultiplexer_2_out15, demultiplexer_2_out16, demultiplexer_2_out17,
       demultiplexer_2_out18, demultiplexer_2_out19, demultiplexer_2_out20, demultiplexer_2_out21,
       demultiplexer_2_out22, demultiplexer_2_out23, demultiplexer_2_out24, demultiplexer_2_out25,
       demultiplexer_2_out26, demultiplexer_2_out27, demultiplexer_2_out28, demultiplexer_2_out29,
       demultiplexer_2_out30, demultiplexer_2_out31, demultiplexer_2_out32, divider_1_out, fpadder_1_out,
       fpdivider_1_out, fpmultiplier_1_out, fpnegator_1_p3, fpsubtractor_1_out, fptoint_1_p3, inttofp_1_p5,
       multiplexer_1_out, multiplexer_2_out, multiplexer_3_out, multiplexer_4_out, multiplexer_5_out,
       multiplexer_6_out, multiplier_1_out, nand_1_out, negator_1_out, nor_1_out, not_1_out, or_1_out,
       random_1_out, register_1_q, shifter_1_out, shifter_2_out, shifter_3_out, shifter_4_out, shifter_5_out,
       subtractor_1_out, xnor_1_out, xor_1_out;

  Demultiplexer #(.select(6), .width(64)) demultiplexer_1 (
    .out0(demultiplexer_1_out0), .out1(demultiplexer_1_out1), .out2(demultiplexer_1_out2),
    .out3(demultiplexer_1_out3), .out4(demultiplexer_1_out4), .out5(demultiplexer_1_out5),
    .out6(demultiplexer_1_out6), .out7(demultiplexer_1_out7), .out8(demultiplexer_1_out8),
    .out9(demultiplexer_1_out9), .out10(demultiplexer_1_out10), .out11(demultiplexer_1_out11),
    .out12(demultiplexer_1_out12), .out13(demultiplexer_1_out13), .out14(demultiplexer_1_out14),
    .out15(demultiplexer_1_out15), .out16(demultiplexer_1_out16), .out17(demultiplexer_1_out17),
    .out18(demultiplexer_1_out18), .out19(demultiplexer_1_out19), .out20(demultiplexer_1_out20),
    .out21(demultiplexer_1_out21), .out22(demultiplexer_1_out22), .out23(demultiplexer_1_out23),
    .out24(demultiplexer_1_out24), .out25(demultiplexer_1_out25), .out26(demultiplexer_1_out26),
    .out27(demultiplexer_1_out27), .out28(demultiplexer_1_out28), .out29(demultiplexer_1_out29),
    .out30(demultiplexer_1_out30), .out31(demultiplexer_1_out31), .out32(demultiplexer_1_out32),
    .sel(operation1));  // open: out33, out34, out35, out36, out37, out38, out39, out40, out41, out42, out43, out44, out45, out46, out47, out48, out49, out50, out51, out52, out53, out54, out55, out56, out57, out58, out59, out60, out61, out62, out63, in
  Demultiplexer #(.select(6), .width(64)) demultiplexer_2 (
    .out0(demultiplexer_2_out0), .out1(demultiplexer_2_out1), .out2(demultiplexer_2_out2),
    .out3(demultiplexer_2_out3), .out4(demultiplexer_2_out4), .out5(demultiplexer_2_out5),
    .out6(demultiplexer_2_out6), .out7(demultiplexer_2_out7), .out8(demultiplexer_2_out8),
    .out9(demultiplexer_2_out9), .out10(demultiplexer_2_out10), .out11(demultiplexer_2_out11),
    .out12(demultiplexer_2_out12), .out13(demultiplexer_2_out13), .out14(demultiplexer_2_out14),
    .out15(demultiplexer_2_out15), .out16(demultiplexer_2_out16), .out17(demultiplexer_2_out17),
    .out18(demultiplexer_2_out18), .out19(demultiplexer_2_out19), .out20(demultiplexer_2_out20),
    .out21(demultiplexer_2_out21), .out22(demultiplexer_2_out22), .out23(demultiplexer_2_out23),
    .out24(demultiplexer_2_out24), .out25(demultiplexer_2_out25), .out26(demultiplexer_2_out26),
    .out27(demultiplexer_2_out27), .out28(demultiplexer_2_out28), .out29(demultiplexer_2_out29),
    .out30(demultiplexer_2_out30), .out31(demultiplexer_2_out31), .out32(demultiplexer_2_out32),
    .sel(operation1));  // open: out33, out34, out35, out36, out37, out38, out39, out40, out41, out42, out43, out44, out45, out46, out47, out48, out49, out50, out51, out52, out53, out54, out55, out56, out57, out58, out59, out60, out61, out62, out63, in
  Comparator #(.width(64)) comparator_1 (
    .a(demultiplexer_2_out25), .b({64{1'b0}}), .gt(comparator_1_gt));  // open: eq, lt
  Comparator #(.width(64)) comparator_2 (
    .a(demultiplexer_1_out26), .b(demultiplexer_2_out26), .gt(comparator_2_gt));  // open: eq, lt
  Comparator #(.width(64)) comparator_3 (
    .a(demultiplexer_1_out27), .b(demultiplexer_2_out27), .eq(comparator_3_eq));  // open: gt, lt
  Comparator #(.width(64)) comparator_4 (
    .a(demultiplexer_1_out28), .b(demultiplexer_2_out28), .lt(comparator_4_lt));  // open: gt, eq
  // FPComparator #(.fpwidth(64)) fpcomparator_1: pin names not known; wires that end beside it: demultiplexer_1_out29, demultiplexer_2_out29, fpcomparator_1_p3
  // FPComparator #(.fpwidth(64)) fpcomparator_2: pin names not known; wires that end beside it: demultiplexer_1_out30, demultiplexer_2_out30, fpcomparator_2_p3
  // FPComparator #(.fpwidth(64)) fpcomparator_3: pin names not known; wires that end beside it: demultiplexer_1_out31, demultiplexer_2_out31, fpcomparator_3_p3, demultiplexer_1_out32, demultiplexer_2_out32
  Random #(.seed(69420), .width(64)) random_1 (.clk(clock_1_out), .out(random_1_out));  // open: clr, next
  Clock clock_1 (.out(clock_1_out));
  FPAdder #(.fpwidth(64)) fpadder_1 (.a(demultiplexer_1_out0), .b(demultiplexer_2_out0), .out(fpadder_1_out));
  FPSubtractor #(.fpwidth(64)) fpsubtractor_1 (
    .a(demultiplexer_1_out1), .b(demultiplexer_2_out1), .out(fpsubtractor_1_out));
  FPMultiplier #(.fpwidth(64)) fpmultiplier_1 (
    .a(demultiplexer_1_out2), .b(demultiplexer_2_out2), .out(fpmultiplier_1_out));
  FPDivider #(.fpwidth(64)) fpdivider_1 (.a(demultiplexer_1_out3), .b(demultiplexer_2_out3), .out(fpdivider_1_out));
  // FPNegator #(.fpwidth(64)) fpnegator_1: pin names not known; wires that end beside it: demultiplexer_2_out4, demultiplexer_1_out4, fpnegator_1_p3
  // FPToInt #(.fpwidth(64), .width(64)) fptoint_1: pin names not known; wires that end beside it: demultiplexer_2_out5, demultiplexer_1_out5, fptoint_1_p3
  Adder #(.width(64)) adder_1 (
    .a(demultiplexer_1_out6), .b(demultiplexer_2_out6), .out(adder_1_out));  // open: cin, cout
  Subtractor #(.width(64)) subtractor_1 (
    .a(demultiplexer_1_out7), .b(demultiplexer_2_out7), .out(subtractor_1_out));  // open: bin, bout
  Multiplier #(.mode("twosComplement"), .width(64)) multiplier_1 (
    .a(demultiplexer_1_out8), .b(demultiplexer_2_out8), .out(multiplier_1_out));  // open: cin, cout
  Divider #(.mode("twosComplement"), .width(64)) divider_1 (
    .a(demultiplexer_1_out9), .b(demultiplexer_2_out9), .out(divider_1_out));  // open: upper, rem
  Negator #(.width(64)) negator_1 (.in(demultiplexer_1_out10), .out(negator_1_out));
  // IntToFP #(.fpwidth(64), .width(64)) inttofp_1: pin names not known; wires that end beside it: demultiplexer_2_out10, demultiplexer_2_out11, demultiplexer_2_out12, demultiplexer_1_out11, inttofp_1_p5
  assign not_1_out = ~demultiplexer_1_out12;  // NOT_Gate not_1, 64 bits wide
  assign and_1_out = demultiplexer_1_out13 & demultiplexer_2_out13;  // AND_Gate and_1, 64 bits wide
  assign or_1_out = demultiplexer_1_out14 | demultiplexer_2_out14;  // OR_Gate or_1, 64 bits wide
  assign xor_1_out = demultiplexer_1_out15 ^ demultiplexer_2_out15;  // XOR_Gate xor_1, 64 bits wide
  assign nand_1_out = ~(demultiplexer_1_out16 & demultiplexer_2_out16);  // NAND_Gate nand_1, 64 bits wide
  assign nor_1_out = ~(demultiplexer_1_out17 | demultiplexer_2_out17);  // NOR_Gate nor_1, 64 bits wide
  assign xnor_1_out = ~(demultiplexer_1_out18 ^ demultiplexer_2_out18);  // XNOR_Gate xnor_1, 64 bits wide
  Shifter #(.width(64)) shifter_1 (.in(demultiplexer_1_out19), .\dist (bitselector_1_out), .out(shifter_1_out));
  BitSelector #(.group(6), .width(64)) bitselector_1 (
    .in(demultiplexer_2_out19), .out(bitselector_1_out), .sel(4'b0000));
  Shifter #(.shift("lr"), .width(64)) shifter_2 (
    .in(demultiplexer_1_out20), .\dist (bitselector_2_out), .out(shifter_2_out));
  BitSelector #(.group(6), .width(64)) bitselector_2 (
    .in(demultiplexer_2_out20), .out(bitselector_2_out), .sel(4'b0000));
  Shifter #(.shift("ar"), .width(64)) shifter_3 (
    .in(demultiplexer_1_out21), .\dist (bitselector_3_out), .out(shifter_3_out));
  BitSelector #(.group(6), .width(64)) bitselector_3 (
    .in(demultiplexer_2_out21), .out(bitselector_3_out), .sel(4'b0000));
  Shifter #(.shift("rl"), .width(64)) shifter_4 (
    .in(demultiplexer_1_out22), .\dist (bitselector_4_out), .out(shifter_4_out));
  BitSelector #(.group(6), .width(64)) bitselector_4 (
    .in(demultiplexer_2_out22), .out(bitselector_4_out), .sel(4'b0000));
  Shifter #(.shift("rr"), .width(64)) shifter_5 (
    .in(demultiplexer_1_out23), .\dist (bitselector_5_out), .out(shifter_5_out));
  BitSelector #(.group(6), .width(64)) bitselector_5 (
    .in(demultiplexer_2_out23), .out(bitselector_5_out), .sel(4'b0000));
  Register #(.trigger("high"), .width(64)) register_1 (
    .D(demultiplexer_1_out25), .clk(comparator_1_gt), .Q(register_1_q));  // open: en, clr
  Multiplexer #(.width(64)) multiplexer_1 (
    .in0({64{1'b0}}), .in1(64'h1), .out(multiplexer_1_out), .sel(comparator_2_gt));
  Multiplexer #(.width(64)) multiplexer_2 (
    .in0({64{1'b0}}), .in1(64'h1), .out(multiplexer_2_out), .sel(comparator_3_eq));
  Multiplexer #(.width(64)) multiplexer_3 (
    .in0({64{1'b0}}), .in1(64'h1), .out(multiplexer_3_out), .sel(comparator_4_lt));
  Multiplexer #(.width(64)) multiplexer_4 (
    .in0({64{1'b0}}), .in1(64'h1), .out(multiplexer_4_out), .sel(fpcomparator_1_p3));
  Multiplexer #(.width(64)) multiplexer_5 (
    .in0({64{1'b0}}), .in1(64'h1), .out(multiplexer_5_out), .sel(fpcomparator_2_p3));
  Multiplexer #(.width(64)) multiplexer_6 (
    .in0({64{1'b0}}), .in1(64'h1), .out(multiplexer_6_out), .sel(fpcomparator_3_p3));
  Multiplexer #(.select(6), .width(64)) multiplexer_7 (
    .in0(fpadder_1_out), .in1(fpsubtractor_1_out), .in2(fpmultiplier_1_out), .in3(fpdivider_1_out),
    .in4(fpnegator_1_p3), .in5(fptoint_1_p3), .in6(adder_1_out), .in7(subtractor_1_out),
    .in8(multiplier_1_out), .in9(divider_1_out), .in10(negator_1_out), .in11(inttofp_1_p5), .in12(not_1_out),
    .in13(and_1_out), .in14(or_1_out), .in15(xor_1_out), .in16(nand_1_out), .in17(nor_1_out),
    .in18(xnor_1_out), .in19(shifter_1_out), .in20(shifter_2_out), .in21(shifter_3_out),
    .in22(shifter_4_out), .in23(shifter_5_out), .in24(rom1), .in25(register_1_q), .in26(multiplexer_1_out),
    .in27(multiplexer_2_out), .in28(multiplexer_3_out), .in29(multiplexer_4_out), .in30(multiplexer_5_out),
    .in31(multiplexer_6_out), .in32(random_1_out), .sel(operation1));  // open: in33, in34, in35, in36, in37, in38, in39, in40, in41, in42, in43, in44, in45, in46, in47, in48, in49, in50, in51, in52, in53, in54, in55, in56, in57, in58, in59, in60, in61, in62, in63, out
endmodule

module muxfpga (
);

  wire clock_1_out;
  wire [7:0] bitselector_1_out, bitselector_2_out, bitselector_3_out, bitselector_4_out;
  wire [63:0] multiplexer_1_out, multiplexer_2_out, multiplexer_3_out, multiplexer_4_out, multiplexer_5_out,
       multiplexer_6_out, multiplexer_7_out, multiplexer_8_out, multiplexer_9_out, multiplexer_10_out,
       multiplexer_11_out, multiplexer_12_out, muxalu_1_output1, muxalu_2_output1, muxalu_3_output1,
       muxalu_4_output1, muxalu_5_output1, muxalu_6_output1, muxalu_7_output1, muxalu_8_output1,
       register_1_q, register_2_q, register_3_q, register_4_q, register_5_q, register_6_q, register_7_q,
       register_8_q, undriven, undriven_2, undriven_3, undriven_4, undriven_5, undriven_6, undriven_7,
       undriven_8, undriven_9, undriven_10, undriven_11, undriven_12;

  muxalu muxalu_1 (
    .input1(multiplexer_5_out), .input2(multiplexer_7_out), .operation1(6'b111000), .rom1(64'h2),
    .output1(muxalu_1_output1));
  muxalu muxalu_2 (
    .input1(multiplexer_9_out), .input2(multiplexer_11_out), .operation1(6'b000110), .rom1({64{1'b0}}),
    .output1(muxalu_2_output1));
  muxalu muxalu_3 (
    .input1(undriven_12), .input2(undriven_11), .operation1(6'b111000), .rom1(64'h3),
    .output1(muxalu_3_output1));
  muxalu muxalu_4 (
    .input1(undriven_10), .input2(undriven_9), .operation1(6'b111000), .rom1(64'h5),
    .output1(muxalu_4_output1));
  muxalu muxalu_5 (
    .input1(undriven_8), .input2(undriven_7), .operation1(6'b111000), .rom1(64'h11),
    .output1(muxalu_5_output1));
  muxalu muxalu_6 (
    .input1(undriven_6), .input2(undriven_5), .operation1(6'b111000), .rom1(64'h12),
    .output1(muxalu_6_output1));
  muxalu muxalu_7 (
    .input1(undriven_4), .input2(undriven_3), .operation1(6'b111000), .rom1(64'h13),
    .output1(muxalu_7_output1));
  muxalu muxalu_8 (
    .input1(undriven_2), .input2(undriven), .operation1(6'b111000), .rom1(64'h14), .output1(muxalu_8_output1));
  Clock clock_1 (.out(clock_1_out));
  Register #(.width(64)) register_1 (.D(muxalu_1_output1), .clk(clock_1_out), .Q(register_1_q));  // open: en, clr
  Register #(.width(64)) register_2 (.D(muxalu_2_output1), .clk(clock_1_out), .Q(register_2_q));  // open: en, clr
  Register #(.width(64)) register_3 (.D(muxalu_3_output1), .clk(clock_1_out), .Q(register_3_q));  // open: en, clr
  Register #(.width(64)) register_4 (.D(muxalu_4_output1), .clk(clock_1_out), .Q(register_4_q));  // open: en, clr
  Register #(.width(64)) register_5 (.D(muxalu_5_output1), .clk(clock_1_out), .Q(register_5_q));  // open: en, clr
  Register #(.width(64)) register_6 (.D(muxalu_6_output1), .clk(clock_1_out), .Q(register_6_q));  // open: en, clr
  Register #(.width(64)) register_7 (.D(muxalu_7_output1), .clk(clock_1_out), .Q(register_7_q));  // open: en, clr
  Register #(.width(64)) register_8 (.D(muxalu_8_output1), .clk(clock_1_out), .Q(register_8_q));  // open: en, clr
  Multiplexer #(.width(64)) multiplexer_1 (
    .in0({64{1'b0}}), .in1(multiplexer_6_out), .out(multiplexer_1_out), .sel(1'b0));
  Multiplexer #(.width(64)) multiplexer_2 (
    .in0({64{1'b0}}), .in1(multiplexer_8_out), .out(multiplexer_2_out), .sel(1'b0));
  Multiplexer #(.width(64)) multiplexer_3 (.in0(64'h3), .in1(multiplexer_10_out), .out(multiplexer_3_out), .sel(1'b0));
  Multiplexer #(.width(64)) multiplexer_4 (
    .in0({64{1'b0}}), .in1(multiplexer_12_out), .out(multiplexer_4_out), .sel(1'b1));
  BitSelector #(.group(8), .width(64)) bitselector_1 (.in(multiplexer_1_out), .out(bitselector_1_out), .sel(3'b000));
  BitSelector #(.group(8), .width(64)) bitselector_2 (.in(multiplexer_2_out), .out(bitselector_2_out), .sel(3'b000));
  BitSelector #(.group(8), .width(64)) bitselector_3 (.in(multiplexer_3_out), .out(bitselector_3_out), .sel(3'b000));
  BitSelector #(.group(8), .width(64)) bitselector_4 (.in(multiplexer_4_out), .out(bitselector_4_out), .sel(3'b000));
  Multiplexer #(.select(8), .width(64)) multiplexer_5 (
    .in0(register_1_q), .in1(register_2_q), .in2(register_3_q), .in3(register_4_q), .in4(register_5_q),
    .in5(register_6_q), .in6(register_7_q), .in7(register_8_q), .out(multiplexer_5_out),
    .sel(bitselector_1_out));  // open: in8, in9, in10, in11, in12, in13, in14, in15, in16, in17, in18, in19, in20, in21, in22, in23, in24, in25, in26, in27, in28, in29, in30, in31, in32, in33, in34, in35, in36, in37, in38, in39, in40, in41, in42, in43, in44, in45, in46, in47, in48, in49, in50, in51, in52, in53, in54, in55, in56, in57, in58, in59, in60, in61, in62, in63, in64, in65, in66, in67, in68, in69, in70, in71, in72, in73, in74, in75, in76, in77, in78, in79, in80, in81, in82, in83, in84, in85, in86, in87, in88, in89, in90, in91, in92, in93, in94, in95, in96, in97, in98, in99, in100, in101, in102, in103, in104, in105, in106, in107, in108, in109, in110, in111, in112, in113, in114, in115, in116, in117, in118, in119, in120, in121, in122, in123, in124, in125, in126, in127, in128, in129, in130, in131, in132, in133, in134, in135, in136, in137, in138, in139, in140, in141, in142, in143, in144, in145, in146, in147, in148, in149, in150, in151, in152, in153, in154, in155, in156, in157, in158, in159, in160, in161, in162, in163, in164, in165, in166, in167, in168, in169, in170, in171, in172, in173, in174, in175, in176, in177, in178, in179, in180, in181, in182, in183, in184, in185, in186, in187, in188, in189, in190, in191, in192, in193, in194, in195, in196, in197, in198, in199, in200, in201, in202, in203, in204, in205, in206, in207, in208, in209, in210, in211, in212, in213, in214, in215, in216, in217, in218, in219, in220, in221, in222, in223, in224, in225, in226, in227, in228, in229, in230, in231, in232, in233, in234, in235, in236, in237, in238, in239, in240, in241, in242, in243, in244, in245, in246, in247, in248, in249, in250, in251, in252, in253, in254, in255
  Multiplexer #(.select(8), .width(64)) multiplexer_6 (
    .in0(register_1_q), .in1(register_2_q), .in2(register_3_q), .in3(register_4_q), .in4(register_5_q),
    .in5(register_6_q), .in6(register_7_q), .in7(register_8_q), .out(multiplexer_6_out), .sel({8{1'b0}}));  // open: in8, in9, in10, in11, in12, in13, in14, in15, in16, in17, in18, in19, in20, in21, in22, in23, in24, in25, in26, in27, in28, in29, in30, in31, in32, in33, in34, in35, in36, in37, in38, in39, in40, in41, in42, in43, in44, in45, in46, in47, in48, in49, in50, in51, in52, in53, in54, in55, in56, in57, in58, in59, in60, in61, in62, in63, in64, in65, in66, in67, in68, in69, in70, in71, in72, in73, in74, in75, in76, in77, in78, in79, in80, in81, in82, in83, in84, in85, in86, in87, in88, in89, in90, in91, in92, in93, in94, in95, in96, in97, in98, in99, in100, in101, in102, in103, in104, in105, in106, in107, in108, in109, in110, in111, in112, in113, in114, in115, in116, in117, in118, in119, in120, in121, in122, in123, in124, in125, in126, in127, in128, in129, in130, in131, in132, in133, in134, in135, in136, in137, in138, in139, in140, in141, in142, in143, in144, in145, in146, in147, in148, in149, in150, in151, in152, in153, in154, in155, in156, in157, in158, in159, in160, in161, in162, in163, in164, in165, in166, in167, in168, in169, in170, in171, in172, in173, in174, in175, in176, in177, in178, in179, in180, in181, in182, in183, in184, in185, in186, in187, in188, in189, in190, in191, in192, in193, in194, in195, in196, in197, in198, in199, in200, in201, in202, in203, in204, in205, in206, in207, in208, in209, in210, in211, in212, in213, in214, in215, in216, in217, in218, in219, in220, in221, in222, in223, in224, in225, in226, in227, in228, in229, in230, in231, in232, in233, in234, in235, in236, in237, in238, in239, in240, in241, in242, in243, in244, in245, in246, in247, in248, in249, in250, in251, in252, in253, in254, in255
  Multiplexer #(.select(8), .width(64)) multiplexer_7 (
    .in0(register_1_q), .in1(register_2_q), .in2(register_3_q), .in3(register_4_q), .in4(register_5_q),
    .in5(register_6_q), .in6(register_7_q), .in7(register_8_q), .out(multiplexer_7_out),
    .sel(bitselector_2_out));  // open: in8, in9, in10, in11, in12, in13, in14, in15, in16, in17, in18, in19, in20, in21, in22, in23, in24, in25, in26, in27, in28, in29, in30, in31, in32, in33, in34, in35, in36, in37, in38, in39, in40, in41, in42, in43, in44, in45, in46, in47, in48, in49, in50, in51, in52, in53, in54, in55, in56, in57, in58, in59, in60, in61, in62, in63, in64, in65, in66, in67, in68, in69, in70, in71, in72, in73, in74, in75, in76, in77, in78, in79, in80, in81, in82, in83, in84, in85, in86, in87, in88, in89, in90, in91, in92, in93, in94, in95, in96, in97, in98, in99, in100, in101, in102, in103, in104, in105, in106, in107, in108, in109, in110, in111, in112, in113, in114, in115, in116, in117, in118, in119, in120, in121, in122, in123, in124, in125, in126, in127, in128, in129, in130, in131, in132, in133, in134, in135, in136, in137, in138, in139, in140, in141, in142, in143, in144, in145, in146, in147, in148, in149, in150, in151, in152, in153, in154, in155, in156, in157, in158, in159, in160, in161, in162, in163, in164, in165, in166, in167, in168, in169, in170, in171, in172, in173, in174, in175, in176, in177, in178, in179, in180, in181, in182, in183, in184, in185, in186, in187, in188, in189, in190, in191, in192, in193, in194, in195, in196, in197, in198, in199, in200, in201, in202, in203, in204, in205, in206, in207, in208, in209, in210, in211, in212, in213, in214, in215, in216, in217, in218, in219, in220, in221, in222, in223, in224, in225, in226, in227, in228, in229, in230, in231, in232, in233, in234, in235, in236, in237, in238, in239, in240, in241, in242, in243, in244, in245, in246, in247, in248, in249, in250, in251, in252, in253, in254, in255
  Multiplexer #(.select(8), .width(64)) multiplexer_8 (
    .in0(register_1_q), .in1(register_2_q), .in2(register_3_q), .in3(register_4_q), .out(multiplexer_8_out),
    .sel({8{1'b0}}));  // open: in4, in5, in6, in7, in8, in9, in10, in11, in12, in13, in14, in15, in16, in17, in18, in19, in20, in21, in22, in23, in24, in25, in26, in27, in28, in29, in30, in31, in32, in33, in34, in35, in36, in37, in38, in39, in40, in41, in42, in43, in44, in45, in46, in47, in48, in49, in50, in51, in52, in53, in54, in55, in56, in57, in58, in59, in60, in61, in62, in63, in64, in65, in66, in67, in68, in69, in70, in71, in72, in73, in74, in75, in76, in77, in78, in79, in80, in81, in82, in83, in84, in85, in86, in87, in88, in89, in90, in91, in92, in93, in94, in95, in96, in97, in98, in99, in100, in101, in102, in103, in104, in105, in106, in107, in108, in109, in110, in111, in112, in113, in114, in115, in116, in117, in118, in119, in120, in121, in122, in123, in124, in125, in126, in127, in128, in129, in130, in131, in132, in133, in134, in135, in136, in137, in138, in139, in140, in141, in142, in143, in144, in145, in146, in147, in148, in149, in150, in151, in152, in153, in154, in155, in156, in157, in158, in159, in160, in161, in162, in163, in164, in165, in166, in167, in168, in169, in170, in171, in172, in173, in174, in175, in176, in177, in178, in179, in180, in181, in182, in183, in184, in185, in186, in187, in188, in189, in190, in191, in192, in193, in194, in195, in196, in197, in198, in199, in200, in201, in202, in203, in204, in205, in206, in207, in208, in209, in210, in211, in212, in213, in214, in215, in216, in217, in218, in219, in220, in221, in222, in223, in224, in225, in226, in227, in228, in229, in230, in231, in232, in233, in234, in235, in236, in237, in238, in239, in240, in241, in242, in243, in244, in245, in246, in247, in248, in249, in250, in251, in252, in253, in254, in255
  Multiplexer #(.select(8), .width(64)) multiplexer_9 (
    .in0(register_1_q), .in1(register_2_q), .in2(register_3_q), .in3(register_4_q), .out(multiplexer_9_out),
    .sel(bitselector_3_out));  // open: in4, in5, in6, in7, in8, in9, in10, in11, in12, in13, in14, in15, in16, in17, in18, in19, in20, in21, in22, in23, in24, in25, in26, in27, in28, in29, in30, in31, in32, in33, in34, in35, in36, in37, in38, in39, in40, in41, in42, in43, in44, in45, in46, in47, in48, in49, in50, in51, in52, in53, in54, in55, in56, in57, in58, in59, in60, in61, in62, in63, in64, in65, in66, in67, in68, in69, in70, in71, in72, in73, in74, in75, in76, in77, in78, in79, in80, in81, in82, in83, in84, in85, in86, in87, in88, in89, in90, in91, in92, in93, in94, in95, in96, in97, in98, in99, in100, in101, in102, in103, in104, in105, in106, in107, in108, in109, in110, in111, in112, in113, in114, in115, in116, in117, in118, in119, in120, in121, in122, in123, in124, in125, in126, in127, in128, in129, in130, in131, in132, in133, in134, in135, in136, in137, in138, in139, in140, in141, in142, in143, in144, in145, in146, in147, in148, in149, in150, in151, in152, in153, in154, in155, in156, in157, in158, in159, in160, in161, in162, in163, in164, in165, in166, in167, in168, in169, in170, in171, in172, in173, in174, in175, in176, in177, in178, in179, in180, in181, in182, in183, in184, in185, in186, in187, in188, in189, in190, in191, in192, in193, in194, in195, in196, in197, in198, in199, in200, in201, in202, in203, in204, in205, in206, in207, in208, in209, in210, in211, in212, in213, in214, in215, in216, in217, in218, in219, in220, in221, in222, in223, in224, in225, in226, in227, in228, in229, in230, in231, in232, in233, in234, in235, in236, in237, in238, in239, in240, in241, in242, in243, in244, in245, in246, in247, in248, in249, in250, in251, in252, in253, in254, in255
  Multiplexer #(.select(8), .width(64)) multiplexer_10 (
    .in0(register_1_q), .in1(register_2_q), .in2(register_3_q), .in3(register_4_q), .out(multiplexer_10_out),
    .sel({8{1'b0}}));  // open: in4, in5, in6, in7, in8, in9, in10, in11, in12, in13, in14, in15, in16, in17, in18, in19, in20, in21, in22, in23, in24, in25, in26, in27, in28, in29, in30, in31, in32, in33, in34, in35, in36, in37, in38, in39, in40, in41, in42, in43, in44, in45, in46, in47, in48, in49, in50, in51, in52, in53, in54, in55, in56, in57, in58, in59, in60, in61, in62, in63, in64, in65, in66, in67, in68, in69, in70, in71, in72, in73, in74, in75, in76, in77, in78, in79, in80, in81, in82, in83, in84, in85, in86, in87, in88, in89, in90, in91, in92, in93, in94, in95, in96, in97, in98, in99, in100, in101, in102, in103, in104, in105, in106, in107, in108, in109, in110, in111, in112, in113, in114, in115, in116, in117, in118, in119, in120, in121, in122, in123, in124, in125, in126, in127, in128, in129, in130, in131, in132, in133, in134, in135, in136, in137, in138, in139, in140, in141, in142, in143, in144, in145, in146, in147, in148, in149, in150, in151, in152, in153, in154, in155, in156, in157, in158, in159, in160, in161, in162, in163, in164, in165, in166, in167, in168, in169, in170, in171, in172, in173, in174, in175, in176, in177, in178, in179, in180, in181, in182, in183, in184, in185, in186, in187, in188, in189, in190, in191, in192, in193, in194, in195, in196, in197, in198, in199, in200, in201, in202, in203, in204, in205, in206, in207, in208, in209, in210, in211, in212, in213, in214, in215, in216, in217, in218, in219, in220, in221, in222, in223, in224, in225, in226, in227, in228, in229, in230, in231, in232, in233, in234, in235, in236, in237, in238, in239, in240, in241, in242, in243, in244, in245, in246, in247, in248, in249, in250, in251, in252, in253, in254, in255
  Multiplexer #(.select(8), .width(64)) multiplexer_11 (
    .in0(register_1_q), .in1(register_2_q), .in2(register_3_q), .in3(register_4_q), .out(multiplexer_11_out),
    .sel(bitselector_4_out));  // open: in4, in5, in6, in7, in8, in9, in10, in11, in12, in13, in14, in15, in16, in17, in18, in19, in20, in21, in22, in23, in24, in25, in26, in27, in28, in29, in30, in31, in32, in33, in34, in35, in36, in37, in38, in39, in40, in41, in42, in43, in44, in45, in46, in47, in48, in49, in50, in51, in52, in53, in54, in55, in56, in57, in58, in59, in60, in61, in62, in63, in64, in65, in66, in67, in68, in69, in70, in71, in72, in73, in74, in75, in76, in77, in78, in79, in80, in81, in82, in83, in84, in85, in86, in87, in88, in89, in90, in91, in92, in93, in94, in95, in96, in97, in98, in99, in100, in101, in102, in103, in104, in105, in106, in107, in108, in109, in110, in111, in112, in113, in114, in115, in116, in117, in118, in119, in120, in121, in122, in123, in124, in125, in126, in127, in128, in129, in130, in131, in132, in133, in134, in135, in136, in137, in138, in139, in140, in141, in142, in143, in144, in145, in146, in147, in148, in149, in150, in151, in152, in153, in154, in155, in156, in157, in158, in159, in160, in161, in162, in163, in164, in165, in166, in167, in168, in169, in170, in171, in172, in173, in174, in175, in176, in177, in178, in179, in180, in181, in182, in183, in184, in185, in186, in187, in188, in189, in190, in191, in192, in193, in194, in195, in196, in197, in198, in199, in200, in201, in202, in203, in204, in205, in206, in207, in208, in209, in210, in211, in212, in213, in214, in215, in216, in217, in218, in219, in220, in221, in222, in223, in224, in225, in226, in227, in228, in229, in230, in231, in232, in233, in234, in235, in236, in237, in238, in239, in240, in241, in242, in243, in244, in245, in246, in247, in248, in249, in250, in251, in252, in253, in254, in255
  Multiplexer #(.select(8), .width(64)) multiplexer_12 (
    .in0(register_1_q), .in1(register_2_q), .in2(register_3_q), .in3(register_4_q), .out(multiplexer_12_out),
    .sel({8{1'b0}}));  // open: in4, in5, in6, in7, in8, in9, in10, in11, in12, in13, in14, in15, in16, in17, in18, in19, in20, in21, in22, in23, in24, in25, in26, in27, in28, in29, in30, in31, in32, in33, in34, in35, in36, in37, in38, in39, in40, in41, in42, in43, in44, in45, in46, in47, in48, in49, in50, in51, in52, in53, in54, in55, in56, in57, in58, in59, in60, in61, in62, in63, in64, in65, in66, in67, in68, in69, in70, in71, in72, in73, in74, in75, in76, in77, in78, in79, in80, in81, in82, in83, in84, in85, in86, in87, in88, in89, in90, in91, in92, in93, in94, in95, in96, in97, in98, in99, in100, in101, in102, in103, in104, in105, in106, in107, in108, in109, in110, in111, in112, in113, in114, in115, in116, in117, in118, in119, in120, in121, in122, in123, in124, in125, in126, in127, in128, in129, in130, in131, in132, in133, in134, in135, in136, in137, in138, in139, in140, in141, in142, in143, in144, in145, in146, in147, in148, in149, in150, in151, in152, in153, in154, in155, in156, in157, in158, in159, in160, in161, in162, in163, in164, in165, in166, in167, in168, in169, in170, in171, in172, in173, in174, in175, in176, in177, in178, in179, in180, in181, in182, in183, in184, in185, in186, in187, in188, in189, in190, in191, in192, in193, in194, in195, in196, in197, in198, in199, in200, in201, in202, in203, in204, in205, in206, in207, in208, in209, in210, in211, in212, in213, in214, in215, in216, in217, in218, in219, in220, in221, in222, in223, in224, in225, in226, in227, in228, in229, in230, in231, in232, in233, in234, in235, in236, in237, in238, in239, in240, in241, in242, in243, in244, in245, in246, in247, in248, in249, in250, in251, in252, in253, in254, in255
endmodule

module muxselector (
  input  [63:0] direct1,
  input  isindirect1,
  input  [63:0] indirect1,
  input  [63:0] direct2,
  input  isindirect2,
  input  [63:0] indirect2,
  input  [63:0] input1,
  input  [63:0] input33,
  input  [63:0] input65,
  input  [63:0] input97,
  input  [63:0] input129,
  input  [63:0] input161,
  input  [63:0] input193,
  input  [63:0] input225,
  input  [63:0] input2,
  input  [63:0] input34,
  input  [63:0] input66,
  input  [63:0] input98,
  input  [63:0] input130,
  input  [63:0] input162,
  input  [63:0] input194,
  input  [63:0] input226,
  input  [63:0] input3,
  input  [63:0] input35,
  input  [63:0] input67,
  input  [63:0] input99,
  input  [63:0] input131,
  input  [63:0] input163,
  input  [63:0] input195,
  input  [63:0] input227,
  input  [63:0] input4,
  input  [63:0] input36,
  input  [63:0] input68,
  input  [63:0] input100,
  input  [63:0] input132,
  input  [63:0] input164,
  input  [63:0] input196,
  input  [63:0] input228,
  input  [63:0] input5,
  input  [63:0] input37,
  input  [63:0] input69,
  input  [63:0] input101,
  input  [63:0] input133,
  input  [63:0] input165,
  input  [63:0] input197,
  input  [63:0] input229,
  input  [63:0] input6,
  input  [63:0] input38,
  input  [63:0] input70,
  input  [63:0] input102,
  input  [63:0] input134,
  input  [63:0] input166,
  input  [63:0] input198,
  input  [63:0] input230,
  input  [63:0] input7,
  input  [63:0] input39,
  input  [63:0] input71,
  input  [63:0] input103,
  input  [63:0] input135,
  input  [63:0] input167,
  input  [63:0] input199,
  input  [63:0] input231,
  input  [63:0] input8,
  input  [63:0] input40,
  input  [63:0] input72,
  input  [63:0] input104,
  input  [63:0] input136,
  input  [63:0] input168,
  input  [63:0] input200,
  input  [63:0] input232,
  input  [63:0] input9,
  input  [63:0] input41,
  input  [63:0] input73,
  input  [63:0] input105,
  input  [63:0] input137,
  input  [63:0] input169,
  input  [63:0] input201,
  input  [63:0] input233,
  input  [63:0] input10,
  input  [63:0] input42,
  input  [63:0] input74,
  input  [63:0] input106,
  input  [63:0] input138,
  input  [63:0] input170,
  input  [63:0] input202,
  input  [63:0] input234,
  input  [63:0] input11,
  input  [63:0] input43,
  input  [63:0] input75,
  input  [63:0] input107,
  input  [63:0] input139,
  input  [63:0] input171,
  input  [63:0] input203,
  input  [63:0] input235,
  input  [63:0] input12,
  input  [63:0] input44,
  input  [63:0] input76,
  input  [63:0] input108,
  input  [63:0] input140,
  input  [63:0] input172,
  input  [63:0] input204,
  input  [63:0] input236,
  input  [63:0] input13,
  input  [63:0] input45,
  input  [63:0] input77,
  input  [63:0] input109,
  input  [63:0] input141,
  input  [63:0] input173,
  input  [63:0] input205,
  input  [63:0] input237,
  input  [63:0] input14,
  input  [63:0] input46,
  input  [63:0] input78,
  input  [63:0] input110,
  input  [63:0] input142,
  input  [63:0] input174,
  input  [63:0] input206,
  input  [63:0] input238,
  input  [63:0] input15,
  input  [63:0] input47,
  input  [63:0] input79,
  input  [63:0] input111,
  input  [63:0] input143,
  input  [63:0] input175,
  input  [63:0] input207,
  input  [63:0] input239,
  input  [63:0] input16,
  input  [63:0] input48,
  input  [63:0] input80,
  input  [63:0] input112,
  input  [63:0] input144,
  input  [63:0] input176,
  input  [63:0] input208,
  input  [63:0] input240,
  input  [63:0] input17,
  input  [63:0] input49,
  input  [63:0] input81,
  input  [63:0] input113,
  input  [63:0] input145,
  input  [63:0] input177,
  input  [63:0] input209,
  input  [63:0] input241,
  input  [63:0] input18,
  input  [63:0] input50,
  input  [63:0] input82,
  input  [63:0] input114,
  input  [63:0] input146,
  input  [63:0] input178,
  input  [63:0] input210,
  input  [63:0] input242,
  input  [63:0] input19,
  input  [63:0] input51,
  input  [63:0] input83,
  input  [63:0] input115,
  input  [63:0] input147,
  input  [63:0] input179,
  input  [63:0] input211,
  input  [63:0] input243,
  input  [63:0] input20,
  input  [63:0] input52,
  input  [63:0] input84,
  input  [63:0] input116,
  input  [63:0] input148,
  input  [63:0] input180,
  input  [63:0] input212,
  input  [63:0] input244,
  input  [63:0] input21,
  input  [63:0] input53,
  input  [63:0] input85,
  input  [63:0] input117,
  input  [63:0] input149,
  input  [63:0] input181,
  input  [63:0] input213,
  input  [63:0] input245,
  input  [63:0] input22,
  input  [63:0] input54,
  input  [63:0] input86,
  input  [63:0] input118,
  input  [63:0] input150,
  input  [63:0] input182,
  input  [63:0] input214,
  input  [63:0] input246,
  input  [63:0] input23,
  input  [63:0] input55,
  input  [63:0] input87,
  input  [63:0] input119,
  input  [63:0] input151,
  input  [63:0] input183,
  input  [63:0] input215,
  input  [63:0] input247,
  input  [63:0] input24,
  input  [63:0] input56,
  input  [63:0] input88,
  input  [63:0] input120,
  input  [63:0] input152,
  input  [63:0] input184,
  input  [63:0] input216,
  input  [63:0] input248,
  input  [63:0] input25,
  input  [63:0] input57,
  input  [63:0] input89,
  input  [63:0] input121,
  input  [63:0] input153,
  input  [63:0] input185,
  input  [63:0] input217,
  input  [63:0] input249,
  input  [63:0] input26,
  input  [63:0] input58,
  input  [63:0] input90,
  input  [63:0] input122,
  input  [63:0] input154,
  input  [63:0] input186,
  input  [63:0] input218,
  input  [63:0] input250,
  input  [63:0] input27,
  input  [63:0] input59,
  input  [63:0] input91,
  input  [63:0] input123,
  input  [63:0] input155,
  input  [63:0] input187,
  input  [63:0] input219,
  input  [63:0] input251,
  input  [63:0] input28,
  input  [63:0] input60,
  input  [63:0] input92,
  input  [63:0] input124,
  input  [63:0] input156,
  input  [63:0] input188,
  input  [63:0] input220,
  input  [63:0] input252,
  input  [63:0] input29,
  input  [63:0] input61,
  input  [63:0] input93,
  input  [63:0] input125,
  input  [63:0] input157,
  input  [63:0] input189,
  input  [63:0] input221,
  input  [63:0] input253,
  input  [63:0] input30,
  input  [63:0] input62,
  input  [63:0] input94,
  input  [63:0] input126,
  input  [63:0] input158,
  input  [63:0] input190,
  input  [63:0] input222,
  input  [63:0] input254,
  input  [63:0] input31,
  input  [63:0] input63,
  input  [63:0] input95,
  input  [63:0] input127,
  input  [63:0] input159,
  input  [63:0] input191,
  input  [63:0] input223,
  input  [63:0] input255,
  input  [63:0] input32,
  input  [63:0] input64,
  input  [63:0] input96,
  input  [63:0] input128,
  input  [63:0] input160,
  input  [63:0] input192,
  input  [63:0] input224,
  input  [63:0] input256,
  output [63:0] output1,
  output [63:0] output2
);

  wire [7:0] bitselector_1_out, bitselector_2_out, bitselector_3_out, bitselector_4_out;
  wire [63:0] multiplexer_1_out, multiplexer_2_out, multiplexer_4_out, multiplexer_6_out;

  Multiplexer #(.width(64)) multiplexer_1 (
    .in0(direct1), .in1(multiplexer_4_out), .out(multiplexer_1_out), .sel(isindirect1));
  Multiplexer #(.width(64)) multiplexer_2 (
    .in0(direct2), .in1(multiplexer_6_out), .out(multiplexer_2_out), .sel(isindirect2));
  BitSelector #(.group(8), .width(64)) bitselector_1 (.in(multiplexer_1_out), .out(bitselector_1_out), .sel(3'b000));
  BitSelector #(.group(8), .width(64)) bitselector_2 (.in(indirect1), .out(bitselector_2_out), .sel(3'b000));
  BitSelector #(.group(8), .width(64)) bitselector_3 (.in(multiplexer_2_out), .out(bitselector_3_out), .sel(3'b000));
  BitSelector #(.group(8), .width(64)) bitselector_4 (.in(indirect2), .out(bitselector_4_out), .sel(3'b000));
  Multiplexer #(.select(8), .width(64)) multiplexer_3 (
    .in0(input1), .in1(input2), .in2(input3), .in3(input4), .in4(input5), .in5(input6), .in6(input7),
    .in7(input8), .in8(input9), .in9(input10), .in10(input11), .in11(input12), .in12(input13),
    .in13(input14), .in14(input15), .in15(input16), .in16(input17), .in17(input18), .in18(input19),
    .in19(input20), .in20(input21), .in21(input22), .in22(input23), .in23(input24), .in24(input25),
    .in25(input26), .in26(input27), .in27(input28), .in28(input29), .in29(input30), .in30(input31),
    .in31(input32), .in32(input33), .in33(input34), .in34(input35), .in35(input36), .in36(input37),
    .in37(input38), .in38(input39), .in39(input40), .in40(input41), .in41(input42), .in42(input43),
    .in43(input44), .in44(input45), .in45(input46), .in46(input47), .in47(input48), .in48(input49),
    .in49(input50), .in50(input51), .in51(input52), .in52(input53), .in53(input54), .in54(input55),
    .in55(input56), .in56(input57), .in57(input58), .in58(input59), .in59(input60), .in60(input61),
    .in61(input62), .in62(input63), .in63(input64), .in64(input65), .in65(input66), .in66(input67),
    .in67(input68), .in68(input69), .in69(input70), .in70(input71), .in71(input72), .in72(input73),
    .in73(input74), .in74(input75), .in75(input76), .in76(input77), .in77(input78), .in78(input79),
    .in79(input80), .in80(input81), .in81(input82), .in82(input83), .in83(input84), .in84(input85),
    .in85(input86), .in86(input87), .in87(input88), .in88(input89), .in89(input90), .in90(input91),
    .in91(input92), .in92(input93), .in93(input94), .in94(input95), .in95(input96), .in96(input97),
    .in97(input98), .in98(input99), .in99(input100), .in100(input101), .in101(input102), .in102(input103),
    .in103(input104), .in104(input105), .in105(input106), .in106(input107), .in107(input108),
    .in108(input109), .in109(input110), .in110(input111), .in111(input112), .in112(input113),
    .in113(input114), .in114(input115), .in115(input116), .in116(input117), .in117(input118),
    .in118(input119), .in119(input120), .in120(input121), .in121(input122), .in122(input123),
    .in123(input124), .in124(input125), .in125(input126), .in126(input127), .in127(input128),
    .in128(input129), .in129(input130), .in130(input131), .in131(input132), .in132(input133),
    .in133(input134), .in134(input135), .in135(input136), .in136(input137), .in137(input138),
    .in138(input139), .in139(input140), .in140(input141), .in141(input142), .in142(input143),
    .in143(input144), .in144(input145), .in145(input146), .in146(input147), .in147(input148),
    .in148(input149), .in149(input150), .in150(input151), .in151(input152), .in152(input153),
    .in153(input154), .in154(input155), .in155(input156), .in156(input157), .in157(input158),
    .in158(input159), .in159(input160), .in160(input161), .in161(input162), .in162(input163),
    .in163(input164), .in164(input165), .in165(input166), .in166(input167), .in167(input168),
    .in168(input169), .in169(input170), .in170(input171), .in171(input172), .in172(input173),
    .in173(input174), .in174(input175), .in175(input176), .in176(input177), .in177(input178),
    .in178(input179), .in179(input180), .in180(input181), .in181(input182), .in182(input183),
    .in183(input184), .in184(input185), .in185(input186), .in186(input187), .in187(input188),
    .in188(input189), .in189(input190), .in190(input191), .in191(input192), .in192(input193),
    .in193(input194), .in194(input195), .in195(input196), .in196(input197), .in197(input198),
    .in198(input199), .in199(input200), .in200(input201), .in201(input202), .in202(input203),
    .in203(input204), .in204(input205), .in205(input206), .in206(input207), .in207(input208),
    .in208(input209), .in209(input210), .in210(input211), .in211(input212), .in212(input213),
    .in213(input214), .in214(input215), .in215(input216), .in216(input217), .in217(input218),
    .in218(input219), .in219(input220), .in220(input221), .in221(input222), .in222(input223),
    .in223(input224), .in224(input225), .in225(input226), .in226(input227), .in227(input228),
    .in228(input229), .in229(input230), .in230(input231), .in231(input232), .in232(input233),
    .in233(input234), .in234(input235), .in235(input236), .in236(input237), .in237(input238),
    .in238(input239), .in239(input240), .in240(input241), .in241(input242), .in242(input243),
    .in243(input244), .in244(input245), .in245(input246), .in246(input247), .in247(input248),
    .in248(input249), .in249(input250), .in250(input251), .in251(input252), .in252(input253),
    .in253(input254), .in254(input255), .in255(input256), .out(output1), .sel(bitselector_1_out));
  Multiplexer #(.select(8), .width(64)) multiplexer_4 (
    .in0(input1), .in1(input2), .in2(input3), .in3(input4), .in4(input5), .in5(input6), .in6(input7),
    .in7(input8), .in8(input9), .in9(input10), .in10(input11), .in11(input12), .in12(input13),
    .in13(input14), .in14(input15), .in15(input16), .in16(input17), .in17(input18), .in18(input19),
    .in19(input20), .in20(input21), .in21(input22), .in22(input23), .in23(input24), .in24(input25),
    .in25(input26), .in26(input27), .in27(input28), .in28(input29), .in29(input30), .in30(input31),
    .in31(input32), .in32(input33), .in33(input34), .in34(input35), .in35(input36), .in36(input37),
    .in37(input38), .in38(input39), .in39(input40), .in40(input41), .in41(input42), .in42(input43),
    .in43(input44), .in44(input45), .in45(input46), .in46(input47), .in47(input48), .in48(input49),
    .in49(input50), .in50(input51), .in51(input52), .in52(input53), .in53(input54), .in54(input55),
    .in55(input56), .in56(input57), .in57(input58), .in58(input59), .in59(input60), .in60(input61),
    .in61(input62), .in62(input63), .in63(input64), .in64(input65), .in65(input66), .in66(input67),
    .in67(input68), .in68(input69), .in69(input70), .in70(input71), .in71(input72), .in72(input73),
    .in73(input74), .in74(input75), .in75(input76), .in76(input77), .in77(input78), .in78(input79),
    .in79(input80), .in80(input81), .in81(input82), .in82(input83), .in83(input84), .in84(input85),
    .in85(input86), .in86(input87), .in87(input88), .in88(input89), .in89(input90), .in90(input91),
    .in91(input92), .in92(input93), .in93(input94), .in94(input95), .in95(input96), .in96(input97),
    .in97(input98), .in98(input99), .in99(input100), .in100(input101), .in101(input102), .in102(input103),
    .in103(input104), .in104(input105), .in105(input106), .in106(input107), .in107(input108),
    .in108(input109), .in109(input110), .in110(input111), .in111(input112), .in112(input113),
    .in113(input114), .in114(input115), .in115(input116), .in116(input117), .in117(input118),
    .in118(input119), .in119(input120), .in120(input121), .in121(input122), .in122(input123),
    .in123(input124), .in124(input125), .in125(input126), .in126(input127), .in127(input128),
    .in128(input129), .in129(input130), .in130(input131), .in131(input132), .in132(input133),
    .in133(input134), .in134(input135), .in135(input136), .in136(input137), .in137(input138),
    .in138(input139), .in139(input140), .in140(input141), .in141(input142), .in142(input143),
    .in143(input144), .in144(input145), .in145(input146), .in146(input147), .in147(input148),
    .in148(input149), .in149(input150), .in150(input151), .in151(input152), .in152(input153),
    .in153(input154), .in154(input155), .in155(input156), .in156(input157), .in157(input158),
    .in158(input159), .in159(input160), .in160(input161), .in161(input162), .in162(input163),
    .in163(input164), .in164(input165), .in165(input166), .in166(input167), .in167(input168),
    .in168(input169), .in169(input170), .in170(input171), .in171(input172), .in172(input173),
    .in173(input174), .in174(input175), .in175(input176), .in176(input177), .in177(input178),
    .in178(input179), .in179(input180), .in180(input181), .in181(input182), .in182(input183),
    .in183(input184), .in184(input185), .in185(input186), .in186(input187), .in187(input188),
    .in188(input189), .in189(input190), .in190(input191), .in191(input192), .in192(input193),
    .in193(input194), .in194(input195), .in195(input196), .in196(input197), .in197(input198),
    .in198(input199), .in199(input200), .in200(input201), .in201(input202), .in202(input203),
    .in203(input204), .in204(input205), .in205(input206), .in206(input207), .in207(input208),
    .in208(input209), .in209(input210), .in210(input211), .in211(input212), .in212(input213),
    .in213(input214), .in214(input215), .in215(input216), .in216(input217), .in217(input218),
    .in218(input219), .in219(input220), .in220(input221), .in221(input222), .in222(input223),
    .in223(input224), .in224(input225), .in225(input226), .in226(input227), .in227(input228),
    .in228(input229), .in229(input230), .in230(input231), .in231(input232), .in232(input233),
    .in233(input234), .in234(input235), .in235(input236), .in236(input237), .in237(input238),
    .in238(input239), .in239(input240), .in240(input241), .in241(input242), .in242(input243),
    .in243(input244), .in244(input245), .in245(input246), .in246(input247), .in247(input248),
    .in248(input249), .in249(input250), .in250(input251), .in251(input252), .in252(input253),
    .in253(input254), .in254(input255), .in255(input256), .out(multiplexer_4_out), .sel(bitselector_2_out));
  Multiplexer #(.select(8), .width(64)) multiplexer_5 (
    .in0(input1), .in1(input2), .in2(input3), .in3(input4), .in4(input5), .in5(input6), .in6(input7),
    .in7(input8), .in8(input9), .in9(input10), .in10(input11), .in11(input12), .in12(input13),
    .in13(input14), .in14(input15), .in15(input16), .in16(input17), .in17(input18), .in18(input19),
    .in19(input20), .in20(input21), .in21(input22), .in22(input23), .in23(input24), .in24(input25),
    .in25(input26), .in26(input27), .in27(input28), .in28(input29), .in29(input30), .in30(input31),
    .in31(input32), .in32(input33), .in33(input34), .in34(input35), .in35(input36), .in36(input37),
    .in37(input38), .in38(input39), .in39(input40), .in40(input41), .in41(input42), .in42(input43),
    .in43(input44), .in44(input45), .in45(input46), .in46(input47), .in47(input48), .in48(input49),
    .in49(input50), .in50(input51), .in51(input52), .in52(input53), .in53(input54), .in54(input55),
    .in55(input56), .in56(input57), .in57(input58), .in58(input59), .in59(input60), .in60(input61),
    .in61(input62), .in62(input63), .in63(input64), .in64(input65), .in65(input66), .in66(input67),
    .in67(input68), .in68(input69), .in69(input70), .in70(input71), .in71(input72), .in72(input73),
    .in73(input74), .in74(input75), .in75(input76), .in76(input77), .in77(input78), .in78(input79),
    .in79(input80), .in80(input81), .in81(input82), .in82(input83), .in83(input84), .in84(input85),
    .in85(input86), .in86(input87), .in87(input88), .in88(input89), .in89(input90), .in90(input91),
    .in91(input92), .in92(input93), .in93(input94), .in94(input95), .in95(input96), .in96(input97),
    .in97(input98), .in98(input99), .in99(input100), .in100(input101), .in101(input102), .in102(input103),
    .in103(input104), .in104(input105), .in105(input106), .in106(input107), .in107(input108),
    .in108(input109), .in109(input110), .in110(input111), .in111(input112), .in112(input113),
    .in113(input114), .in114(input115), .in115(input116), .in116(input117), .in117(input118),
    .in118(input119), .in119(input120), .in120(input121), .in121(input122), .in122(input123),
    .in123(input124), .in124(input125), .in125(input126), .in126(input127), .in127(input128),
    .in128(input129), .in129(input130), .in130(input131), .in131(input132), .in132(input133),
    .in133(input134), .in134(input135), .in135(input136), .in136(input137), .in137(input138),
    .in138(input139), .in139(input140), .in140(input141), .in141(input142), .in142(input143),
    .in143(input144), .in144(input145), .in145(input146), .in146(input147), .in147(input148),
    .in148(input149), .in149(input150), .in150(input151), .in151(input152), .in152(input153),
    .in153(input154), .in154(input155), .in155(input156), .in156(input157), .in157(input158),
    .in158(input159), .in159(input160), .in160(input161), .in161(input162), .in162(input163),
    .in163(input164), .in164(input165), .in165(input166), .in166(input167), .in167(input168),
    .in168(input169), .in169(input170), .in170(input171), .in171(input172), .in172(input173),
    .in173(input174), .in174(input175), .in175(input176), .in176(input177), .in177(input178),
    .in178(input179), .in179(input180), .in180(input181), .in181(input182), .in182(input183),
    .in183(input184), .in184(input185), .in185(input186), .in186(input187), .in187(input188),
    .in188(input189), .in189(input190), .in190(input191), .in191(input192), .in192(input193),
    .in193(input194), .in194(input195), .in195(input196), .in196(input197), .in197(input198),
    .in198(input199), .in199(input200), .in200(input201), .in201(input202), .in202(input203),
    .in203(input204), .in204(input205), .in205(input206), .in206(input207), .in207(input208),
    .in208(input209), .in209(input210), .in210(input211), .in211(input212), .in212(input213),
    .in213(input214), .in214(input215), .in215(input216), .in216(input217), .in217(input218),
    .in218(input219), .in219(input220), .in220(input221), .in221(input222), .in222(input223),
    .in223(input224), .in224(input225), .in225(input226), .in226(input227), .in227(input228),
    .in228(input229), .in229(input230), .in230(input231), .in231(input232), .in232(input233),
    .in233(input234), .in234(input235), .in235(input236), .in236(input237), .in237(input238),
    .in238(input239), .in239(input240), .in240(input241), .in241(input242), .in242(input243),
    .in243(input244), .in244(input245), .in245(input246), .in246(input247), .in247(input248),
    .in248(input249), .in249(input250), .in250(input251), .in251(input252), .in252(input253),
    .in253(input254), .in254(input255), .in255(input256), .out(output2), .sel(bitselector_3_out));
  Multiplexer #(.select(8), .width(64)) multiplexer_6 (
    .in0(input1), .in1(input2), .in2(input3), .in3(input4), .in4(input5), .in5(input6), .in6(input7),
    .in7(input8), .in8(input9), .in9(input10), .in10(input11), .in11(input12), .in12(input13),
    .in13(input14), .in14(input15), .in15(input16), .in16(input17), .in17(input18), .in18(input19),
    .in19(input20), .in20(input21), .in21(input22), .in22(input23), .in23(input24), .in24(input25),
    .in25(input26), .in26(input27), .in27(input28), .in28(input29), .in29(input30), .in30(input31),
    .in31(input32), .in32(input33), .in33(input34), .in34(input35), .in35(input36), .in36(input37),
    .in37(input38), .in38(input39), .in39(input40), .in40(input41), .in41(input42), .in42(input43),
    .in43(input44), .in44(input45), .in45(input46), .in46(input47), .in47(input48), .in48(input49),
    .in49(input50), .in50(input51), .in51(input52), .in52(input53), .in53(input54), .in54(input55),
    .in55(input56), .in56(input57), .in57(input58), .in58(input59), .in59(input60), .in60(input61),
    .in61(input62), .in62(input63), .in63(input64), .in64(input65), .in65(input66), .in66(input67),
    .in67(input68), .in68(input69), .in69(input70), .in70(input71), .in71(input72), .in72(input73),
    .in73(input74), .in74(input75), .in75(input76), .in76(input77), .in77(input78), .in78(input79),
    .in79(input80), .in80(input81), .in81(input82), .in82(input83), .in83(input84), .in84(input85),
    .in85(input86), .in86(input87), .in87(input88), .in88(input89), .in89(input90), .in90(input91),
    .in91(input92), .in92(input93), .in93(input94), .in94(input95), .in95(input96), .in96(input97),
    .in97(input98), .in98(input99), .in99(input100), .in100(input101), .in101(input102), .in102(input103),
    .in103(input104), .in104(input105), .in105(input106), .in106(input107), .in107(input108),
    .in108(input109), .in109(input110), .in110(input111), .in111(input112), .in112(input113),
    .in113(input114), .in114(input115), .in115(input116), .in116(input117), .in117(input118),
    .in118(input119), .in119(input120), .in120(input121), .in121(input122), .in122(input123),
    .in123(input124), .in124(input125), .in125(input126), .in126(input127), .in127(input128),
    .in128(input129), .in129(input130), .in130(input131), .in131(input132), .in132(input133),
    .in133(input134), .in134(input135), .in135(input136), .in136(input137), .in137(input138),
    .in138(input139), .in139(input140), .in140(input141), .in141(input142), .in142(input143),
    .in143(input144), .in144(input145), .in145(input146), .in146(input147), .in147(input148),
    .in148(input149), .in149(input150), .in150(input151), .in151(input152), .in152(input153),
    .in153(input154), .in154(input155), .in155(input156), .in156(input157), .in157(input158),
    .in158(input159), .in159(input160), .in160(input161), .in161(input162), .in162(input163),
    .in163(input164), .in164(input165), .in165(input166), .in166(input167), .in167(input168),
    .in168(input169), .in169(input170), .in170(input171), .in171(input172), .in172(input173),
    .in173(input174), .in174(input175), .in175(input176), .in176(input177), .in177(input178),
    .in178(input179), .in179(input180), .in180(input181), .in181(input182), .in182(input183),
    .in183(input184), .in184(input185), .in185(input186), .in186(input187), .in187(input188),
    .in188(input189), .in189(input190), .in190(input191), .in191(input192), .in192(input193),
    .in193(input194), .in194(input195), .in195(input196), .in196(input197), .in197(input198),
    .in198(input199), .in199(input200), .in200(input201), .in201(input202), .in202(input203),
    .in203(input204), .in204(input205), .in205(input206), .in206(input207), .in207(input208),
    .in208(input209), .in209(input210), .in210(input211), .in211(input212), .in212(input213),
    .in213(input214), .in214(input215), .in215(input216), .in216(input217), .in217(input218),
    .in218(input219), .in219(input220), .in220(input221), .in221(input222), .in222(input223),
    .in223(input224), .in224(input225), .in225(input226), .in226(input227), .in227(input228),
    .in228(input229), .in229(input230), .in230(input231), .in231(input232), .in232(input233),
    .in233(input234), .in234(input235), .in235(input236), .in236(input237), .in237(input238),
    .in238(input239), .in239(input240), .in240(input241), .in241(input242), .in242(input243),
    .in243(input244), .in244(input245), .in245(input246), .in246(input247), .in247(input248),
    .in248(input249), .in249(input250), .in250(input251), .in251(input252), .in252(input253),
    .in253(input254), .in254(input255), .in255(input256), .out(multiplexer_6_out), .sel(bitselector_4_out));

  // Other names for the same wires on the sheet: i1[63:0] = input1; i2[63:0] = input2; i3[63:0] = input3;
  //   i4[63:0] = input4; i5[63:0] = input5; i6[63:0] = input6; i7[63:0] = input7; i8[63:0] = input8;
  //   i9[63:0] = input9; i10[63:0] = input10; i11[63:0] = input11; i12[63:0] = input12; i13[63:0] = input13;
  //   i14[63:0] = input14; i15[63:0] = input15; i16[63:0] = input16; i17[63:0] = input17; i18[63:0] = input18;
  //   i19[63:0] = input19; i20[63:0] = input20; i21[63:0] = input21; i22[63:0] = input22; i23[63:0] = input23;
  //   i24[63:0] = input24; i25[63:0] = input25; i26[63:0] = input26; i27[63:0] = input27; i28[63:0] = input28;
  //   i29[63:0] = input29; i30[63:0] = input30; i31[63:0] = input31; i32[63:0] = input32; i33[63:0] = input33;
  //   i34[63:0] = input34; i35[63:0] = input35; i36[63:0] = input36; i37[63:0] = input37; i38[63:0] = input38;
  //   i39[63:0] = input39; i40[63:0] = input40; i41[63:0] = input41; i42[63:0] = input42; i43[63:0] = input43;
  //   i44[63:0] = input44; i45[63:0] = input45; i46[63:0] = input46; i47[63:0] = input47; i48[63:0] = input48;
  //   i49[63:0] = input49; i50[63:0] = input50; i51[63:0] = input51; i52[63:0] = input52; i53[63:0] = input53;
  //   i54[63:0] = input54; i55[63:0] = input55; i56[63:0] = input56; i57[63:0] = input57; i58[63:0] = input58;
  //   i59[63:0] = input59; i60[63:0] = input60; i61[63:0] = input61; i62[63:0] = input62; i63[63:0] = input63;
  //   i64[63:0] = input64; i65[63:0] = input65; i66[63:0] = input66; i67[63:0] = input67; i68[63:0] = input68;
  //   i69[63:0] = input69; i70[63:0] = input70; i71[63:0] = input71; i72[63:0] = input72; i73[63:0] = input73;
  //   i74[63:0] = input74; i75[63:0] = input75; i76[63:0] = input76; i77[63:0] = input77; i78[63:0] = input78;
  //   i79[63:0] = input79; i80[63:0] = input80; i81[63:0] = input81; i82[63:0] = input82; i83[63:0] = input83;
  //   i84[63:0] = input84; i85[63:0] = input85; i86[63:0] = input86; i87[63:0] = input87; i88[63:0] = input88;
  //   i89[63:0] = input89; i90[63:0] = input90; i91[63:0] = input91; i92[63:0] = input92; i93[63:0] = input93;
  //   i94[63:0] = input94; i95[63:0] = input95; i96[63:0] = input96; i97[63:0] = input97; i98[63:0] = input98;
  //   i99[63:0] = input99; i100[63:0] = input100; i101[63:0] = input101; i102[63:0] = input102; i103[63:0] = input103;
  //   i104[63:0] = input104; i105[63:0] = input105; i106[63:0] = input106; i107[63:0] = input107;
  //   i108[63:0] = input108; i109[63:0] = input109; i110[63:0] = input110; i111[63:0] = input111;
  //   i112[63:0] = input112; i113[63:0] = input113; i114[63:0] = input114; i115[63:0] = input115;
  //   i116[63:0] = input116; i117[63:0] = input117; i118[63:0] = input118; i119[63:0] = input119;
  //   i120[63:0] = input120; i121[63:0] = input121; i122[63:0] = input122; i123[63:0] = input123;
  //   i124[63:0] = input124; i125[63:0] = input125; i126[63:0] = input126; i127[63:0] = input127;
  //   i128[63:0] = input128; i129[63:0] = input129; i130[63:0] = input130; i131[63:0] = input131;
  //   i132[63:0] = input132; i133[63:0] = input133; i134[63:0] = input134; i135[63:0] = input135;
  //   i136[63:0] = input136; i137[63:0] = input137; i138[63:0] = input138; i139[63:0] = input139;
  //   i140[63:0] = input140; i141[63:0] = input141; i142[63:0] = input142; i143[63:0] = input143;
  //   i144[63:0] = input144; i145[63:0] = input145; i146[63:0] = input146; i147[63:0] = input147;
  //   i148[63:0] = input148; i149[63:0] = input149; i150[63:0] = input150; i151[63:0] = input151;
  //   i152[63:0] = input152; i153[63:0] = input153; i154[63:0] = input154; i155[63:0] = input155;
  //   i156[63:0] = input156; i157[63:0] = input157; i158[63:0] = input158; i159[63:0] = input159;
  //   i160[63:0] = input160; i161[63:0] = input161; i162[63:0] = input162; i163[63:0] = input163;
  //   i164[63:0] = input164; i165[63:0] = input165; i166[63:0] = input166; i167[63:0] = input167;
  //   i168[63:0] = input168; i169[63:0] = input169; i170[63:0] = input170; i171[63:0] = input171;
  //   i172[63:0] = input172; i173[63:0] = input173; i174[63:0] = input174; i175[63:0] = input175;
  //   i176[63:0] = input176; i177[63:0] = input177; i178[63:0] = input178; i179[63:0] = input179;
  //   i180[63:0] = input180; i181[63:0] = input181; i182[63:0] = input182; i183[63:0] = input183;
  //   i184[63:0] = input184; i185[63:0] = input185; i186[63:0] = input186; i187[63:0] = input187;
  //   i188[63:0] = input188; i189[63:0] = input189; i190[63:0] = input190; i191[63:0] = input191;
  //   i192[63:0] = input192; i193[63:0] = input193; i194[63:0] = input194; i195[63:0] = input195;
  //   i196[63:0] = input196; i197[63:0] = input197; i198[63:0] = input198; i199[63:0] = input199;
  //   i200[63:0] = input200; i201[63:0] = input201; i202[63:0] = input202; i203[63:0] = input203;
  //   i204[63:0] = input204; i205[63:0] = input205; i206[63:0] = input206; i207[63:0] = input207;
  //   i208[63:0] = input208; i209[63:0] = input209; i210[63:0] = input210; i211[63:0] = input211;
  //   i212[63:0] = input212; i213[63:0] = input213; i214[63:0] = input214; i215[63:0] = input215;
  //   i216[63:0] = input216; i217[63:0] = input217; i218[63:0] = input218; i219[63:0] = input219;
  //   i220[63:0] = input220; i221[63:0] = input221; i222[63:0] = input222; i223[63:0] = input223;
  //   i224[63:0] = input224; i225[63:0] = input225; i226[63:0] = input226; i227[63:0] = input227;
  //   i228[63:0] = input228; i229[63:0] = input229; i230[63:0] = input230; i231[63:0] = input231;
  //   i232[63:0] = input232; i233[63:0] = input233; i234[63:0] = input234; i235[63:0] = input235;
  //   i236[63:0] = input236; i237[63:0] = input237; i238[63:0] = input238; i239[63:0] = input239;
  //   i240[63:0] = input240; i241[63:0] = input241; i242[63:0] = input242; i243[63:0] = input243;
  //   i244[63:0] = input244; i245[63:0] = input245; i246[63:0] = input246; i247[63:0] = input247;
  //   i248[63:0] = input248; i249[63:0] = input249; i250[63:0] = input250; i251[63:0] = input251;
  //   i252[63:0] = input252; i253[63:0] = input253; i254[63:0] = input254; i255[63:0] = input255;
  //   i256[63:0] = input256
endmodule
