// Logisim project muxflpalu.circ as structural Verilog: 2 circuits, main circuit main
module main (
);

  wire fpcomparator_1_p3;
  wire [63:0] flpadd64_1_output1, fpadder_1_out;

  // Probe on 64'h400921fb54442d18
  // Probe on 64'h4005bf0a8b145769
  FPAdder #(.fpwidth(64)) fpadder_1 (.a(64'h400921fb54442d18), .b(64'h4005bf0a8b145769), .out(fpadder_1_out));
  flpadd64 flpadd64_1 (.input1(64'h400921fb54442d18), .input2(64'h4005bf0a8b145769), .output1(flpadd64_1_output1));
  // Probe on fpadder_1_out
  // Probe on flpadd64_1_output1
  // FPComparator #(.fpwidth(64)) fpcomparator_1: pin names not known; wires that end beside it: fpadder_1_out, flpadd64_1_output1, fpcomparator_1_p3
  LED led_1 (.in(fpcomparator_1_p3));
endmodule

module flpadd64 (
  input  [63:0] input1,
  input  [63:0] input2,
  output [63:0] output1
);

  wire comparator_1_lt, not_1_out;
  wire [5:0] bitselector_1_out, bitselector_2_out;
  wire [10:0] multiplexer_2_out, subtractor_1_out, subtractor_2_out;
  wire [51:0] bitselector_3_out;
  wire [52:0] adder_1_out, multiplexer_1_out, multiplexer_3_out, multiplexer_4_out, multiplexer_5_out,
       multiplexer_6_out, negator_1_out, negator_2_out, negator_3_out, shifter_1_out, shifter_2_out;
  wire [63:0] undriven, undriven_2;
  wire [63:63] comparator_2_lt;

  // Probe on input1
  // Probe on input2
  BitSelector #(.group(6), .width(11)) bitselector_1 (.in(subtractor_1_out), .out(bitselector_1_out), .sel(1'b0));
  Subtractor #(.width(11)) subtractor_1 (
    .a(undriven[62:52]), .b(undriven_2[62:52]), .out(subtractor_1_out));  // open: bin, bout
  Comparator #(.mode("unsigned"), .width(11)) comparator_1 (
    .a(undriven[62:52]), .b(undriven_2[62:52]), .lt(comparator_1_lt));  // open: gt, eq
  Subtractor #(.width(11)) subtractor_2 (
    .a(undriven_2[62:52]), .b(undriven[62:52]), .out(subtractor_2_out));  // open: bin, bout
  BitSelector #(.group(6), .width(11)) bitselector_2 (.in(subtractor_2_out), .out(bitselector_2_out), .sel(1'b0));
  Shifter #(.shift("lr"), .width(53)) shifter_1 (
    .in({1'b1, undriven[51:0]}), .\dist (bitselector_1_out), .out(shifter_1_out));
  not not_1 (not_1_out, comparator_1_lt);
  Shifter #(.shift("lr"), .width(53)) shifter_2 (
    .in({1'b1, undriven_2[51:0]}), .\dist (bitselector_2_out), .out(shifter_2_out));
  Multiplexer #(.width(53)) multiplexer_1 (
    .in0({1'b1, undriven[51:0]}), .in1(shifter_1_out), .out(multiplexer_1_out), .sel(not_1_out));
  Negator #(.width(53)) negator_1 (.in(multiplexer_1_out), .out(negator_1_out));
  Multiplexer #(.width(11)) multiplexer_2 (
    .in0(undriven[62:52]), .in1(undriven_2[62:52]), .out(multiplexer_2_out), .sel(comparator_1_lt));
  Multiplexer #(.width(53)) multiplexer_3 (
    .in0(shifter_2_out), .in1({1'b1, undriven_2[51:0]}), .out(multiplexer_3_out), .sel(comparator_1_lt));
  Multiplexer #(.width(53)) multiplexer_4 (
    .in0(multiplexer_1_out), .in1(negator_1_out), .out(multiplexer_4_out), .sel(undriven[63]));
  Multiplexer #(.width(53)) multiplexer_5 (
    .in0(multiplexer_3_out), .in1(negator_2_out), .out(multiplexer_5_out), .sel(undriven_2[63]));
  Negator #(.width(53)) negator_2 (.in(multiplexer_3_out), .out(negator_2_out));
  Adder #(.width(53)) adder_1 (.a(multiplexer_4_out), .b(multiplexer_5_out), .out(adder_1_out));  // open: cin, cout
  Negator #(.width(53)) negator_3 (.in(adder_1_out), .out(negator_3_out));
  Comparator #(.mode("unsigned"), .width(53)) comparator_2 (
    .a(adder_1_out), .b({53{1'b0}}), .lt(comparator_2_lt[63]));  // open: gt, eq
  Multiplexer #(.width(53)) multiplexer_6 (
    .in0(adder_1_out), .in1(negator_3_out), .out(multiplexer_6_out), .sel(comparator_2_lt[63]));
  BitSelector #(.group(52), .width(53)) bitselector_3 (.in(multiplexer_6_out), .out(bitselector_3_out), .sel(1'b0));
  // Probe on 64'h40177082efac4240

  assign output1 = 64'h40177082efac4240;
endmodule
