// Logisim project muxrisccore.circ as structural Verilog: 2 circuits, main circuit core
module core (
);

  wire alu_1_we, and_1_out, and_2_out, and_3_out, and_4_out, and_5_out, and_6_out, and_8_out, and_9_out,
       and_11_out, and_12_out, and_14_out, and_15_out, and_16_out, and_17_out, and_18_out, and_20_out,
       and_21_out, and_23_out, and_24_out, and_26_out, and_27_out, and_29_out, and_30_out, and_31_out,
       and_32_out, cart1_p29, clock_1_out, clock_3_out, clock_5_out, clock_6_out, clock_9_out, clock_10_out,
       clock_12_out, clock_13_out, clock_15_out, clock_16_out, clock_18_out, clock_20_out, clock_22_out,
       clock_23_out, clock_25_out, clock_26_out, clock_28_out, clock_29_out, clock_30_out, clock_32_out,
       clock_33_out, comparator_1_eq, comparator_2_gt, comparator_3_eq, comparator_4_eq, comparator_5_eq,
       comparator_6_eq, comparator_7_eq, comparator_8_eq, comparator_9_eq, comparator_10_eq,
       comparator_11_eq, comparator_12_eq, comparator_13_eq, comparator_14_eq, comparator_15_eq,
       comparator_16_eq, comparator_17_eq, comparator_18_eq, comparator_19_eq, comparator_20_eq,
       comparator_21_eq, comparator_22_eq, comparator_22_gt, comparator_22_lt, comparator_23_eq,
       comparator_24_eq, comparator_25_eq, comparator_26_eq, comparator_27_eq, comparator_28_eq,
       comparator_29_eq, comparator_30_eq, comparator_31_eq, comparator_31_gt, comparator_31_lt,
       comparator_32_eq, not_1_out, not_2_out, not_3_out, not_4_out, not_5_out, not_6_out, not_7_out,
       not_8_out, not_9_out, not_10_out, not_11_out, not_12_out, not_13_out, not_14_out, not_15_out,
       or_1_out, or_2_out, or_4_out, random_1_p1, random_1_p2, random_2_p1, random_2_p2, random_3_p1,
       random_3_p2, random_4_p1, random_5_p1, random_5_p2, random_6_p1, random_6_p2, random_7_p1,
       random_7_p2, random_8_p1, random_8_p2, register_1_q, regX_p2, regX_p11, rgb_video_1_p1;
  wire [1:0] bitselector_30_out, bitselector_35_out;
  wire [2:0] bitselector_15_out, bitselector_16_out, bitselector_17_out, bitselector_18_out,
       bitselector_19_out, bitselector_20_out, bitselector_21_out, bitselector_22_out;
  wire [3:0] bitselector_7_out, bitselector_8_out, bitselector_12_out, bitselector_13_out;
  wire [7:0] bitselector_5_out, bitselector_6_out, bitselector_11_out, bitselector_14_out,
       bitselector_25_out, bitselector_27_out, bitselector_29_out;
  wire [8:0] bitselector_31_out, bitselector_33_out;
  wire [15:0] bitselector_1_out, bitselector_2_out, bitselector_3_out, bitselector_4_out, bitselector_10_out,
       bitselector_23_out, bitselector_24_out, bitselector_26_out;
  wire [17:0] bitselector_32_out;
  wire [23:0] bitselector_34_out, bitselector_37_out, ram1_p2;
  wire [31:0] bitselector_9_out, counter_1_q;
  wire [63:0] alu_1_outx, alu_2_outx, alu_3_outx, alu_4_outx, alu_5_outx, alu_6_outx, alu_7_outx, alu_8_outx,
       cart1_p31, cart1_p32, cart1_p33, cart1_p34, cart1_p35, cart1_p36, cart1_p37, cart1_p38, cart1_p39,
       counter_2_q, counter_3_q, counter_4_q, counter_5_q, counter_6_q, counter_7_q, counter_8_q,
       counter_9_q, counter_10_q, counter_11_q, counter_12_q, counter_13_q, counter_14_q, counter_15_q,
       counter_16_q, counter_17_q, counter_18_q, multiplexer_2_out, multiplexer_3_out, multiplexer_4_out,
       multiplexer_6_out, multiplexer_7_out, multiplexer_8_out, multiplexer_11_out, multiplexer_12_out,
       multiplexer_13_out, multiplexer_15_out, multiplexer_17_out, multiplexer_18_out, multiplexer_20_out,
       multiplexer_21_out, multiplexer_22_out, multiplexer_24_out, multiplexer_25_out, multiplexer_26_out,
       multiplexer_27_out, multiplexer_28_out, multiplexer_29_out, multiplexer_30_out, multiplexer_31_out,
       multiplexer_32_out, multiplexer_33_out, multiplexer_34_out, ram1_p3, regX_p12, regX_p13, regX_p14,
       regX_p15, regX_p16, regX_p17, regX_p18, regX_p19, regX_p20, regX_p21, regX_p22, regX_p23, regX_p24,
       regX_p25, regX_p26, regX_p27, regY_p10, regY_p11, regY_p12, regY_p13, regY_p14, regY_p15, regY_p16,
       regY_p17, regZ_p10, regZ_p11, regZ_p12, regZ_p13, regZ_p14, regZ_p15, regZ_p16, regZ_p17, rom1_p9,
       rom1_p10, rom1_p11, rom1_p12, rom1_p13, rom1_p14, rom1_p15, rom1_p16, undriven, undriven_2,
       undriven_3, undriven_4, undriven_5, undriven_6, undriven_7, undriven_8;

  BitSelector #(.group(16), .width(64)) bitselector_1 (.in(multiplexer_26_out), .out(bitselector_1_out), .sel(2'b11));
  BitSelector #(.group(16), .width(64)) bitselector_2 (.in(multiplexer_26_out), .out(bitselector_2_out), .sel(2'b10));
  BitSelector #(.group(16), .width(64)) bitselector_3 (.in(multiplexer_26_out), .out(bitselector_3_out), .sel(2'b01));
  BitSelector #(.group(16), .width(64)) bitselector_4 (.in(multiplexer_26_out), .out(bitselector_4_out), .sel(2'b00));
  BitSelector #(.group(8), .width(16)) bitselector_5 (.in(bitselector_4_out), .out(bitselector_5_out), .sel(1'b1));
  BitSelector #(.group(8), .width(16)) bitselector_6 (.in(bitselector_4_out), .out(bitselector_6_out), .sel(1'b0));
  BitSelector #(.group(4)) bitselector_7 (.in(bitselector_6_out), .out(bitselector_7_out), .sel(1'b0));
  BitSelector #(.group(4)) bitselector_8 (.in(bitselector_6_out), .out(bitselector_8_out), .sel(1'b1));
  BitSelector #(.group(32), .width(64)) bitselector_9 (.in(regY_p10), .out(bitselector_9_out), .sel(1'b0));
  BitSelector #(.group(16), .width(64)) bitselector_10 (.in(regY_p10), .out(bitselector_10_out), .sel(2'b00));
  BitSelector #(.group(8), .width(64)) bitselector_11 (.in(regY_p10), .out(bitselector_11_out), .sel(3'b000));
  Comparator #(.mode("unsigned")) comparator_1 (
    .a(bitselector_6_out), .b(8'he0), .eq(comparator_1_eq));  // open: gt, lt
  BitSelector #(.group(4)) bitselector_12 (.in(bitselector_6_out), .out(bitselector_12_out), .sel(1'b0));
  BitSelector #(.group(4)) bitselector_13 (.in(bitselector_6_out), .out(bitselector_13_out), .sel(1'b1));
  Comparator #(.mode("unsigned"), .width(4)) comparator_2 (
    .a(bitselector_7_out), .b(4'b0000), .gt(comparator_2_gt));  // open: eq, lt
  Comparator #(.mode("unsigned")) comparator_3 (
    .a(bitselector_6_out), .b({8{1'b0}}), .eq(comparator_3_eq));  // open: gt, lt
  Counter #(.max('hffffffff), .width(32)) counter_1 (
    .load(or_1_out), .D({32{1'b0}}), .count(comparator_3_eq), .Q(counter_1_q), .clk(clock_1_out));  // open: carry, up, clr
  Clock clock_1 (.out(clock_1_out));
  Comparator #(.mode("unsigned")) comparator_4 (
    .a(bitselector_6_out), .b(8'h10), .eq(comparator_4_eq));  // open: gt, lt
  Comparator #(.mode("unsigned")) comparator_5 (
    .a(bitselector_6_out), .b(8'h20), .eq(comparator_5_eq));  // open: gt, lt
  Comparator #(.mode("unsigned"), .width(64)) comparator_6 (
    .a(regY_p10), .b({64{1'b0}}), .eq(comparator_6_eq));  // open: gt, lt
  Comparator #(.mode("unsigned")) comparator_7 (
    .a(bitselector_6_out), .b(8'h30), .eq(comparator_7_eq));  // open: gt, lt
  Comparator #(.mode("unsigned"), .width(32)) comparator_8 (
    .a(bitselector_9_out), .b({32{1'b0}}), .eq(comparator_8_eq));  // open: gt, lt
  Comparator #(.mode("unsigned")) comparator_9 (
    .a(bitselector_6_out), .b(8'h40), .eq(comparator_9_eq));  // open: gt, lt
  Comparator #(.mode("unsigned"), .width(16)) comparator_10 (
    .a(bitselector_10_out), .b({16{1'b0}}), .eq(comparator_10_eq));  // open: gt, lt
  Comparator #(.mode("unsigned")) comparator_11 (
    .a(bitselector_6_out), .b(8'h50), .eq(comparator_11_eq));  // open: gt, lt
  Comparator #(.mode("unsigned")) comparator_12 (
    .a(bitselector_11_out), .b({8{1'b0}}), .eq(comparator_12_eq));  // open: gt, lt
  Comparator #(.mode("unsigned")) comparator_13 (
    .a(bitselector_6_out), .b(8'h60), .eq(comparator_13_eq));  // open: gt, lt
  Comparator #(.mode("unsigned")) comparator_14 (
    .a(bitselector_6_out), .b(8'h70), .eq(comparator_14_eq));  // open: gt, lt
  Comparator #(.mode("unsigned")) comparator_15 (
    .a(bitselector_6_out), .b(8'h80), .eq(comparator_15_eq));  // open: gt, lt
  Comparator #(.mode("unsigned")) comparator_16 (
    .a(bitselector_6_out), .b(8'h90), .eq(comparator_16_eq));  // open: gt, lt
  Comparator #(.mode("unsigned")) comparator_17 (
    .a(bitselector_6_out), .b(8'ha0), .eq(comparator_17_eq));  // open: gt, lt
  Comparator #(.mode("unsigned")) comparator_18 (
    .a(bitselector_6_out), .b(8'hb0), .eq(comparator_18_eq));  // open: gt, lt
  Comparator #(.mode("unsigned")) comparator_19 (
    .a(bitselector_6_out), .b(8'hc0), .eq(comparator_19_eq));  // open: gt, lt
  Comparator #(.mode("unsigned")) comparator_20 (
    .a(bitselector_6_out), .b(8'hd0), .eq(comparator_20_eq));  // open: gt, lt
  Comparator #(.mode("unsigned")) comparator_21 (
    .a(bitselector_6_out), .b(8'hf0), .eq(comparator_21_eq));  // open: gt, lt
  Comparator #(.mode("unsigned"), .width(32)) comparator_22 (
    .a(counter_1_q), .b({bitselector_2_out, bitselector_3_out}), .gt(comparator_22_gt),
    .eq(comparator_22_eq), .lt(comparator_22_lt));
  and and_1 (and_1_out, comparator_5_eq, not_1_out);
  not not_1 (not_1_out, comparator_6_eq);
  and and_2 (and_2_out, comparator_7_eq, not_2_out);
  not not_2 (not_2_out, comparator_8_eq);
  and and_3 (and_3_out, comparator_9_eq, not_3_out);
  not not_3 (not_3_out, comparator_10_eq);
  and and_4 (and_4_out, comparator_11_eq, not_4_out);
  not not_4 (not_4_out, comparator_12_eq);
  BitSelector #(.group(8), .width(16)) bitselector_14 (.in(bitselector_3_out), .out(bitselector_14_out), .sel(1'b0));
  // RAM #(.addrWidth(16), .dataWidth(64), .enables("line"), .line("octo"), .misaligned("true")) regX: pin names not known; wires that end beside it: bitselector_1_out, regX_p2, regX_p2, bitselector_5_out[1], bitselector_5_out[2], bitselector_5_out[3], bitselector_5_out[4], bitselector_5_out[5], bitselector_5_out[6], bitselector_5_out[7], regX_p11, regX_p12, regX_p13, regX_p14, regX_p15, regX_p16, regX_p17, regX_p18, regX_p19, regX_p20, regX_p21, regX_p22, regX_p23, regX_p24, regX_p25, regX_p26, regX_p27
  Clock clock_2 (.out(regX_p11));
  or or_1 (or_1_out, comparator_22_gt, comparator_22_eq);
  and and_5 (and_5_out, comparator_22_lt, comparator_3_eq);
  or or_2 (or_2_out, comparator_4_eq, and_1_out, and_2_out, and_3_out, and_4_out);
  or or_3 (regX_p2, comparator_13_eq, comparator_14_eq, comparator_15_eq, comparator_16_eq, comparator_17_eq, comparator_18_eq, comparator_19_eq, comparator_20_eq, comparator_1_eq, alu_1_we);
  BitSelector #(.group(3), .width(64)) bitselector_15 (.in(regY_p10), .out(bitselector_15_out), .sel({5{1'b0}}));
  Multiplexer #(.width(64)) multiplexer_1 (
    .in0(multiplexer_2_out), .in1(alu_1_outx), .out(regX_p12), .sel(comparator_2_gt));
  Multiplexer #(.select(4), .width(64)) multiplexer_2 (
    .in6({{32{1'b0}}, bitselector_2_out, bitselector_3_out}),
    .in7({bitselector_2_out, bitselector_3_out, bitselector_2_out, bitselector_3_out}),
    .in8({bitselector_3_out, bitselector_3_out, bitselector_3_out, bitselector_3_out}),
    .in9({bitselector_14_out, bitselector_14_out, bitselector_14_out, bitselector_14_out, bitselector_14_out, bitselector_14_out, bitselector_14_out, bitselector_14_out}),
    .in10(counter_2_q), .in11(undriven), .in12(multiplexer_3_out), .in13(counter_3_q),
    .in14(multiplexer_27_out), .out(multiplexer_2_out), .sel(bitselector_8_out));  // open: in0, in1, in2, in3, in4, in5, in15
  not not_5 (not_5_out, comparator_23_eq);
  Comparator #(.width(64)) comparator_23 (.a({64{1'b0}}), .b(regZ_p10), .eq(comparator_23_eq));  // open: gt, lt
  and and_6 (and_6_out, not_5_out, comparator_17_eq);
  Counter #(.max('hffffffffffffffff), .width(64)) counter_2 (
    .load(and_6_out), .D(regY_p10), .Q(counter_2_q), .clk(clock_3_out));  // open: count, carry, up, clr
  Clock clock_3 (.out(clock_3_out));
  // Random #(.seed(12345667), .width(64)) random_1: pin names not known; wires that end beside it: random_1_p1, random_1_p2
  Clock clock_4 (.out(random_1_p1));
  and and_7 (random_1_p2, not_5_out, comparator_18_eq);
  Multiplexer #(.select(3), .width(64)) multiplexer_3 (
    .in0({64{1'b0}}), .in1(64'h1), .in2(64'h65536), .in3(64'h1000000), .in4(64'h200), .in5(64'h200),
    .in6(64'h12a05f200), .in7({64{1'b0}}), .out(multiplexer_3_out), .sel(bitselector_15_out));
  and and_8 (and_8_out, not_5_out, comparator_20_eq);
  Counter #(.max('hffffffffffffffff), .width(64)) counter_3 (
    .load(and_8_out), .D(regY_p10), .Q(counter_3_q), .clk(clock_5_out));  // open: count, carry, up, clr
  Clock #(.lowDuration(9)) clock_5 (.out(clock_5_out));
  alu alu_1 (
    .argX(regX_p20), .argY(regY_p10), .argZ(regZ_p10), .op(bitselector_12_out), .\var (bitselector_13_out),
    .outX(alu_1_outx), .we(alu_1_we));
  Comparator #(.width(64)) comparator_24 (.a({64{1'b0}}), .b(regZ_p11), .eq(comparator_24_eq));  // open: gt, lt
  and and_9 (and_9_out, not_6_out, comparator_17_eq);
  Clock clock_6 (.out(clock_6_out));
  // Random #(.seed(12345668), .width(64)) random_2: pin names not known; wires that end beside it: random_2_p1, random_2_p2
  Clock clock_7 (.out(random_2_p1));
  and and_10 (random_2_p2, not_6_out, comparator_18_eq);
  BitSelector #(.group(3), .width(64)) bitselector_16 (.in(regY_p11), .out(bitselector_16_out), .sel({5{1'b0}}));
  Multiplexer #(.select(3), .width(64)) multiplexer_4 (
    .in0({64{1'b0}}), .in1(64'h1), .in2(64'h65536), .in3(64'h1000000), .in4(64'h200), .in5(64'h200),
    .in6(64'h12a05f200), .in7({64{1'b0}}), .out(multiplexer_4_out), .sel(bitselector_16_out));
  and and_11 (and_11_out, not_6_out, comparator_20_eq);
  alu alu_2 (
    .argX(regX_p21), .argY(regY_p11), .argZ(regZ_p11), .op(bitselector_12_out), .\var (bitselector_13_out),
    .outX(alu_2_outx));  // open: we
  // DualRAM #(.addrWidth(16), .dataWidth(64), .enables("line"), .line("octo"), .misaligned("true"), .\type ("nonvolatile")) regY: pin names not known; wires that end beside it: bitselector_2_out, bitselector_1_out, regX_p2, regX_p2, bitselector_5_out[1], bitselector_5_out[2], bitselector_5_out[3], bitselector_5_out[4], bitselector_5_out[5], regY_p10, regY_p11, regY_p12, regY_p13, regY_p14, regY_p15, regY_p16, regY_p17
  Clock clock_8 ();  // open: out
  Multiplexer #(.width(64)) multiplexer_5 (
    .in0(multiplexer_6_out), .in1(alu_2_outx), .out(regX_p13), .sel(comparator_2_gt));
  Multiplexer #(.select(4), .width(64)) multiplexer_6 (
    .in6({{32{1'b0}}, bitselector_2_out, bitselector_3_out}),
    .in7({bitselector_2_out, bitselector_3_out, bitselector_2_out, bitselector_3_out}),
    .in8({bitselector_3_out, bitselector_3_out, bitselector_3_out, bitselector_3_out}),
    .in9({bitselector_14_out, bitselector_14_out, bitselector_14_out, bitselector_14_out, bitselector_14_out, bitselector_14_out, bitselector_14_out, bitselector_14_out}),
    .in10(counter_4_q), .in11(undriven_2), .in12(multiplexer_4_out), .in13(counter_5_q),
    .in14(multiplexer_28_out), .out(multiplexer_6_out), .sel(bitselector_8_out));  // open: in0, in1, in2, in3, in4, in5, in15
  not not_6 (not_6_out, comparator_24_eq);
  Counter #(.max('hffffffffffffffff), .width(64)) counter_4 (
    .load(and_9_out), .D(regY_p11), .Q(counter_4_q), .clk(clock_6_out));  // open: count, carry, up, clr
  Counter #(.max('hffffffffffffffff), .width(64)) counter_5 (
    .load(and_11_out), .D(regY_p11), .Q(counter_5_q), .clk(clock_9_out));  // open: count, carry, up, clr
  Clock #(.lowDuration(9)) clock_9 (.out(clock_9_out));
  Multiplexer #(.select(4), .width(64)) multiplexer_7 (
    .in6({{32{1'b0}}, bitselector_2_out, bitselector_3_out}),
    .in7({bitselector_2_out, bitselector_3_out, bitselector_2_out, bitselector_3_out}),
    .in8({bitselector_3_out, bitselector_3_out, bitselector_3_out, bitselector_3_out}),
    .in9({bitselector_14_out, bitselector_14_out, bitselector_14_out, bitselector_14_out, bitselector_14_out, bitselector_14_out, bitselector_14_out, bitselector_14_out}),
    .in10(counter_6_q), .in11(undriven_3), .in12(multiplexer_8_out), .in13(counter_7_q),
    .in14(multiplexer_29_out), .out(multiplexer_7_out), .sel(bitselector_8_out));  // open: in0, in1, in2, in3, in4, in5, in15
  not not_7 (not_7_out, comparator_25_eq);
  Comparator #(.width(64)) comparator_25 (.a({64{1'b0}}), .b(regZ_p12), .eq(comparator_25_eq));  // open: gt, lt
  and and_12 (and_12_out, not_7_out, comparator_17_eq);
  Counter #(.max('hffffffffffffffff), .width(64)) counter_6 (
    .load(and_12_out), .D(regY_p12), .Q(counter_6_q), .clk(clock_10_out));  // open: count, carry, up, clr
  Clock clock_10 (.out(clock_10_out));
  // Random #(.seed(12345669), .width(64)) random_3: pin names not known; wires that end beside it: random_3_p1, random_3_p2
  Clock clock_11 (.out(random_3_p1));
  and and_13 (random_3_p2, not_7_out, comparator_18_eq);
  BitSelector #(.group(3), .width(64)) bitselector_17 (.in(regY_p12), .out(bitselector_17_out), .sel({5{1'b0}}));
  Multiplexer #(.select(3), .width(64)) multiplexer_8 (
    .in0({64{1'b0}}), .in1(64'h1), .in2(64'h65536), .in3(64'h1000000), .in4(64'h200), .in5(64'h200),
    .in6(64'h12a05f200), .in7({64{1'b0}}), .out(multiplexer_8_out), .sel(bitselector_17_out));
  and and_14 (and_14_out, not_7_out, comparator_20_eq);
  Counter #(.max('hffffffffffffffff), .width(64)) counter_7 (
    .load(and_14_out), .D(regY_p12), .Q(counter_7_q), .clk(clock_12_out));  // open: count, carry, up, clr
  Clock #(.lowDuration(9)) clock_12 (.out(clock_12_out));
  alu alu_3 (
    .argX(regX_p22), .argY(regY_p12), .argZ(regZ_p12), .op(bitselector_12_out), .\var (bitselector_13_out),
    .outX(alu_3_outx));  // open: we
  Multiplexer #(.width(64)) multiplexer_9 (
    .in0(multiplexer_7_out), .in1(alu_3_outx), .out(regX_p14), .sel(comparator_2_gt));
  and and_15 (and_15_out, not_8_out, comparator_17_eq);
  and and_16 (and_16_out, not_8_out, comparator_18_eq);
  BitSelector #(.group(3), .width(64)) bitselector_18 (.in(regY_p13), .out(bitselector_18_out), .sel({5{1'b0}}));
  and and_17 (and_17_out, not_8_out, comparator_20_eq);
  alu alu_4 (
    .argX(regX_p23), .argY(regY_p13), .argZ(regZ_p13), .op(bitselector_12_out), .\var (bitselector_13_out),
    .outX(alu_4_outx));  // open: we
  Multiplexer #(.width(64)) multiplexer_10 (
    .in0(multiplexer_11_out), .in1(alu_4_outx), .out(regX_p15), .sel(comparator_2_gt));
  Multiplexer #(.select(4), .width(64)) multiplexer_11 (
    .in6({{32{1'b0}}, bitselector_2_out, bitselector_3_out}),
    .in7({bitselector_2_out, bitselector_3_out, bitselector_2_out, bitselector_3_out}),
    .in8({bitselector_3_out, bitselector_3_out, bitselector_3_out, bitselector_3_out}),
    .in9({bitselector_14_out, bitselector_14_out, bitselector_14_out, bitselector_14_out, bitselector_14_out, bitselector_14_out, bitselector_14_out, bitselector_14_out}),
    .in10(counter_8_q), .in11(undriven_4), .in12(multiplexer_12_out), .in13(counter_9_q),
    .in14(multiplexer_30_out), .out(multiplexer_11_out), .sel(bitselector_8_out));  // open: in0, in1, in2, in3, in4, in5, in15
  not not_8 (not_8_out, comparator_26_eq);
  Comparator #(.width(64)) comparator_26 (.a({64{1'b0}}), .b(regZ_p13), .eq(comparator_26_eq));  // open: gt, lt
  Counter #(.max('hffffffffffffffff), .width(64)) counter_8 (
    .load(and_15_out), .D(regY_p13), .Q(counter_8_q), .clk(clock_13_out));  // open: count, carry, up, clr
  Clock clock_13 (.out(clock_13_out));
  // Random #(.seed(12345670), .width(64)) random_4: pin names not known; wires that end beside it: random_4_p1, and_16_out
  Clock clock_14 (.out(random_4_p1));
  Multiplexer #(.select(3), .width(64)) multiplexer_12 (
    .in0({64{1'b0}}), .in1(64'h1), .in2(64'h65536), .in3(64'h1000000), .in4(64'h200), .in5(64'h200),
    .in6(64'h12a05f200), .in7({64{1'b0}}), .out(multiplexer_12_out), .sel(bitselector_18_out));
  Counter #(.max('hffffffffffffffff), .width(64)) counter_9 (
    .load(and_17_out), .D(regY_p13), .Q(counter_9_q), .clk(clock_15_out));  // open: count, carry, up, clr
  Clock #(.lowDuration(9)) clock_15 (.out(clock_15_out));
  Comparator #(.width(64)) comparator_27 (.a({64{1'b0}}), .b(regZ_p14), .eq(comparator_27_eq));  // open: gt, lt
  and and_18 (and_18_out, not_9_out, comparator_17_eq);
  Clock clock_16 (.out(clock_16_out));
  // Random #(.seed(12345671), .width(64)) random_5: pin names not known; wires that end beside it: random_5_p1, random_5_p2
  Clock clock_17 (.out(random_5_p1));
  and and_19 (random_5_p2, not_9_out, comparator_18_eq);
  BitSelector #(.group(3), .width(64)) bitselector_19 (.in(regY_p14), .out(bitselector_19_out), .sel({5{1'b0}}));
  Multiplexer #(.select(3), .width(64)) multiplexer_13 (
    .in0({64{1'b0}}), .in1(64'h1), .in2(64'h65536), .in3(64'h1000000), .in4(64'h200), .in5(64'h200),
    .in6(64'h12a05f200), .in7({64{1'b0}}), .out(multiplexer_13_out), .sel(bitselector_19_out));
  and and_20 (and_20_out, not_9_out, comparator_20_eq);
  Clock #(.lowDuration(9)) clock_18 (.out(clock_18_out));
  alu alu_5 (
    .argX(regX_p24), .argY(regY_p14), .argZ(regZ_p14), .op(bitselector_12_out), .\var (bitselector_13_out),
    .outX(alu_5_outx));  // open: we
  // DualRAM #(.addrWidth(16), .dataWidth(64), .enables("line"), .line("octo"), .misaligned("true"), .\type ("nonvolatile")) regZ: pin names not known; wires that end beside it: bitselector_3_out, bitselector_1_out, regX_p2, regX_p2, bitselector_5_out[1], bitselector_5_out[2], bitselector_5_out[3], bitselector_5_out[4], bitselector_5_out[5], regZ_p10, regZ_p11, regZ_p12, regZ_p13, regZ_p14, regZ_p15, regZ_p16, regZ_p17
  Clock clock_19 ();  // open: out
  Multiplexer #(.width(64)) multiplexer_14 (
    .in0(multiplexer_15_out), .in1(alu_5_outx), .out(regX_p16), .sel(comparator_2_gt));
  Multiplexer #(.select(4), .width(64)) multiplexer_15 (
    .in6({{32{1'b0}}, bitselector_2_out, bitselector_3_out}),
    .in7({bitselector_2_out, bitselector_3_out, bitselector_2_out, bitselector_3_out}),
    .in8({bitselector_3_out, bitselector_3_out, bitselector_3_out, bitselector_3_out}),
    .in9({bitselector_14_out, bitselector_14_out, bitselector_14_out, bitselector_14_out, bitselector_14_out, bitselector_14_out, bitselector_14_out, bitselector_14_out}),
    .in10(counter_10_q), .in11(undriven_5), .in12(multiplexer_13_out), .in13(counter_11_q),
    .in14(multiplexer_31_out), .out(multiplexer_15_out), .sel(bitselector_8_out));  // open: in0, in1, in2, in3, in4, in5, in15
  not not_9 (not_9_out, comparator_27_eq);
  Counter #(.max('hffffffffffffffff), .width(64)) counter_10 (
    .load(and_18_out), .D(regY_p14), .Q(counter_10_q), .clk(clock_16_out));  // open: count, carry, up, clr
  Counter #(.max('hffffffffffffffff), .width(64)) counter_11 (
    .load(and_20_out), .D(regY_p14), .Q(counter_11_q), .clk(clock_18_out));  // open: count, carry, up, clr
  BitSelector #(.group(3), .width(64)) bitselector_20 (.in(regY_p15), .out(bitselector_20_out), .sel({5{1'b0}}));
  Multiplexer #(.width(64)) multiplexer_16 (
    .in0(multiplexer_17_out), .in1(alu_6_outx), .out(regX_p17), .sel(comparator_2_gt));
  Multiplexer #(.select(4), .width(64)) multiplexer_17 (
    .in6({{32{1'b0}}, bitselector_2_out, bitselector_3_out}),
    .in7({bitselector_2_out, bitselector_3_out, bitselector_2_out, bitselector_3_out}),
    .in8({bitselector_3_out, bitselector_3_out, bitselector_3_out, bitselector_3_out}),
    .in9({bitselector_14_out, bitselector_14_out, bitselector_14_out, bitselector_14_out, bitselector_14_out, bitselector_14_out, bitselector_14_out, bitselector_14_out}),
    .in10(counter_12_q), .in11(undriven_6), .in12(multiplexer_18_out), .in13(counter_13_q),
    .in14(multiplexer_32_out), .out(multiplexer_17_out), .sel(bitselector_8_out));  // open: in0, in1, in2, in3, in4, in5, in15
  not not_10 (not_10_out, comparator_28_eq);
  Comparator #(.width(64)) comparator_28 (.a({64{1'b0}}), .b(regZ_p15), .eq(comparator_28_eq));  // open: gt, lt
  and and_21 (and_21_out, not_10_out, comparator_17_eq);
  Counter #(.max('hffffffffffffffff), .width(64)) counter_12 (
    .load(and_21_out), .D(regY_p15), .Q(counter_12_q), .clk(clock_20_out));  // open: count, carry, up, clr
  Clock clock_20 (.out(clock_20_out));
  // Random #(.seed(12345672), .width(64)) random_6: pin names not known; wires that end beside it: random_6_p1, random_6_p2
  Clock clock_21 (.out(random_6_p1));
  and and_22 (random_6_p2, not_10_out, comparator_18_eq);
  Multiplexer #(.select(3), .width(64)) multiplexer_18 (
    .in0({64{1'b0}}), .in1(64'h1), .in2(64'h65536), .in3(64'h1000000), .in4(64'h200), .in5(64'h200),
    .in6(64'h12a05f200), .in7({64{1'b0}}), .out(multiplexer_18_out), .sel(bitselector_20_out));
  and and_23 (and_23_out, not_10_out, comparator_20_eq);
  Counter #(.max('hffffffffffffffff), .width(64)) counter_13 (
    .load(and_23_out), .D(regY_p15), .Q(counter_13_q), .clk(clock_22_out));  // open: count, carry, up, clr
  Clock #(.lowDuration(9)) clock_22 (.out(clock_22_out));
  alu alu_6 (
    .argX(regX_p25), .argY(regY_p15), .argZ(regZ_p15), .op(bitselector_12_out), .\var (bitselector_13_out),
    .outX(alu_6_outx));  // open: we
  Comparator #(.width(64)) comparator_29 (.a({64{1'b0}}), .b(regZ_p16), .eq(comparator_29_eq));  // open: gt, lt
  and and_24 (and_24_out, not_11_out, comparator_17_eq);
  // Random #(.seed(12345673), .width(64)) random_7: pin names not known; wires that end beside it: random_7_p1, random_7_p2
  and and_25 (random_7_p2, not_11_out, comparator_18_eq);
  BitSelector #(.group(3), .width(64)) bitselector_21 (.in(regY_p16), .out(bitselector_21_out), .sel({5{1'b0}}));
  and and_26 (and_26_out, not_11_out, comparator_20_eq);
  alu alu_7 (
    .argX(regX_p26), .argY(regY_p16), .argZ(regZ_p16), .op(bitselector_12_out), .\var (bitselector_13_out),
    .outX(alu_7_outx));  // open: we
  Multiplexer #(.width(64)) multiplexer_19 (
    .in0(multiplexer_20_out), .in1(alu_7_outx), .out(regX_p18), .sel(comparator_2_gt));
  Multiplexer #(.select(4), .width(64)) multiplexer_20 (
    .in6({{32{1'b0}}, bitselector_2_out, bitselector_3_out}),
    .in7({bitselector_2_out, bitselector_3_out, bitselector_2_out, bitselector_3_out}),
    .in8({bitselector_3_out, bitselector_3_out, bitselector_3_out, bitselector_3_out}),
    .in9({bitselector_14_out, bitselector_14_out, bitselector_14_out, bitselector_14_out, bitselector_14_out, bitselector_14_out, bitselector_14_out, bitselector_14_out}),
    .in10(counter_14_q), .in11(undriven_7), .in12(multiplexer_21_out), .in13(counter_15_q),
    .in14(multiplexer_33_out), .out(multiplexer_20_out), .sel(bitselector_8_out));  // open: in0, in1, in2, in3, in4, in5, in15
  not not_11 (not_11_out, comparator_29_eq);
  Counter #(.max('hffffffffffffffff), .width(64)) counter_14 (
    .load(and_24_out), .D(regY_p16), .Q(counter_14_q), .clk(clock_23_out));  // open: count, carry, up, clr
  Clock clock_23 (.out(clock_23_out));
  Clock clock_24 (.out(random_7_p1));
  Multiplexer #(.select(3), .width(64)) multiplexer_21 (
    .in0({64{1'b0}}), .in1(64'h1), .in2(64'h65536), .in3(64'h1000000), .in4(64'h200), .in5(64'h200),
    .in6(64'h12a05f200), .in7({64{1'b0}}), .out(multiplexer_21_out), .sel(bitselector_21_out));
  Counter #(.max('hffffffffffffffff), .width(64)) counter_15 (
    .load(and_26_out), .D(regY_p16), .Q(counter_15_q), .clk(clock_25_out));  // open: count, carry, up, clr
  Clock #(.lowDuration(9)) clock_25 (.out(clock_25_out));
  not not_12 (not_12_out, comparator_30_eq);
  Comparator #(.width(64)) comparator_30 (.a({64{1'b0}}), .b(regZ_p17), .eq(comparator_30_eq));  // open: gt, lt
  and and_27 (and_27_out, not_12_out, comparator_17_eq);
  Counter #(.max('hffffffffffffffff), .width(64)) counter_16 (
    .load(and_27_out), .D(regY_p17), .Q(counter_16_q), .clk(clock_26_out));  // open: count, carry, up, clr
  Clock clock_26 (.out(clock_26_out));
  // Random #(.seed(12345674), .width(64)) random_8: pin names not known; wires that end beside it: random_8_p1, random_8_p2
  Clock clock_27 (.out(random_8_p1));
  and and_28 (random_8_p2, not_12_out, comparator_18_eq);
  BitSelector #(.group(3), .width(64)) bitselector_22 (.in(regY_p17), .out(bitselector_22_out), .sel({5{1'b0}}));
  Multiplexer #(.select(3), .width(64)) multiplexer_22 (
    .in0({64{1'b0}}), .in1(64'h1), .in2(64'h65536), .in3(64'h1000000), .in4(64'h200), .in5(64'h200),
    .in6(64'h12a05f200), .in7({64{1'b0}}), .out(multiplexer_22_out), .sel(bitselector_22_out));
  and and_29 (and_29_out, not_12_out, comparator_20_eq);
  Clock #(.lowDuration(9)) clock_28 (.out(clock_28_out));
  alu alu_8 (
    .argX(regX_p27), .argY(regY_p17), .argZ(regZ_p17), .op(bitselector_12_out), .\var (bitselector_13_out),
    .outX(alu_8_outx));  // open: we
  Multiplexer #(.width(64)) multiplexer_23 (
    .in0(multiplexer_24_out), .in1(alu_8_outx), .out(regX_p19), .sel(comparator_2_gt));
  Multiplexer #(.select(4), .width(64)) multiplexer_24 (
    .in6({{32{1'b0}}, bitselector_2_out, bitselector_3_out}),
    .in7({bitselector_2_out, bitselector_3_out, bitselector_2_out, bitselector_3_out}),
    .in8({bitselector_3_out, bitselector_3_out, bitselector_3_out, bitselector_3_out}),
    .in9({bitselector_14_out, bitselector_14_out, bitselector_14_out, bitselector_14_out, bitselector_14_out, bitselector_14_out, bitselector_14_out, bitselector_14_out}),
    .in10(counter_16_q), .in11(undriven_8), .in12(multiplexer_22_out), .in13(counter_17_q),
    .in14(multiplexer_34_out), .out(multiplexer_24_out), .sel(bitselector_8_out));  // open: in0, in1, in2, in3, in4, in5, in15
  Counter #(.max('hffffffffffffffff), .width(64)) counter_17 (
    .load(and_29_out), .D(regY_p17), .Q(counter_17_q), .clk(clock_28_out));  // open: count, carry, up, clr
  BitSelector #(.group(16), .width(64)) bitselector_23 (.in(regX_p20), .out(bitselector_23_out), .sel(2'b00));
  BitSelector #(.group(16), .width(64)) bitselector_24 (.in(regX_p20), .out(bitselector_24_out), .sel(2'b01));
  BitSelector #(.group(8), .width(16)) bitselector_25 (.in(bitselector_23_out), .out(bitselector_25_out), .sel(1'b0));
  BitSelector #(.group(16), .width(64)) bitselector_26 (.in(regX_p20), .out(bitselector_26_out), .sel(2'b10));
  BitSelector #(.group(8), .width(16)) bitselector_27 (.in(bitselector_24_out), .out(bitselector_27_out), .sel(1'b0));
  BitSelector #(.group(16), .width(64)) bitselector_28 (.in(regX_p20), .sel(2'b11));  // open: out
  BitSelector #(.group(8), .width(16)) bitselector_29 (.in(bitselector_26_out), .out(bitselector_29_out), .sel(1'b0));
  Register #(.trigger("falling"), .width(1)) register_1 (
    .D(1'b1), .en(not_13_out), .Q(register_1_q), .clk(clock_29_out));  // open: clr
  Clock clock_29 (.out(clock_29_out));
  BitSelector #(.group(2), .width(64)) bitselector_30 (.in(regY_p10), .out(bitselector_30_out), .sel({5{1'b1}}));
  BitSelector #(.group(9), .width(64)) bitselector_31 (.in(regY_p10), .out(bitselector_31_out), .sel(3'b001));
  BitSelector #(.group(18), .width(64)) bitselector_32 (.in(regY_p10), .out(bitselector_32_out), .sel(2'b00));
  Multiplexer #(.width(64)) multiplexer_25 (
    .in0(64'hc000000000000000), .in1(regX_p20), .out(multiplexer_25_out), .sel(register_1_q));
  or or_4 (or_4_out, or_2_out, not_13_out);
  not not_13 (not_13_out, register_1_q);
  and and_30 (and_30_out, comparator_21_eq, comparator_31_gt);
  Comparator #(.mode("unsigned"), .width(2)) comparator_31 (
    .a(bitselector_30_out), .b(2'b01), .gt(comparator_31_gt), .eq(comparator_31_eq), .lt(comparator_31_lt));
  BitSelector #(.group(9), .width(64)) bitselector_33 (.in(regY_p10), .out(bitselector_33_out), .sel(3'b000));
  not not_14 (not_14_out, and_5_out);
  Clock clock_30 (.out(clock_30_out));
  not not_15 (not_15_out, comparator_31_lt);
  // RGB_Video #(.cursor("No Cursor"), .height(512), .scale(1), .width(512)) rgb_video_1: pin names not known; wires that end beside it: rgb_video_1_p1, and_30_out, bitselector_31_out, bitselector_33_out, {bitselector_25_out, bitselector_27_out, bitselector_29_out}
  Clock clock_31 (.out(rgb_video_1_p1));
  BitSelector #(.group(24), .width(64)) bitselector_34 (.in(counter_18_q), .out(bitselector_34_out), .sel(2'b00));
  Counter #(.max('hffffffffffffffff), .trigger("falling"), .width(64)) counter_18 (
    .load(or_4_out), .D(multiplexer_25_out), .count(not_14_out), .Q(counter_18_q), .clk(clock_30_out));  // open: carry, up, clr
  and and_31 (and_31_out, comparator_31_lt, comparator_21_eq);
  and and_32 (and_32_out, comparator_31_eq, comparator_21_eq);
  RAM #(.addrWidth(18), .dataWidth(64), .enables("line")) disp1 (
    .addr(bitselector_32_out), .we(and_30_out), .clk(clock_32_out), .din(regX_p20));  // open: dout
  Clock clock_32 (.out(clock_32_out));
  BitSelector #(.group(2), .width(64)) bitselector_35 (.in(counter_18_q), .out(bitselector_35_out), .sel({5{1'b1}}));
  // DualRAM #(.addrWidth(24), .dataWidth(64), .enables("line"), .line("octo"), .misaligned("true"), .\type ("nonvolatile")) ram1: pin names not known; wires that end beside it: bitselector_34_out, ram1_p2, ram1_p3
  BitSelector #(.group(24), .width(64)) bitselector_36 (.in(regY_p10), .out(ram1_p2), .sel(2'b00));
  Clock clock_33 (.out(clock_33_out));
  BitSelector #(.group(24), .width(64)) bitselector_37 (.in(regY_p10), .out(bitselector_37_out), .sel(2'b00));
  // RAM #(.addrWidth(24), .dataWidth(64), .enables("line"), .line("octo"), .misaligned("true")) cart1: pin names not known; wires that end beside it: and_31_out, and_31_out, bitselector_5_out[1], bitselector_5_out[2], bitselector_5_out[3], bitselector_5_out[4], bitselector_5_out[5], bitselector_5_out[6], bitselector_5_out[7], clock_33_out, regX_p20, regX_p21, regX_p22, regX_p23, regX_p24, regX_p25, regX_p26, regX_p27, bitselector_37_out, and_32_out, and_32_out, bitselector_5_out[1], bitselector_5_out[2], bitselector_5_out[3], bitselector_5_out[4], bitselector_5_out[5], bitselector_5_out[6], bitselector_5_out[7], cart1_p29, regX_p20, cart1_p31, cart1_p32, cart1_p33, cart1_p34, cart1_p35, cart1_p36, cart1_p37, cart1_p38, cart1_p39
  Clock clock_34 (.out(cart1_p29));
  // ROM #(.addrWidth(24), .dataWidth(64), .line("octo"), .misaligned("true")) rom1: pin names not known; wires that end beside it: regX_p21, regX_p22, regX_p23, regX_p24, regX_p25, regX_p26, regX_p27, bitselector_34_out, rom1_p9, rom1_p10, rom1_p11, rom1_p12, rom1_p13, rom1_p14, rom1_p15, rom1_p16
  Comparator #(.mode("unsigned"), .width(2)) comparator_32 (
    .a(bitselector_35_out), .b(2'b11), .eq(comparator_32_eq));  // open: gt, lt
  Multiplexer #(.width(64)) multiplexer_26 (
    .in0(ram1_p3), .in1(rom1_p16), .out(multiplexer_26_out), .sel(comparator_32_eq));
  Multiplexer #(.width(64)) multiplexer_27 (
    .in0(cart1_p31), .in1(cart1_p39), .out(multiplexer_27_out), .sel(not_15_out));
  Multiplexer #(.width(64)) multiplexer_28 (.in0(cart1_p32), .in1(rom1_p9), .out(multiplexer_28_out), .sel(not_15_out));
  Multiplexer #(.width(64)) multiplexer_29 (
    .in0(cart1_p33), .in1(rom1_p10), .out(multiplexer_29_out), .sel(not_15_out));
  Multiplexer #(.width(64)) multiplexer_30 (
    .in0(cart1_p34), .in1(rom1_p11), .out(multiplexer_30_out), .sel(not_15_out));
  Multiplexer #(.width(64)) multiplexer_31 (
    .in0(cart1_p35), .in1(rom1_p12), .out(multiplexer_31_out), .sel(not_15_out));
  Multiplexer #(.width(64)) multiplexer_32 (
    .in0(cart1_p36), .in1(rom1_p13), .out(multiplexer_32_out), .sel(not_15_out));
  Multiplexer #(.width(64)) multiplexer_33 (
    .in0(cart1_p37), .in1(rom1_p14), .out(multiplexer_33_out), .sel(not_15_out));
  Multiplexer #(.width(64)) multiplexer_34 (
    .in0(cart1_p38), .in1(rom1_p15), .out(multiplexer_34_out), .sel(not_15_out));

  // Notes on the sheet:
  //   contents of rom1 (hex, n*v repeats v):
  //   400000000060 2000000200060 3000000080360 5000000100060 6c00000000060 a0000000f0060 b000000000060
  //   60006000200a1 60006000a0022 200a1 70000000000e0 70007000500b1 c000700000001 b000c00000020
  //   1000000030003 1000100030003 4000400030003 1000010000ffe0 1000040000fff0 8000400070013 9000800000011
  //   6000900000020 b000000000010
endmodule
module alu (
  input  [63:0] argX,
  input  [63:0] argY,
  input  [63:0] argZ,
  input  [3:0] op,
  input  [3:0] \var ,
  output [63:0] outX,
  output we
);

  wire adder_1_cout, adder_4_cout, adder_5_cout, adder_10_cout, adder_11_cout, adder_12_cout, adder_13_cout,
       adder_22_cout, adder_23_cout, adder_24_cout, adder_25_cout, adder_26_cout, adder_27_cout,
       adder_28_cout, adder_29_cout, bitfinder_1_found, bitfinder_2_found, bitfinder_3_found,
       bitfinder_4_found, bitfinder_5_found, bitfinder_6_found, bitfinder_7_found, bitfinder_8_found,
       bitfinder_9_found, bitfinder_10_found, bitfinder_11_found, bitfinder_12_found, bitfinder_13_found,
       bitfinder_14_found, bitfinder_15_found, bitfinder_16_found, bitfinder_17_found, bitfinder_18_found,
       bitfinder_19_found, bitfinder_20_found, bitfinder_21_found, bitfinder_22_found, bitfinder_23_found,
       bitfinder_24_found, bitfinder_25_found, bitfinder_26_found, bitfinder_27_found, bitfinder_28_found,
       bitfinder_29_found, bitfinder_30_found, bitfinder_31_found, bitfinder_32_found, bitfinder_33_found,
       bitfinder_34_found, bitfinder_35_found, bitfinder_36_found, bitfinder_37_found, bitfinder_38_found,
       bitfinder_39_found, bitfinder_40_found, bitfinder_41_found, bitfinder_42_found, bitfinder_43_found,
       bitfinder_44_found, bitfinder_45_found, bitfinder_46_found, bitfinder_47_found, bitfinder_48_found,
       bitfinder_49_found, bitfinder_50_found, bitfinder_51_found, bitfinder_52_found, bitfinder_53_found,
       bitfinder_54_found, bitfinder_55_found, bitfinder_56_found, bitfinder_57_found, bitfinder_58_found,
       bitfinder_59_found, bitfinder_60_found, comparator_1_eq, comparator_2_eq, comparator_2_lt,
       comparator_3_eq, comparator_4_eq, comparator_5_eq, comparator_6_eq, comparator_7_eq, comparator_8_eq,
       comparator_8_lt, comparator_9_eq, comparator_10_eq, comparator_11_eq, comparator_12_eq,
       comparator_13_eq, comparator_14_eq, comparator_15_eq, comparator_16_eq, comparator_17_eq,
       comparator_18_eq, comparator_19_eq, comparator_19_lt, comparator_20_eq, comparator_20_lt,
       comparator_21_eq, comparator_21_lt, comparator_22_eq, comparator_22_lt, comparator_23_eq,
       comparator_24_eq, comparator_25_eq, comparator_25_lt, comparator_26_eq, comparator_26_lt,
       comparator_27_eq, comparator_27_lt, comparator_28_eq, comparator_28_lt, comparator_29_eq,
       comparator_29_lt, comparator_30_eq, comparator_30_lt, comparator_31_eq, comparator_31_lt,
       comparator_32_eq, comparator_32_lt, comparator_33_eq, comparator_34_eq, comparator_35_eq,
       comparator_36_eq, comparator_37_eq, comparator_37_lt, comparator_38_eq, comparator_38_lt,
       comparator_39_eq, comparator_39_lt, comparator_40_eq, comparator_40_lt, comparator_41_eq,
       comparator_41_lt, comparator_42_eq, comparator_42_lt, comparator_43_eq, comparator_43_lt,
       comparator_44_eq, comparator_44_lt, comparator_45_eq, comparator_45_lt, comparator_46_eq,
       comparator_46_lt, comparator_47_eq, comparator_47_lt, comparator_48_eq, comparator_48_lt,
       comparator_49_eq, comparator_49_lt, comparator_50_eq, comparator_50_lt, comparator_51_eq,
       comparator_51_lt, comparator_52_eq, comparator_52_lt, comparator_53_eq, comparator_54_eq,
       comparator_55_eq, comparator_56_eq, comparator_57_eq, comparator_58_eq, comparator_59_eq,
       comparator_60_eq, fpclassificator_1_p2, fpclassificator_1_p3, fpclassificator_2_p4,
       fpclassificator_3_p2, fpclassificator_4_p4, fpclassificator_5_p2, fpclassificator_6_p4,
       fpclassificator_7_p2, fpclassificator_8_p2, fpclassificator_9_p2, fpclassificator_10_p4,
       fpclassificator_11_p2, fpclassificator_12_p2, fpclassificator_13_p2, fpclassificator_14_p2,
       fpclassificator_15_p2, fpclassificator_16_p2, fpclassificator_17_p2, fpclassificator_18_p2,
       fpclassificator_19_p2, fpclassificator_20_p2, fpclassificator_21_p2, fpclassificator_22_p2,
       fpclassificator_23_p2, fpclassificator_24_p2, fpclassificator_25_p2, fpclassificator_26_p2,
       fpclassificator_27_p2, fpclassificator_28_p2, fpclassificator_29_p2, fpcomparator_1_p6,
       fpcomparator_1_p7, fpcomparator_2_p3, fpcomparator_2_p4, fpcomparator_3_p3, fpcomparator_3_p4,
       fpcomparator_4_p3, fpcomparator_4_p4, fpcomparator_5_p3, fpcomparator_5_p4, fpcomparator_6_p3,
       fpcomparator_6_p4, fpcomparator_7_p3, fpcomparator_7_p4, fpcomparator_8_p3, fpcomparator_8_p4,
       fpcomparator_9_p3, fpcomparator_9_p4, fpcomparator_10_p3, fpcomparator_10_p4, fpcomparator_11_p3,
       fpcomparator_11_p4, fpcomparator_12_p3, fpcomparator_12_p4, fpcomparator_13_p3, fpcomparator_13_p4,
       fpcomparator_14_p3, fpcomparator_14_p4, fpcomparator_15_p3, fpcomparator_15_p4, fpcomparator_16_p3,
       fpcomparator_16_p4, fpcomparator_17_p3, fpcomparator_17_p4, fpcomparator_18_p3, fpcomparator_18_p4,
       fpcomparator_19_p3, fpcomparator_19_p4, fpcomparator_20_p3, fpcomparator_20_p4, fpcomparator_21_p3,
       fpcomparator_21_p4, fpcomparator_22_p3, fpcomparator_22_p4, fpcomparator_23_p3, fpcomparator_23_p4,
       fpcomparator_24_p3, fpcomparator_24_p4, fpcomparator_25_p3, fpcomparator_25_p4, fpcomparator_26_p3,
       fpcomparator_26_p4, fpcomparator_27_p3, fpcomparator_27_p4, fpcomparator_28_p3, fpcomparator_28_p4,
       fpcomparator_29_p3, fpcomparator_29_p4, fpcomparator_30_p3, fpcomparator_30_p4, not_2_out, not_3_out,
       not_4_out, not_5_out, not_6_out, not_7_out, not_8_out, not_9_out, not_10_out, not_11_out, not_12_out,
       not_13_out, not_14_out, not_15_out, not_16_out, subtractor_1_bout, subtractor_4_bout,
       subtractor_5_bout, subtractor_10_bout, subtractor_11_bout, subtractor_12_bout, subtractor_13_bout,
       subtractor_22_bout, subtractor_23_bout, subtractor_24_bout, subtractor_25_bout, subtractor_26_bout,
       subtractor_27_bout, subtractor_28_bout, subtractor_29_bout;
  wire [2:0] bitfinder_29_index, bitfinder_30_index, bitfinder_31_index, bitfinder_32_index,
       bitfinder_33_index, bitfinder_34_index, bitfinder_35_index, bitfinder_36_index, bitfinder_37_index,
       bitfinder_38_index, bitfinder_39_index, bitfinder_40_index, bitfinder_41_index, bitfinder_42_index,
       bitfinder_43_index, bitfinder_44_index, bitfinder_45_index, bitfinder_46_index, bitfinder_47_index,
       bitfinder_48_index, bitfinder_49_index, bitfinder_50_index, bitfinder_51_index, bitfinder_52_index,
       bitfinder_53_index, bitfinder_54_index, bitfinder_55_index, bitfinder_56_index, bitfinder_57_index,
       bitfinder_58_index, bitfinder_59_index, bitfinder_60_index, bitselector_12_out, bitselector_13_out,
       bitselector_14_out, bitselector_15_out, bitselector_16_out, bitselector_17_out, bitselector_18_out,
       bitselector_19_out;
  wire [3:0] bitadder_8_out, bitadder_9_out, bitadder_10_out, bitadder_11_out, bitadder_12_out,
       bitadder_13_out, bitadder_14_out, bitadder_15_out, bitfinder_13_index, bitfinder_14_index,
       bitfinder_15_index, bitfinder_16_index, bitfinder_17_index, bitfinder_18_index, bitfinder_19_index,
       bitfinder_20_index, bitfinder_21_index, bitfinder_22_index, bitfinder_23_index, bitfinder_24_index,
       bitfinder_25_index, bitfinder_26_index, bitfinder_27_index, bitfinder_28_index, bitselector_8_out,
       bitselector_9_out, bitselector_10_out, bitselector_11_out;
  wire [4:0] bitadder_4_out, bitadder_5_out, bitadder_6_out, bitadder_7_out, bitfinder_5_index,
       bitfinder_6_index, bitfinder_7_index, bitfinder_8_index, bitfinder_9_index, bitfinder_10_index,
       bitfinder_11_index, bitfinder_12_index, bitselector_6_out, bitselector_7_out;
  wire [5:0] bitadder_2_out, bitadder_3_out, bitfinder_1_index, bitfinder_2_index, bitfinder_3_index,
       bitfinder_4_index, bitselector_5_out;
  wire [6:0] bitadder_1_out;
  wire [7:0] bit_extender_79_out, bit_extender_80_out, bit_extender_81_out, bit_extender_82_out,
       bit_extender_83_out, bit_extender_84_out, bit_extender_85_out, bit_extender_86_out,
       bit_extender_95_out, bit_extender_96_out, bit_extender_97_out, bit_extender_98_out,
       bit_extender_99_out, bit_extender_100_out, bit_extender_101_out, bit_extender_102_out,
       bit_extender_103_out, bit_extender_104_out, bit_extender_105_out, bit_extender_106_out,
       bit_extender_107_out, bit_extender_108_out, bit_extender_109_out, bit_extender_110_out,
       bit_extender_111_out, bit_extender_112_out, bit_extender_113_out, bit_extender_114_out,
       bit_extender_115_out, bit_extender_116_out, bit_extender_117_out, bit_extender_118_out,
       bitselector_1_out, bitselector_2_out, bitselector_3_out, bitselector_4_out, buffer_9_out,
       buffer_10_out, buffer_11_out, buffer_12_out, buffer_13_out, buffer_14_out, buffer_15_out,
       buffer_16_out, fplogarithm_9_p2, fplogarithm_10_p2, fplogarithm_11_p2, fplogarithm_12_p2,
       fplogarithm_13_p2, fplogarithm_14_p2, fplogarithm_15_p2, fplogarithm_16_p2;
  wire [15:0] bit_extender_11_out, bit_extender_12_out, bit_extender_13_out, bit_extender_14_out,
       bit_extender_43_out, bit_extender_44_out, bit_extender_45_out, bit_extender_46_out,
       bit_extender_47_out, bit_extender_48_out, bit_extender_49_out, bit_extender_50_out,
       bit_extender_51_out, bit_extender_52_out, bit_extender_53_out, bit_extender_54_out,
       bit_extender_55_out, bit_extender_56_out, bit_extender_57_out, bit_extender_58_out, buffer_5_out,
       buffer_6_out, buffer_7_out, buffer_8_out, fplogarithm_5_p2, fplogarithm_6_p2, fplogarithm_7_p2,
       fplogarithm_8_p2;
  wire [31:0] bit_extender_8_out, bit_extender_9_out, bit_extender_17_out, bit_extender_18_out,
       bit_extender_23_out, bit_extender_24_out, bit_extender_25_out, bit_extender_26_out,
       bit_extender_27_out, bit_extender_28_out, buffer_3_out, buffer_4_out, fplogarithm_3_p2,
       fplogarithm_4_p2, fptofp_12_p2, fptofp_13_p2;
  wire [63:0] adder_1_out, adder_3_out, adder_9_out, adder_21_out, and_1_out, bit_extender_1_out,
       bit_extender_2_out, bit_extender_3_out, bit_extender_4_out, bit_extender_5_out, bit_extender_6_out,
       bit_extender_7_out, bit_extender_10_out, bit_extender_15_out, bit_extender_16_out,
       bit_extender_20_out, bit_extender_22_out, bit_extender_30_out, bit_extender_32_out,
       bit_extender_34_out, bit_extender_38_out, bit_extender_42_out, bit_extender_62_out,
       bit_extender_66_out, bit_extender_70_out, bit_extender_78_out, bit_extender_94_out,
       bit_extender_126_out, bit_extender_134_out, bit_extender_142_out, buffer_1_out, buffer_2_out,
       divider_1_out, divider_1_rem, divider_3_out, divider_5_rem, divider_9_out, divider_13_rem,
       divider_21_out, divider_29_rem, fpabsolute_1_p2, fpabsolute_3_p2, fpabsolute_7_p2, fpabsolute_15_p2,
       fpadder_1_out, fpadder_3_out, fpadder_7_out, fpadder_15_out, fpdivider_1_out, fpdivider_3_out,
       fpdivider_7_out, fpdivider_15_out, fpexponentiator_1_p1, fpexponentiator_2_p2, fpexponentiator_4_p3,
       fpexponentiator_6_p2, fpexponentiator_10_p3, fpexponentiator_14_p2, fpexponentiator_22_p3,
       fpexponentiator_30_p2, fplogarithm_1_p3, fplogarithm_2_p2, fplogarithm_18_p3, fplogarithm_22_p3,
       fplogarithm_30_p3, fpminmax_1_p1, fpminmax_1_p2, fpminmax_3_p3, fpminmax_5_p3, fpminmax_9_p3,
       fpminmax_13_p3, fpminmax_21_p3, fpminmax_29_p3, fpmultiplier_1_out, fpmultiplier_3_out,
       fpmultiplier_7_out, fpmultiplier_15_out, fpnegator_1_p2, fpnegator_3_p2, fpnegator_7_p2,
       fpnegator_15_p2, fpsquareroot_1_p1, fpsquareroot_3_p2, fpsquareroot_7_p2, fpsquareroot_15_p2,
       fpsubtractor_1_out, fpsubtractor_3_out, fpsubtractor_7_out, fpsubtractor_15_out, fptofp_8_p2,
       fptofp_14_p2, fptoint_1_p1, fptoint_2_p1, fptoint_3_p1, fptoint_4_p1, fptoint_6_p2, fptoint_8_p2,
       fptoint_10_p2, fptoint_12_p2, fptoint_16_p2, fptoint_20_p2, fptoint_24_p2, fptoint_28_p2,
       fptoint_36_p2, fptoint_44_p2, fptoint_52_p2, fptoint_60_p2, fptrigonometry_1_p1, fptrigonometry_1_p2,
       fptrigonometry_1_p3, fptrigonometry_2_p2, fptrigonometry_2_p3, fptrigonometry_2_p4,
       fptrigonometry_4_p2, fptrigonometry_4_p3, fptrigonometry_4_p4, fptrigonometry_6_p2,
       fptrigonometry_6_p3, fptrigonometry_6_p4, fptrigonometry_10_p2, fptrigonometry_10_p3,
       fptrigonometry_10_p4, fptrigonometry_14_p2, fptrigonometry_14_p3, fptrigonometry_14_p4,
       fptrigonometry_22_p2, fptrigonometry_22_p3, fptrigonometry_22_p4, fptrigonometry_30_p2,
       fptrigonometry_30_p3, fptrigonometry_30_p4, inttofp_1_p2, inttofp_3_p2, inttofp_7_p2, inttofp_15_p2,
       multiplexer_1_out, multiplexer_2_out, multiplexer_3_out, multiplexer_4_out, multiplexer_5_out,
       multiplexer_6_out, multiplexer_7_out, multiplexer_8_out, multiplexer_9_out, multiplexer_10_out,
       multiplexer_11_out, multiplexer_12_out, multiplexer_13_out, multiplexer_14_out, multiplexer_15_out,
       multiplexer_16_out, multiplexer_17_out, multiplexer_18_out, multiplexer_20_out, multiplexer_22_out,
       multiplexer_24_out, multiplexer_25_out, multiplexer_26_out, multiplexer_27_out, multiplexer_28_out,
       multiplexer_29_out, multiplexer_30_out, multiplexer_31_out, multiplexer_32_out, multiplexer_33_out,
       multiplexer_35_out, multiplexer_38_out, multiplexer_39_out, multiplexer_41_out, multiplexer_44_out,
       multiplexer_45_out, multiplexer_49_out, multiplexer_50_out, multiplexer_51_out, multiplexer_53_out,
       multiplexer_55_out, multiplexer_59_out, multiplexer_66_out, multiplexer_70_out, multiplexer_71_out,
       multiplexer_77_out, multiplexer_81_out, multiplexer_83_out, multiplexer_92_out, multiplexer_97_out,
       multiplexer_98_out, multiplexer_100_out, multiplexer_105_out, multiplexer_107_out,
       multiplexer_117_out, multiplexer_132_out, multiplexer_133_out, multiplexer_143_out,
       multiplexer_151_out, multiplexer_157_out, multiplexer_167_out, multiplexer_173_out,
       multiplexer_186_out, multiplexer_193_out, multiplexer_199_out, multiplexer_205_out,
       multiplexer_211_out, multiplier_1_cout, multiplier_1_out, multiplier_3_out, multiplier_5_cout,
       multiplier_9_out, multiplier_13_cout, multiplier_21_out, multiplier_29_cout, nand_1_out,
       negator_1_out, negator_3_out, negator_7_out, negator_15_out, nor_1_out, not_1_out, or_1_out,
       shifter_1_out, shifter_2_out, shifter_3_out, shifter_4_out, shifter_5_out, shifter_7_out,
       shifter_9_out, shifter_11_out, shifter_13_out, shifter_15_out, shifter_19_out, shifter_23_out,
       shifter_27_out, shifter_31_out, shifter_35_out, shifter_43_out, shifter_51_out, shifter_59_out,
       shifter_67_out, shifter_75_out, subtractor_1_out, subtractor_3_out, subtractor_9_out,
       subtractor_21_out, xnor_1_out, xor_1_out;
  wire [63:8] fptofp_4_p2;
  wire [63:16] fptofp_2_p2;
  wire [63:32] fptofp_1_p3;

  Comparator #(.mode("unsigned"), .width(4)) comparator_1 (.a(op), .b(4'b0001), .eq(comparator_1_eq));  // open: gt, lt
  Comparator #(.width(64)) comparator_2 (
    .a(argY), .b({64{1'b0}}), .eq(comparator_2_eq), .lt(comparator_2_lt));  // open: gt
  // FPComparator #(.fpwidth(64)) fpcomparator_1: pin names not known; wires that end beside it: argX, argY, argZ, argY, {64{1'b0}}, fpcomparator_1_p6, fpcomparator_1_p7
  Comparator #(.mode("unsigned"), .width(4)) comparator_3 (.a(op), .b(4'b0010), .eq(comparator_3_eq));  // open: gt, lt
  assign or_1_out = argY | argZ;  // OR_Gate or_1, 64 bits wide
  assign not_1_out = ~argY;  // NOT_Gate not_1, 64 bits wide
  assign buffer_1_out = argY;  // Buffer buffer_1, 64 bits wide
  Comparator #(.mode("unsigned"), .width(4)) comparator_4 (.a(op), .b(4'b0011), .eq(comparator_4_eq));  // open: gt, lt
  Adder #(.width(64)) adder_1 (.a(argZ), .b(argY), .out(adder_1_out), .cout(adder_1_cout));  // open: cin
  assign bit_extender_1_out = {{63{1'b0}}, adder_1_cout};  // Bit_Extender bit_extender_1
  Comparator #(.mode("unsigned"), .width(4)) comparator_5 (.a(op), .b(4'b0100), .eq(comparator_5_eq));  // open: gt, lt
  FPAdder #(.fpwidth(64)) fpadder_1 (.a(argY), .b(argZ), .out(fpadder_1_out));
  Comparator #(.mode("unsigned"), .width(4)) comparator_6 (.a(op), .b(4'b0101), .eq(comparator_6_eq));  // open: gt, lt
  // FPToFP #(.fpwidthin(64)) fptofp_1: pin names not known; wires that end beside it: argX, argY, fptofp_1_p3
  Multiplexer #(.select(4), .width(64)) multiplexer_1 (
    .in0(multiplexer_2_out), .in1(multiplexer_7_out), .in2(multiplexer_8_out), .in3(multiplexer_9_out),
    .in4(bit_extender_3_out), .in5(multiplexer_11_out), .in6(multiplexer_12_out), .in7(multiplexer_13_out),
    .in8(multiplexer_15_out), .in9(bit_extender_4_out), .in10(shifter_1_out), .in11(shifter_2_out),
    .in12(shifter_3_out), .in13(shifter_4_out), .in14(shifter_5_out), .out(multiplexer_1_out), .sel(\var ));  // open: in15
  Multiplexer #(.width(64)) multiplexer_2 (
    .in0({64{1'b0}}), .in1(64'h1), .out(multiplexer_2_out), .sel(comparator_2_eq));
  Multiplexer #(.select(4), .width(64)) multiplexer_3 (
    .in0(buffer_1_out), .in1(not_1_out), .in2(or_1_out), .in3(and_1_out), .in4(nand_1_out), .in5(nor_1_out),
    .in6(xor_1_out), .in7(xnor_1_out), .in10({argY[31:0], argY[31:0]}),
    .in11({argY[47:32], argY[47:32], argY[15:0], argY[15:0]}),
    .in12({bitselector_4_out, bitselector_4_out, bitselector_3_out, bitselector_3_out, bitselector_2_out, bitselector_2_out, bitselector_1_out, bitselector_1_out}),
    .in13(bit_extender_7_out), .in14({bit_extender_9_out, bit_extender_8_out}),
    .in15({bit_extender_14_out, bit_extender_13_out, bit_extender_12_out, bit_extender_11_out}),
    .out(multiplexer_3_out), .sel(\var ));  // open: in8, in9
  assign nand_1_out = ~(argY & argZ);  // NAND_Gate nand_1, 64 bits wide
  assign and_1_out = argY & argZ;  // AND_Gate and_1, 64 bits wide
  Multiplexer #(.select(4), .width(64)) multiplexer_4 (
    .in0(adder_1_out), .in1(subtractor_1_out), .in2(multiplier_1_out), .in3(divider_1_out),
    .in4(negator_1_out), .in5(bit_extender_1_out), .in6(bit_extender_2_out), .in7(multiplier_1_cout),
    .in8(divider_1_rem), .in9(multiplexer_10_out), .in10(multiplexer_14_out), .in11(multiplexer_16_out),
    .in12(multiplexer_17_out), .in13(multiplexer_18_out), .in14(bit_extender_16_out),
    .in15(fpexponentiator_2_p2), .out(multiplexer_4_out), .sel(\var ));
  Subtractor #(.width(64)) subtractor_1 (
    .a(argY), .b(argZ), .out(subtractor_1_out), .bout(subtractor_1_bout));  // open: bin
  Multiplexer #(.select(4), .width(64)) multiplexer_5 (
    .in0(fpadder_1_out), .in1(fpsubtractor_1_out), .in2(fpmultiplier_1_out), .in3(fpdivider_1_out),
    .in4(fpnegator_1_p2), .in5(fptrigonometry_1_p1), .in6(fptrigonometry_1_p2), .in7(fptrigonometry_1_p3),
    .in8(fplogarithm_1_p3), .in9(fpexponentiator_1_p1), .in10(fptrigonometry_2_p2),
    .in11(fptrigonometry_2_p3), .in12(fptrigonometry_2_p4), .in13(fpsquareroot_1_p1), .in14(fpminmax_1_p1),
    .in15(fpminmax_1_p2), .out(multiplexer_5_out), .sel(\var ));
  FPSubtractor #(.fpwidth(64)) fpsubtractor_1 (.a(argY), .b(argZ), .out(fpsubtractor_1_out));
  Multiplexer #(.select(4), .width(64)) multiplexer_6 (
    .in0({fptofp_1_p3, fptofp_1_p3}),
    .in1({fptofp_2_p2[63:48], fptofp_2_p2[63:48], fptofp_2_p2[31:16], fptofp_2_p2[31:16]}),
    .in2({fptofp_4_p2[63:56], fptofp_4_p2[63:56], fptofp_4_p2[47:40], fptofp_4_p2[47:40], fptofp_4_p2[31:24], fptofp_4_p2[31:24], fptofp_4_p2[15:8], fptofp_4_p2[15:8]}),
    .in3(fptofp_8_p2), .in4({fptofp_13_p2, fptofp_12_p2}), .in5(fptofp_14_p2), .in6(fplogarithm_2_p2),
    .in7({fplogarithm_3_p2, fplogarithm_4_p2}),
    .in8({fplogarithm_5_p2, fplogarithm_6_p2, fplogarithm_7_p2, fplogarithm_8_p2}),
    .in9({fplogarithm_9_p2, fplogarithm_10_p2, fplogarithm_11_p2, fplogarithm_12_p2, fplogarithm_13_p2, fplogarithm_14_p2, fplogarithm_15_p2, fplogarithm_16_p2}),
    .in10(inttofp_1_p2), .in11(fptoint_1_p1), .in12(fptoint_2_p1), .in13(fptoint_3_p1), .in14(fptoint_4_p1),
    .in15(fpabsolute_1_p2), .out(multiplexer_6_out), .sel(\var ));
  // FPToFP #(.fpwidthout(16)) fptofp_2: pin names not known; wires that end beside it: argY[31:0], fptofp_2_p2[31:16]
  // FPToFP #(.fpwidthout(16)) fptofp_3: pin names not known; wires that end beside it: argY[63:32], fptofp_2_p2[63:48]
  Multiplexer #(.width(64)) multiplexer_7 (
    .in0({64{1'b0}}), .in1(64'h1), .out(multiplexer_7_out), .sel(comparator_2_lt));
  Multiplexer #(.width(64)) multiplexer_8 (
    .in0({64{1'b0}}), .in1(64'h1), .out(multiplexer_8_out), .sel(fpcomparator_1_p6));
  assign nor_1_out = ~(argY | argZ);  // NOR_Gate nor_1, 64 bits wide
  assign xnor_1_out = ~(argY ^ argZ);  // XNOR_Gate xnor_1, 64 bits wide
  assign xor_1_out = argY ^ argZ;  // XOR_Gate xor_1, 64 bits wide
  assign bit_extender_2_out = {{63{1'b0}}, subtractor_1_bout};  // Bit_Extender bit_extender_2
  FPMultiplier #(.fpwidth(64)) fpmultiplier_1 (.a(argY), .b(argZ), .out(fpmultiplier_1_out));
  Multiplexer #(.width(64)) multiplexer_9 (
    .in0({64{1'b0}}), .in1(64'h1), .out(multiplexer_9_out), .sel(fpcomparator_1_p7));
  Multiplier #(.mode("twosComplement"), .width(64)) multiplier_1 (
    .a(argY), .b(argZ), .out(multiplier_1_out), .cout(multiplier_1_cout));  // open: cin
  FPDivider #(.fpwidth(64)) fpdivider_1 (.a(argY), .b(argZ), .out(fpdivider_1_out));
  // FPToFP #(.fpwidthin(16), .fpwidthout(8)) fptofp_4: pin names not known; wires that end beside it: argY[15:0], fptofp_4_p2[15:8]
  // FPToFP #(.fpwidthin(16), .fpwidthout(8)) fptofp_5: pin names not known; wires that end beside it: argY[31:16], fptofp_4_p2[31:24]
  // FPToFP #(.fpwidthin(16), .fpwidthout(8)) fptofp_6: pin names not known; wires that end beside it: argY[47:32], fptofp_4_p2[47:40]
  // FPToFP #(.fpwidthin(16), .fpwidthout(8)) fptofp_7: pin names not known; wires that end beside it: argY[63:48], fptofp_4_p2[63:56]
  // FPClassificator #(.fpwidth(64)) fpclassificator_1: pin names not known; wires that end beside it: argY, fpclassificator_1_p2, fpclassificator_1_p3
  Divider #(.mode("twosComplement"), .width(64)) divider_1 (
    .a(argY), .b(argZ), .out(divider_1_out), .rem(divider_1_rem));  // open: upper
  // FPNegator #(.fpwidth(64)) fpnegator_1: pin names not known; wires that end beside it: argY, fpnegator_1_p2, argY
  // FPTrigonometry #(.fpwidth(64)) fptrigonometry_1: pin names not known; wires that end beside it: fptrigonometry_1_p1, fptrigonometry_1_p2, fptrigonometry_1_p3
  assign bit_extender_3_out = {{63{1'b0}}, fpclassificator_1_p2};  // Bit_Extender bit_extender_3
  Negator #(.width(64)) negator_1 (.in(argY), .out(negator_1_out));
  // FPToFP #(.fpwidthin(8), .fpwidthout(16)) fptofp_8: pin names not known; wires that end beside it: argY[7:0], fptofp_8_p2[15:0]
  // FPToFP #(.fpwidthin(8), .fpwidthout(16)) fptofp_9: pin names not known; wires that end beside it: argY[23:16], fptofp_8_p2[31:16]
  // FPToFP #(.fpwidthin(8), .fpwidthout(16)) fptofp_10: pin names not known; wires that end beside it: argY[39:32], fptofp_8_p2[47:32]
  // FPToFP #(.fpwidthin(8), .fpwidthout(16)) fptofp_11: pin names not known; wires that end beside it: argY[55:48], fptofp_8_p2[63:48]
  assign bit_extender_4_out = {{63{1'b0}}, fpclassificator_1_p3};  // Bit_Extender bit_extender_4
  Multiplexer #(.width(64)) multiplexer_10 (.in0(argX), .in1(buffer_2_out), .out(multiplexer_10_out), .sel(not_2_out));
  assign buffer_2_out = argY;  // Buffer buffer_2, 64 bits wide
  not not_2 (not_2_out, comparator_7_eq);
  Comparator #(.mode("unsigned"), .width(64)) comparator_7 (
    .a(argZ), .b({64{1'b0}}), .eq(comparator_7_eq));  // open: gt, lt
  // FPTrigonometry #(.fpwidth(64), .\type ("arc")) fptrigonometry_2: pin names not known; wires that end beside it: argY, fptrigonometry_2_p2, fptrigonometry_2_p3, fptrigonometry_2_p4
  // FPToFP #(.fpwidthin(16)) fptofp_12: pin names not known; wires that end beside it: argY[15:0], fptofp_12_p2
  // FPToFP #(.fpwidthin(16)) fptofp_13: pin names not known; wires that end beside it: argY[47:32], fptofp_13_p2
  Comparator #(.width(64)) comparator_8 (.a(argY), .b(argZ), .eq(comparator_8_eq), .lt(comparator_8_lt));  // open: gt
  // FPComparator #(.fpwidth(64)) fpcomparator_2: pin names not known; wires that end beside it: argY, argZ, fpcomparator_2_p3, fpcomparator_2_p4
  // FPLogarithm #(.fpwidth(64)) fplogarithm_1: pin names not known; wires that end beside it: argY, argZ, fplogarithm_1_p3, argY, argZ
  Multiplexer #(.width(64)) multiplexer_11 (
    .in0({64{1'b0}}), .in1(64'h1), .out(multiplexer_11_out), .sel(comparator_8_eq));
  Multiplexer #(.width(64)) multiplexer_12 (
    .in0({64{1'b0}}), .in1(64'h1), .out(multiplexer_12_out), .sel(comparator_8_lt));
  assign bit_extender_5_out = {{58{1'b0}}, bitfinder_1_index};  // Bit_Extender bit_extender_5
  BitFinder #(.width(64)) bitfinder_1 (.in(argY), .index(bitfinder_1_index), .found(bitfinder_1_found));
  // FPExponentiator #(.fpwidth(64)) fpexponentiator_1: pin names not known; wires that end beside it: fpexponentiator_1_p1, argY
  // FPToFP #(.fpwidthout(64)) fptofp_14: pin names not known; wires that end beside it: argY[31:0], fptofp_14_p2
  Multiplexer #(.width(64)) multiplexer_13 (
    .in0({64{1'b0}}), .in1(64'h1), .out(multiplexer_13_out), .sel(fpcomparator_2_p3));
  Multiplexer #(.width(64)) multiplexer_14 (
    .in0({64{1'b1}}), .in1(bit_extender_5_out), .out(multiplexer_14_out), .sel(bitfinder_1_found));
  // FPSquareRoot #(.fpwidth(64)) fpsquareroot_1: pin names not known; wires that end beside it: fpsquareroot_1_p1, argY, argZ
  // FPLogarithm #(.fpwidth(64), .mode("log")) fplogarithm_2: pin names not known; wires that end beside it: argY, fplogarithm_2_p2
  Multiplexer #(.width(64)) multiplexer_15 (
    .in0({64{1'b0}}), .in1(64'h1), .out(multiplexer_15_out), .sel(fpcomparator_2_p4));
  BitSelector #(.group(8), .width(16)) bitselector_1 (.in(argY[15:0]), .out(bitselector_1_out), .sel(1'b0));
  BitSelector #(.group(8), .width(16)) bitselector_2 (.in(argY[31:16]), .out(bitselector_2_out), .sel(1'b0));
  BitSelector #(.group(8), .width(16)) bitselector_3 (.in(argY[47:32]), .out(bitselector_3_out), .sel(1'b0));
  BitSelector #(.group(8), .width(16)) bitselector_4 (.in(argY[63:48]), .out(bitselector_4_out), .sel(1'b0));
  BitFinder #(.\type ("high1"), .width(64)) bitfinder_2 (
    .in(argY), .index(bitfinder_2_index), .found(bitfinder_2_found));
  // FPMinMax #(.fpwidth(64)) fpminmax_1: pin names not known; wires that end beside it: fpminmax_1_p1, fpminmax_1_p2
  // FPLogarithm #(.mode("log")) fplogarithm_3: pin names not known; wires that end beside it: argY[63:32], fplogarithm_3_p2
  // FPLogarithm #(.mode("log")) fplogarithm_4: pin names not known; wires that end beside it: argY[31:0], fplogarithm_4_p2
  Shifter #(.width(64)) shifter_1 (.in(argY), .\dist (bitselector_5_out), .out(shifter_1_out));
  BitSelector #(.group(6), .width(64)) bitselector_5 (.in(argZ), .out(bitselector_5_out), .sel(4'b0000));
  assign bit_extender_6_out = {{58{1'b0}}, bitfinder_2_index};  // Bit_Extender bit_extender_6
  Multiplexer #(.width(64)) multiplexer_16 (
    .in0({64{1'b1}}), .in1(bit_extender_6_out), .out(multiplexer_16_out), .sel(bitfinder_2_found));
  Shifter #(.shift("lr"), .width(64)) shifter_2 (.in(argY), .\dist (bitselector_5_out), .out(shifter_2_out));
  assign bit_extender_7_out = {{32{argY[31]}}, argY[31:0]};  // Bit_Extender bit_extender_7
  BitFinder #(.\type ("low0"), .width(64)) bitfinder_3 (
    .in(argY), .index(bitfinder_3_index), .found(bitfinder_3_found));
  // FPLogarithm #(.fpwidth(16), .mode("log")) fplogarithm_5: pin names not known; wires that end beside it: argY[63:48], fplogarithm_5_p2
  // FPLogarithm #(.fpwidth(16), .mode("log")) fplogarithm_6: pin names not known; wires that end beside it: argY[47:32], fplogarithm_6_p2
  // FPLogarithm #(.fpwidth(16), .mode("log")) fplogarithm_7: pin names not known; wires that end beside it: argY[31:16], fplogarithm_7_p2
  // FPLogarithm #(.fpwidth(16), .mode("log")) fplogarithm_8: pin names not known; wires that end beside it: argY[15:0], fplogarithm_8_p2
  Shifter #(.shift("ar"), .width(64)) shifter_3 (.in(argY), .\dist (bitselector_5_out), .out(shifter_3_out));
  assign bit_extender_8_out = {{16{argY[15]}}, argY[15:0]};  // Bit_Extender bit_extender_8
  assign bit_extender_9_out = {{16{argY[47]}}, argY[47:32]};  // Bit_Extender bit_extender_9
  assign bit_extender_10_out = {{58{1'b0}}, bitfinder_3_index};  // Bit_Extender bit_extender_10
  Shifter #(.shift("rl"), .width(64)) shifter_4 (.in(argY), .\dist (bitselector_5_out), .out(shifter_4_out));
  Multiplexer #(.width(64)) multiplexer_17 (
    .in0({64{1'b1}}), .in1(bit_extender_10_out), .out(multiplexer_17_out), .sel(bitfinder_3_found));
  // FPLogarithm #(.fpwidth(8), .mode("log")) fplogarithm_9: pin names not known; wires that end beside it: argY[63:56], fplogarithm_9_p2
  // FPLogarithm #(.fpwidth(8), .mode("log")) fplogarithm_10: pin names not known; wires that end beside it: argY[55:48], fplogarithm_10_p2
  // FPLogarithm #(.fpwidth(8), .mode("log")) fplogarithm_11: pin names not known; wires that end beside it: argY[47:40], fplogarithm_11_p2
  // FPLogarithm #(.fpwidth(8), .mode("log")) fplogarithm_12: pin names not known; wires that end beside it: argY[39:32], fplogarithm_12_p2
  // FPLogarithm #(.fpwidth(8), .mode("log")) fplogarithm_13: pin names not known; wires that end beside it: argY[31:24], fplogarithm_13_p2
  // FPLogarithm #(.fpwidth(8), .mode("log")) fplogarithm_14: pin names not known; wires that end beside it: argY[23:16], fplogarithm_14_p2
  // FPLogarithm #(.fpwidth(8), .mode("log")) fplogarithm_15: pin names not known; wires that end beside it: argY[15:8], fplogarithm_15_p2
  // FPLogarithm #(.fpwidth(8), .mode("log")) fplogarithm_16: pin names not known; wires that end beside it: argY[7:0], fplogarithm_16_p2
  Shifter #(.shift("rr"), .width(64)) shifter_5 (.in(argY), .\dist (bitselector_5_out), .out(shifter_5_out));
  assign bit_extender_11_out = {{8{argY[7]}}, argY[7:0]};  // Bit_Extender bit_extender_11
  assign bit_extender_12_out = {{8{argY[23]}}, argY[23:16]};  // Bit_Extender bit_extender_12
  assign bit_extender_13_out = {{8{argY[39]}}, argY[39:32]};  // Bit_Extender bit_extender_13
  assign bit_extender_14_out = {{8{argY[55]}}, argY[55:48]};  // Bit_Extender bit_extender_14
  assign bit_extender_15_out = {{58{1'b0}}, bitfinder_4_index};  // Bit_Extender bit_extender_15
  BitFinder #(.\type ("high0"), .width(64)) bitfinder_4 (
    .in(argY), .index(bitfinder_4_index), .found(bitfinder_4_found));
  Multiplexer #(.width(64)) multiplexer_18 (
    .in0({64{1'b1}}), .in1(bit_extender_15_out), .out(multiplexer_18_out), .sel(bitfinder_4_found));
  // IntToFP #(.fpwidth(64), .width(64)) inttofp_1: pin names not known; wires that end beside it: argY, inttofp_1_p2, argY
  BitAdder #(.width(64)) bitadder_1 (.in0(argY), .out(bitadder_1_out));
  // FPToInt #(.fpwidth(64), .width(64)) fptoint_1: pin names not known; wires that end beside it: fptoint_1_p1, argY
  assign bit_extender_16_out = {{57{1'b0}}, bitadder_1_out};  // Bit_Extender bit_extender_16
  // FPToInt #(.fpwidth(64), .mode("floor"), .width(64)) fptoint_2: pin names not known; wires that end beside it: fptoint_2_p1, argY
  // FPExponentiator #(.fpwidth(64), .mode("exp")) fpexponentiator_2: pin names not known; wires that end beside it: argY, fpexponentiator_2_p2
  // FPToInt #(.fpwidth(64), .mode("ceil"), .width(64)) fptoint_3: pin names not known; wires that end beside it: fptoint_3_p1, argY
  // FPToInt #(.fpwidth(64), .mode("truncate"), .width(64)) fptoint_4: pin names not known; wires that end beside it: fptoint_4_p1
  or or_2 (we, comparator_1_eq, comparator_3_eq, comparator_4_eq, comparator_5_eq, comparator_6_eq, comparator_9_eq, comparator_10_eq, comparator_11_eq, comparator_12_eq, comparator_13_eq, comparator_14_eq, comparator_15_eq, comparator_16_eq, comparator_17_eq, comparator_18_eq);
  // FPAbsolute #(.fpwidth(64)) fpabsolute_1: pin names not known; wires that end beside it: argY, fpabsolute_1_p2
  Multiplexer #(.select(4), .width(64)) multiplexer_19 (
    .in1(multiplexer_1_out), .in2(multiplexer_3_out), .in3(multiplexer_4_out), .in4(multiplexer_5_out),
    .in5(multiplexer_6_out), .in6(multiplexer_20_out), .in7(multiplexer_22_out), .in8(multiplexer_24_out),
    .in9(multiplexer_25_out), .in10(multiplexer_26_out), .in11(multiplexer_27_out),
    .in12(multiplexer_28_out), .in13(multiplexer_29_out), .in14(multiplexer_30_out),
    .in15(multiplexer_31_out), .out(outX), .sel(op));  // open: in0
  Comparator #(.mode("unsigned"), .width(4)) comparator_9 (.a(op), .b(4'b0110), .eq(comparator_9_eq));  // open: gt, lt
  Comparator #(.mode("unsigned"), .width(4)) comparator_10 (
    .a(op), .b(4'b0111), .eq(comparator_10_eq));  // open: gt, lt
  Comparator #(.mode("unsigned"), .width(4)) comparator_11 (
    .a(op), .b(4'b1000), .eq(comparator_11_eq));  // open: gt, lt
  Comparator #(.mode("unsigned"), .width(4)) comparator_12 (
    .a(op), .b(4'b1001), .eq(comparator_12_eq));  // open: gt, lt
  Comparator #(.mode("unsigned"), .width(4)) comparator_13 (
    .a(op), .b(4'b1010), .eq(comparator_13_eq));  // open: gt, lt
  Comparator #(.mode("unsigned"), .width(4)) comparator_14 (
    .a(op), .b(4'b1011), .eq(comparator_14_eq));  // open: gt, lt
  Comparator #(.mode("unsigned"), .width(4)) comparator_15 (
    .a(op), .b(4'b1100), .eq(comparator_15_eq));  // open: gt, lt
  Comparator #(.mode("unsigned"), .width(4)) comparator_16 (
    .a(op), .b(4'b1101), .eq(comparator_16_eq));  // open: gt, lt
  Comparator #(.mode("unsigned"), .width(4)) comparator_17 (
    .a(op), .b(4'b1110), .eq(comparator_17_eq));  // open: gt, lt
  Comparator #(.mode("unsigned"), .width(4)) comparator_18 (
    .a(op), .b(4'b1111), .eq(comparator_18_eq));  // open: gt, lt
  BitSelector #(.group(5), .width(32)) bitselector_6 (.in(argZ[31:0]), .out(bitselector_6_out), .sel(3'b000));
  BitSelector #(.group(5), .width(32)) bitselector_7 (.in(argZ[63:32]), .out(bitselector_7_out), .sel(3'b000));
  BitFinder #(.width(32)) bitfinder_5 (.in(argY[63:32]), .index(bitfinder_5_index), .found(bitfinder_5_found));
  BitFinder #(.width(32)) bitfinder_6 (.in(argY[31:0]), .index(bitfinder_6_index), .found(bitfinder_6_found));
  Multiplexer #(.select(4), .width(64)) multiplexer_20 (
    .in0(multiplexer_32_out), .in1(multiplexer_38_out), .in2(multiplexer_44_out), .in3(multiplexer_50_out),
    .in4(bit_extender_30_out), .in5(multiplexer_59_out), .in6(multiplexer_71_out), .in7(multiplexer_83_out),
    .in8(multiplexer_97_out), .in9(bit_extender_62_out), .in10(multiplexer_133_out),
    .in11(multiplexer_157_out), .in12(multiplexer_186_out), .in13(multiplexer_205_out),
    .in14(bit_extender_134_out), .out(multiplexer_20_out), .sel(\var ));  // open: in15
  Multiplexer #(.width(32)) multiplexer_21 (
    .in0({32{1'b0}}), .in1(32'h1), .out(multiplexer_32_out[63:32]), .sel(comparator_19_eq));
  Comparator #(.width(32)) comparator_19 (
    .a(argY[63:32]), .b({32{1'b0}}), .eq(comparator_19_eq), .lt(comparator_19_lt));  // open: gt
  Comparator #(.width(32)) comparator_20 (
    .a(argY[31:0]), .b({32{1'b0}}), .eq(comparator_20_eq), .lt(comparator_20_lt));  // open: gt
  Multiplexer #(.select(4), .width(64)) multiplexer_22 (
    .in0(multiplexer_33_out), .in1(multiplexer_39_out), .in2(multiplexer_45_out), .in3(multiplexer_51_out),
    .in4(bit_extender_32_out), .in5(multiplexer_66_out), .in6(multiplexer_77_out), .in7(multiplexer_98_out),
    .in8(multiplexer_107_out), .in9(bit_extender_70_out), .in10(multiplexer_143_out),
    .in11(multiplexer_173_out), .in12(multiplexer_199_out), .in13(multiplexer_211_out),
    .in14(bit_extender_142_out), .in15(fpexponentiator_6_p2), .out(multiplexer_22_out), .sel(\var ));
  Multiplexer #(.width(32)) multiplexer_23 (
    .in0({32{1'b0}}), .in1(32'h1), .out(multiplexer_33_out[63:32]), .sel(comparator_21_eq));
  Comparator #(.width(32)) comparator_21 (
    .a(argY[63:32]), .b(argZ[63:32]), .eq(comparator_21_eq), .lt(comparator_21_lt));  // open: gt
  Comparator #(.width(32)) comparator_22 (
    .a(argY[31:0]), .b(argZ[31:0]), .eq(comparator_22_eq), .lt(comparator_22_lt));  // open: gt
  Multiplexer #(.select(4), .width(64)) multiplexer_24 (
    .in0(shifter_7_out), .in1(shifter_9_out), .in2(shifter_11_out), .in3(shifter_13_out),
    .in4(shifter_15_out), .in5(shifter_19_out), .in6(shifter_23_out), .in7(shifter_27_out),
    .in8(shifter_31_out), .in9(shifter_35_out), .in10(shifter_43_out), .in11(shifter_51_out),
    .in12(shifter_59_out), .in13(shifter_67_out), .in14(shifter_75_out), .in15(fpexponentiator_14_p2),
    .out(multiplexer_24_out), .sel(\var ));
  Shifter #(.width(32)) shifter_6 (.in(argY[63:32]), .\dist (bitselector_7_out), .out(shifter_7_out[63:32]));
  Shifter #(.width(32)) shifter_7 (.in(argY[31:0]), .\dist (bitselector_6_out), .out(shifter_7_out[31:0]));
  Multiplexer #(.select(4), .width(64)) multiplexer_25 (
    .in0(adder_3_out), .in1(subtractor_3_out), .in2(multiplier_3_out), .in3(divider_3_out),
    .in4(negator_3_out), .in5(adder_9_out), .in6(subtractor_9_out), .in7(multiplier_9_out),
    .in8(divider_9_out), .in9(negator_7_out), .in10(adder_21_out), .in11(subtractor_21_out),
    .in12(multiplier_21_out), .in13(divider_21_out), .in14(negator_15_out), .in15(fpexponentiator_30_p2),
    .out(multiplexer_25_out), .sel(\var ));
  Adder #(.width(32)) adder_2 (.a(argY[63:32]), .b(argZ[63:32]), .out(adder_3_out[63:32]));  // open: cin, cout
  Adder #(.width(32)) adder_3 (.a(argY[31:0]), .b(argZ[31:0]), .out(adder_3_out[31:0]));  // open: cin, cout
  Multiplexer #(.select(4), .width(64)) multiplexer_26 (
    .in0(bit_extender_20_out), .in1(bit_extender_22_out), .in2(multiplier_5_cout), .in3(divider_5_rem),
    .in4(multiplexer_53_out), .in5(bit_extender_38_out), .in6(bit_extender_42_out), .in7(multiplier_13_cout),
    .in8(divider_13_rem), .in9(multiplexer_100_out), .in10(bit_extender_78_out), .in11(bit_extender_94_out),
    .in12(multiplier_29_cout), .in13(divider_29_rem), .in14(multiplexer_193_out), .in15(fpminmax_3_p3),
    .out(multiplexer_26_out), .sel(\var ));
  Adder #(.width(32)) adder_4 (.a(argY[63:32]), .b(argZ[63:32]), .cout(adder_4_cout));  // open: out, cin
  Adder #(.width(32)) adder_5 (.a(argY[31:0]), .b(argZ[31:0]), .cout(adder_5_cout));  // open: out, cin
  Multiplexer #(.select(4), .width(64)) multiplexer_27 (
    .in0(multiplexer_35_out), .in1(multiplexer_41_out), .in2(multiplexer_49_out), .in3(multiplexer_55_out),
    .in4(bit_extender_34_out), .in5(multiplexer_70_out), .in6(multiplexer_81_out), .in7(multiplexer_92_out),
    .in8(multiplexer_105_out), .in9(bit_extender_66_out), .in10(multiplexer_117_out),
    .in11(multiplexer_132_out), .in12(multiplexer_151_out), .in13(multiplexer_167_out),
    .in14(bit_extender_126_out), .in15(fpminmax_5_p3), .out(multiplexer_27_out), .sel(\var ));
  assign bit_extender_17_out = {{27{1'b0}}, bitfinder_5_index};  // Bit_Extender bit_extender_17
  assign bit_extender_18_out = {{27{1'b0}}, bitfinder_6_index};  // Bit_Extender bit_extender_18
  Multiplexer #(.select(4), .width(64)) multiplexer_28 (
    .in0(fpadder_3_out), .in1(fpsubtractor_3_out), .in2(fpmultiplier_3_out), .in3(fpdivider_3_out),
    .in4(fpnegator_3_p2), .in5(fpadder_7_out), .in6(fpsubtractor_7_out), .in7(fpmultiplier_7_out),
    .in8(fpdivider_7_out), .in9(fpnegator_7_p2), .in10(fpadder_15_out), .in11(fpsubtractor_15_out),
    .in12(fpmultiplier_15_out), .in13(fpdivider_15_out), .in14(fpnegator_15_p2), .in15(fpminmax_9_p3),
    .out(multiplexer_28_out), .sel(\var ));
  FPAdder fpadder_2 (.a(argY[63:32]), .b(argZ[63:32]), .out(fpadder_3_out[63:32]));
  FPAdder fpadder_3 (.a(argY[31:0]), .b(argZ[31:0]), .out(fpadder_3_out[31:0]));
  Multiplexer #(.select(4), .width(64)) multiplexer_29 (
    .in0(fptrigonometry_4_p2), .in1(fptrigonometry_4_p3), .in2(fptrigonometry_4_p4), .in3(fplogarithm_18_p3),
    .in4(fpexponentiator_4_p3), .in5(fptrigonometry_10_p2), .in6(fptrigonometry_10_p3),
    .in7(fptrigonometry_10_p4), .in8(fplogarithm_22_p3), .in9(fpexponentiator_10_p3),
    .in10(fptrigonometry_30_p2), .in11(fptrigonometry_30_p3), .in12(fptrigonometry_30_p4),
    .in13(fplogarithm_30_p3), .in14(fpexponentiator_22_p3), .in15(fpminmax_13_p3), .out(multiplexer_29_out),
    .sel(\var ));
  // FPTrigonometry fptrigonometry_3: pin names not known; wires that end beside it: argY[63:32], fptrigonometry_4_p2[63:32], fptrigonometry_4_p3[63:32], fptrigonometry_4_p4[63:32]
  // FPTrigonometry fptrigonometry_4: pin names not known; wires that end beside it: argY[31:0], fptrigonometry_4_p2[31:0], fptrigonometry_4_p3[31:0], fptrigonometry_4_p4[31:0]
  Multiplexer #(.select(4), .width(64)) multiplexer_30 (
    .in0(fptrigonometry_6_p2), .in1(fptrigonometry_6_p3), .in2(fptrigonometry_6_p4), .in3(fpsquareroot_3_p2),
    .in4(fpabsolute_3_p2), .in5(fptrigonometry_14_p2), .in6(fptrigonometry_14_p3),
    .in7(fptrigonometry_14_p4), .in8(fpsquareroot_7_p2), .in9(fpabsolute_7_p2), .in10(fptrigonometry_22_p2),
    .in11(fptrigonometry_22_p3), .in12(fptrigonometry_22_p4), .in13(fpsquareroot_15_p2),
    .in14(fpabsolute_15_p2), .in15(fpminmax_21_p3), .out(multiplexer_30_out), .sel(\var ));
  // FPTrigonometry #(.\type ("arc")) fptrigonometry_5: pin names not known; wires that end beside it: argY[63:32], fptrigonometry_6_p2[63:32], fptrigonometry_6_p3[63:32], fptrigonometry_6_p4[63:32]
  // FPTrigonometry #(.\type ("arc")) fptrigonometry_6: pin names not known; wires that end beside it: argY[31:0], fptrigonometry_6_p2[31:0], fptrigonometry_6_p3[31:0], fptrigonometry_6_p4[31:0]
  Multiplexer #(.select(4), .width(64)) multiplexer_31 (
    .in0(inttofp_3_p2), .in1(fptoint_6_p2), .in2(fptoint_8_p2), .in3(fptoint_10_p2), .in4(fptoint_12_p2),
    .in5(inttofp_7_p2), .in6(fptoint_16_p2), .in7(fptoint_20_p2), .in8(fptoint_24_p2), .in9(fptoint_28_p2),
    .in10(inttofp_15_p2), .in11(fptoint_36_p2), .in12(fptoint_44_p2), .in13(fptoint_52_p2),
    .in14(fptoint_60_p2), .in15(fpminmax_29_p3), .out(multiplexer_31_out), .sel(\var ));
  // IntToFP #(.width(32)) inttofp_2: pin names not known; wires that end beside it: argY[63:32], inttofp_3_p2[63:32]
  // IntToFP #(.width(32)) inttofp_3: pin names not known; wires that end beside it: argY[31:0], inttofp_3_p2[31:0]
  Multiplexer #(.width(32)) multiplexer_32 (
    .in0({32{1'b0}}), .in1(32'h1), .out(multiplexer_32_out[31:0]), .sel(comparator_20_eq));
  Multiplexer #(.width(32)) multiplexer_33 (
    .in0({32{1'b0}}), .in1(32'h1), .out(multiplexer_33_out[31:0]), .sel(comparator_22_eq));
  Shifter #(.shift("lr"), .width(32)) shifter_8 (
    .in(argY[63:32]), .\dist (bitselector_7_out), .out(shifter_9_out[63:32]));
  Shifter #(.shift("lr"), .width(32)) shifter_9 (
    .in(argY[31:0]), .\dist (bitselector_6_out), .out(shifter_9_out[31:0]));
  Subtractor #(.width(32)) subtractor_2 (
    .a(argY[63:32]), .b(argZ[63:32]), .out(subtractor_3_out[63:32]));  // open: bin, bout
  Subtractor #(.width(32)) subtractor_3 (
    .a(argY[31:0]), .b(argZ[31:0]), .out(subtractor_3_out[31:0]));  // open: bin, bout
  assign bit_extender_20_out[63:32] = {{31{1'b0}}, adder_4_cout};  // Bit_Extender bit_extender_19
  assign bit_extender_20_out[31:0] = {{31{1'b0}}, adder_5_cout};  // Bit_Extender bit_extender_20
  Multiplexer #(.width(32)) multiplexer_34 (
    .in0({32{1'b1}}), .in1(bit_extender_17_out), .out(multiplexer_35_out[63:32]), .sel(bitfinder_5_found));
  Multiplexer #(.width(32)) multiplexer_35 (
    .in0({32{1'b1}}), .in1(bit_extender_18_out), .out(multiplexer_35_out[31:0]), .sel(bitfinder_6_found));
  FPSubtractor fpsubtractor_2 (.a(argY[63:32]), .b(argZ[63:32]), .out(fpsubtractor_3_out[63:32]));
  FPSubtractor fpsubtractor_3 (.a(argY[31:0]), .b(argZ[31:0]), .out(fpsubtractor_3_out[31:0]));
  // FPToInt #(.width(32)) fptoint_5: pin names not known; wires that end beside it: argY[63:32], fptoint_6_p2[63:32]
  // FPToInt #(.width(32)) fptoint_6: pin names not known; wires that end beside it: argY[31:0], fptoint_6_p2[31:0]
  Multiplexer #(.width(32)) multiplexer_36 (
    .in0({32{1'b0}}), .in1(32'h1), .out(multiplexer_38_out[63:32]), .sel(comparator_19_lt));
  Multiplexer #(.width(32)) multiplexer_37 (
    .in0({32{1'b0}}), .in1(32'h1), .out(multiplexer_39_out[63:32]), .sel(comparator_21_lt));
  Subtractor #(.width(32)) subtractor_4 (.a(argY[63:32]), .b(argZ[63:32]), .bout(subtractor_4_bout));  // open: out, bin
  Subtractor #(.width(32)) subtractor_5 (.a(argY[31:0]), .b(argZ[31:0]), .bout(subtractor_5_bout));  // open: out, bin
  BitFinder #(.\type ("high1"), .width(32)) bitfinder_7 (
    .in(argY[63:32]), .index(bitfinder_7_index), .found(bitfinder_7_found));
  BitFinder #(.\type ("high1"), .width(32)) bitfinder_8 (
    .in(argY[31:0]), .index(bitfinder_8_index), .found(bitfinder_8_found));
  Multiplexer #(.width(32)) multiplexer_38 (
    .in0({32{1'b0}}), .in1(32'h1), .out(multiplexer_38_out[31:0]), .sel(comparator_20_lt));
  Multiplexer #(.width(32)) multiplexer_39 (
    .in0({32{1'b0}}), .in1(32'h1), .out(multiplexer_39_out[31:0]), .sel(comparator_22_lt));
  Shifter #(.shift("ar"), .width(32)) shifter_10 (
    .in(argY[63:32]), .\dist (bitselector_7_out), .out(shifter_11_out[63:32]));
  Shifter #(.shift("ar"), .width(32)) shifter_11 (
    .in(argY[31:0]), .\dist (bitselector_6_out), .out(shifter_11_out[31:0]));
  Multiplier #(.mode("twosComplement"), .width(32)) multiplier_2 (
    .a(argY[63:32]), .b(argZ[63:32]), .out(multiplier_3_out[63:32]));  // open: cin, cout
  Multiplier #(.mode("twosComplement"), .width(32)) multiplier_3 (
    .a(argY[31:0]), .b(argZ[31:0]), .out(multiplier_3_out[31:0]));  // open: cin, cout
  assign bit_extender_22_out[63:32] = {{31{1'b0}}, subtractor_4_bout};  // Bit_Extender bit_extender_21
  assign bit_extender_22_out[31:0] = {{31{1'b0}}, subtractor_5_bout};  // Bit_Extender bit_extender_22
  assign bit_extender_23_out = {{27{1'b0}}, bitfinder_7_index};  // Bit_Extender bit_extender_23
  Multiplexer #(.width(32)) multiplexer_40 (
    .in0({32{1'b1}}), .in1(bit_extender_23_out), .out(multiplexer_41_out[63:32]), .sel(bitfinder_7_found));
  assign bit_extender_24_out = {{27{1'b0}}, bitfinder_8_index};  // Bit_Extender bit_extender_24
  Multiplexer #(.width(32)) multiplexer_41 (
    .in0({32{1'b1}}), .in1(bit_extender_24_out), .out(multiplexer_41_out[31:0]), .sel(bitfinder_8_found));
  FPMultiplier fpmultiplier_2 (.a(argY[63:32]), .b(argZ[63:32]), .out(fpmultiplier_3_out[63:32]));
  FPMultiplier fpmultiplier_3 (.a(argY[31:0]), .b(argZ[31:0]), .out(fpmultiplier_3_out[31:0]));
  // FPToInt #(.mode("floor"), .width(32)) fptoint_7: pin names not known; wires that end beside it: argY[63:32], fptoint_8_p2[63:32]
  // FPToInt #(.mode("floor"), .width(32)) fptoint_8: pin names not known; wires that end beside it: argY[31:0], fptoint_8_p2[31:0]
  Multiplexer #(.width(32)) multiplexer_42 (
    .in0({32{1'b0}}), .in1(32'h1), .out(multiplexer_44_out[63:32]), .sel(fpcomparator_3_p3));
  // FPComparator fpcomparator_3: pin names not known; wires that end beside it: argY[63:32], {32{1'b0}}, fpcomparator_3_p3, fpcomparator_3_p4
  // FPComparator fpcomparator_4: pin names not known; wires that end beside it: argY[31:0], {32{1'b0}}, fpcomparator_4_p3, fpcomparator_4_p4
  Multiplexer #(.width(32)) multiplexer_43 (
    .in0({32{1'b0}}), .in1(32'h1), .out(multiplexer_45_out[63:32]), .sel(fpcomparator_5_p3));
  // FPComparator fpcomparator_5: pin names not known; wires that end beside it: argY[63:32], argZ[63:32], fpcomparator_5_p3, fpcomparator_5_p4
  // FPComparator fpcomparator_6: pin names not known; wires that end beside it: argY[31:0], argZ[31:0], fpcomparator_6_p3, fpcomparator_6_p4
  Shifter #(.shift("rl"), .width(32)) shifter_12 (
    .in(argY[63:32]), .\dist (bitselector_7_out), .out(shifter_13_out[63:32]));
  Shifter #(.shift("rl"), .width(32)) shifter_13 (
    .in(argY[31:0]), .\dist (bitselector_6_out), .out(shifter_13_out[31:0]));
  Divider #(.mode("twosComplement"), .width(32)) divider_2 (
    .a(argY[63:32]), .b(argZ[63:32]), .out(divider_3_out[63:32]));  // open: upper, rem
  Divider #(.mode("twosComplement"), .width(32)) divider_3 (
    .a(argY[31:0]), .b(argZ[31:0]), .out(divider_3_out[31:0]));  // open: upper, rem
  Multiplier #(.mode("twosComplement"), .width(32)) multiplier_4 (
    .a(argY[63:32]), .b(argZ[63:32]), .cout(multiplier_5_cout[63:32]));  // open: out, cin
  Multiplier #(.mode("twosComplement"), .width(32)) multiplier_5 (
    .a(argY[31:0]), .b(argZ[31:0]), .cout(multiplier_5_cout[31:0]));  // open: out, cin
  BitFinder #(.\type ("low0"), .width(32)) bitfinder_9 (
    .in(argY[63:32]), .index(bitfinder_9_index), .found(bitfinder_9_found));
  BitFinder #(.\type ("low0"), .width(32)) bitfinder_10 (
    .in(argY[31:0]), .index(bitfinder_10_index), .found(bitfinder_10_found));
  FPDivider fpdivider_2 (.a(argY[63:32]), .b(argZ[63:32]), .out(fpdivider_3_out[63:32]));
  FPDivider fpdivider_3 (.a(argY[31:0]), .b(argZ[31:0]), .out(fpdivider_3_out[31:0]));
  // FPLogarithm fplogarithm_17: pin names not known; wires that end beside it: argY[63:32], argZ[63:32], fplogarithm_18_p3[63:32]
  // FPLogarithm fplogarithm_18: pin names not known; wires that end beside it: argY[31:0], argZ[31:0], fplogarithm_18_p3[31:0]
  // FPSquareRoot fpsquareroot_2: pin names not known; wires that end beside it: argY[63:32], fpsquareroot_3_p2[63:32]
  // FPSquareRoot fpsquareroot_3: pin names not known; wires that end beside it: argY[31:0], fpsquareroot_3_p2[31:0]
  // FPToInt #(.mode("ceil"), .width(32)) fptoint_9: pin names not known; wires that end beside it: argY[63:32], fptoint_10_p2[63:32]
  // FPToInt #(.mode("ceil"), .width(32)) fptoint_10: pin names not known; wires that end beside it: argY[31:0], fptoint_10_p2[31:0]
  Multiplexer #(.width(32)) multiplexer_44 (
    .in0({32{1'b0}}), .in1(32'h1), .out(multiplexer_44_out[31:0]), .sel(fpcomparator_4_p3));
  Multiplexer #(.width(32)) multiplexer_45 (
    .in0({32{1'b0}}), .in1(32'h1), .out(multiplexer_45_out[31:0]), .sel(fpcomparator_6_p3));
  Shifter #(.shift("rr"), .width(32)) shifter_14 (
    .in(argY[63:32]), .\dist (bitselector_7_out), .out(shifter_15_out[63:32]));
  Shifter #(.shift("rr"), .width(32)) shifter_15 (
    .in(argY[31:0]), .\dist (bitselector_6_out), .out(shifter_15_out[31:0]));
  Negator #(.width(32)) negator_2 (.in(argY[63:32]), .out(negator_3_out[63:32]));
  Negator #(.width(32)) negator_3 (.in(argY[31:0]), .out(negator_3_out[31:0]));
  assign bit_extender_25_out = {{27{1'b0}}, bitfinder_9_index};  // Bit_Extender bit_extender_25
  assign bit_extender_26_out = {{27{1'b0}}, bitfinder_10_index};  // Bit_Extender bit_extender_26
  // FPNegator fpnegator_2: pin names not known; wires that end beside it: argY[63:32], fpnegator_3_p2[63:32]
  // FPNegator fpnegator_3: pin names not known; wires that end beside it: argY[31:0], fpnegator_3_p2[31:0]
  // FPExponentiator fpexponentiator_3: pin names not known; wires that end beside it: argY[63:32], argZ[63:32], fpexponentiator_4_p3[63:32]
  // FPExponentiator fpexponentiator_4: pin names not known; wires that end beside it: argY[31:0], argZ[31:0], fpexponentiator_4_p3[31:0]
  // FPAbsolute fpabsolute_2: pin names not known; wires that end beside it: argY[31:0], fpabsolute_3_p2[63:32]
  // FPAbsolute fpabsolute_3: pin names not known; wires that end beside it: argY[63:32], fpabsolute_3_p2[31:0]
  // FPToInt #(.mode("truncate"), .width(32)) fptoint_11: pin names not known; wires that end beside it: argY[63:32], fptoint_12_p2[63:32]
  // FPToInt #(.mode("truncate"), .width(32)) fptoint_12: pin names not known; wires that end beside it: argY[31:0], fptoint_12_p2[31:0]
  Multiplexer #(.width(32)) multiplexer_46 (
    .in0({32{1'b0}}), .in1(32'h1), .out(multiplexer_50_out[63:32]), .sel(fpcomparator_3_p4));
  Multiplexer #(.width(32)) multiplexer_47 (
    .in0({32{1'b0}}), .in1(32'h1), .out(multiplexer_51_out[63:32]), .sel(fpcomparator_5_p4));
  Divider #(.mode("twosComplement"), .width(32)) divider_4 (
    .a(argY[63:32]), .b(argZ[63:32]), .rem(divider_5_rem[63:32]));  // open: out, upper
  Divider #(.mode("twosComplement"), .width(32)) divider_5 (
    .a(argY[31:0]), .b(argZ[31:0]), .rem(divider_5_rem[31:0]));  // open: out, upper
  Multiplexer #(.width(32)) multiplexer_48 (
    .in0({32{1'b1}}), .in1(bit_extender_25_out), .out(multiplexer_49_out[63:32]), .sel(bitfinder_9_found));
  Multiplexer #(.width(32)) multiplexer_49 (
    .in0({32{1'b1}}), .in1(bit_extender_26_out), .out(multiplexer_49_out[31:0]), .sel(bitfinder_10_found));
  Multiplexer #(.width(32)) multiplexer_50 (
    .in0({32{1'b0}}), .in1(32'h1), .out(multiplexer_50_out[31:0]), .sel(fpcomparator_4_p4));
  Multiplexer #(.width(32)) multiplexer_51 (
    .in0({32{1'b0}}), .in1(32'h1), .out(multiplexer_51_out[31:0]), .sel(fpcomparator_6_p4));
  Multiplexer #(.width(32)) multiplexer_52 (
    .in0(argX[63:32]), .in1(buffer_3_out), .out(multiplexer_53_out[63:32]), .sel(not_3_out));
  assign buffer_3_out = argY[63:32];  // Buffer buffer_3, 32 bits wide
  BitFinder #(.\type ("high0"), .width(32)) bitfinder_11 (
    .in(argY[63:32]), .index(bitfinder_11_index), .found(bitfinder_11_found));
  BitFinder #(.\type ("high0"), .width(32)) bitfinder_12 (
    .in(argY[31:0]), .index(bitfinder_12_index), .found(bitfinder_12_found));
  // FPClassificator fpclassificator_2: pin names not known; wires that end beside it: {32{1'b0}}, 32'h1, argY[63:32], fpclassificator_2_p4
  // FPClassificator fpclassificator_3: pin names not known; wires that end beside it: argY[31:0], fpclassificator_3_p2
  // FPClassificator fpclassificator_4: pin names not known; wires that end beside it: {32{1'b0}}, 32'h1, argY[63:32], fpclassificator_4_p4
  // FPClassificator fpclassificator_5: pin names not known; wires that end beside it: argY[31:0], fpclassificator_5_p2
  BitSelector #(.group(4), .width(16)) bitselector_8 (.in(argZ[15:0]), .out(bitselector_8_out), .sel(2'b00));
  BitSelector #(.group(4), .width(16)) bitselector_9 (.in(argZ[31:16]), .out(bitselector_9_out), .sel(2'b00));
  BitSelector #(.group(4), .width(16)) bitselector_10 (.in(argZ[47:32]), .out(bitselector_10_out), .sel(2'b00));
  BitSelector #(.group(4), .width(16)) bitselector_11 (.in(argZ[63:48]), .out(bitselector_11_out), .sel(2'b00));
  Multiplexer #(.width(32)) multiplexer_53 (
    .in0(argX[31:0]), .in1(buffer_4_out), .out(multiplexer_53_out[31:0]), .sel(not_4_out));
  assign buffer_4_out = argY[31:0];  // Buffer buffer_4, 32 bits wide
  not not_3 (not_3_out, comparator_23_eq);
  Comparator #(.mode("unsigned"), .width(32)) comparator_23 (
    .a(argZ[63:32]), .b({32{1'b0}}), .eq(comparator_23_eq));  // open: gt, lt
  not not_4 (not_4_out, comparator_24_eq);
  Comparator #(.mode("unsigned"), .width(32)) comparator_24 (
    .a(argZ[31:0]), .b({32{1'b0}}), .eq(comparator_24_eq));  // open: gt, lt
  assign bit_extender_27_out = {{27{1'b0}}, bitfinder_11_index};  // Bit_Extender bit_extender_27
  Multiplexer #(.width(32)) multiplexer_54 (
    .in0({32{1'b1}}), .in1(bit_extender_27_out), .out(multiplexer_55_out[63:32]), .sel(bitfinder_11_found));
  assign bit_extender_28_out = {{27{1'b0}}, bitfinder_12_index};  // Bit_Extender bit_extender_28
  Multiplexer #(.width(32)) multiplexer_55 (
    .in0({32{1'b1}}), .in1(bit_extender_28_out), .out(multiplexer_55_out[31:0]), .sel(bitfinder_12_found));
  FPAdder #(.fpwidth(16)) fpadder_4 (.a(argY[63:48]), .b(argZ[63:48]), .out(fpadder_7_out[63:48]));
  FPAdder #(.fpwidth(16)) fpadder_5 (.a(argY[47:32]), .b(argZ[47:32]), .out(fpadder_7_out[47:32]));
  FPAdder #(.fpwidth(16)) fpadder_6 (.a(argY[31:16]), .b(argZ[31:16]), .out(fpadder_7_out[31:16]));
  FPAdder #(.fpwidth(16)) fpadder_7 (.a(argY[15:0]), .b(argZ[15:0]), .out(fpadder_7_out[15:0]));
  // FPTrigonometry #(.fpwidth(16)) fptrigonometry_7: pin names not known; wires that end beside it: argY[63:48], fptrigonometry_10_p2[63:48], fptrigonometry_10_p3[63:48], fptrigonometry_10_p4[63:48]
  // FPTrigonometry #(.fpwidth(16)) fptrigonometry_8: pin names not known; wires that end beside it: argY[47:32], fptrigonometry_10_p2[47:32], fptrigonometry_10_p3[47:32], fptrigonometry_10_p4[47:32]
  // FPTrigonometry #(.fpwidth(16)) fptrigonometry_9: pin names not known; wires that end beside it: argY[31:16], fptrigonometry_10_p2[31:16], fptrigonometry_10_p3[31:16], fptrigonometry_10_p4[31:16]
  // FPTrigonometry #(.fpwidth(16)) fptrigonometry_10: pin names not known; wires that end beside it: argY[15:0], fptrigonometry_10_p2[15:0], fptrigonometry_10_p3[15:0], fptrigonometry_10_p4[15:0]
  // FPTrigonometry #(.fpwidth(16), .\type ("arc")) fptrigonometry_11: pin names not known; wires that end beside it: argY[63:48], fptrigonometry_14_p2[63:48], fptrigonometry_14_p3[63:48], fptrigonometry_14_p4[63:48]
  // FPTrigonometry #(.fpwidth(16), .\type ("arc")) fptrigonometry_12: pin names not known; wires that end beside it: argY[47:32], fptrigonometry_14_p2[47:32], fptrigonometry_14_p3[47:32], fptrigonometry_14_p4[47:32]
  // FPTrigonometry #(.fpwidth(16), .\type ("arc")) fptrigonometry_13: pin names not known; wires that end beside it: argY[31:16], fptrigonometry_14_p2[31:16], fptrigonometry_14_p3[31:16], fptrigonometry_14_p4[31:16]
  // FPTrigonometry #(.fpwidth(16), .\type ("arc")) fptrigonometry_14: pin names not known; wires that end beside it: argY[15:0], fptrigonometry_14_p2[15:0], fptrigonometry_14_p3[15:0], fptrigonometry_14_p4[15:0]
  // IntToFP #(.fpwidth(16), .width(16)) inttofp_4: pin names not known; wires that end beside it: argY[63:48], inttofp_7_p2[63:48]
  // IntToFP #(.fpwidth(16), .width(16)) inttofp_5: pin names not known; wires that end beside it: argY[47:32], inttofp_7_p2[47:32]
  // IntToFP #(.fpwidth(16), .width(16)) inttofp_6: pin names not known; wires that end beside it: argY[31:16], inttofp_7_p2[31:16]
  // IntToFP #(.fpwidth(16), .width(16)) inttofp_7: pin names not known; wires that end beside it: argY[15:0], inttofp_7_p2[15:0]
  assign bit_extender_30_out[63:32] = {{31{1'b0}}, fpclassificator_2_p4};  // Bit_Extender bit_extender_29
  assign bit_extender_30_out[31:0] = {{31{1'b0}}, fpclassificator_3_p2};  // Bit_Extender bit_extender_30
  assign bit_extender_32_out[63:32] = {{31{1'b0}}, fpclassificator_4_p4};  // Bit_Extender bit_extender_31
  assign bit_extender_32_out[31:0] = {{31{1'b0}}, fpclassificator_5_p2};  // Bit_Extender bit_extender_32
  Shifter #(.width(16)) shifter_16 (.in(argY[63:48]), .\dist (bitselector_11_out), .out(shifter_19_out[63:48]));
  Shifter #(.width(16)) shifter_17 (.in(argY[47:32]), .\dist (bitselector_10_out), .out(shifter_19_out[47:32]));
  Shifter #(.width(16)) shifter_18 (.in(argY[31:16]), .\dist (bitselector_9_out), .out(shifter_19_out[31:16]));
  Shifter #(.width(16)) shifter_19 (.in(argY[15:0]), .\dist (bitselector_8_out), .out(shifter_19_out[15:0]));
  Adder #(.width(16)) adder_6 (.a(argY[63:48]), .b(argZ[63:48]), .out(adder_9_out[63:48]));  // open: cin, cout
  Adder #(.width(16)) adder_7 (.a(argY[47:32]), .b(argZ[47:32]), .out(adder_9_out[47:32]));  // open: cin, cout
  Adder #(.width(16)) adder_8 (.a(argY[31:16]), .b(argZ[31:16]), .out(adder_9_out[31:16]));  // open: cin, cout
  Adder #(.width(16)) adder_9 (.a(argY[15:0]), .b(argZ[15:0]), .out(adder_9_out[15:0]));  // open: cin, cout
  // FPMinMax fpminmax_2: pin names not known; wires that end beside it: argY[63:32], argZ[63:32], fpminmax_3_p3[63:32]
  // FPMinMax fpminmax_3: pin names not known; wires that end beside it: argY[31:0], argZ[31:0], fpminmax_3_p3[31:0]
  BitAdder #(.width(32)) bitadder_2 (.in0(argY[63:32]), .out(bitadder_2_out));
  BitAdder #(.width(32)) bitadder_3 (.in0(argY[31:0]), .out(bitadder_3_out));
  assign bit_extender_34_out[63:32] = {{26{1'b0}}, bitadder_2_out};  // Bit_Extender bit_extender_33
  assign bit_extender_34_out[31:0] = {{26{1'b0}}, bitadder_3_out};  // Bit_Extender bit_extender_34
  FPSubtractor #(.fpwidth(16)) fpsubtractor_4 (.a(argY[63:48]), .b(argZ[63:48]), .out(fpsubtractor_7_out[63:48]));
  FPSubtractor #(.fpwidth(16)) fpsubtractor_5 (.a(argY[47:32]), .b(argZ[47:32]), .out(fpsubtractor_7_out[47:32]));
  FPSubtractor #(.fpwidth(16)) fpsubtractor_6 (.a(argY[31:16]), .b(argZ[31:16]), .out(fpsubtractor_7_out[31:16]));
  FPSubtractor #(.fpwidth(16)) fpsubtractor_7 (.a(argY[15:0]), .b(argZ[15:0]), .out(fpsubtractor_7_out[15:0]));
  // FPToInt #(.fpwidth(16), .width(16)) fptoint_13: pin names not known; wires that end beside it: argY[63:48], fptoint_16_p2[63:48]
  // FPToInt #(.fpwidth(16), .width(16)) fptoint_14: pin names not known; wires that end beside it: argY[47:32], fptoint_16_p2[47:32]
  // FPToInt #(.fpwidth(16), .width(16)) fptoint_15: pin names not known; wires that end beside it: argY[31:16], fptoint_16_p2[31:16]
  // FPToInt #(.fpwidth(16), .width(16)) fptoint_16: pin names not known; wires that end beside it: argY[15:0], fptoint_16_p2[15:0]
  // FPExponentiator #(.mode("exp")) fpexponentiator_5: pin names not known; wires that end beside it: argY[63:32], fpexponentiator_6_p2[63:32]
  // FPExponentiator #(.mode("exp")) fpexponentiator_6: pin names not known; wires that end beside it: argY[31:0], fpexponentiator_6_p2[31:0]
  Subtractor #(.width(16)) subtractor_6 (
    .a(argY[63:48]), .b(argZ[63:48]), .out(subtractor_9_out[63:48]));  // open: bin, bout
  Subtractor #(.width(16)) subtractor_7 (
    .a(argY[47:32]), .b(argZ[47:32]), .out(subtractor_9_out[47:32]));  // open: bin, bout
  Subtractor #(.width(16)) subtractor_8 (
    .a(argY[31:16]), .b(argZ[31:16]), .out(subtractor_9_out[31:16]));  // open: bin, bout
  Subtractor #(.width(16)) subtractor_9 (
    .a(argY[15:0]), .b(argZ[15:0]), .out(subtractor_9_out[15:0]));  // open: bin, bout
  // FPMinMax fpminmax_4: pin names not known; wires that end beside it: argY[63:32], argZ[63:32], fpminmax_5_p3[63:32]
  // FPMinMax fpminmax_5: pin names not known; wires that end beside it: argY[31:0], argZ[31:0], fpminmax_5_p3[31:0]
  Multiplexer #(.width(16)) multiplexer_56 (
    .in0({16{1'b0}}), .in1(16'h1), .out(multiplexer_59_out[63:48]), .sel(comparator_25_eq));
  Comparator #(.width(16)) comparator_25 (
    .a(argY[63:48]), .b({16{1'b0}}), .eq(comparator_25_eq), .lt(comparator_25_lt));  // open: gt
  Comparator #(.width(16)) comparator_26 (
    .a(argY[47:32]), .b({16{1'b0}}), .eq(comparator_26_eq), .lt(comparator_26_lt));  // open: gt
  Comparator #(.width(16)) comparator_27 (
    .a(argY[31:16]), .b({16{1'b0}}), .eq(comparator_27_eq), .lt(comparator_27_lt));  // open: gt
  Comparator #(.width(16)) comparator_28 (
    .a(argY[15:0]), .b({16{1'b0}}), .eq(comparator_28_eq), .lt(comparator_28_lt));  // open: gt
  Shifter #(.shift("lr"), .width(16)) shifter_20 (
    .in(argY[63:48]), .\dist (bitselector_11_out), .out(shifter_23_out[63:48]));
  Shifter #(.shift("lr"), .width(16)) shifter_21 (
    .in(argY[47:32]), .\dist (bitselector_10_out), .out(shifter_23_out[47:32]));
  Shifter #(.shift("lr"), .width(16)) shifter_22 (
    .in(argY[31:16]), .\dist (bitselector_9_out), .out(shifter_23_out[31:16]));
  Shifter #(.shift("lr"), .width(16)) shifter_23 (
    .in(argY[15:0]), .\dist (bitselector_8_out), .out(shifter_23_out[15:0]));
  Adder #(.width(16)) adder_10 (.a(argY[63:48]), .b(argZ[63:48]), .cout(adder_10_cout));  // open: out, cin
  Adder #(.width(16)) adder_11 (.a(argY[47:32]), .b(argZ[47:32]), .cout(adder_11_cout));  // open: out, cin
  Adder #(.width(16)) adder_12 (.a(argY[31:16]), .b(argZ[31:16]), .cout(adder_12_cout));  // open: out, cin
  Adder #(.width(16)) adder_13 (.a(argY[15:0]), .b(argZ[15:0]), .cout(adder_13_cout));  // open: out, cin
  Multiplexer #(.width(16)) multiplexer_57 (
    .in0({16{1'b0}}), .in1(16'h1), .out(multiplexer_59_out[47:32]), .sel(comparator_26_eq));
  Multiplier #(.mode("twosComplement"), .width(16)) multiplier_6 (
    .a(argY[63:48]), .b(argZ[63:48]), .out(multiplier_9_out[63:48]));  // open: cin, cout
  Multiplier #(.mode("twosComplement"), .width(16)) multiplier_7 (
    .a(argY[47:32]), .b(argZ[47:32]), .out(multiplier_9_out[47:32]));  // open: cin, cout
  Multiplier #(.mode("twosComplement"), .width(16)) multiplier_8 (
    .a(argY[31:16]), .b(argZ[31:16]), .out(multiplier_9_out[31:16]));  // open: cin, cout
  Multiplier #(.mode("twosComplement"), .width(16)) multiplier_9 (
    .a(argY[15:0]), .b(argZ[15:0]), .out(multiplier_9_out[15:0]));  // open: cin, cout
  assign bit_extender_38_out[63:48] = {{15{1'b0}}, adder_10_cout};  // Bit_Extender bit_extender_35
  assign bit_extender_38_out[47:32] = {{15{1'b0}}, adder_11_cout};  // Bit_Extender bit_extender_36
  assign bit_extender_38_out[31:16] = {{15{1'b0}}, adder_12_cout};  // Bit_Extender bit_extender_37
  assign bit_extender_38_out[15:0] = {{15{1'b0}}, adder_13_cout};  // Bit_Extender bit_extender_38
  FPMultiplier #(.fpwidth(16)) fpmultiplier_4 (.a(argY[63:48]), .b(argZ[63:48]), .out(fpmultiplier_7_out[63:48]));
  FPMultiplier #(.fpwidth(16)) fpmultiplier_5 (.a(argY[47:32]), .b(argZ[47:32]), .out(fpmultiplier_7_out[47:32]));
  FPMultiplier #(.fpwidth(16)) fpmultiplier_6 (.a(argY[31:16]), .b(argZ[31:16]), .out(fpmultiplier_7_out[31:16]));
  FPMultiplier #(.fpwidth(16)) fpmultiplier_7 (.a(argY[15:0]), .b(argZ[15:0]), .out(fpmultiplier_7_out[15:0]));
  // FPToInt #(.fpwidth(16), .mode("floor"), .width(16)) fptoint_17: pin names not known; wires that end beside it: argY[63:48], fptoint_20_p2[63:48]
  // FPToInt #(.fpwidth(16), .mode("floor"), .width(16)) fptoint_18: pin names not known; wires that end beside it: argY[47:32], fptoint_20_p2[47:32]
  // FPToInt #(.fpwidth(16), .mode("floor"), .width(16)) fptoint_19: pin names not known; wires that end beside it: argY[31:16], fptoint_20_p2[31:16]
  // FPToInt #(.fpwidth(16), .mode("floor"), .width(16)) fptoint_20: pin names not known; wires that end beside it: argY[15:0], fptoint_20_p2[15:0]
  Multiplexer #(.width(16)) multiplexer_58 (
    .in0({16{1'b0}}), .in1(16'h1), .out(multiplexer_59_out[31:16]), .sel(comparator_27_eq));
  Comparator #(.width(16)) comparator_29 (
    .a(argY[63:48]), .b(argZ[63:48]), .eq(comparator_29_eq), .lt(comparator_29_lt));  // open: gt
  Comparator #(.width(16)) comparator_30 (
    .a(argY[47:32]), .b(argZ[47:32]), .eq(comparator_30_eq), .lt(comparator_30_lt));  // open: gt
  Comparator #(.width(16)) comparator_31 (
    .a(argY[31:16]), .b(argZ[31:16]), .eq(comparator_31_eq), .lt(comparator_31_lt));  // open: gt
  Comparator #(.width(16)) comparator_32 (
    .a(argY[15:0]), .b(argZ[15:0]), .eq(comparator_32_eq), .lt(comparator_32_lt));  // open: gt
  Shifter #(.shift("ar"), .width(16)) shifter_24 (
    .in(argY[63:48]), .\dist (bitselector_11_out), .out(shifter_27_out[63:48]));
  Shifter #(.shift("ar"), .width(16)) shifter_25 (
    .in(argY[47:32]), .\dist (bitselector_10_out), .out(shifter_27_out[47:32]));
  Shifter #(.shift("ar"), .width(16)) shifter_26 (
    .in(argY[31:16]), .\dist (bitselector_9_out), .out(shifter_27_out[31:16]));
  Shifter #(.shift("ar"), .width(16)) shifter_27 (
    .in(argY[15:0]), .\dist (bitselector_8_out), .out(shifter_27_out[15:0]));
  Multiplexer #(.width(16)) multiplexer_59 (
    .in0({16{1'b0}}), .in1(16'h1), .out(multiplexer_59_out[15:0]), .sel(comparator_28_eq));
  Multiplexer #(.width(16)) multiplexer_60 (
    .in0({16{1'b0}}), .in1(16'h1), .out(multiplexer_71_out[63:48]), .sel(comparator_25_lt));
  Multiplexer #(.width(16)) multiplexer_61 (
    .in0({16{1'b0}}), .in1(16'h1), .out(multiplexer_66_out[63:48]), .sel(comparator_29_eq));
  Subtractor #(.width(16)) subtractor_10 (
    .a(argY[63:48]), .b(argZ[63:48]), .bout(subtractor_10_bout));  // open: out, bin
  Subtractor #(.width(16)) subtractor_11 (
    .a(argY[47:32]), .b(argZ[47:32]), .bout(subtractor_11_bout));  // open: out, bin
  Subtractor #(.width(16)) subtractor_12 (
    .a(argY[31:16]), .b(argZ[31:16]), .bout(subtractor_12_bout));  // open: out, bin
  Subtractor #(.width(16)) subtractor_13 (.a(argY[15:0]), .b(argZ[15:0]), .bout(subtractor_13_bout));  // open: out, bin
  BitFinder #(.width(16)) bitfinder_13 (.in(argY[63:48]), .index(bitfinder_13_index), .found(bitfinder_13_found));
  BitFinder #(.width(16)) bitfinder_14 (.in(argY[47:32]), .index(bitfinder_14_index), .found(bitfinder_14_found));
  BitFinder #(.width(16)) bitfinder_15 (.in(argY[31:16]), .index(bitfinder_15_index), .found(bitfinder_15_found));
  BitFinder #(.width(16)) bitfinder_16 (.in(argY[15:0]), .index(bitfinder_16_index), .found(bitfinder_16_found));
  FPDivider #(.fpwidth(16)) fpdivider_4 (.a(argY[63:48]), .b(argZ[63:48]), .out(fpdivider_7_out[63:48]));
  FPDivider #(.fpwidth(16)) fpdivider_5 (.a(argY[47:32]), .b(argZ[47:32]), .out(fpdivider_7_out[47:32]));
  FPDivider #(.fpwidth(16)) fpdivider_6 (.a(argY[31:16]), .b(argZ[31:16]), .out(fpdivider_7_out[31:16]));
  FPDivider #(.fpwidth(16)) fpdivider_7 (.a(argY[15:0]), .b(argZ[15:0]), .out(fpdivider_7_out[15:0]));
  // FPLogarithm #(.fpwidth(16)) fplogarithm_19: pin names not known; wires that end beside it: argY[63:48], argZ[63:48], fplogarithm_22_p3[63:48]
  // FPLogarithm #(.fpwidth(16)) fplogarithm_20: pin names not known; wires that end beside it: argY[47:32], argZ[47:32], fplogarithm_22_p3[47:32]
  // FPLogarithm #(.fpwidth(16)) fplogarithm_21: pin names not known; wires that end beside it: argY[31:16], argZ[31:16], fplogarithm_22_p3[31:16]
  // FPLogarithm #(.fpwidth(16)) fplogarithm_22: pin names not known; wires that end beside it: argY[15:0], argZ[15:0], fplogarithm_22_p3[15:0]
  // FPSquareRoot #(.fpwidth(16)) fpsquareroot_4: pin names not known; wires that end beside it: argY[63:48], fpsquareroot_7_p2[63:48]
  // FPSquareRoot #(.fpwidth(16)) fpsquareroot_5: pin names not known; wires that end beside it: argY[47:32], fpsquareroot_7_p2[47:32]
  // FPSquareRoot #(.fpwidth(16)) fpsquareroot_6: pin names not known; wires that end beside it: argY[31:16], fpsquareroot_7_p2[31:16]
  // FPSquareRoot #(.fpwidth(16)) fpsquareroot_7: pin names not known; wires that end beside it: argY[15:0], fpsquareroot_7_p2[15:0]
  // FPToInt #(.fpwidth(16), .mode("ceil"), .width(16)) fptoint_21: pin names not known; wires that end beside it: argY[63:48], fptoint_24_p2[63:48]
  // FPToInt #(.fpwidth(16), .mode("ceil"), .width(16)) fptoint_22: pin names not known; wires that end beside it: argY[47:32], fptoint_24_p2[47:32]
  // FPToInt #(.fpwidth(16), .mode("ceil"), .width(16)) fptoint_23: pin names not known; wires that end beside it: argY[31:16], fptoint_24_p2[31:16]
  // FPToInt #(.fpwidth(16), .mode("ceil"), .width(16)) fptoint_24: pin names not known; wires that end beside it: argY[15:0], fptoint_24_p2[15:0]
  Multiplexer #(.width(16)) multiplexer_62 (
    .in0({16{1'b0}}), .in1(16'h1), .out(multiplexer_71_out[47:32]), .sel(comparator_26_lt));
  Multiplexer #(.width(16)) multiplexer_63 (
    .in0({16{1'b0}}), .in1(16'h1), .out(multiplexer_66_out[47:32]), .sel(comparator_30_eq));
  Multiplexer #(.width(16)) multiplexer_64 (
    .in0({16{1'b0}}), .in1(16'h1), .out(multiplexer_66_out[31:16]), .sel(comparator_31_eq));
  Shifter #(.shift("rl"), .width(16)) shifter_28 (
    .in(argY[63:48]), .\dist (bitselector_11_out), .out(shifter_31_out[63:48]));
  Shifter #(.shift("rl"), .width(16)) shifter_29 (
    .in(argY[47:32]), .\dist (bitselector_10_out), .out(shifter_31_out[47:32]));
  Shifter #(.shift("rl"), .width(16)) shifter_30 (
    .in(argY[31:16]), .\dist (bitselector_9_out), .out(shifter_31_out[31:16]));
  Shifter #(.shift("rl"), .width(16)) shifter_31 (
    .in(argY[15:0]), .\dist (bitselector_8_out), .out(shifter_31_out[15:0]));
  Divider #(.mode("twosComplement"), .width(16)) divider_6 (
    .a(argY[63:48]), .b(argZ[63:48]), .out(divider_9_out[63:48]));  // open: upper, rem
  Divider #(.mode("twosComplement"), .width(16)) divider_7 (
    .a(argY[47:32]), .b(argZ[47:32]), .out(divider_9_out[47:32]));  // open: upper, rem
  Divider #(.mode("twosComplement"), .width(16)) divider_8 (
    .a(argY[31:16]), .b(argZ[31:16]), .out(divider_9_out[31:16]));  // open: upper, rem
  Divider #(.mode("twosComplement"), .width(16)) divider_9 (
    .a(argY[15:0]), .b(argZ[15:0]), .out(divider_9_out[15:0]));  // open: upper, rem
  assign bit_extender_42_out[63:48] = {{15{1'b0}}, subtractor_10_bout};  // Bit_Extender bit_extender_39
  assign bit_extender_42_out[47:32] = {{15{1'b0}}, subtractor_11_bout};  // Bit_Extender bit_extender_40
  assign bit_extender_42_out[31:16] = {{15{1'b0}}, subtractor_12_bout};  // Bit_Extender bit_extender_41
  assign bit_extender_42_out[15:0] = {{15{1'b0}}, subtractor_13_bout};  // Bit_Extender bit_extender_42
  assign bit_extender_43_out = {{12{1'b0}}, bitfinder_13_index};  // Bit_Extender bit_extender_43
  assign bit_extender_44_out = {{12{1'b0}}, bitfinder_14_index};  // Bit_Extender bit_extender_44
  assign bit_extender_45_out = {{12{1'b0}}, bitfinder_15_index};  // Bit_Extender bit_extender_45
  assign bit_extender_46_out = {{12{1'b0}}, bitfinder_16_index};  // Bit_Extender bit_extender_46
  Multiplexer #(.width(16)) multiplexer_65 (
    .in0({16{1'b0}}), .in1(16'h1), .out(multiplexer_71_out[31:16]), .sel(comparator_27_lt));
  Multiplexer #(.width(16)) multiplexer_66 (
    .in0({16{1'b0}}), .in1(16'h1), .out(multiplexer_66_out[15:0]), .sel(comparator_32_eq));
  Multiplexer #(.width(16)) multiplexer_67 (
    .in0({16{1'b1}}), .in1(bit_extender_43_out), .out(multiplexer_70_out[63:48]), .sel(bitfinder_13_found));
  Multiplexer #(.width(16)) multiplexer_68 (
    .in0({16{1'b1}}), .in1(bit_extender_44_out), .out(multiplexer_70_out[47:32]), .sel(bitfinder_14_found));
  Multiplexer #(.width(16)) multiplexer_69 (
    .in0({16{1'b1}}), .in1(bit_extender_45_out), .out(multiplexer_70_out[31:16]), .sel(bitfinder_15_found));
  Multiplexer #(.width(16)) multiplexer_70 (
    .in0({16{1'b1}}), .in1(bit_extender_46_out), .out(multiplexer_70_out[15:0]), .sel(bitfinder_16_found));
  // FPNegator #(.fpwidth(16)) fpnegator_4: pin names not known; wires that end beside it: argY[63:48], fpnegator_7_p2[63:48]
  // FPNegator #(.fpwidth(16)) fpnegator_5: pin names not known; wires that end beside it: argY[47:32], fpnegator_7_p2[47:32]
  // FPNegator #(.fpwidth(16)) fpnegator_6: pin names not known; wires that end beside it: argY[31:16], fpnegator_7_p2[31:16]
  // FPNegator #(.fpwidth(16)) fpnegator_7: pin names not known; wires that end beside it: argY[15:0], fpnegator_7_p2[15:0]
  // FPExponentiator #(.fpwidth(16)) fpexponentiator_7: pin names not known; wires that end beside it: argY[63:48], argZ[63:48], fpexponentiator_10_p3[63:48]
  // FPExponentiator #(.fpwidth(16)) fpexponentiator_8: pin names not known; wires that end beside it: argY[47:32], argZ[47:32], fpexponentiator_10_p3[47:32]
  // FPExponentiator #(.fpwidth(16)) fpexponentiator_9: pin names not known; wires that end beside it: argY[31:16], argZ[31:16], fpexponentiator_10_p3[31:16]
  // FPExponentiator #(.fpwidth(16)) fpexponentiator_10: pin names not known; wires that end beside it: argY[15:0], argZ[15:0], fpexponentiator_10_p3[15:0]
  // FPAbsolute #(.fpwidth(16)) fpabsolute_4: pin names not known; wires that end beside it: argY[63:48], fpabsolute_7_p2[63:48]
  // FPAbsolute #(.fpwidth(16)) fpabsolute_5: pin names not known; wires that end beside it: argY[47:32], fpabsolute_7_p2[47:32]
  // FPAbsolute #(.fpwidth(16)) fpabsolute_6: pin names not known; wires that end beside it: argY[31:16], fpabsolute_7_p2[31:16]
  // FPAbsolute #(.fpwidth(16)) fpabsolute_7: pin names not known; wires that end beside it: argY[15:0], fpabsolute_7_p2[15:0]
  // FPToInt #(.fpwidth(16), .mode("truncate"), .width(16)) fptoint_25: pin names not known; wires that end beside it: argY[63:48], fptoint_28_p2[63:48]
  // FPToInt #(.fpwidth(16), .mode("truncate"), .width(16)) fptoint_26: pin names not known; wires that end beside it: argY[47:32], fptoint_28_p2[47:32]
  // FPToInt #(.fpwidth(16), .mode("truncate"), .width(16)) fptoint_27: pin names not known; wires that end beside it: argY[31:16], fptoint_28_p2[31:16]
  // FPToInt #(.fpwidth(16), .mode("truncate"), .width(16)) fptoint_28: pin names not known; wires that end beside it: argY[15:0], fptoint_28_p2[15:0]
  Multiplexer #(.width(16)) multiplexer_71 (
    .in0({16{1'b0}}), .in1(16'h1), .out(multiplexer_71_out[15:0]), .sel(comparator_28_lt));
  Multiplexer #(.width(16)) multiplexer_72 (
    .in0({16{1'b0}}), .in1(16'h1), .out(multiplexer_77_out[63:48]), .sel(comparator_29_lt));
  Shifter #(.shift("rr"), .width(16)) shifter_32 (
    .in(argY[63:48]), .\dist (bitselector_11_out), .out(shifter_35_out[63:48]));
  Shifter #(.shift("rr"), .width(16)) shifter_33 (
    .in(argY[47:32]), .\dist (bitselector_10_out), .out(shifter_35_out[47:32]));
  Shifter #(.shift("rr"), .width(16)) shifter_34 (
    .in(argY[31:16]), .\dist (bitselector_9_out), .out(shifter_35_out[31:16]));
  Shifter #(.shift("rr"), .width(16)) shifter_35 (
    .in(argY[15:0]), .\dist (bitselector_8_out), .out(shifter_35_out[15:0]));
  Negator #(.width(16)) negator_4 (.in(argY[63:48]), .out(negator_7_out[63:48]));
  Negator #(.width(16)) negator_5 (.in(argY[47:32]), .out(negator_7_out[47:32]));
  Negator #(.width(16)) negator_6 (.in(argY[31:16]), .out(negator_7_out[31:16]));
  Negator #(.width(16)) negator_7 (.in(argY[15:0]), .out(negator_7_out[15:0]));
  Multiplier #(.mode("twosComplement"), .width(16)) multiplier_10 (
    .a(argY[63:48]), .b(argZ[63:48]), .cout(multiplier_13_cout[63:48]));  // open: out, cin
  Multiplier #(.mode("twosComplement"), .width(16)) multiplier_11 (
    .a(argY[47:32]), .b(argZ[47:32]), .cout(multiplier_13_cout[47:32]));  // open: out, cin
  Multiplier #(.mode("twosComplement"), .width(16)) multiplier_12 (
    .a(argY[31:16]), .b(argZ[31:16]), .cout(multiplier_13_cout[31:16]));  // open: out, cin
  Multiplier #(.mode("twosComplement"), .width(16)) multiplier_13 (
    .a(argY[15:0]), .b(argZ[15:0]), .cout(multiplier_13_cout[15:0]));  // open: out, cin
  BitFinder #(.\type ("high1"), .width(16)) bitfinder_17 (
    .in(argY[63:48]), .index(bitfinder_17_index), .found(bitfinder_17_found));
  BitFinder #(.\type ("high1"), .width(16)) bitfinder_18 (
    .in(argY[47:32]), .index(bitfinder_18_index), .found(bitfinder_18_found));
  BitFinder #(.\type ("high1"), .width(16)) bitfinder_19 (
    .in(argY[31:16]), .index(bitfinder_19_index), .found(bitfinder_19_found));
  BitFinder #(.\type ("high1"), .width(16)) bitfinder_20 (
    .in(argY[15:0]), .index(bitfinder_20_index), .found(bitfinder_20_found));
  Multiplexer #(.width(16)) multiplexer_73 (
    .in0({16{1'b0}}), .in1(16'h1), .out(multiplexer_83_out[63:48]), .sel(fpcomparator_7_p3));
  // FPComparator #(.fpwidth(16)) fpcomparator_7: pin names not known; wires that end beside it: argY[63:48], {16{1'b0}}, fpcomparator_7_p3, fpcomparator_7_p4
  // FPComparator #(.fpwidth(16)) fpcomparator_8: pin names not known; wires that end beside it: argY[47:32], {16{1'b0}}, fpcomparator_8_p3, fpcomparator_8_p4
  // FPComparator #(.fpwidth(16)) fpcomparator_9: pin names not known; wires that end beside it: argY[31:16], {16{1'b0}}, fpcomparator_9_p3, fpcomparator_9_p4
  // FPComparator #(.fpwidth(16)) fpcomparator_10: pin names not known; wires that end beside it: argY[15:0], {16{1'b0}}, fpcomparator_10_p3, fpcomparator_10_p4
  Multiplexer #(.width(16)) multiplexer_74 (
    .in0({16{1'b0}}), .in1(16'h1), .out(multiplexer_77_out[47:32]), .sel(comparator_30_lt));
  Multiplexer #(.width(16)) multiplexer_75 (
    .in0({16{1'b0}}), .in1(16'h1), .out(multiplexer_77_out[31:16]), .sel(comparator_31_lt));
  assign bit_extender_47_out = {{12{1'b0}}, bitfinder_17_index};  // Bit_Extender bit_extender_47
  assign bit_extender_48_out = {{12{1'b0}}, bitfinder_18_index};  // Bit_Extender bit_extender_48
  assign bit_extender_49_out = {{12{1'b0}}, bitfinder_19_index};  // Bit_Extender bit_extender_49
  assign bit_extender_50_out = {{12{1'b0}}, bitfinder_20_index};  // Bit_Extender bit_extender_50
  // FPMinMax #(.fpwidth(16)) fpminmax_6: pin names not known; wires that end beside it: argY[63:48], argZ[63:48], fpminmax_9_p3[63:48]
  // FPMinMax #(.fpwidth(16)) fpminmax_7: pin names not known; wires that end beside it: argY[47:32], argZ[47:32], fpminmax_9_p3[47:32]
  // FPMinMax #(.fpwidth(16)) fpminmax_8: pin names not known; wires that end beside it: argY[31:16], argZ[31:16], fpminmax_9_p3[31:16]
  // FPMinMax #(.fpwidth(16)) fpminmax_9: pin names not known; wires that end beside it: argY[15:0], argZ[15:0], fpminmax_9_p3[15:0]
  // FPMinMax #(.fpwidth(16)) fpminmax_10: pin names not known; wires that end beside it: argY[63:48], argZ[63:48], fpminmax_13_p3[63:48]
  // FPMinMax #(.fpwidth(16)) fpminmax_11: pin names not known; wires that end beside it: argY[47:32], argZ[47:32], fpminmax_13_p3[47:32]
  // FPMinMax #(.fpwidth(16)) fpminmax_12: pin names not known; wires that end beside it: argY[31:16], argZ[31:16], fpminmax_13_p3[31:16]
  // FPMinMax #(.fpwidth(16)) fpminmax_13: pin names not known; wires that end beside it: argY[15:0], argZ[15:0], fpminmax_13_p3[15:0]
  Multiplexer #(.width(16)) multiplexer_76 (
    .in0({16{1'b0}}), .in1(16'h1), .out(multiplexer_83_out[47:32]), .sel(fpcomparator_8_p3));
  Multiplexer #(.width(16)) multiplexer_77 (
    .in0({16{1'b0}}), .in1(16'h1), .out(multiplexer_77_out[15:0]), .sel(comparator_32_lt));
  // FPExponentiator #(.fpwidth(16), .mode("exp")) fpexponentiator_11: pin names not known; wires that end beside it: argY[63:48], fpexponentiator_14_p2[63:48]
  // FPExponentiator #(.fpwidth(16), .mode("exp")) fpexponentiator_12: pin names not known; wires that end beside it: argY[47:32], fpexponentiator_14_p2[47:32]
  // FPExponentiator #(.fpwidth(16), .mode("exp")) fpexponentiator_13: pin names not known; wires that end beside it: argY[31:16], fpexponentiator_14_p2[31:16]
  // FPExponentiator #(.fpwidth(16), .mode("exp")) fpexponentiator_14: pin names not known; wires that end beside it: argY[15:0], fpexponentiator_14_p2[15:0]
  Divider #(.mode("twosComplement"), .width(16)) divider_10 (
    .a(argY[63:48]), .b(argZ[63:48]), .rem(divider_13_rem[63:48]));  // open: out, upper
  Divider #(.mode("twosComplement"), .width(16)) divider_11 (
    .a(argY[47:32]), .b(argZ[47:32]), .rem(divider_13_rem[47:32]));  // open: out, upper
  Divider #(.mode("twosComplement"), .width(16)) divider_12 (
    .a(argY[31:16]), .b(argZ[31:16]), .rem(divider_13_rem[31:16]));  // open: out, upper
  Divider #(.mode("twosComplement"), .width(16)) divider_13 (
    .a(argY[15:0]), .b(argZ[15:0]), .rem(divider_13_rem[15:0]));  // open: out, upper
  Multiplexer #(.width(16)) multiplexer_78 (
    .in0({16{1'b1}}), .in1(bit_extender_47_out), .out(multiplexer_81_out[63:48]), .sel(bitfinder_17_found));
  Multiplexer #(.width(16)) multiplexer_79 (
    .in0({16{1'b1}}), .in1(bit_extender_48_out), .out(multiplexer_81_out[47:32]), .sel(bitfinder_18_found));
  Multiplexer #(.width(16)) multiplexer_80 (
    .in0({16{1'b1}}), .in1(bit_extender_49_out), .out(multiplexer_81_out[31:16]), .sel(bitfinder_19_found));
  Multiplexer #(.width(16)) multiplexer_81 (
    .in0({16{1'b1}}), .in1(bit_extender_50_out), .out(multiplexer_81_out[15:0]), .sel(bitfinder_20_found));
  Multiplexer #(.width(16)) multiplexer_82 (
    .in0({16{1'b0}}), .in1(16'h1), .out(multiplexer_83_out[31:16]), .sel(fpcomparator_9_p3));
  BitFinder #(.\type ("low0"), .width(16)) bitfinder_21 (
    .in(argY[63:48]), .index(bitfinder_21_index), .found(bitfinder_21_found));
  BitFinder #(.\type ("low0"), .width(16)) bitfinder_22 (
    .in(argY[47:32]), .index(bitfinder_22_index), .found(bitfinder_22_found));
  BitFinder #(.\type ("low0"), .width(16)) bitfinder_23 (
    .in(argY[31:16]), .index(bitfinder_23_index), .found(bitfinder_23_found));
  BitFinder #(.\type ("low0"), .width(16)) bitfinder_24 (
    .in(argY[15:0]), .index(bitfinder_24_index), .found(bitfinder_24_found));
  // FPTrigonometry #(.fpwidth(8), .\type ("arc")) fptrigonometry_15: pin names not known; wires that end beside it: argY[63:56], fptrigonometry_22_p2[63:56], fptrigonometry_22_p3[63:56], fptrigonometry_22_p4[63:56]
  // FPTrigonometry #(.fpwidth(8), .\type ("arc")) fptrigonometry_16: pin names not known; wires that end beside it: argY[55:48], fptrigonometry_22_p2[55:48], fptrigonometry_22_p3[55:48], fptrigonometry_22_p4[55:48]
  // FPTrigonometry #(.fpwidth(8), .\type ("arc")) fptrigonometry_17: pin names not known; wires that end beside it: argY[47:40], fptrigonometry_22_p2[47:40], fptrigonometry_22_p3[47:40], fptrigonometry_22_p4[47:40]
  // FPTrigonometry #(.fpwidth(8), .\type ("arc")) fptrigonometry_18: pin names not known; wires that end beside it: argY[39:32], fptrigonometry_22_p2[39:32], fptrigonometry_22_p3[39:32], fptrigonometry_22_p4[39:32]
  // FPTrigonometry #(.fpwidth(8), .\type ("arc")) fptrigonometry_19: pin names not known; wires that end beside it: argY[31:24], fptrigonometry_22_p2[31:24], fptrigonometry_22_p3[31:24], fptrigonometry_22_p4[31:24]
  // FPTrigonometry #(.fpwidth(8), .\type ("arc")) fptrigonometry_20: pin names not known; wires that end beside it: argY[23:16], fptrigonometry_22_p2[23:16], fptrigonometry_22_p3[23:16], fptrigonometry_22_p4[23:16]
  // FPTrigonometry #(.fpwidth(8), .\type ("arc")) fptrigonometry_21: pin names not known; wires that end beside it: argY[15:8], fptrigonometry_22_p2[15:8], fptrigonometry_22_p3[15:8], fptrigonometry_22_p4[15:8]
  // FPTrigonometry #(.fpwidth(8), .\type ("arc")) fptrigonometry_22: pin names not known; wires that end beside it: argY[7:0], fptrigonometry_22_p2[7:0], fptrigonometry_22_p3[7:0], fptrigonometry_22_p4[7:0]
  // IntToFP #(.fpwidth(8)) inttofp_8: pin names not known; wires that end beside it: argY[63:56], inttofp_15_p2[63:56]
  // IntToFP #(.fpwidth(8)) inttofp_9: pin names not known; wires that end beside it: argY[55:48], inttofp_15_p2[55:48]
  // IntToFP #(.fpwidth(8)) inttofp_10: pin names not known; wires that end beside it: argY[47:40], inttofp_15_p2[47:40]
  // IntToFP #(.fpwidth(8)) inttofp_11: pin names not known; wires that end beside it: argY[39:32], inttofp_15_p2[39:32]
  // IntToFP #(.fpwidth(8)) inttofp_12: pin names not known; wires that end beside it: argY[31:24], inttofp_15_p2[31:24]
  // IntToFP #(.fpwidth(8)) inttofp_13: pin names not known; wires that end beside it: argY[23:16], inttofp_15_p2[23:16]
  // IntToFP #(.fpwidth(8)) inttofp_14: pin names not known; wires that end beside it: argY[15:8], inttofp_15_p2[15:8]
  // IntToFP #(.fpwidth(8)) inttofp_15: pin names not known; wires that end beside it: argY[7:0], inttofp_15_p2[7:0]
  Multiplexer #(.width(16)) multiplexer_83 (
    .in0({16{1'b0}}), .in1(16'h1), .out(multiplexer_83_out[15:0]), .sel(fpcomparator_10_p3));
  Multiplexer #(.width(16)) multiplexer_84 (
    .in0({16{1'b0}}), .in1(16'h1), .out(multiplexer_97_out[63:48]), .sel(fpcomparator_7_p4));
  Multiplexer #(.width(16)) multiplexer_85 (
    .in0({16{1'b0}}), .in1(16'h1), .out(multiplexer_98_out[63:48]), .sel(fpcomparator_11_p3));
  // FPComparator #(.fpwidth(16)) fpcomparator_11: pin names not known; wires that end beside it: argY[63:48], argZ[63:48], fpcomparator_11_p3, fpcomparator_11_p4
  // FPComparator #(.fpwidth(16)) fpcomparator_12: pin names not known; wires that end beside it: argY[47:32], argZ[47:32], fpcomparator_12_p3, fpcomparator_12_p4
  // FPComparator #(.fpwidth(16)) fpcomparator_13: pin names not known; wires that end beside it: argY[31:16], argZ[31:16], fpcomparator_13_p3, fpcomparator_13_p4
  // FPComparator #(.fpwidth(16)) fpcomparator_14: pin names not known; wires that end beside it: argY[15:0], argZ[15:0], fpcomparator_14_p3, fpcomparator_14_p4
  Adder adder_14 (.a(argY[63:56]), .b(argZ[63:56]), .out(adder_21_out[63:56]));  // open: cin, cout
  Adder adder_15 (.a(argY[55:48]), .b(argZ[55:48]), .out(adder_21_out[55:48]));  // open: cin, cout
  Adder adder_16 (.a(argY[47:40]), .b(argZ[47:40]), .out(adder_21_out[47:40]));  // open: cin, cout
  Adder adder_17 (.a(argY[39:32]), .b(argZ[39:32]), .out(adder_21_out[39:32]));  // open: cin, cout
  Adder adder_18 (.a(argY[31:24]), .b(argZ[31:24]), .out(adder_21_out[31:24]));  // open: cin, cout
  Adder adder_19 (.a(argY[23:16]), .b(argZ[23:16]), .out(adder_21_out[23:16]));  // open: cin, cout
  Adder adder_20 (.a(argY[15:8]), .b(argZ[15:8]), .out(adder_21_out[15:8]));  // open: cin, cout
  Adder adder_21 (.a(argY[7:0]), .b(argZ[7:0]), .out(adder_21_out[7:0]));  // open: cin, cout
  assign bit_extender_51_out = {{12{1'b0}}, bitfinder_21_index};  // Bit_Extender bit_extender_51
  assign bit_extender_52_out = {{12{1'b0}}, bitfinder_22_index};  // Bit_Extender bit_extender_52
  assign bit_extender_53_out = {{12{1'b0}}, bitfinder_23_index};  // Bit_Extender bit_extender_53
  assign bit_extender_54_out = {{12{1'b0}}, bitfinder_24_index};  // Bit_Extender bit_extender_54
  Multiplexer #(.width(16)) multiplexer_86 (
    .in0({16{1'b0}}), .in1(16'h1), .out(multiplexer_97_out[47:32]), .sel(fpcomparator_8_p4));
  Multiplexer #(.width(16)) multiplexer_87 (
    .in0({16{1'b0}}), .in1(16'h1), .out(multiplexer_98_out[47:32]), .sel(fpcomparator_12_p3));
  BitSelector #(.group(3)) bitselector_12 (.in(argZ[7:0]), .out(bitselector_12_out), .sel(2'b00));
  BitSelector #(.group(3)) bitselector_13 (.in(argZ[15:8]), .out(bitselector_13_out), .sel(2'b00));
  BitSelector #(.group(3)) bitselector_14 (.in(argZ[23:16]), .out(bitselector_14_out), .sel(2'b00));
  BitSelector #(.group(3)) bitselector_15 (.in(argZ[31:24]), .out(bitselector_15_out), .sel(2'b00));
  BitSelector #(.group(3)) bitselector_16 (.in(argZ[39:32]), .out(bitselector_16_out), .sel(2'b00));
  BitSelector #(.group(3)) bitselector_17 (.in(argZ[47:40]), .out(bitselector_17_out), .sel(2'b00));
  BitSelector #(.group(3)) bitselector_18 (.in(argZ[55:48]), .out(bitselector_18_out), .sel(2'b00));
  BitSelector #(.group(3)) bitselector_19 (.in(argZ[63:56]), .out(bitselector_19_out), .sel(2'b00));
  Multiplexer #(.width(16)) multiplexer_88 (
    .in0(argX[63:48]), .in1(buffer_5_out), .out(multiplexer_100_out[63:48]), .sel(not_5_out));
  assign buffer_5_out = argY[63:48];  // Buffer buffer_5, 16 bits wide
  not not_5 (not_5_out, comparator_33_eq);
  Comparator #(.mode("unsigned"), .width(16)) comparator_33 (
    .a(argZ[63:48]), .b({16{1'b0}}), .eq(comparator_33_eq));  // open: gt, lt
  not not_6 (not_6_out, comparator_34_eq);
  Comparator #(.mode("unsigned"), .width(16)) comparator_34 (
    .a(argZ[47:32]), .b({16{1'b0}}), .eq(comparator_34_eq));  // open: gt, lt
  not not_7 (not_7_out, comparator_35_eq);
  Comparator #(.mode("unsigned"), .width(16)) comparator_35 (
    .a(argZ[31:16]), .b({16{1'b0}}), .eq(comparator_35_eq));  // open: gt, lt
  not not_8 (not_8_out, comparator_36_eq);
  Comparator #(.mode("unsigned"), .width(16)) comparator_36 (
    .a(argZ[15:0]), .b({16{1'b0}}), .eq(comparator_36_eq));  // open: gt, lt
  Multiplexer #(.width(16)) multiplexer_89 (
    .in0({16{1'b1}}), .in1(bit_extender_51_out), .out(multiplexer_92_out[63:48]), .sel(bitfinder_21_found));
  Multiplexer #(.width(16)) multiplexer_90 (
    .in0({16{1'b1}}), .in1(bit_extender_52_out), .out(multiplexer_92_out[47:32]), .sel(bitfinder_22_found));
  Multiplexer #(.width(16)) multiplexer_91 (
    .in0({16{1'b1}}), .in1(bit_extender_53_out), .out(multiplexer_92_out[31:16]), .sel(bitfinder_23_found));
  Multiplexer #(.width(16)) multiplexer_92 (
    .in0({16{1'b1}}), .in1(bit_extender_54_out), .out(multiplexer_92_out[15:0]), .sel(bitfinder_24_found));
  Multiplexer #(.width(16)) multiplexer_93 (
    .in0({16{1'b0}}), .in1(16'h1), .out(multiplexer_97_out[31:16]), .sel(fpcomparator_9_p4));
  Multiplexer #(.width(16)) multiplexer_94 (
    .in0({16{1'b0}}), .in1(16'h1), .out(multiplexer_98_out[31:16]), .sel(fpcomparator_13_p3));
  Multiplexer #(.width(16)) multiplexer_95 (
    .in0(argX[47:32]), .in1(buffer_6_out), .out(multiplexer_100_out[47:32]), .sel(not_6_out));
  Multiplexer #(.width(16)) multiplexer_96 (
    .in0(argX[31:16]), .in1(buffer_7_out), .out(multiplexer_100_out[31:16]), .sel(not_7_out));
  assign buffer_6_out = argY[47:32];  // Buffer buffer_6, 16 bits wide
  BitFinder #(.\type ("high0"), .width(16)) bitfinder_25 (
    .in(argY[63:48]), .index(bitfinder_25_index), .found(bitfinder_25_found));
  BitFinder #(.\type ("high0"), .width(16)) bitfinder_26 (
    .in(argY[47:32]), .index(bitfinder_26_index), .found(bitfinder_26_found));
  BitFinder #(.\type ("high0"), .width(16)) bitfinder_27 (
    .in(argY[31:16]), .index(bitfinder_27_index), .found(bitfinder_27_found));
  BitFinder #(.\type ("high0"), .width(16)) bitfinder_28 (
    .in(argY[15:0]), .index(bitfinder_28_index), .found(bitfinder_28_found));
  FPAdder #(.fpwidth(8)) fpadder_8 (.a(argY[63:56]), .b(argZ[63:56]), .out(fpadder_15_out[63:56]));
  FPAdder #(.fpwidth(8)) fpadder_9 (.a(argY[55:48]), .b(argZ[55:48]), .out(fpadder_15_out[55:48]));
  FPAdder #(.fpwidth(8)) fpadder_10 (.a(argY[47:40]), .b(argZ[47:40]), .out(fpadder_15_out[47:40]));
  FPAdder #(.fpwidth(8)) fpadder_11 (.a(argY[39:32]), .b(argZ[39:32]), .out(fpadder_15_out[39:32]));
  FPAdder #(.fpwidth(8)) fpadder_12 (.a(argY[31:24]), .b(argZ[31:24]), .out(fpadder_15_out[31:24]));
  FPAdder #(.fpwidth(8)) fpadder_13 (.a(argY[23:16]), .b(argZ[23:16]), .out(fpadder_15_out[23:16]));
  FPAdder #(.fpwidth(8)) fpadder_14 (.a(argY[15:8]), .b(argZ[15:8]), .out(fpadder_15_out[15:8]));
  FPAdder #(.fpwidth(8)) fpadder_15 (.a(argY[7:0]), .b(argZ[7:0]), .out(fpadder_15_out[7:0]));
  // FPTrigonometry #(.fpwidth(8)) fptrigonometry_23: pin names not known; wires that end beside it: argY[63:56], fptrigonometry_30_p2[63:56], fptrigonometry_30_p3[63:56], fptrigonometry_30_p4[63:56]
  // FPTrigonometry #(.fpwidth(8)) fptrigonometry_24: pin names not known; wires that end beside it: argY[55:48], fptrigonometry_30_p2[55:48], fptrigonometry_30_p3[55:48], fptrigonometry_30_p4[55:48]
  // FPTrigonometry #(.fpwidth(8)) fptrigonometry_25: pin names not known; wires that end beside it: argY[47:40], fptrigonometry_30_p2[47:40], fptrigonometry_30_p3[47:40], fptrigonometry_30_p4[47:40]
  // FPTrigonometry #(.fpwidth(8)) fptrigonometry_26: pin names not known; wires that end beside it: argY[39:32], fptrigonometry_30_p2[39:32], fptrigonometry_30_p3[39:32], fptrigonometry_30_p4[39:32]
  // FPTrigonometry #(.fpwidth(8)) fptrigonometry_27: pin names not known; wires that end beside it: argY[31:24], fptrigonometry_30_p2[31:24], fptrigonometry_30_p3[31:24], fptrigonometry_30_p4[31:24]
  // FPTrigonometry #(.fpwidth(8)) fptrigonometry_28: pin names not known; wires that end beside it: argY[23:16], fptrigonometry_30_p2[23:16], fptrigonometry_30_p3[23:16], fptrigonometry_30_p4[23:16]
  // FPTrigonometry #(.fpwidth(8)) fptrigonometry_29: pin names not known; wires that end beside it: argY[15:8], fptrigonometry_30_p2[15:8], fptrigonometry_30_p3[15:8], fptrigonometry_30_p4[15:8]
  // FPTrigonometry #(.fpwidth(8)) fptrigonometry_30: pin names not known; wires that end beside it: argY[7:0], fptrigonometry_30_p2[7:0], fptrigonometry_30_p3[7:0], fptrigonometry_30_p4[7:0]
  Multiplexer #(.width(16)) multiplexer_97 (
    .in0({16{1'b0}}), .in1(16'h1), .out(multiplexer_97_out[15:0]), .sel(fpcomparator_10_p4));
  Multiplexer #(.width(16)) multiplexer_98 (
    .in0({16{1'b0}}), .in1(16'h1), .out(multiplexer_98_out[15:0]), .sel(fpcomparator_14_p3));
  Multiplexer #(.width(16)) multiplexer_99 (
    .in0({16{1'b0}}), .in1(16'h1), .out(multiplexer_107_out[63:48]), .sel(fpcomparator_11_p4));
  Multiplexer #(.width(16)) multiplexer_100 (
    .in0(argX[15:0]), .in1(buffer_8_out), .out(multiplexer_100_out[15:0]), .sel(not_8_out));
  assign buffer_7_out = argY[31:16];  // Buffer buffer_7, 16 bits wide
  assign buffer_8_out = argY[15:0];  // Buffer buffer_8, 16 bits wide
  assign bit_extender_55_out = {{12{1'b0}}, bitfinder_25_index};  // Bit_Extender bit_extender_55
  assign bit_extender_56_out = {{12{1'b0}}, bitfinder_26_index};  // Bit_Extender bit_extender_56
  assign bit_extender_57_out = {{12{1'b0}}, bitfinder_27_index};  // Bit_Extender bit_extender_57
  assign bit_extender_58_out = {{12{1'b0}}, bitfinder_28_index};  // Bit_Extender bit_extender_58
  // FPToInt #(.fpwidth(8)) fptoint_29: pin names not known; wires that end beside it: argY[63:56], fptoint_36_p2[63:56]
  // FPToInt #(.fpwidth(8)) fptoint_30: pin names not known; wires that end beside it: argY[55:48], fptoint_36_p2[55:48]
  // FPToInt #(.fpwidth(8)) fptoint_31: pin names not known; wires that end beside it: argY[47:40], fptoint_36_p2[47:40]
  // FPToInt #(.fpwidth(8)) fptoint_32: pin names not known; wires that end beside it: argY[39:32], fptoint_36_p2[39:32]
  // FPToInt #(.fpwidth(8)) fptoint_33: pin names not known; wires that end beside it: argY[31:24], fptoint_36_p2[31:24]
  // FPToInt #(.fpwidth(8)) fptoint_34: pin names not known; wires that end beside it: argY[23:16], fptoint_36_p2[23:16]
  // FPToInt #(.fpwidth(8)) fptoint_35: pin names not known; wires that end beside it: argY[15:8], fptoint_36_p2[15:8]
  // FPToInt #(.fpwidth(8)) fptoint_36: pin names not known; wires that end beside it: argY[7:0], fptoint_36_p2[7:0]
  Multiplexer #(.width(16)) multiplexer_101 (
    .in0({16{1'b0}}), .in1(16'h1), .out(multiplexer_107_out[47:32]), .sel(fpcomparator_12_p4));
  Shifter shifter_36 (.in(argY[63:56]), .\dist (bitselector_19_out), .out(shifter_43_out[63:56]));
  Shifter shifter_37 (.in(argY[55:48]), .\dist (bitselector_18_out), .out(shifter_43_out[55:48]));
  Shifter shifter_38 (.in(argY[47:40]), .\dist (bitselector_17_out), .out(shifter_43_out[47:40]));
  Shifter shifter_39 (.in(argY[39:32]), .\dist (bitselector_16_out), .out(shifter_43_out[39:32]));
  Shifter shifter_40 (.in(argY[31:24]), .\dist (bitselector_15_out), .out(shifter_43_out[31:24]));
  Shifter shifter_41 (.in(argY[23:16]), .\dist (bitselector_14_out), .out(shifter_43_out[23:16]));
  Shifter shifter_42 (.in(argY[15:8]), .\dist (bitselector_13_out), .out(shifter_43_out[15:8]));
  Shifter shifter_43 (.in(argY[7:0]), .\dist (bitselector_12_out), .out(shifter_43_out[7:0]));
  Subtractor subtractor_14 (.a(argY[63:56]), .b(argZ[63:56]), .out(subtractor_21_out[63:56]));  // open: bin, bout
  Subtractor subtractor_15 (.a(argY[55:48]), .b(argZ[55:48]), .out(subtractor_21_out[55:48]));  // open: bin, bout
  Subtractor subtractor_16 (.a(argY[47:40]), .b(argZ[47:40]), .out(subtractor_21_out[47:40]));  // open: bin, bout
  Subtractor subtractor_17 (.a(argY[39:32]), .b(argZ[39:32]), .out(subtractor_21_out[39:32]));  // open: bin, bout
  Subtractor subtractor_18 (.a(argY[31:24]), .b(argZ[31:24]), .out(subtractor_21_out[31:24]));  // open: bin, bout
  Subtractor subtractor_19 (.a(argY[23:16]), .b(argZ[23:16]), .out(subtractor_21_out[23:16]));  // open: bin, bout
  Subtractor subtractor_20 (.a(argY[15:8]), .b(argZ[15:8]), .out(subtractor_21_out[15:8]));  // open: bin, bout
  Subtractor subtractor_21 (.a(argY[7:0]), .b(argZ[7:0]), .out(subtractor_21_out[7:0]));  // open: bin, bout
  Multiplexer #(.width(16)) multiplexer_102 (
    .in0({16{1'b1}}), .in1(bit_extender_55_out), .out(multiplexer_105_out[63:48]), .sel(bitfinder_25_found));
  Multiplexer #(.width(16)) multiplexer_103 (
    .in0({16{1'b1}}), .in1(bit_extender_56_out), .out(multiplexer_105_out[47:32]), .sel(bitfinder_26_found));
  Multiplexer #(.width(16)) multiplexer_104 (
    .in0({16{1'b1}}), .in1(bit_extender_57_out), .out(multiplexer_105_out[31:16]), .sel(bitfinder_27_found));
  Multiplexer #(.width(16)) multiplexer_105 (
    .in0({16{1'b1}}), .in1(bit_extender_58_out), .out(multiplexer_105_out[15:0]), .sel(bitfinder_28_found));
  // FPClassificator #(.fpwidth(16)) fpclassificator_6: pin names not known; wires that end beside it: {16{1'b0}}, 16'h1, argY[63:48], fpclassificator_6_p4
  // FPClassificator #(.fpwidth(16)) fpclassificator_7: pin names not known; wires that end beside it: argY[47:32], fpclassificator_7_p2
  // FPClassificator #(.fpwidth(16)) fpclassificator_8: pin names not known; wires that end beside it: argY[31:16], fpclassificator_8_p2
  // FPClassificator #(.fpwidth(16)) fpclassificator_9: pin names not known; wires that end beside it: argY[15:0], fpclassificator_9_p2
  Multiplexer #(.width(16)) multiplexer_106 (
    .in0({16{1'b0}}), .in1(16'h1), .out(multiplexer_107_out[31:16]), .sel(fpcomparator_13_p4));
  BitAdder #(.width(16)) bitadder_4 (.in0(argY[63:48]), .out(bitadder_4_out));
  BitAdder #(.width(16)) bitadder_5 (.in0(argY[47:32]), .out(bitadder_5_out));
  BitAdder #(.width(16)) bitadder_6 (.in0(argY[31:16]), .out(bitadder_6_out));
  BitAdder #(.width(16)) bitadder_7 (.in0(argY[15:0]), .out(bitadder_7_out));
  assign bit_extender_62_out[63:48] = {{15{1'b0}}, fpclassificator_6_p4};  // Bit_Extender bit_extender_59
  assign bit_extender_62_out[47:32] = {{15{1'b0}}, fpclassificator_7_p2};  // Bit_Extender bit_extender_60
  assign bit_extender_62_out[31:16] = {{15{1'b0}}, fpclassificator_8_p2};  // Bit_Extender bit_extender_61
  assign bit_extender_62_out[15:0] = {{15{1'b0}}, fpclassificator_9_p2};  // Bit_Extender bit_extender_62
  Multiplexer #(.width(16)) multiplexer_107 (
    .in0({16{1'b0}}), .in1(16'h1), .out(multiplexer_107_out[15:0]), .sel(fpcomparator_14_p4));
  assign bit_extender_66_out[63:48] = {{11{1'b0}}, bitadder_4_out};  // Bit_Extender bit_extender_63
  assign bit_extender_66_out[47:32] = {{11{1'b0}}, bitadder_5_out};  // Bit_Extender bit_extender_64
  assign bit_extender_66_out[31:16] = {{11{1'b0}}, bitadder_6_out};  // Bit_Extender bit_extender_65
  assign bit_extender_66_out[15:0] = {{11{1'b0}}, bitadder_7_out};  // Bit_Extender bit_extender_66
  FPSubtractor #(.fpwidth(8)) fpsubtractor_8 (.a(argY[63:56]), .b(argZ[63:56]), .out(fpsubtractor_15_out[63:56]));
  FPSubtractor #(.fpwidth(8)) fpsubtractor_9 (.a(argY[55:48]), .b(argZ[55:48]), .out(fpsubtractor_15_out[55:48]));
  FPSubtractor #(.fpwidth(8)) fpsubtractor_10 (.a(argY[47:40]), .b(argZ[47:40]), .out(fpsubtractor_15_out[47:40]));
  FPSubtractor #(.fpwidth(8)) fpsubtractor_11 (.a(argY[39:32]), .b(argZ[39:32]), .out(fpsubtractor_15_out[39:32]));
  FPSubtractor #(.fpwidth(8)) fpsubtractor_12 (.a(argY[31:24]), .b(argZ[31:24]), .out(fpsubtractor_15_out[31:24]));
  FPSubtractor #(.fpwidth(8)) fpsubtractor_13 (.a(argY[23:16]), .b(argZ[23:16]), .out(fpsubtractor_15_out[23:16]));
  FPSubtractor #(.fpwidth(8)) fpsubtractor_14 (.a(argY[15:8]), .b(argZ[15:8]), .out(fpsubtractor_15_out[15:8]));
  FPSubtractor #(.fpwidth(8)) fpsubtractor_15 (.a(argY[7:0]), .b(argZ[7:0]), .out(fpsubtractor_15_out[7:0]));
  // FPToInt #(.fpwidth(8), .mode("floor")) fptoint_37: pin names not known; wires that end beside it: argY[63:56], fptoint_44_p2[63:56]
  // FPToInt #(.fpwidth(8), .mode("floor")) fptoint_38: pin names not known; wires that end beside it: argY[55:48], fptoint_44_p2[55:48]
  // FPToInt #(.fpwidth(8), .mode("floor")) fptoint_39: pin names not known; wires that end beside it: argY[47:40], fptoint_44_p2[47:40]
  // FPToInt #(.fpwidth(8), .mode("floor")) fptoint_40: pin names not known; wires that end beside it: argY[39:32], fptoint_44_p2[39:32]
  // FPToInt #(.fpwidth(8), .mode("floor")) fptoint_41: pin names not known; wires that end beside it: argY[31:24], fptoint_44_p2[31:24]
  // FPToInt #(.fpwidth(8), .mode("floor")) fptoint_42: pin names not known; wires that end beside it: argY[23:16], fptoint_44_p2[23:16]
  // FPToInt #(.fpwidth(8), .mode("floor")) fptoint_43: pin names not known; wires that end beside it: argY[15:8], fptoint_44_p2[15:8]
  // FPToInt #(.fpwidth(8), .mode("floor")) fptoint_44: pin names not known; wires that end beside it: argY[7:0], fptoint_44_p2[7:0]
  Shifter #(.shift("lr")) shifter_44 (.in(argY[63:56]), .\dist (bitselector_19_out), .out(shifter_51_out[63:56]));
  Shifter #(.shift("lr")) shifter_45 (.in(argY[55:48]), .\dist (bitselector_18_out), .out(shifter_51_out[55:48]));
  Shifter #(.shift("lr")) shifter_46 (.in(argY[47:40]), .\dist (bitselector_17_out), .out(shifter_51_out[47:40]));
  Shifter #(.shift("lr")) shifter_47 (.in(argY[39:32]), .\dist (bitselector_16_out), .out(shifter_51_out[39:32]));
  Shifter #(.shift("lr")) shifter_48 (.in(argY[31:24]), .\dist (bitselector_15_out), .out(shifter_51_out[31:24]));
  Shifter #(.shift("lr")) shifter_49 (.in(argY[23:16]), .\dist (bitselector_14_out), .out(shifter_51_out[23:16]));
  Shifter #(.shift("lr")) shifter_50 (.in(argY[15:8]), .\dist (bitselector_13_out), .out(shifter_51_out[15:8]));
  Shifter #(.shift("lr")) shifter_51 (.in(argY[7:0]), .\dist (bitselector_12_out), .out(shifter_51_out[7:0]));
  Multiplier #(.mode("twosComplement")) multiplier_14 (
    .a(argY[63:56]), .b(argZ[63:56]), .out(multiplier_21_out[63:56]));  // open: cin, cout
  Multiplier #(.mode("twosComplement")) multiplier_15 (
    .a(argY[55:48]), .b(argZ[55:48]), .out(multiplier_21_out[55:48]));  // open: cin, cout
  Multiplier #(.mode("twosComplement")) multiplier_16 (
    .a(argY[47:40]), .b(argZ[47:40]), .out(multiplier_21_out[47:40]));  // open: cin, cout
  Multiplier #(.mode("twosComplement")) multiplier_17 (
    .a(argY[39:32]), .b(argZ[39:32]), .out(multiplier_21_out[39:32]));  // open: cin, cout
  Multiplier #(.mode("twosComplement")) multiplier_18 (
    .a(argY[31:24]), .b(argZ[31:24]), .out(multiplier_21_out[31:24]));  // open: cin, cout
  Multiplier #(.mode("twosComplement")) multiplier_19 (
    .a(argY[23:16]), .b(argZ[23:16]), .out(multiplier_21_out[23:16]));  // open: cin, cout
  Multiplier #(.mode("twosComplement")) multiplier_20 (
    .a(argY[15:8]), .b(argZ[15:8]), .out(multiplier_21_out[15:8]));  // open: cin, cout
  Multiplier #(.mode("twosComplement")) multiplier_21 (
    .a(argY[7:0]), .b(argZ[7:0]), .out(multiplier_21_out[7:0]));  // open: cin, cout
  assign bit_extender_70_out[63:48] = {{15{1'b0}}, fpclassificator_10_p4};  // Bit_Extender bit_extender_67
  // FPClassificator #(.fpwidth(16)) fpclassificator_10: pin names not known; wires that end beside it: {16{1'b0}}, 16'h1, argY[63:48], fpclassificator_10_p4
  assign bit_extender_70_out[47:32] = {{15{1'b0}}, fpclassificator_11_p2};  // Bit_Extender bit_extender_68
  // FPClassificator #(.fpwidth(16)) fpclassificator_11: pin names not known; wires that end beside it: argY[47:32], fpclassificator_11_p2
  assign bit_extender_70_out[31:16] = {{15{1'b0}}, fpclassificator_12_p2};  // Bit_Extender bit_extender_69
  // FPClassificator #(.fpwidth(16)) fpclassificator_12: pin names not known; wires that end beside it: argY[31:16], fpclassificator_12_p2
  assign bit_extender_70_out[15:0] = {{15{1'b0}}, fpclassificator_13_p2};  // Bit_Extender bit_extender_70
  // FPClassificator #(.fpwidth(16)) fpclassificator_13: pin names not known; wires that end beside it: argY[15:0], fpclassificator_13_p2
  Adder adder_22 (.a(argY[63:56]), .b(argZ[63:56]), .cout(adder_22_cout));  // open: out, cin
  Adder adder_23 (.a(argY[55:48]), .b(argZ[55:48]), .cout(adder_23_cout));  // open: out, cin
  Adder adder_24 (.a(argY[47:40]), .b(argZ[47:40]), .cout(adder_24_cout));  // open: out, cin
  Adder adder_25 (.a(argY[39:32]), .b(argZ[39:32]), .cout(adder_25_cout));  // open: out, cin
  Adder adder_26 (.a(argY[31:24]), .b(argZ[31:24]), .cout(adder_26_cout));  // open: out, cin
  Adder adder_27 (.a(argY[23:16]), .b(argZ[23:16]), .cout(adder_27_cout));  // open: out, cin
  Adder adder_28 (.a(argY[15:8]), .b(argZ[15:8]), .cout(adder_28_cout));  // open: out, cin
  Adder adder_29 (.a(argY[7:0]), .b(argZ[7:0]), .cout(adder_29_cout));  // open: out, cin
  assign bit_extender_78_out[63:56] = {{7{1'b0}}, adder_22_cout};  // Bit_Extender bit_extender_71
  assign bit_extender_78_out[55:48] = {{7{1'b0}}, adder_23_cout};  // Bit_Extender bit_extender_72
  assign bit_extender_78_out[47:40] = {{7{1'b0}}, adder_24_cout};  // Bit_Extender bit_extender_73
  assign bit_extender_78_out[39:32] = {{7{1'b0}}, adder_25_cout};  // Bit_Extender bit_extender_74
  assign bit_extender_78_out[31:24] = {{7{1'b0}}, adder_26_cout};  // Bit_Extender bit_extender_75
  assign bit_extender_78_out[23:16] = {{7{1'b0}}, adder_27_cout};  // Bit_Extender bit_extender_76
  assign bit_extender_78_out[15:8] = {{7{1'b0}}, adder_28_cout};  // Bit_Extender bit_extender_77
  assign bit_extender_78_out[7:0] = {{7{1'b0}}, adder_29_cout};  // Bit_Extender bit_extender_78
  BitFinder bitfinder_29 (.in(argY[63:56]), .index(bitfinder_29_index), .found(bitfinder_29_found));
  BitFinder bitfinder_30 (.in(argY[55:48]), .index(bitfinder_30_index), .found(bitfinder_30_found));
  BitFinder bitfinder_31 (.in(argY[47:40]), .index(bitfinder_31_index), .found(bitfinder_31_found));
  BitFinder bitfinder_32 (.in(argY[39:32]), .index(bitfinder_32_index), .found(bitfinder_32_found));
  BitFinder bitfinder_33 (.in(argY[31:24]), .index(bitfinder_33_index), .found(bitfinder_33_found));
  BitFinder bitfinder_34 (.in(argY[23:16]), .index(bitfinder_34_index), .found(bitfinder_34_found));
  BitFinder bitfinder_35 (.in(argY[15:8]), .index(bitfinder_35_index), .found(bitfinder_35_found));
  BitFinder bitfinder_36 (.in(argY[7:0]), .index(bitfinder_36_index), .found(bitfinder_36_found));
  FPMultiplier #(.fpwidth(8)) fpmultiplier_8 (.a(argY[63:56]), .b(argZ[63:56]), .out(fpmultiplier_15_out[63:56]));
  FPMultiplier #(.fpwidth(8)) fpmultiplier_9 (.a(argY[55:48]), .b(argZ[55:48]), .out(fpmultiplier_15_out[55:48]));
  FPMultiplier #(.fpwidth(8)) fpmultiplier_10 (.a(argY[47:40]), .b(argZ[47:40]), .out(fpmultiplier_15_out[47:40]));
  FPMultiplier #(.fpwidth(8)) fpmultiplier_11 (.a(argY[39:32]), .b(argZ[39:32]), .out(fpmultiplier_15_out[39:32]));
  FPMultiplier #(.fpwidth(8)) fpmultiplier_12 (.a(argY[31:24]), .b(argZ[31:24]), .out(fpmultiplier_15_out[31:24]));
  FPMultiplier #(.fpwidth(8)) fpmultiplier_13 (.a(argY[23:16]), .b(argZ[23:16]), .out(fpmultiplier_15_out[23:16]));
  FPMultiplier #(.fpwidth(8)) fpmultiplier_14 (.a(argY[15:8]), .b(argZ[15:8]), .out(fpmultiplier_15_out[15:8]));
  FPMultiplier #(.fpwidth(8)) fpmultiplier_15 (.a(argY[7:0]), .b(argZ[7:0]), .out(fpmultiplier_15_out[7:0]));
  Comparator comparator_37 (.a(argY[63:56]), .b({8{1'b0}}), .eq(comparator_37_eq), .lt(comparator_37_lt));  // open: gt
  Comparator comparator_38 (.a(argY[55:48]), .b({8{1'b0}}), .eq(comparator_38_eq), .lt(comparator_38_lt));  // open: gt
  Comparator comparator_39 (.a(argY[47:40]), .b({8{1'b0}}), .eq(comparator_39_eq), .lt(comparator_39_lt));  // open: gt
  Comparator comparator_40 (.a(argY[39:32]), .b({8{1'b0}}), .eq(comparator_40_eq), .lt(comparator_40_lt));  // open: gt
  Comparator comparator_41 (.a(argY[31:24]), .b({8{1'b0}}), .eq(comparator_41_eq), .lt(comparator_41_lt));  // open: gt
  Comparator comparator_42 (.a(argY[23:16]), .b({8{1'b0}}), .eq(comparator_42_eq), .lt(comparator_42_lt));  // open: gt
  Comparator comparator_43 (.a(argY[15:8]), .b({8{1'b0}}), .eq(comparator_43_eq), .lt(comparator_43_lt));  // open: gt
  Comparator comparator_44 (.a(argY[7:0]), .b({8{1'b0}}), .eq(comparator_44_eq), .lt(comparator_44_lt));  // open: gt
  assign bit_extender_79_out = {{5{1'b0}}, bitfinder_29_index};  // Bit_Extender bit_extender_79
  assign bit_extender_80_out = {{5{1'b0}}, bitfinder_30_index};  // Bit_Extender bit_extender_80
  assign bit_extender_81_out = {{5{1'b0}}, bitfinder_31_index};  // Bit_Extender bit_extender_81
  assign bit_extender_82_out = {{5{1'b0}}, bitfinder_32_index};  // Bit_Extender bit_extender_82
  assign bit_extender_83_out = {{5{1'b0}}, bitfinder_33_index};  // Bit_Extender bit_extender_83
  assign bit_extender_84_out = {{5{1'b0}}, bitfinder_34_index};  // Bit_Extender bit_extender_84
  assign bit_extender_85_out = {{5{1'b0}}, bitfinder_35_index};  // Bit_Extender bit_extender_85
  assign bit_extender_86_out = {{5{1'b0}}, bitfinder_36_index};  // Bit_Extender bit_extender_86
  // FPSquareRoot #(.fpwidth(8)) fpsquareroot_8: pin names not known; wires that end beside it: argY[63:56], fpsquareroot_15_p2[63:56]
  // FPSquareRoot #(.fpwidth(8)) fpsquareroot_9: pin names not known; wires that end beside it: argY[55:48], fpsquareroot_15_p2[55:48]
  // FPSquareRoot #(.fpwidth(8)) fpsquareroot_10: pin names not known; wires that end beside it: argY[47:40], fpsquareroot_15_p2[47:40]
  // FPSquareRoot #(.fpwidth(8)) fpsquareroot_11: pin names not known; wires that end beside it: argY[39:32], fpsquareroot_15_p2[39:32]
  // FPSquareRoot #(.fpwidth(8)) fpsquareroot_12: pin names not known; wires that end beside it: argY[31:24], fpsquareroot_15_p2[31:24]
  // FPSquareRoot #(.fpwidth(8)) fpsquareroot_13: pin names not known; wires that end beside it: argY[23:16], fpsquareroot_15_p2[23:16]
  // FPSquareRoot #(.fpwidth(8)) fpsquareroot_14: pin names not known; wires that end beside it: argY[15:8], fpsquareroot_15_p2[15:8]
  // FPSquareRoot #(.fpwidth(8)) fpsquareroot_15: pin names not known; wires that end beside it: argY[7:0], fpsquareroot_15_p2[7:0]
  // FPToInt #(.fpwidth(8), .mode("ceil")) fptoint_45: pin names not known; wires that end beside it: argY[63:56], fptoint_52_p2[63:56]
  // FPToInt #(.fpwidth(8), .mode("ceil")) fptoint_46: pin names not known; wires that end beside it: argY[55:48], fptoint_52_p2[55:48]
  // FPToInt #(.fpwidth(8), .mode("ceil")) fptoint_47: pin names not known; wires that end beside it: argY[47:40], fptoint_52_p2[47:40]
  // FPToInt #(.fpwidth(8), .mode("ceil")) fptoint_48: pin names not known; wires that end beside it: argY[39:32], fptoint_52_p2[39:32]
  // FPToInt #(.fpwidth(8), .mode("ceil")) fptoint_49: pin names not known; wires that end beside it: argY[31:24], fptoint_52_p2[31:24]
  // FPToInt #(.fpwidth(8), .mode("ceil")) fptoint_50: pin names not known; wires that end beside it: argY[23:16], fptoint_52_p2[23:16]
  // FPToInt #(.fpwidth(8), .mode("ceil")) fptoint_51: pin names not known; wires that end beside it: argY[15:8], fptoint_52_p2[15:8]
  // FPToInt #(.fpwidth(8), .mode("ceil")) fptoint_52: pin names not known; wires that end beside it: argY[7:0], fptoint_52_p2[7:0]
  Multiplexer #(.width(8)) multiplexer_108 (
    .in0({8{1'b0}}), .in1(8'h1), .out(multiplexer_133_out[63:56]), .sel(comparator_37_eq));
  Multiplexer #(.width(8)) multiplexer_109 (
    .in0({8{1'b0}}), .in1(8'h1), .out(multiplexer_133_out[55:48]), .sel(comparator_38_eq));
  Shifter #(.shift("ar")) shifter_52 (.in(argY[63:56]), .\dist (bitselector_19_out), .out(shifter_59_out[63:56]));
  Shifter #(.shift("ar")) shifter_53 (.in(argY[55:48]), .\dist (bitselector_18_out), .out(shifter_59_out[55:48]));
  Shifter #(.shift("ar")) shifter_54 (.in(argY[47:40]), .\dist (bitselector_17_out), .out(shifter_59_out[47:40]));
  Shifter #(.shift("ar")) shifter_55 (.in(argY[39:32]), .\dist (bitselector_16_out), .out(shifter_59_out[39:32]));
  Shifter #(.shift("ar")) shifter_56 (.in(argY[31:24]), .\dist (bitselector_15_out), .out(shifter_59_out[31:24]));
  Shifter #(.shift("ar")) shifter_57 (.in(argY[23:16]), .\dist (bitselector_14_out), .out(shifter_59_out[23:16]));
  Shifter #(.shift("ar")) shifter_58 (.in(argY[15:8]), .\dist (bitselector_13_out), .out(shifter_59_out[15:8]));
  Shifter #(.shift("ar")) shifter_59 (.in(argY[7:0]), .\dist (bitselector_12_out), .out(shifter_59_out[7:0]));
  Divider #(.mode("twosComplement")) divider_14 (
    .a(argY[63:56]), .b(argZ[63:56]), .out(divider_21_out[63:56]));  // open: upper, rem
  Divider #(.mode("twosComplement")) divider_15 (
    .a(argY[55:48]), .b(argZ[55:48]), .out(divider_21_out[55:48]));  // open: upper, rem
  Divider #(.mode("twosComplement")) divider_16 (
    .a(argY[47:40]), .b(argZ[47:40]), .out(divider_21_out[47:40]));  // open: upper, rem
  Divider #(.mode("twosComplement")) divider_17 (
    .a(argY[39:32]), .b(argZ[39:32]), .out(divider_21_out[39:32]));  // open: upper, rem
  Divider #(.mode("twosComplement")) divider_18 (
    .a(argY[31:24]), .b(argZ[31:24]), .out(divider_21_out[31:24]));  // open: upper, rem
  Divider #(.mode("twosComplement")) divider_19 (
    .a(argY[23:16]), .b(argZ[23:16]), .out(divider_21_out[23:16]));  // open: upper, rem
  Divider #(.mode("twosComplement")) divider_20 (
    .a(argY[15:8]), .b(argZ[15:8]), .out(divider_21_out[15:8]));  // open: upper, rem
  Divider #(.mode("twosComplement")) divider_21 (
    .a(argY[7:0]), .b(argZ[7:0]), .out(divider_21_out[7:0]));  // open: upper, rem
  Multiplexer #(.width(8)) multiplexer_110 (
    .in0({8{1'b1}}), .in1(bit_extender_79_out), .out(multiplexer_117_out[63:56]), .sel(bitfinder_29_found));
  Multiplexer #(.width(8)) multiplexer_111 (
    .in0({8{1'b1}}), .in1(bit_extender_80_out), .out(multiplexer_117_out[55:48]), .sel(bitfinder_30_found));
  Multiplexer #(.width(8)) multiplexer_112 (
    .in0({8{1'b1}}), .in1(bit_extender_81_out), .out(multiplexer_117_out[47:40]), .sel(bitfinder_31_found));
  Multiplexer #(.width(8)) multiplexer_113 (
    .in0({8{1'b1}}), .in1(bit_extender_82_out), .out(multiplexer_117_out[39:32]), .sel(bitfinder_32_found));
  Multiplexer #(.width(8)) multiplexer_114 (
    .in0({8{1'b1}}), .in1(bit_extender_83_out), .out(multiplexer_117_out[31:24]), .sel(bitfinder_33_found));
  Multiplexer #(.width(8)) multiplexer_115 (
    .in0({8{1'b1}}), .in1(bit_extender_84_out), .out(multiplexer_117_out[23:16]), .sel(bitfinder_34_found));
  Multiplexer #(.width(8)) multiplexer_116 (
    .in0({8{1'b1}}), .in1(bit_extender_85_out), .out(multiplexer_117_out[15:8]), .sel(bitfinder_35_found));
  Multiplexer #(.width(8)) multiplexer_117 (
    .in0({8{1'b1}}), .in1(bit_extender_86_out), .out(multiplexer_117_out[7:0]), .sel(bitfinder_36_found));
  Multiplexer #(.width(8)) multiplexer_118 (
    .in0({8{1'b0}}), .in1(8'h1), .out(multiplexer_133_out[47:40]), .sel(comparator_39_eq));
  Multiplexer #(.width(8)) multiplexer_119 (
    .in0({8{1'b0}}), .in1(8'h1), .out(multiplexer_133_out[39:32]), .sel(comparator_40_eq));
  Subtractor subtractor_22 (.a(argY[63:56]), .b(argZ[63:56]), .bout(subtractor_22_bout));  // open: out, bin
  Subtractor subtractor_23 (.a(argY[55:48]), .b(argZ[55:48]), .bout(subtractor_23_bout));  // open: out, bin
  Subtractor subtractor_24 (.a(argY[47:40]), .b(argZ[47:40]), .bout(subtractor_24_bout));  // open: out, bin
  Subtractor subtractor_25 (.a(argY[39:32]), .b(argZ[39:32]), .bout(subtractor_25_bout));  // open: out, bin
  Subtractor subtractor_26 (.a(argY[31:24]), .b(argZ[31:24]), .bout(subtractor_26_bout));  // open: out, bin
  Subtractor subtractor_27 (.a(argY[23:16]), .b(argZ[23:16]), .bout(subtractor_27_bout));  // open: out, bin
  Subtractor subtractor_28 (.a(argY[15:8]), .b(argZ[15:8]), .bout(subtractor_28_bout));  // open: out, bin
  Subtractor subtractor_29 (.a(argY[7:0]), .b(argZ[7:0]), .bout(subtractor_29_bout));  // open: out, bin
  BitFinder #(.\type ("high1")) bitfinder_37 (.in(argY[63:56]), .index(bitfinder_37_index), .found(bitfinder_37_found));
  BitFinder #(.\type ("high1")) bitfinder_38 (.in(argY[55:48]), .index(bitfinder_38_index), .found(bitfinder_38_found));
  BitFinder #(.\type ("high1")) bitfinder_39 (.in(argY[47:40]), .index(bitfinder_39_index), .found(bitfinder_39_found));
  BitFinder #(.\type ("high1")) bitfinder_40 (.in(argY[39:32]), .index(bitfinder_40_index), .found(bitfinder_40_found));
  BitFinder #(.\type ("high1")) bitfinder_41 (.in(argY[31:24]), .index(bitfinder_41_index), .found(bitfinder_41_found));
  BitFinder #(.\type ("high1")) bitfinder_42 (.in(argY[23:16]), .index(bitfinder_42_index), .found(bitfinder_42_found));
  BitFinder #(.\type ("high1")) bitfinder_43 (.in(argY[15:8]), .index(bitfinder_43_index), .found(bitfinder_43_found));
  BitFinder #(.\type ("high1")) bitfinder_44 (.in(argY[7:0]), .index(bitfinder_44_index), .found(bitfinder_44_found));
  FPDivider #(.fpwidth(8)) fpdivider_8 (.a(argY[63:56]), .b(argZ[63:56]), .out(fpdivider_15_out[63:56]));
  FPDivider #(.fpwidth(8)) fpdivider_9 (.a(argY[55:48]), .b(argZ[55:48]), .out(fpdivider_15_out[55:48]));
  FPDivider #(.fpwidth(8)) fpdivider_10 (.a(argY[47:40]), .b(argZ[47:40]), .out(fpdivider_15_out[47:40]));
  FPDivider #(.fpwidth(8)) fpdivider_11 (.a(argY[39:32]), .b(argZ[39:32]), .out(fpdivider_15_out[39:32]));
  FPDivider #(.fpwidth(8)) fpdivider_12 (.a(argY[31:24]), .b(argZ[31:24]), .out(fpdivider_15_out[31:24]));
  FPDivider #(.fpwidth(8)) fpdivider_13 (.a(argY[23:16]), .b(argZ[23:16]), .out(fpdivider_15_out[23:16]));
  FPDivider #(.fpwidth(8)) fpdivider_14 (.a(argY[15:8]), .b(argZ[15:8]), .out(fpdivider_15_out[15:8]));
  FPDivider #(.fpwidth(8)) fpdivider_15 (.a(argY[7:0]), .b(argZ[7:0]), .out(fpdivider_15_out[7:0]));
  // FPLogarithm #(.fpwidth(8)) fplogarithm_23: pin names not known; wires that end beside it: argY[63:56], argZ[63:56], fplogarithm_30_p3[63:56]
  // FPLogarithm #(.fpwidth(8)) fplogarithm_24: pin names not known; wires that end beside it: argY[55:48], argZ[55:48], fplogarithm_30_p3[55:48]
  // FPLogarithm #(.fpwidth(8)) fplogarithm_25: pin names not known; wires that end beside it: argY[47:40], argZ[47:40], fplogarithm_30_p3[47:40]
  // FPLogarithm #(.fpwidth(8)) fplogarithm_26: pin names not known; wires that end beside it: argY[39:32], argZ[39:32], fplogarithm_30_p3[39:32]
  // FPLogarithm #(.fpwidth(8)) fplogarithm_27: pin names not known; wires that end beside it: argY[31:24], argZ[31:24], fplogarithm_30_p3[31:24]
  // FPLogarithm #(.fpwidth(8)) fplogarithm_28: pin names not known; wires that end beside it: argY[23:16], argZ[23:16], fplogarithm_30_p3[23:16]
  // FPLogarithm #(.fpwidth(8)) fplogarithm_29: pin names not known; wires that end beside it: argY[15:8], argZ[15:8], fplogarithm_30_p3[15:8]
  // FPLogarithm #(.fpwidth(8)) fplogarithm_30: pin names not known; wires that end beside it: argY[7:0], argZ[7:0], fplogarithm_30_p3[7:0]
  Multiplexer #(.width(8)) multiplexer_120 (
    .in0({8{1'b0}}), .in1(8'h1), .out(multiplexer_133_out[31:24]), .sel(comparator_41_eq));
  Multiplexer #(.width(8)) multiplexer_121 (
    .in0({8{1'b0}}), .in1(8'h1), .out(multiplexer_133_out[23:16]), .sel(comparator_42_eq));
  Multiplexer #(.width(8)) multiplexer_122 (
    .in0({8{1'b0}}), .in1(8'h1), .out(multiplexer_143_out[63:56]), .sel(comparator_45_eq));
  Comparator comparator_45 (
    .a(argY[63:56]), .b(argZ[63:56]), .eq(comparator_45_eq), .lt(comparator_45_lt));  // open: gt
  Comparator comparator_46 (
    .a(argY[55:48]), .b(argZ[55:48]), .eq(comparator_46_eq), .lt(comparator_46_lt));  // open: gt
  Comparator comparator_47 (
    .a(argY[47:40]), .b(argZ[47:40]), .eq(comparator_47_eq), .lt(comparator_47_lt));  // open: gt
  Comparator comparator_48 (
    .a(argY[39:32]), .b(argZ[39:32]), .eq(comparator_48_eq), .lt(comparator_48_lt));  // open: gt
  Comparator comparator_49 (
    .a(argY[31:24]), .b(argZ[31:24]), .eq(comparator_49_eq), .lt(comparator_49_lt));  // open: gt
  Comparator comparator_50 (
    .a(argY[23:16]), .b(argZ[23:16]), .eq(comparator_50_eq), .lt(comparator_50_lt));  // open: gt
  Comparator comparator_51 (.a(argY[15:8]), .b(argZ[15:8]), .eq(comparator_51_eq), .lt(comparator_51_lt));  // open: gt
  Comparator comparator_52 (.a(argY[7:0]), .b(argZ[7:0]), .eq(comparator_52_eq), .lt(comparator_52_lt));  // open: gt
  assign bit_extender_94_out[63:56] = {{7{1'b0}}, subtractor_22_bout};  // Bit_Extender bit_extender_87
  assign bit_extender_94_out[55:48] = {{7{1'b0}}, subtractor_23_bout};  // Bit_Extender bit_extender_88
  assign bit_extender_94_out[47:40] = {{7{1'b0}}, subtractor_24_bout};  // Bit_Extender bit_extender_89
  assign bit_extender_94_out[39:32] = {{7{1'b0}}, subtractor_25_bout};  // Bit_Extender bit_extender_90
  assign bit_extender_94_out[31:24] = {{7{1'b0}}, subtractor_26_bout};  // Bit_Extender bit_extender_91
  assign bit_extender_94_out[23:16] = {{7{1'b0}}, subtractor_27_bout};  // Bit_Extender bit_extender_92
  assign bit_extender_94_out[15:8] = {{7{1'b0}}, subtractor_28_bout};  // Bit_Extender bit_extender_93
  assign bit_extender_94_out[7:0] = {{7{1'b0}}, subtractor_29_bout};  // Bit_Extender bit_extender_94
  assign bit_extender_95_out = {{5{1'b0}}, bitfinder_37_index};  // Bit_Extender bit_extender_95
  assign bit_extender_96_out = {{5{1'b0}}, bitfinder_38_index};  // Bit_Extender bit_extender_96
  assign bit_extender_97_out = {{5{1'b0}}, bitfinder_39_index};  // Bit_Extender bit_extender_97
  assign bit_extender_98_out = {{5{1'b0}}, bitfinder_40_index};  // Bit_Extender bit_extender_98
  assign bit_extender_99_out = {{5{1'b0}}, bitfinder_41_index};  // Bit_Extender bit_extender_99
  assign bit_extender_100_out = {{5{1'b0}}, bitfinder_42_index};  // Bit_Extender bit_extender_100
  assign bit_extender_101_out = {{5{1'b0}}, bitfinder_43_index};  // Bit_Extender bit_extender_101
  assign bit_extender_102_out = {{5{1'b0}}, bitfinder_44_index};  // Bit_Extender bit_extender_102
  // FPAbsolute #(.fpwidth(8)) fpabsolute_8: pin names not known; wires that end beside it: argY[63:56], fpabsolute_15_p2[63:56]
  // FPAbsolute #(.fpwidth(8)) fpabsolute_9: pin names not known; wires that end beside it: argY[55:48], fpabsolute_15_p2[55:48]
  // FPAbsolute #(.fpwidth(8)) fpabsolute_10: pin names not known; wires that end beside it: argY[47:40], fpabsolute_15_p2[47:40]
  // FPAbsolute #(.fpwidth(8)) fpabsolute_11: pin names not known; wires that end beside it: argY[39:32], fpabsolute_15_p2[39:32]
  // FPAbsolute #(.fpwidth(8)) fpabsolute_12: pin names not known; wires that end beside it: argY[31:24], fpabsolute_15_p2[31:24]
  // FPAbsolute #(.fpwidth(8)) fpabsolute_13: pin names not known; wires that end beside it: argY[23:16], fpabsolute_15_p2[23:16]
  // FPAbsolute #(.fpwidth(8)) fpabsolute_14: pin names not known; wires that end beside it: argY[15:8], fpabsolute_15_p2[15:8]
  // FPAbsolute #(.fpwidth(8)) fpabsolute_15: pin names not known; wires that end beside it: argY[7:0], fpabsolute_15_p2[7:0]
  // FPToInt #(.fpwidth(8), .mode("truncate")) fptoint_53: pin names not known; wires that end beside it: argY[63:56], fptoint_60_p2[63:56]
  // FPToInt #(.fpwidth(8), .mode("truncate")) fptoint_54: pin names not known; wires that end beside it: argY[55:48], fptoint_60_p2[55:48]
  // FPToInt #(.fpwidth(8), .mode("truncate")) fptoint_55: pin names not known; wires that end beside it: argY[47:40], fptoint_60_p2[47:40]
  // FPToInt #(.fpwidth(8), .mode("truncate")) fptoint_56: pin names not known; wires that end beside it: argY[39:32], fptoint_60_p2[39:32]
  // FPToInt #(.fpwidth(8), .mode("truncate")) fptoint_57: pin names not known; wires that end beside it: argY[31:24], fptoint_60_p2[31:24]
  // FPToInt #(.fpwidth(8), .mode("truncate")) fptoint_58: pin names not known; wires that end beside it: argY[23:16], fptoint_60_p2[23:16]
  // FPToInt #(.fpwidth(8), .mode("truncate")) fptoint_59: pin names not known; wires that end beside it: argY[15:8], fptoint_60_p2[15:8]
  // FPToInt #(.fpwidth(8), .mode("truncate")) fptoint_60: pin names not known; wires that end beside it: argY[7:0], fptoint_60_p2[7:0]
  Multiplexer #(.width(8)) multiplexer_123 (
    .in0({8{1'b0}}), .in1(8'h1), .out(multiplexer_133_out[15:8]), .sel(comparator_43_eq));
  Multiplexer #(.width(8)) multiplexer_124 (
    .in0({8{1'b0}}), .in1(8'h1), .out(multiplexer_143_out[55:48]), .sel(comparator_46_eq));
  Shifter #(.shift("rl")) shifter_60 (.in(argY[63:56]), .\dist (bitselector_19_out), .out(shifter_67_out[63:56]));
  Shifter #(.shift("rl")) shifter_61 (.in(argY[55:48]), .\dist (bitselector_18_out), .out(shifter_67_out[55:48]));
  Shifter #(.shift("rl")) shifter_62 (.in(argY[47:40]), .\dist (bitselector_17_out), .out(shifter_67_out[47:40]));
  Shifter #(.shift("rl")) shifter_63 (.in(argY[39:32]), .\dist (bitselector_16_out), .out(shifter_67_out[39:32]));
  Shifter #(.shift("rl")) shifter_64 (.in(argY[31:24]), .\dist (bitselector_15_out), .out(shifter_67_out[31:24]));
  Shifter #(.shift("rl")) shifter_65 (.in(argY[23:16]), .\dist (bitselector_14_out), .out(shifter_67_out[23:16]));
  Shifter #(.shift("rl")) shifter_66 (.in(argY[15:8]), .\dist (bitselector_13_out), .out(shifter_67_out[15:8]));
  Shifter #(.shift("rl")) shifter_67 (.in(argY[7:0]), .\dist (bitselector_12_out), .out(shifter_67_out[7:0]));
  Negator negator_8 (.in(argY[63:56]), .out(negator_15_out[63:56]));
  Negator negator_9 (.in(argY[55:48]), .out(negator_15_out[55:48]));
  Negator negator_10 (.in(argY[47:40]), .out(negator_15_out[47:40]));
  Negator negator_11 (.in(argY[39:32]), .out(negator_15_out[39:32]));
  Negator negator_12 (.in(argY[31:24]), .out(negator_15_out[31:24]));
  Negator negator_13 (.in(argY[23:16]), .out(negator_15_out[23:16]));
  Negator negator_14 (.in(argY[15:8]), .out(negator_15_out[15:8]));
  Negator negator_15 (.in(argY[7:0]), .out(negator_15_out[7:0]));
  Multiplexer #(.width(8)) multiplexer_125 (
    .in0({8{1'b1}}), .in1(bit_extender_95_out), .out(multiplexer_132_out[63:56]), .sel(bitfinder_37_found));
  Multiplexer #(.width(8)) multiplexer_126 (
    .in0({8{1'b1}}), .in1(bit_extender_96_out), .out(multiplexer_132_out[55:48]), .sel(bitfinder_38_found));
  Multiplexer #(.width(8)) multiplexer_127 (
    .in0({8{1'b1}}), .in1(bit_extender_97_out), .out(multiplexer_132_out[47:40]), .sel(bitfinder_39_found));
  Multiplexer #(.width(8)) multiplexer_128 (
    .in0({8{1'b1}}), .in1(bit_extender_98_out), .out(multiplexer_132_out[39:32]), .sel(bitfinder_40_found));
  Multiplexer #(.width(8)) multiplexer_129 (
    .in0({8{1'b1}}), .in1(bit_extender_99_out), .out(multiplexer_132_out[31:24]), .sel(bitfinder_41_found));
  Multiplexer #(.width(8)) multiplexer_130 (
    .in0({8{1'b1}}), .in1(bit_extender_100_out), .out(multiplexer_132_out[23:16]), .sel(bitfinder_42_found));
  Multiplexer #(.width(8)) multiplexer_131 (
    .in0({8{1'b1}}), .in1(bit_extender_101_out), .out(multiplexer_132_out[15:8]), .sel(bitfinder_43_found));
  Multiplexer #(.width(8)) multiplexer_132 (
    .in0({8{1'b1}}), .in1(bit_extender_102_out), .out(multiplexer_132_out[7:0]), .sel(bitfinder_44_found));
  Multiplexer #(.width(8)) multiplexer_133 (
    .in0({8{1'b0}}), .in1(8'h1), .out(multiplexer_133_out[7:0]), .sel(comparator_44_eq));
  Multiplexer #(.width(8)) multiplexer_134 (
    .in0({8{1'b0}}), .in1(8'h1), .out(multiplexer_143_out[47:40]), .sel(comparator_47_eq));
  Multiplexer #(.width(8)) multiplexer_135 (
    .in0({8{1'b0}}), .in1(8'h1), .out(multiplexer_143_out[39:32]), .sel(comparator_48_eq));
  // FPExponentiator #(.fpwidth(8)) fpexponentiator_15: pin names not known; wires that end beside it: argY[63:56], argZ[63:56], fpexponentiator_22_p3[63:56]
  // FPExponentiator #(.fpwidth(8)) fpexponentiator_16: pin names not known; wires that end beside it: argY[55:48], argZ[55:48], fpexponentiator_22_p3[55:48]
  // FPExponentiator #(.fpwidth(8)) fpexponentiator_17: pin names not known; wires that end beside it: argY[47:40], argZ[47:40], fpexponentiator_22_p3[47:40]
  // FPExponentiator #(.fpwidth(8)) fpexponentiator_18: pin names not known; wires that end beside it: argY[39:32], argZ[39:32], fpexponentiator_22_p3[39:32]
  // FPExponentiator #(.fpwidth(8)) fpexponentiator_19: pin names not known; wires that end beside it: argY[31:24], argZ[31:24], fpexponentiator_22_p3[31:24]
  // FPExponentiator #(.fpwidth(8)) fpexponentiator_20: pin names not known; wires that end beside it: argY[23:16], argZ[23:16], fpexponentiator_22_p3[23:16]
  // FPExponentiator #(.fpwidth(8)) fpexponentiator_21: pin names not known; wires that end beside it: argY[15:8], argZ[15:8], fpexponentiator_22_p3[15:8]
  // FPExponentiator #(.fpwidth(8)) fpexponentiator_22: pin names not known; wires that end beside it: argY[7:0], argZ[7:0], fpexponentiator_22_p3[7:0]
  Multiplexer #(.width(8)) multiplexer_136 (
    .in0({8{1'b0}}), .in1(8'h1), .out(multiplexer_157_out[63:56]), .sel(comparator_37_lt));
  Multiplexer #(.width(8)) multiplexer_137 (
    .in0({8{1'b0}}), .in1(8'h1), .out(multiplexer_143_out[31:24]), .sel(comparator_49_eq));
  BitFinder #(.\type ("low0")) bitfinder_45 (.in(argY[63:56]), .index(bitfinder_45_index), .found(bitfinder_45_found));
  BitFinder #(.\type ("low0")) bitfinder_46 (.in(argY[55:48]), .index(bitfinder_46_index), .found(bitfinder_46_found));
  BitFinder #(.\type ("low0")) bitfinder_47 (.in(argY[47:40]), .index(bitfinder_47_index), .found(bitfinder_47_found));
  BitFinder #(.\type ("low0")) bitfinder_48 (.in(argY[39:32]), .index(bitfinder_48_index), .found(bitfinder_48_found));
  BitFinder #(.\type ("low0")) bitfinder_49 (.in(argY[31:24]), .index(bitfinder_49_index), .found(bitfinder_49_found));
  BitFinder #(.\type ("low0")) bitfinder_50 (.in(argY[23:16]), .index(bitfinder_50_index), .found(bitfinder_50_found));
  BitFinder #(.\type ("low0")) bitfinder_51 (.in(argY[15:8]), .index(bitfinder_51_index), .found(bitfinder_51_found));
  BitFinder #(.\type ("low0")) bitfinder_52 (.in(argY[7:0]), .index(bitfinder_52_index), .found(bitfinder_52_found));
  // FPNegator #(.fpwidth(8)) fpnegator_8: pin names not known; wires that end beside it: argY[63:56], fpnegator_15_p2[63:56]
  // FPNegator #(.fpwidth(8)) fpnegator_9: pin names not known; wires that end beside it: argY[55:48], fpnegator_15_p2[55:48]
  // FPNegator #(.fpwidth(8)) fpnegator_10: pin names not known; wires that end beside it: argY[47:40], fpnegator_15_p2[47:40]
  // FPNegator #(.fpwidth(8)) fpnegator_11: pin names not known; wires that end beside it: argY[39:32], fpnegator_15_p2[39:32]
  // FPNegator #(.fpwidth(8)) fpnegator_12: pin names not known; wires that end beside it: argY[31:24], fpnegator_15_p2[31:24]
  // FPNegator #(.fpwidth(8)) fpnegator_13: pin names not known; wires that end beside it: argY[23:16], fpnegator_15_p2[23:16]
  // FPNegator #(.fpwidth(8)) fpnegator_14: pin names not known; wires that end beside it: argY[15:8], fpnegator_15_p2[15:8]
  // FPNegator #(.fpwidth(8)) fpnegator_15: pin names not known; wires that end beside it: argY[7:0], fpnegator_15_p2[7:0]
  // FPMinMax #(.fpwidth(8)) fpminmax_14: pin names not known; wires that end beside it: argY[63:56], argZ[63:56], fpminmax_21_p3[63:56]
  // FPMinMax #(.fpwidth(8)) fpminmax_15: pin names not known; wires that end beside it: argY[55:48], argZ[55:48], fpminmax_21_p3[55:48]
  // FPMinMax #(.fpwidth(8)) fpminmax_16: pin names not known; wires that end beside it: argY[47:40], argZ[47:40], fpminmax_21_p3[47:40]
  // FPMinMax #(.fpwidth(8)) fpminmax_17: pin names not known; wires that end beside it: argY[39:32], argZ[39:32], fpminmax_21_p3[39:32]
  // FPMinMax #(.fpwidth(8)) fpminmax_18: pin names not known; wires that end beside it: argY[31:24], argZ[31:24], fpminmax_21_p3[31:24]
  // FPMinMax #(.fpwidth(8)) fpminmax_19: pin names not known; wires that end beside it: argY[23:16], argZ[23:16], fpminmax_21_p3[23:16]
  // FPMinMax #(.fpwidth(8)) fpminmax_20: pin names not known; wires that end beside it: argY[15:8], argZ[15:8], fpminmax_21_p3[15:8]
  // FPMinMax #(.fpwidth(8)) fpminmax_21: pin names not known; wires that end beside it: argY[7:0], argZ[7:0], fpminmax_21_p3[7:0]
  // FPMinMax #(.fpwidth(8)) fpminmax_22: pin names not known; wires that end beside it: argY[63:56], argZ[63:56], fpminmax_29_p3[63:56]
  // FPMinMax #(.fpwidth(8)) fpminmax_23: pin names not known; wires that end beside it: argY[55:48], argZ[55:48], fpminmax_29_p3[55:48]
  // FPMinMax #(.fpwidth(8)) fpminmax_24: pin names not known; wires that end beside it: argY[47:40], argZ[47:40], fpminmax_29_p3[47:40]
  // FPMinMax #(.fpwidth(8)) fpminmax_25: pin names not known; wires that end beside it: argY[39:32], argZ[39:32], fpminmax_29_p3[39:32]
  // FPMinMax #(.fpwidth(8)) fpminmax_26: pin names not known; wires that end beside it: argY[31:24], argZ[31:24], fpminmax_29_p3[31:24]
  // FPMinMax #(.fpwidth(8)) fpminmax_27: pin names not known; wires that end beside it: argY[23:16], argZ[23:16], fpminmax_29_p3[23:16]
  // FPMinMax #(.fpwidth(8)) fpminmax_28: pin names not known; wires that end beside it: argY[15:8], argZ[15:8], fpminmax_29_p3[15:8]
  // FPMinMax #(.fpwidth(8)) fpminmax_29: pin names not known; wires that end beside it: argY[7:0], argZ[7:0], fpminmax_29_p3[7:0]
  Multiplexer #(.width(8)) multiplexer_138 (
    .in0({8{1'b0}}), .in1(8'h1), .out(multiplexer_157_out[55:48]), .sel(comparator_38_lt));
  Multiplexer #(.width(8)) multiplexer_139 (
    .in0({8{1'b0}}), .in1(8'h1), .out(multiplexer_143_out[23:16]), .sel(comparator_50_eq));
  Shifter #(.shift("rr")) shifter_68 (.in(argY[63:56]), .\dist (bitselector_19_out), .out(shifter_75_out[63:56]));
  Shifter #(.shift("rr")) shifter_69 (.in(argY[55:48]), .\dist (bitselector_18_out), .out(shifter_75_out[55:48]));
  Shifter #(.shift("rr")) shifter_70 (.in(argY[47:40]), .\dist (bitselector_17_out), .out(shifter_75_out[47:40]));
  Shifter #(.shift("rr")) shifter_71 (.in(argY[39:32]), .\dist (bitselector_16_out), .out(shifter_75_out[39:32]));
  Shifter #(.shift("rr")) shifter_72 (.in(argY[31:24]), .\dist (bitselector_15_out), .out(shifter_75_out[31:24]));
  Shifter #(.shift("rr")) shifter_73 (.in(argY[23:16]), .\dist (bitselector_14_out), .out(shifter_75_out[23:16]));
  Shifter #(.shift("rr")) shifter_74 (.in(argY[15:8]), .\dist (bitselector_13_out), .out(shifter_75_out[15:8]));
  Shifter #(.shift("rr")) shifter_75 (.in(argY[7:0]), .\dist (bitselector_12_out), .out(shifter_75_out[7:0]));
  // FPExponentiator #(.fpwidth(8), .mode("exp")) fpexponentiator_23: pin names not known; wires that end beside it: argY[63:56], fpexponentiator_30_p2[63:56]
  // FPExponentiator #(.fpwidth(8), .mode("exp")) fpexponentiator_24: pin names not known; wires that end beside it: argY[55:48], fpexponentiator_30_p2[55:48]
  // FPExponentiator #(.fpwidth(8), .mode("exp")) fpexponentiator_25: pin names not known; wires that end beside it: argY[47:40], fpexponentiator_30_p2[47:40]
  // FPExponentiator #(.fpwidth(8), .mode("exp")) fpexponentiator_26: pin names not known; wires that end beside it: argY[39:32], fpexponentiator_30_p2[39:32]
  // FPExponentiator #(.fpwidth(8), .mode("exp")) fpexponentiator_27: pin names not known; wires that end beside it: argY[31:24], fpexponentiator_30_p2[31:24]
  // FPExponentiator #(.fpwidth(8), .mode("exp")) fpexponentiator_28: pin names not known; wires that end beside it: argY[23:16], fpexponentiator_30_p2[23:16]
  // FPExponentiator #(.fpwidth(8), .mode("exp")) fpexponentiator_29: pin names not known; wires that end beside it: argY[15:8], fpexponentiator_30_p2[15:8]
  // FPExponentiator #(.fpwidth(8), .mode("exp")) fpexponentiator_30: pin names not known; wires that end beside it: argY[7:0], fpexponentiator_30_p2[7:0]
  Multiplier #(.mode("twosComplement")) multiplier_22 (
    .a(argY[63:56]), .b(argZ[63:56]), .cout(multiplier_29_cout[63:56]));  // open: out, cin
  Multiplier #(.mode("twosComplement")) multiplier_23 (
    .a(argY[55:48]), .b(argZ[55:48]), .cout(multiplier_29_cout[55:48]));  // open: out, cin
  Multiplier #(.mode("twosComplement")) multiplier_24 (
    .a(argY[47:40]), .b(argZ[47:40]), .cout(multiplier_29_cout[47:40]));  // open: out, cin
  Multiplier #(.mode("twosComplement")) multiplier_25 (
    .a(argY[39:32]), .b(argZ[39:32]), .cout(multiplier_29_cout[39:32]));  // open: out, cin
  Multiplier #(.mode("twosComplement")) multiplier_26 (
    .a(argY[31:24]), .b(argZ[31:24]), .cout(multiplier_29_cout[31:24]));  // open: out, cin
  Multiplier #(.mode("twosComplement")) multiplier_27 (
    .a(argY[23:16]), .b(argZ[23:16]), .cout(multiplier_29_cout[23:16]));  // open: out, cin
  Multiplier #(.mode("twosComplement")) multiplier_28 (
    .a(argY[15:8]), .b(argZ[15:8]), .cout(multiplier_29_cout[15:8]));  // open: out, cin
  Multiplier #(.mode("twosComplement")) multiplier_29 (
    .a(argY[7:0]), .b(argZ[7:0]), .cout(multiplier_29_cout[7:0]));  // open: out, cin
  assign bit_extender_103_out = {{5{1'b0}}, bitfinder_45_index};  // Bit_Extender bit_extender_103
  assign bit_extender_104_out = {{5{1'b0}}, bitfinder_46_index};  // Bit_Extender bit_extender_104
  assign bit_extender_105_out = {{5{1'b0}}, bitfinder_47_index};  // Bit_Extender bit_extender_105
  assign bit_extender_106_out = {{5{1'b0}}, bitfinder_48_index};  // Bit_Extender bit_extender_106
  assign bit_extender_107_out = {{5{1'b0}}, bitfinder_49_index};  // Bit_Extender bit_extender_107
  assign bit_extender_108_out = {{5{1'b0}}, bitfinder_50_index};  // Bit_Extender bit_extender_108
  assign bit_extender_109_out = {{5{1'b0}}, bitfinder_51_index};  // Bit_Extender bit_extender_109
  assign bit_extender_110_out = {{5{1'b0}}, bitfinder_52_index};  // Bit_Extender bit_extender_110
  Multiplexer #(.width(8)) multiplexer_140 (
    .in0({8{1'b0}}), .in1(8'h1), .out(multiplexer_157_out[47:40]), .sel(comparator_39_lt));
  Multiplexer #(.width(8)) multiplexer_141 (
    .in0({8{1'b0}}), .in1(8'h1), .out(multiplexer_157_out[39:32]), .sel(comparator_40_lt));
  Multiplexer #(.width(8)) multiplexer_142 (
    .in0({8{1'b0}}), .in1(8'h1), .out(multiplexer_143_out[15:8]), .sel(comparator_51_eq));
  Multiplexer #(.width(8)) multiplexer_143 (
    .in0({8{1'b0}}), .in1(8'h1), .out(multiplexer_143_out[7:0]), .sel(comparator_52_eq));
  Multiplexer #(.width(8)) multiplexer_144 (
    .in0({8{1'b1}}), .in1(bit_extender_103_out), .out(multiplexer_151_out[63:56]), .sel(bitfinder_45_found));
  Multiplexer #(.width(8)) multiplexer_145 (
    .in0({8{1'b1}}), .in1(bit_extender_104_out), .out(multiplexer_151_out[55:48]), .sel(bitfinder_46_found));
  Multiplexer #(.width(8)) multiplexer_146 (
    .in0({8{1'b1}}), .in1(bit_extender_105_out), .out(multiplexer_151_out[47:40]), .sel(bitfinder_47_found));
  Multiplexer #(.width(8)) multiplexer_147 (
    .in0({8{1'b1}}), .in1(bit_extender_106_out), .out(multiplexer_151_out[39:32]), .sel(bitfinder_48_found));
  Multiplexer #(.width(8)) multiplexer_148 (
    .in0({8{1'b1}}), .in1(bit_extender_107_out), .out(multiplexer_151_out[31:24]), .sel(bitfinder_49_found));
  Multiplexer #(.width(8)) multiplexer_149 (
    .in0({8{1'b1}}), .in1(bit_extender_108_out), .out(multiplexer_151_out[23:16]), .sel(bitfinder_50_found));
  Multiplexer #(.width(8)) multiplexer_150 (
    .in0({8{1'b1}}), .in1(bit_extender_109_out), .out(multiplexer_151_out[15:8]), .sel(bitfinder_51_found));
  Multiplexer #(.width(8)) multiplexer_151 (
    .in0({8{1'b1}}), .in1(bit_extender_110_out), .out(multiplexer_151_out[7:0]), .sel(bitfinder_52_found));
  Multiplexer #(.width(8)) multiplexer_152 (
    .in0({8{1'b0}}), .in1(8'h1), .out(multiplexer_157_out[31:24]), .sel(comparator_41_lt));
  Multiplexer #(.width(8)) multiplexer_153 (
    .in0({8{1'b0}}), .in1(8'h1), .out(multiplexer_157_out[23:16]), .sel(comparator_42_lt));
  Multiplexer #(.width(8)) multiplexer_154 (
    .in0({8{1'b0}}), .in1(8'h1), .out(multiplexer_173_out[63:56]), .sel(comparator_45_lt));
  Multiplexer #(.width(8)) multiplexer_155 (
    .in0({8{1'b0}}), .in1(8'h1), .out(multiplexer_173_out[55:48]), .sel(comparator_46_lt));
  BitFinder #(.\type ("high0")) bitfinder_53 (.in(argY[63:56]), .index(bitfinder_53_index), .found(bitfinder_53_found));
  BitFinder #(.\type ("high0")) bitfinder_54 (.in(argY[55:48]), .index(bitfinder_54_index), .found(bitfinder_54_found));
  BitFinder #(.\type ("high0")) bitfinder_55 (.in(argY[47:40]), .index(bitfinder_55_index), .found(bitfinder_55_found));
  BitFinder #(.\type ("high0")) bitfinder_56 (.in(argY[39:32]), .index(bitfinder_56_index), .found(bitfinder_56_found));
  BitFinder #(.\type ("high0")) bitfinder_57 (.in(argY[31:24]), .index(bitfinder_57_index), .found(bitfinder_57_found));
  BitFinder #(.\type ("high0")) bitfinder_58 (.in(argY[23:16]), .index(bitfinder_58_index), .found(bitfinder_58_found));
  BitFinder #(.\type ("high0")) bitfinder_59 (.in(argY[15:8]), .index(bitfinder_59_index), .found(bitfinder_59_found));
  BitFinder #(.\type ("high0")) bitfinder_60 (.in(argY[7:0]), .index(bitfinder_60_index), .found(bitfinder_60_found));
  Multiplexer #(.width(8)) multiplexer_156 (
    .in0({8{1'b0}}), .in1(8'h1), .out(multiplexer_157_out[15:8]), .sel(comparator_43_lt));
  Multiplexer #(.width(8)) multiplexer_157 (
    .in0({8{1'b0}}), .in1(8'h1), .out(multiplexer_157_out[7:0]), .sel(comparator_44_lt));
  Multiplexer #(.width(8)) multiplexer_158 (
    .in0({8{1'b0}}), .in1(8'h1), .out(multiplexer_173_out[47:40]), .sel(comparator_47_lt));
  assign bit_extender_111_out = {{5{1'b0}}, bitfinder_53_index};  // Bit_Extender bit_extender_111
  assign bit_extender_112_out = {{5{1'b0}}, bitfinder_54_index};  // Bit_Extender bit_extender_112
  assign bit_extender_113_out = {{5{1'b0}}, bitfinder_55_index};  // Bit_Extender bit_extender_113
  assign bit_extender_114_out = {{5{1'b0}}, bitfinder_56_index};  // Bit_Extender bit_extender_114
  assign bit_extender_115_out = {{5{1'b0}}, bitfinder_57_index};  // Bit_Extender bit_extender_115
  assign bit_extender_116_out = {{5{1'b0}}, bitfinder_58_index};  // Bit_Extender bit_extender_116
  assign bit_extender_117_out = {{5{1'b0}}, bitfinder_59_index};  // Bit_Extender bit_extender_117
  assign bit_extender_118_out = {{5{1'b0}}, bitfinder_60_index};  // Bit_Extender bit_extender_118
  Multiplexer #(.width(8)) multiplexer_159 (
    .in0({8{1'b0}}), .in1(8'h1), .out(multiplexer_173_out[39:32]), .sel(comparator_48_lt));
  Divider #(.mode("twosComplement")) divider_22 (
    .a(argY[63:56]), .b(argZ[63:56]), .rem(divider_29_rem[63:56]));  // open: out, upper
  Divider #(.mode("twosComplement")) divider_23 (
    .a(argY[55:48]), .b(argZ[55:48]), .rem(divider_29_rem[55:48]));  // open: out, upper
  Divider #(.mode("twosComplement")) divider_24 (
    .a(argY[47:40]), .b(argZ[47:40]), .rem(divider_29_rem[47:40]));  // open: out, upper
  Divider #(.mode("twosComplement")) divider_25 (
    .a(argY[39:32]), .b(argZ[39:32]), .rem(divider_29_rem[39:32]));  // open: out, upper
  Divider #(.mode("twosComplement")) divider_26 (
    .a(argY[31:24]), .b(argZ[31:24]), .rem(divider_29_rem[31:24]));  // open: out, upper
  Divider #(.mode("twosComplement")) divider_27 (
    .a(argY[23:16]), .b(argZ[23:16]), .rem(divider_29_rem[23:16]));  // open: out, upper
  Divider #(.mode("twosComplement")) divider_28 (
    .a(argY[15:8]), .b(argZ[15:8]), .rem(divider_29_rem[15:8]));  // open: out, upper
  Divider #(.mode("twosComplement")) divider_29 (
    .a(argY[7:0]), .b(argZ[7:0]), .rem(divider_29_rem[7:0]));  // open: out, upper
  Multiplexer #(.width(8)) multiplexer_160 (
    .in0({8{1'b1}}), .in1(bit_extender_111_out), .out(multiplexer_167_out[63:56]), .sel(bitfinder_53_found));
  Multiplexer #(.width(8)) multiplexer_161 (
    .in0({8{1'b1}}), .in1(bit_extender_112_out), .out(multiplexer_167_out[55:48]), .sel(bitfinder_54_found));
  Multiplexer #(.width(8)) multiplexer_162 (
    .in0({8{1'b1}}), .in1(bit_extender_113_out), .out(multiplexer_167_out[47:40]), .sel(bitfinder_55_found));
  Multiplexer #(.width(8)) multiplexer_163 (
    .in0({8{1'b1}}), .in1(bit_extender_114_out), .out(multiplexer_167_out[39:32]), .sel(bitfinder_56_found));
  Multiplexer #(.width(8)) multiplexer_164 (
    .in0({8{1'b1}}), .in1(bit_extender_115_out), .out(multiplexer_167_out[31:24]), .sel(bitfinder_57_found));
  Multiplexer #(.width(8)) multiplexer_165 (
    .in0({8{1'b1}}), .in1(bit_extender_116_out), .out(multiplexer_167_out[23:16]), .sel(bitfinder_58_found));
  Multiplexer #(.width(8)) multiplexer_166 (
    .in0({8{1'b1}}), .in1(bit_extender_117_out), .out(multiplexer_167_out[15:8]), .sel(bitfinder_59_found));
  Multiplexer #(.width(8)) multiplexer_167 (
    .in0({8{1'b1}}), .in1(bit_extender_118_out), .out(multiplexer_167_out[7:0]), .sel(bitfinder_60_found));
  Multiplexer #(.width(8)) multiplexer_168 (
    .in0({8{1'b0}}), .in1(8'h1), .out(multiplexer_173_out[31:24]), .sel(comparator_49_lt));
  Multiplexer #(.width(8)) multiplexer_169 (
    .in0({8{1'b0}}), .in1(8'h1), .out(multiplexer_173_out[23:16]), .sel(comparator_50_lt));
  // FPComparator #(.fpwidth(8)) fpcomparator_15: pin names not known; wires that end beside it: argY[63:56], {8{1'b0}}, fpcomparator_15_p3, fpcomparator_15_p4
  // FPComparator #(.fpwidth(8)) fpcomparator_16: pin names not known; wires that end beside it: argY[55:48], {8{1'b0}}, fpcomparator_16_p3, fpcomparator_16_p4
  // FPComparator #(.fpwidth(8)) fpcomparator_17: pin names not known; wires that end beside it: argY[47:40], {8{1'b0}}, fpcomparator_17_p3, fpcomparator_17_p4
  // FPComparator #(.fpwidth(8)) fpcomparator_18: pin names not known; wires that end beside it: argY[39:32], {8{1'b0}}, fpcomparator_18_p3, fpcomparator_18_p4
  // FPComparator #(.fpwidth(8)) fpcomparator_19: pin names not known; wires that end beside it: argY[31:24], {8{1'b0}}, fpcomparator_19_p3, fpcomparator_19_p4
  // FPComparator #(.fpwidth(8)) fpcomparator_20: pin names not known; wires that end beside it: argY[23:16], {8{1'b0}}, fpcomparator_20_p3, fpcomparator_20_p4
  // FPComparator #(.fpwidth(8)) fpcomparator_21: pin names not known; wires that end beside it: argY[15:8], {8{1'b0}}, fpcomparator_21_p3, fpcomparator_21_p4
  // FPComparator #(.fpwidth(8)) fpcomparator_22: pin names not known; wires that end beside it: argY[7:0], {8{1'b0}}, fpcomparator_22_p3, fpcomparator_22_p4
  Multiplexer #(.width(8)) multiplexer_170 (
    .in0({8{1'b0}}), .in1(8'h1), .out(multiplexer_173_out[15:8]), .sel(comparator_51_lt));
  BitAdder bitadder_8 (.in0(argY[63:56]), .out(bitadder_8_out));
  BitAdder bitadder_9 (.in0(argY[55:48]), .out(bitadder_9_out));
  BitAdder bitadder_10 (.in0(argY[47:40]), .out(bitadder_10_out));
  BitAdder bitadder_11 (.in0(argY[39:32]), .out(bitadder_11_out));
  BitAdder bitadder_12 (.in0(argY[31:24]), .out(bitadder_12_out));
  BitAdder bitadder_13 (.in0(argY[23:16]), .out(bitadder_13_out));
  BitAdder bitadder_14 (.in0(argY[15:8]), .out(bitadder_14_out));
  BitAdder bitadder_15 (.in0(argY[7:0]), .out(bitadder_15_out));
  Multiplexer #(.width(8)) multiplexer_171 (
    .in0({8{1'b0}}), .in1(8'h1), .out(multiplexer_186_out[63:56]), .sel(fpcomparator_15_p3));
  Multiplexer #(.width(8)) multiplexer_172 (
    .in0({8{1'b0}}), .in1(8'h1), .out(multiplexer_186_out[55:48]), .sel(fpcomparator_16_p3));
  Multiplexer #(.width(8)) multiplexer_173 (
    .in0({8{1'b0}}), .in1(8'h1), .out(multiplexer_173_out[7:0]), .sel(comparator_52_lt));
  assign bit_extender_126_out[63:56] = {{4{1'b0}}, bitadder_8_out};  // Bit_Extender bit_extender_119
  assign bit_extender_126_out[55:48] = {{4{1'b0}}, bitadder_9_out};  // Bit_Extender bit_extender_120
  assign bit_extender_126_out[47:40] = {{4{1'b0}}, bitadder_10_out};  // Bit_Extender bit_extender_121
  assign bit_extender_126_out[39:32] = {{4{1'b0}}, bitadder_11_out};  // Bit_Extender bit_extender_122
  assign bit_extender_126_out[31:24] = {{4{1'b0}}, bitadder_12_out};  // Bit_Extender bit_extender_123
  assign bit_extender_126_out[23:16] = {{4{1'b0}}, bitadder_13_out};  // Bit_Extender bit_extender_124
  assign bit_extender_126_out[15:8] = {{4{1'b0}}, bitadder_14_out};  // Bit_Extender bit_extender_125
  assign bit_extender_126_out[7:0] = {{4{1'b0}}, bitadder_15_out};  // Bit_Extender bit_extender_126
  Multiplexer #(.width(8)) multiplexer_174 (
    .in0({8{1'b0}}), .in1(8'h1), .out(multiplexer_186_out[47:40]), .sel(fpcomparator_17_p3));
  Multiplexer #(.width(8)) multiplexer_175 (
    .in0(argX[63:56]), .in1(buffer_9_out), .out(multiplexer_193_out[63:56]), .sel(not_9_out));
  assign buffer_9_out = argY[63:56];  // Buffer buffer_9, 8 bits wide
  Comparator #(.mode("unsigned")) comparator_53 (
    .a(argZ[63:56]), .b({8{1'b0}}), .eq(comparator_53_eq));  // open: gt, lt
  Comparator #(.mode("unsigned")) comparator_54 (
    .a(argZ[55:48]), .b({8{1'b0}}), .eq(comparator_54_eq));  // open: gt, lt
  Comparator #(.mode("unsigned")) comparator_55 (
    .a(argZ[47:40]), .b({8{1'b0}}), .eq(comparator_55_eq));  // open: gt, lt
  Comparator #(.mode("unsigned")) comparator_56 (
    .a(argZ[39:32]), .b({8{1'b0}}), .eq(comparator_56_eq));  // open: gt, lt
  Comparator #(.mode("unsigned")) comparator_57 (
    .a(argZ[31:24]), .b({8{1'b0}}), .eq(comparator_57_eq));  // open: gt, lt
  Comparator #(.mode("unsigned")) comparator_58 (
    .a(argZ[23:16]), .b({8{1'b0}}), .eq(comparator_58_eq));  // open: gt, lt
  Comparator #(.mode("unsigned")) comparator_59 (.a(argZ[15:8]), .b({8{1'b0}}), .eq(comparator_59_eq));  // open: gt, lt
  Comparator #(.mode("unsigned")) comparator_60 (.a(argZ[7:0]), .b({8{1'b0}}), .eq(comparator_60_eq));  // open: gt, lt
  Multiplexer #(.width(8)) multiplexer_176 (
    .in0({8{1'b0}}), .in1(8'h1), .out(multiplexer_186_out[39:32]), .sel(fpcomparator_18_p3));
  Multiplexer #(.width(8)) multiplexer_177 (
    .in0(argX[55:48]), .in1(buffer_10_out), .out(multiplexer_193_out[55:48]), .sel(not_10_out));
  assign buffer_10_out = argY[55:48];  // Buffer buffer_10, 8 bits wide
  not not_9 (not_9_out, comparator_53_eq);
  not not_10 (not_10_out, comparator_54_eq);
  not not_11 (not_11_out, comparator_55_eq);
  not not_12 (not_12_out, comparator_56_eq);
  not not_13 (not_13_out, comparator_57_eq);
  not not_14 (not_14_out, comparator_58_eq);
  not not_15 (not_15_out, comparator_59_eq);
  not not_16 (not_16_out, comparator_60_eq);
  Multiplexer #(.width(8)) multiplexer_178 (
    .in0({8{1'b0}}), .in1(8'h1), .out(multiplexer_186_out[31:24]), .sel(fpcomparator_19_p3));
  Multiplexer #(.width(8)) multiplexer_179 (
    .in0({8{1'b0}}), .in1(8'h1), .out(multiplexer_186_out[23:16]), .sel(fpcomparator_20_p3));
  Multiplexer #(.width(8)) multiplexer_180 (
    .in0({8{1'b0}}), .in1(8'h1), .out(multiplexer_199_out[63:56]), .sel(fpcomparator_23_p3));
  // FPComparator #(.fpwidth(8)) fpcomparator_23: pin names not known; wires that end beside it: argY[63:56], argZ[63:56], fpcomparator_23_p3, fpcomparator_23_p4
  // FPComparator #(.fpwidth(8)) fpcomparator_24: pin names not known; wires that end beside it: argY[55:48], argZ[55:48], fpcomparator_24_p3, fpcomparator_24_p4
  // FPComparator #(.fpwidth(8)) fpcomparator_25: pin names not known; wires that end beside it: argY[47:40], argZ[47:40], fpcomparator_25_p3, fpcomparator_25_p4
  // FPComparator #(.fpwidth(8)) fpcomparator_26: pin names not known; wires that end beside it: argY[39:32], argZ[39:32], fpcomparator_26_p3, fpcomparator_26_p4
  // FPComparator #(.fpwidth(8)) fpcomparator_27: pin names not known; wires that end beside it: argY[31:24], argZ[31:24], fpcomparator_27_p3, fpcomparator_27_p4
  // FPComparator #(.fpwidth(8)) fpcomparator_28: pin names not known; wires that end beside it: argY[23:16], argZ[23:16], fpcomparator_28_p3, fpcomparator_28_p4
  // FPComparator #(.fpwidth(8)) fpcomparator_29: pin names not known; wires that end beside it: argY[15:8], argZ[15:8], fpcomparator_29_p3, fpcomparator_29_p4
  // FPComparator #(.fpwidth(8)) fpcomparator_30: pin names not known; wires that end beside it: argY[7:0], argZ[7:0], fpcomparator_30_p3, fpcomparator_30_p4
  Multiplexer #(.width(8)) multiplexer_181 (
    .in0(argX[47:40]), .in1(buffer_11_out), .out(multiplexer_193_out[47:40]), .sel(not_11_out));
  Multiplexer #(.width(8)) multiplexer_182 (
    .in0(argX[39:32]), .in1(buffer_12_out), .out(multiplexer_193_out[39:32]), .sel(not_12_out));
  assign buffer_11_out = argY[47:40];  // Buffer buffer_11, 8 bits wide
  assign buffer_12_out = argY[39:32];  // Buffer buffer_12, 8 bits wide
  Multiplexer #(.width(8)) multiplexer_183 (
    .in0({8{1'b0}}), .in1(8'h1), .out(multiplexer_186_out[15:8]), .sel(fpcomparator_21_p3));
  Multiplexer #(.width(8)) multiplexer_184 (
    .in0({8{1'b0}}), .in1(8'h1), .out(multiplexer_199_out[55:48]), .sel(fpcomparator_24_p3));
  Multiplexer #(.width(8)) multiplexer_185 (
    .in0(argX[31:24]), .in1(buffer_13_out), .out(multiplexer_193_out[31:24]), .sel(not_13_out));
  assign buffer_13_out = argY[31:24];  // Buffer buffer_13, 8 bits wide
  Multiplexer #(.width(8)) multiplexer_186 (
    .in0({8{1'b0}}), .in1(8'h1), .out(multiplexer_186_out[7:0]), .sel(fpcomparator_22_p3));
  Multiplexer #(.width(8)) multiplexer_187 (
    .in0({8{1'b0}}), .in1(8'h1), .out(multiplexer_199_out[47:40]), .sel(fpcomparator_25_p3));
  Multiplexer #(.width(8)) multiplexer_188 (
    .in0({8{1'b0}}), .in1(8'h1), .out(multiplexer_199_out[39:32]), .sel(fpcomparator_26_p3));
  Multiplexer #(.width(8)) multiplexer_189 (
    .in0(argX[23:16]), .in1(buffer_14_out), .out(multiplexer_193_out[23:16]), .sel(not_14_out));
  assign buffer_14_out = argY[23:16];  // Buffer buffer_14, 8 bits wide
  Multiplexer #(.width(8)) multiplexer_190 (
    .in0({8{1'b0}}), .in1(8'h1), .out(multiplexer_205_out[63:56]), .sel(fpcomparator_15_p4));
  Multiplexer #(.width(8)) multiplexer_191 (
    .in0({8{1'b0}}), .in1(8'h1), .out(multiplexer_199_out[31:24]), .sel(fpcomparator_27_p3));
  Multiplexer #(.width(8)) multiplexer_192 (
    .in0(argX[15:8]), .in1(buffer_15_out), .out(multiplexer_193_out[15:8]), .sel(not_15_out));
  Multiplexer #(.width(8)) multiplexer_193 (
    .in0(argX[7:0]), .in1(buffer_16_out), .out(multiplexer_193_out[7:0]), .sel(not_16_out));
  assign buffer_15_out = argY[15:8];  // Buffer buffer_15, 8 bits wide
  assign buffer_16_out = argY[7:0];  // Buffer buffer_16, 8 bits wide
  Multiplexer #(.width(8)) multiplexer_194 (
    .in0({8{1'b0}}), .in1(8'h1), .out(multiplexer_205_out[55:48]), .sel(fpcomparator_16_p4));
  Multiplexer #(.width(8)) multiplexer_195 (
    .in0({8{1'b0}}), .in1(8'h1), .out(multiplexer_199_out[23:16]), .sel(fpcomparator_28_p3));
  Multiplexer #(.width(8)) multiplexer_196 (
    .in0({8{1'b0}}), .in1(8'h1), .out(multiplexer_205_out[47:40]), .sel(fpcomparator_17_p4));
  Multiplexer #(.width(8)) multiplexer_197 (
    .in0({8{1'b0}}), .in1(8'h1), .out(multiplexer_205_out[39:32]), .sel(fpcomparator_18_p4));
  Multiplexer #(.width(8)) multiplexer_198 (
    .in0({8{1'b0}}), .in1(8'h1), .out(multiplexer_199_out[15:8]), .sel(fpcomparator_29_p3));
  Multiplexer #(.width(8)) multiplexer_199 (
    .in0({8{1'b0}}), .in1(8'h1), .out(multiplexer_199_out[7:0]), .sel(fpcomparator_30_p3));
  Multiplexer #(.width(8)) multiplexer_200 (
    .in0({8{1'b0}}), .in1(8'h1), .out(multiplexer_205_out[31:24]), .sel(fpcomparator_19_p4));
  Multiplexer #(.width(8)) multiplexer_201 (
    .in0({8{1'b0}}), .in1(8'h1), .out(multiplexer_205_out[23:16]), .sel(fpcomparator_20_p4));
  Multiplexer #(.width(8)) multiplexer_202 (
    .in0({8{1'b0}}), .in1(8'h1), .out(multiplexer_211_out[63:56]), .sel(fpcomparator_23_p4));
  Multiplexer #(.width(8)) multiplexer_203 (
    .in0({8{1'b0}}), .in1(8'h1), .out(multiplexer_211_out[55:48]), .sel(fpcomparator_24_p4));
  Multiplexer #(.width(8)) multiplexer_204 (
    .in0({8{1'b0}}), .in1(8'h1), .out(multiplexer_205_out[15:8]), .sel(fpcomparator_21_p4));
  Multiplexer #(.width(8)) multiplexer_205 (
    .in0({8{1'b0}}), .in1(8'h1), .out(multiplexer_205_out[7:0]), .sel(fpcomparator_22_p4));
  Multiplexer #(.width(8)) multiplexer_206 (
    .in0({8{1'b0}}), .in1(8'h1), .out(multiplexer_211_out[47:40]), .sel(fpcomparator_25_p4));
  Multiplexer #(.width(8)) multiplexer_207 (
    .in0({8{1'b0}}), .in1(8'h1), .out(multiplexer_211_out[39:32]), .sel(fpcomparator_26_p4));
  Multiplexer #(.width(8)) multiplexer_208 (
    .in0({8{1'b0}}), .in1(8'h1), .out(multiplexer_211_out[31:24]), .sel(fpcomparator_27_p4));
  Multiplexer #(.width(8)) multiplexer_209 (
    .in0({8{1'b0}}), .in1(8'h1), .out(multiplexer_211_out[23:16]), .sel(fpcomparator_28_p4));
  Multiplexer #(.width(8)) multiplexer_210 (
    .in0({8{1'b0}}), .in1(8'h1), .out(multiplexer_211_out[15:8]), .sel(fpcomparator_29_p4));
  assign bit_extender_134_out[63:56] = {{7{1'b0}}, fpclassificator_14_p2};  // Bit_Extender bit_extender_127
  // FPClassificator #(.fpwidth(8)) fpclassificator_14: pin names not known; wires that end beside it: argY[63:56], fpclassificator_14_p2
  assign bit_extender_134_out[55:48] = {{7{1'b0}}, fpclassificator_15_p2};  // Bit_Extender bit_extender_128
  // FPClassificator #(.fpwidth(8)) fpclassificator_15: pin names not known; wires that end beside it: argY[55:48], fpclassificator_15_p2
  assign bit_extender_134_out[47:40] = {{7{1'b0}}, fpclassificator_16_p2};  // Bit_Extender bit_extender_129
  // FPClassificator #(.fpwidth(8)) fpclassificator_16: pin names not known; wires that end beside it: argY[47:40], fpclassificator_16_p2
  assign bit_extender_134_out[39:32] = {{7{1'b0}}, fpclassificator_17_p2};  // Bit_Extender bit_extender_130
  // FPClassificator #(.fpwidth(8)) fpclassificator_17: pin names not known; wires that end beside it: argY[39:32], fpclassificator_17_p2
  assign bit_extender_134_out[31:24] = {{7{1'b0}}, fpclassificator_18_p2};  // Bit_Extender bit_extender_131
  // FPClassificator #(.fpwidth(8)) fpclassificator_18: pin names not known; wires that end beside it: argY[31:24], fpclassificator_18_p2
  assign bit_extender_134_out[23:16] = {{7{1'b0}}, fpclassificator_19_p2};  // Bit_Extender bit_extender_132
  // FPClassificator #(.fpwidth(8)) fpclassificator_19: pin names not known; wires that end beside it: argY[23:16], fpclassificator_19_p2
  assign bit_extender_134_out[15:8] = {{7{1'b0}}, fpclassificator_20_p2};  // Bit_Extender bit_extender_133
  // FPClassificator #(.fpwidth(8)) fpclassificator_20: pin names not known; wires that end beside it: argY[15:8], fpclassificator_20_p2
  assign bit_extender_134_out[7:0] = {{7{1'b0}}, fpclassificator_21_p2};  // Bit_Extender bit_extender_134
  // FPClassificator #(.fpwidth(8)) fpclassificator_21: pin names not known; wires that end beside it: argY[7:0], fpclassificator_21_p2
  Multiplexer #(.width(8)) multiplexer_211 (
    .in0({8{1'b0}}), .in1(8'h1), .out(multiplexer_211_out[7:0]), .sel(fpcomparator_30_p4));
  // FPClassificator #(.fpwidth(8)) fpclassificator_22: pin names not known; wires that end beside it: argY[63:56], fpclassificator_22_p2
  // FPClassificator #(.fpwidth(8)) fpclassificator_23: pin names not known; wires that end beside it: argY[55:48], fpclassificator_23_p2
  // FPClassificator #(.fpwidth(8)) fpclassificator_24: pin names not known; wires that end beside it: argY[47:40], fpclassificator_24_p2
  // FPClassificator #(.fpwidth(8)) fpclassificator_25: pin names not known; wires that end beside it: argY[39:32], fpclassificator_25_p2
  // FPClassificator #(.fpwidth(8)) fpclassificator_26: pin names not known; wires that end beside it: argY[31:24], fpclassificator_26_p2
  // FPClassificator #(.fpwidth(8)) fpclassificator_27: pin names not known; wires that end beside it: argY[23:16], fpclassificator_27_p2
  // FPClassificator #(.fpwidth(8)) fpclassificator_28: pin names not known; wires that end beside it: argY[15:8], fpclassificator_28_p2
  // FPClassificator #(.fpwidth(8)) fpclassificator_29: pin names not known; wires that end beside it: argY[7:0], fpclassificator_29_p2, argX, argY, argZ
  assign bit_extender_142_out[63:56] = {{7{1'b0}}, fpclassificator_22_p2};  // Bit_Extender bit_extender_135
  assign bit_extender_142_out[55:48] = {{7{1'b0}}, fpclassificator_23_p2};  // Bit_Extender bit_extender_136
  assign bit_extender_142_out[47:40] = {{7{1'b0}}, fpclassificator_24_p2};  // Bit_Extender bit_extender_137
  assign bit_extender_142_out[39:32] = {{7{1'b0}}, fpclassificator_25_p2};  // Bit_Extender bit_extender_138
  assign bit_extender_142_out[31:24] = {{7{1'b0}}, fpclassificator_26_p2};  // Bit_Extender bit_extender_139
  assign bit_extender_142_out[23:16] = {{7{1'b0}}, fpclassificator_27_p2};  // Bit_Extender bit_extender_140
  assign bit_extender_142_out[15:8] = {{7{1'b0}}, fpclassificator_28_p2};  // Bit_Extender bit_extender_141
  assign bit_extender_142_out[7:0] = {{7{1'b0}}, fpclassificator_29_p2};  // Bit_Extender bit_extender_142
endmodule
